// Logisim project CS2003_U202015375_汪宇飞_LOGISIM_FPGA.circ as structural Verilog: 25 circuits, main circuit ◇单周期RISC-V
module \单周期RISC_V  (
  input  IR1,
  input  IR2,
  input  IR3,
  output RegWrite,
  output MemWrite,
  output [31:0] PC,
  output [31:0] IR,
  output [31:0] RDin,
  output [31:0] MDin,
  output [31:0] LedData
);

  wire and_3_out, and_4_out, and_5_out, and_6_out, Beq, Bltu, Bne, Branch, CLK, clock_1_out, comparator_2_eq,
       comparator_2_lt, comparator_3_eq, d_ff_1_q, ecall, Go, halt, IR1_t, IR2_t, IR3_t, IRA, IRB, IRC, JAL,
       JALR, LB, LBlow7, Ledout, nand_1_out, not_1_out, not_3_out, or_3_out, or_5_out, REMU, RST, tunnel,
       tunnel_t, URET, W1, W2, W3, \单周期硬布线控制器_1_alu_src , \单周期硬布线控制器_1_lb , \单周期硬布线控制器_1_memtoreg ,
       \单周期硬布线控制器_1_s_type ;
  wire [1:0] LB01;
  wire [3:0] \单周期硬布线控制器_1_alu_op ;
  wire [4:0] multiplexer_2_out, multiplexer_3_out;
  wire [7:0] multiplexer_9_out;
  wire [11:0] multiplexer_4_out;
  wire [12:0] CNT_num;
  wire [15:0] \总周期数 ;
  wire [19:0] shifter_2_out;
  wire [31:0] alu_1_result, bit_extender_1_out, bit_extender_2_out, bit_extender_3_out, bit_extender_4_out,
       bit_extender_5_out, BranAddr, JALAddr, JALRAddr, LBAddr, MData, multiplexer_1_out, multiplexer_5_out,
       multiplexer_7_out, multiplexer_8_out, multiplexer_10_out, not_2_out, PC_4, R1Data, R2, shifter_1_out;
  wire [31:2] multiplexer_6_out;

  Button \u_继续运行  (.out(Go));
  Button _1 (.out(IRA));
  Button _2 (.out(IRB));
  Button _3 (.out(IRC));
  LED #(.active("true")) led_1 (.in(W1));
  LED #(.active("true")) led_2 (.in(W2));
  LED #(.active("true")) led_3 (.in(W3));
  Multiplexer #(.select(3), .width(32), .disabled("Z"), .enable("false")) multiplexer_1 (
    .in0(PC_4), .in1(BranAddr), .in2(JALAddr), .in4(JALRAddr), .out(multiplexer_1_out),
    .sel({JALR, JAL, Branch}));  // open: in3, in5, in6, in7
  Hex_Digit_Display hex_digit_display_1 (.value(LedData[31:28]));  // open: dp
  Register #(.width(32), .trigger("rising"), .Select("low")) u_PC (
    .D(multiplexer_1_out), .en(not_1_out), .Q(PC), .clk(CLK), .clr(RST));
  not not_1 (not_1_out, halt);
  Hex_Digit_Display hex_digit_display_2 (.value(LedData[27:24]));  // open: dp
  Hex_Digit_Display hex_digit_display_3 (.value(LedData[23:20]));  // open: dp
  Hex_Digit_Display hex_digit_display_4 (.value(LedData[15:12]));  // open: dp
  Hex_Digit_Display hex_digit_display_5 (.value(LedData[19:16]));  // open: dp
  // RiscV_Probe riscv_probe_1: pin names not known; wires that end beside it: IR
  Adder #(.width(32)) adder_1 (.a(PC), .b(32'h4), .out(PC_4));  // open: cin, cout
  Hex_Digit_Display hex_digit_display_6 (.value(LedData[7:4]));  // open: dp
  Hex_Digit_Display hex_digit_display_7 (.value(LedData[11:8]));  // open: dp
  // Probe on \总周期数 
  and and_1 (LB, LBlow7, \单周期硬布线控制器_1_lb );
  ROM #(.addrWidth(10), .dataWidth(32), .Select("high")) rom_1 (.addr(PC[11:2]), .data(IR));
  Hex_Digit_Display hex_digit_display_8 (.value(LedData[3:0]));  // open: dp
  \单周期硬布线控制器  \u_单周期硬布线控制器_1  (
    .Funct({IR[30], IR[25], IR[14:12]}), .OP(IR[6:2]), .ALU_OP(\单周期硬布线控制器_1_alu_op ),
    .MemToReg(\单周期硬布线控制器_1_memtoreg ), .MemWrite(MemWrite), .ALU_SRC(\单周期硬布线控制器_1_alu_src ),
    .RegWrite(RegWrite), .ecall(ecall), .S_type(\单周期硬布线控制器_1_s_type ), .Jalr(JALR), .Beq(Beq), .JAL(JAL),
    .Bne(Bne), .in_3(IR[21]), .uret(URET), .BLTU(Bltu), .LB(\单周期硬布线控制器_1_lb ), .REMU(REMU));
  Multiplexer #(.select(1), .width(5), .disabled("Z"), .enable("false")) multiplexer_2 (
    .in0(IR[19:15]), .in1(5'b10001), .out(multiplexer_2_out), .sel(ecall));
  Multiplexer #(.select(1), .width(5), .disabled("Z"), .enable("false")) multiplexer_3 (
    .in0(IR[24:20]), .in1(5'b01010), .out(multiplexer_3_out), .sel(ecall));
  Multiplexer #(.select(1), .width(12), .disabled("Z"), .enable("false")) multiplexer_4 (
    .in0(IR[31:20]), .in1({IR[31:25], IR[11:7]}), .out(multiplexer_4_out), .sel(\单周期硬布线控制器_1_s_type ));
  assign bit_extender_1_out = {{20{IR[31]}}, {IR[31], IR[7], IR[30:25], IR[11:8]}};  // Bit_Extender bit_extender_1
  assign bit_extender_2_out = {{20{IR[31]}}, IR[31:20]};  // Bit_Extender bit_extender_2
  Comparator #(.width(7), .mode("twosComplement")) comparator_1 (
    .a(IR[6:0]), .b(7'b0000011), .eq(LBlow7));  // open: gt, lt
  or or_1 (IR1_t, IR1, IRA);
  assign bit_extender_3_out = {{20{multiplexer_4_out[11]}}, multiplexer_4_out};  // Bit_Extender bit_extender_3
  Shifter #(.width(32), .shift("ll")) shifter_1 (.in(bit_extender_1_out), .\dist (5'b00001), .out(shifter_1_out));
  assign bit_extender_4_out = {{12{shifter_2_out[19]}}, shifter_2_out};  // Bit_Extender bit_extender_4
  Shifter #(.width(20), .shift("ll")) shifter_2 (
    .in({IR[31], IR[19:12], IR[20], IR[30:21]}), .\dist (5'b00001), .out(shifter_2_out));
  Adder #(.width(32)) adder_2 (.a(bit_extender_2_out), .b(R1Data), .out(LBAddr));  // open: cin, cout
  or or_2 (IR2_t, IR2, IRB);
  or or_3 (or_3_out, LB, RegWrite);
  Regfile_UP regfile_up_1 (
    .Din(RDin), .Clk(CLK), .R1(R1Data), .R2(MDin), .WE(or_3_out), .W_num(IR[11:7]),
    .R1_num(multiplexer_2_out), .R2_num(multiplexer_3_out));
  Adder #(.width(32)) adder_3 (.a(shifter_1_out), .b(PC), .out(BranAddr));  // open: cin, cout
  Adder #(.width(32)) adder_4 (.a(bit_extender_4_out), .b(PC), .out(JALAddr));  // open: cin, cout
  assign JALRAddr = LBAddr & not_2_out;  // AND_Gate and_2, 32 bits wide
  assign not_2_out = ~32'h1;  // NOT_Gate not_2, 32 bits wide
  or or_4 (IR3_t, IR3, IRC);
  Multiplexer #(.select(1), .width(32), .disabled("Z"), .enable("false")) multiplexer_5 (
    .in0(MDin), .in1(bit_extender_3_out), .out(multiplexer_5_out), .sel(\单周期硬布线控制器_1_alu_src ));
  ALU alu_1 (
    .X(R1Data), .Y(multiplexer_5_out), .AluOP(\单周期硬布线控制器_1_alu_op ), .Equal(tunnel_t), .Result(alu_1_result),
    .Result_2(R2), .out_6(tunnel));  // open: out_4
  Multiplexer #(.select(1), .width(32), .disabled("Z"), .enable("false")) multiplexer_6 (
    .in0(alu_1_result), .in1(LBAddr), .out({multiplexer_6_out, LB01}), .sel(LB));
  RAM #(.addrWidth(10), .dataWidth(32), .bus("separate"), .Select("high")) ram_1 (
    .addr(multiplexer_6_out[11:2]), .din(MDin), .data(MData), .str(MemWrite), .clk(CLK), .clr(RST));  // open: sel, ld
  Multiplexer #(.select(1), .width(32), .disabled("Z"), .enable("false")) multiplexer_7 (
    .in0(alu_1_result), .in1(MData), .out(multiplexer_7_out), .sel(\单周期硬布线控制器_1_memtoreg ));
  Multiplexer #(.select(1), .width(32), .disabled("Z"), .enable("false")) multiplexer_8 (
    .in0(multiplexer_7_out), .in1(PC_4), .out(multiplexer_8_out), .sel(or_5_out));
  or or_5 (or_5_out, JAL, JALR);
  Multiplexer #(.select(2), .width(8), .disabled("Z"), .enable("false")) multiplexer_9 (
    .in0(MData[7:0]), .in1(MData[15:8]), .in2(MData[23:16]), .in3(MData[31:24]), .out(multiplexer_9_out),
    .sel(LB01));
  D_Flip_Flop #(.trigger("high"), .Pre_Clr_Positions("LEGACY"), .NegatePresetClear("false"), .enable("true"), .NewFFLayout("false")) d_ff_1 (.Q(d_ff_1_q));  // open: clk, D, Qn, preset, en, reset
  // Probe on 13'h2f
  Multiplexer #(.select(1), .width(32), .disabled("Z"), .enable("false")) multiplexer_10 (
    .in0(multiplexer_8_out), .in1(R2), .out(multiplexer_10_out), .sel(REMU));
  assign bit_extender_5_out = {{24{multiplexer_9_out[7]}}, multiplexer_9_out};  // Bit_Extender bit_extender_5
  Comparator #(.width(13), .mode("twosComplement")) comparator_2 (
    .a(CNT_num), .b(13'h2f), .eq(comparator_2_eq), .lt(comparator_2_lt));  // open: gt
  Clock #(.highDuration(1), .lowDuration(1)) clock_1 (.out(clock_1_out));
  Multiplexer #(.select(1), .width(32), .disabled("Z"), .enable("false")) multiplexer_11 (
    .in0(multiplexer_10_out), .in1(bit_extender_5_out), .out(RDin), .sel(LB));
  Counter #(.width(13), .max('h1fff), .ongoal("stay"), .trigger("rising"), .behavior("old")) counter_1 (
    .count(comparator_2_lt), .Q(CNT_num), .clk(clock_1_out));  // open: load, D, carry, clr, preset
  nand nand_1 (nand_1_out, d_ff_1_q, comparator_2_eq);
  Comparator #(.width(32), .mode("twosComplement")) comparator_3 (
    .a(R1Data), .b(32'h22), .eq(comparator_3_eq));  // open: gt, lt
  Register #(.width(32), .trigger("rising"), .Select("low")) register_1 (
    .D(MDin), .en(Ledout), .Q(LedData), .clk(CLK), .clr(RST));
  and and_3 (and_3_out, tunnel_t, Beq);
  and and_4 (and_4_out, ~tunnel_t, Bne);  // AND_Gate
  and and_5 (and_5_out, tunnel, Bltu);
  assign CLK = nand_1_out ? clock_1_out : 1'bz;  // Controlled_Buffer controlled_buffer_1
  Pull_Resistor #(.pull(1)) pull_resistor_1 (.node(CLK));
  or or_6 (Branch, and_3_out, and_4_out, and_5_out);
  and and_6 (and_6_out, ecall, ~comparator_3_eq);  // AND_Gate
  and and_7 (Ledout, ecall, comparator_3_eq);
  not not_3 (not_3_out, halt);
  Counter #(.width(16), .max('hffff), .ongoal("wrap"), .trigger("rising"), .behavior("new")) counter_2 (
    .count(not_3_out), .Q(\总周期数 ), .clk(CLK));  // open: load, D, carry, clr, preset, down
  Counter #(.width(1), .max('h1), .ongoal("wrap"), .trigger("rising"), .behavior("old")) counter_3 (
    .load(and_6_out), .D(and_6_out), .count(1'b0), .Q(halt), .clk(CLK), .clr(Go));  // open: carry, preset

  // Other names for the same wires on the sheet: R2Data[31:0] = MDin

  // Notes on the sheet:
  //   中断源
  //   中断等待指示
  //   数码管输出应该用寄存器锁存，否则显示数据只能一闪而过
  //   数码管输出
  //   指令探针
  //   指令存储器
  //   指令字
  //   contents of rom_1 (hex, n*v repeats v):
  //   100493 100006f 100493 200913 300993 100006f 100493 200913 300993 100006f 100493 200913 300993
  //   100006f 100493 200913 300993 3c8000ef 100413 100493 1f49493 900533 2200893 73 24d493 48463 fedff06f
  //   900533 2200893 73 100493 249493 900533 2200893 73 48463 fedff06f 100493 1f49493 900533 2200893 73
  //   4034d493 900533 2200893 73 4044d493 900533 2200893 73 4044d493 900533 2200893 73 4044d493 900533
  //   2200893 73 4044d493 900533 2200893 73 4044d493 900533 2200893 73 4044d493 900533 2200893 73 4044d493
  //   900533 2200893 73 100413 1f41993 41f9d993 433 c00913 300b13 140413 f47413 800293 100313 499993
  //   89e9b3 1300533 2200893 73 406282b3 fe0294e3 140413 f00f93 1f47433 1c41413 800293 100313 49d993
  //   89e9b3 1300533 2200893 73 406282b3 fe0294e3 1c45413 406b0b33 b0463 f95ff06f 2b3 fff2c293 829293
  //   ff2e293 500533 2200893 73 fff00413 493 84a023 140413 448493 84a023 140413 448493 84a023 140413
  //   448493 84a023 140413 448493 84a023 140413 448493 84a023 140413 448493 84a023 140413 448493 84a023
  //   140413 448493 84a023 140413 448493 84a023 140413 448493 84a023 140413 448493 84a023 140413 448493
  //   84a023 140413 448493 84a023 140413 448493 84a023 140413 448493 84a023 140413 448493 140413 433
  //   3c00493 42983 4aa03 149a2b3 28663 134a023 1442023 ffc48493 fe9412e3 800533 2200893 73 440413 3c00493
  //   fc9416e3 3200893 73 200293 1100493 849493 1148493 900533 2200893 73 2000e13 25484b3 900533 2200893
  //   73 fffe0e13 fe0e16e3 a00893 73 8800493 849493 4848493 8700913 891913 5490913 2997933 1091913
  //   11096913 1200533 2200893 73 a00893 73 313 1000e13 8400493 849493 8348493 400913 891913 490913 849493
  //   8248493 849493 8148493 891913 490913 891913 490913 932023 12484b3 430313 fffe0e13 fe0e18e3 2000e13
  //   313 30483 900533 2200893 73 130313 fffe0e13 fe0e14e3 a00893 73 ff100493 900533 2200893 73 148493
  //   fe9068e3 900533 2200893 73 a00893 73 a00893 73 413 140413 800533 2200893 73 240413 800533 2200893 73
  //   340413 800533 2200893 73 440413 800533 2200893 73 540413 800533 2200893 73 640413 800533 2200893 73
  //   740413 800533 2200893 73 840413 800533 2200893 2200893 73 8067
  //   JAL
  //   JALR
  //   URET
  //   Beq
  //   Bne
  //   MemToReg
  //   MemWrite
  //   AluOP
  //   AluSrcB
  //   RegWrite
  //   为方便自动评测，需要输出PC，IR，寄存器堆写如数据RDin
  //   RAM写使能MemWrite、RAM写入数据MDin等信号
  //   数据存储器
  //   控制位
  //   暂停节拍，不能为0
  //   戳工具置1进入计数暂停模式，ctrl+k时钟自动运行到对应节拍暂停
  //   ctrl+k关闭时钟连续运行，将控制位置零，进入单步调试模式调试
  //   用这个时钟源需要去掉电路中的其他时钟源
  //   可计数暂停的时钟源
endmodule

// 单周期硬布线控制器
module \单周期硬布线控制器  (
  input  [4:0] OP,
  input  [4:0] Funct,
  input  in_3,
  output [3:0] ALU_OP,
  output uret,
  output MemToReg,
  output ecall,
  output MemWrite,
  output ALU_SRC,
  output RegWrite,
  output S_type,
  output Beq,
  output Bne,
  output Jalr,
  output JAL,
  output BLTU,
  output LB,
  output REMU
);

  wire \控制信号自动生成_1_ecall ;

  \运算控制器自动生成  \u_运算控制器自动生成_1  (
    .OP2(OP[0]), .OP3(OP[1]), .OP4(OP[2]), .OP5(OP[3]), .OP6(OP[4]), .F12(Funct[0]), .F13(Funct[1]),
    .F14(Funct[2]), .F25(Funct[3]), .F30(Funct[4]), .S0(ALU_OP[0]), .S1(ALU_OP[1]), .S2(ALU_OP[2]),
    .S3(ALU_OP[3]));
  \控制信号自动生成  \u_控制信号自动生成_1  (
    .OP2(OP[0]), .OP3(OP[1]), .MemToReg(MemToReg), .OP4(OP[2]), .OP5(OP[3]), .OP6(OP[4]), .F12(Funct[0]),
    .F13(Funct[1]), .MemWrite(MemWrite), .F14(Funct[2]), .F25(Funct[3]), .F30(Funct[4]), .ALU_SRC(ALU_SRC),
    .RegWrite(RegWrite), .ecall(\控制信号自动生成_1_ecall ), .S_Type(S_type), .BEQ(Beq), .BNE(Bne), .JALR(Jalr),
    .JAL(JAL), .BLTU(BLTU), .LB(LB), .REMU(REMU));
  and and_1 (uret, in_3, \控制信号自动生成_1_ecall );
  and and_2 (ecall, ~in_3, \控制信号自动生成_1_ecall );  // AND_Gate

  // Other names for the same wires on the sheet: IR21 = in_3; OP_CODE[4:0] = OP

  // Notes on the sheet:
  //   运算器控制器，根据指令生成运算器功能选择信号
  //   控制信号生成，产生数据通路需要的其他控制信号
endmodule

// 运算器控制器
module \运算控制器自动生成  (
  input  OP2,
  input  OP3,
  input  OP4,
  input  OP5,
  input  OP6,
  input  F12,
  input  F13,
  input  F14,
  input  F25,
  input  F30,
  output S0,
  output S1,
  output S2,
  output S3
);

  wire and_1_out, and_2_out, and_3_out, and_4_out, and_5_out, and_6_out, and_7_out, and_8_out, and_9_out,
       and_10_out, and_11_out, and_12_out, and_13_out, and_14_out, and_15_out, and_16_out, and_17_out,
       and_18_out, and_19_out, and_20_out, and_21_out, and_22_out, and_23_out, and_24_out, and_25_out,
       and_26_out, and_27_out, and_28_out, and_29_out, and_30_out, and_31_out, and_32_out, and_33_out,
       and_34_out, and_35_out, and_36_out, and_37_out, and_38_out, and_39_out, not_1_out, not_2_out,
       not_3_out, not_4_out, not_5_out, not_6_out, not_7_out, not_8_out, not_9_out, not_10_out, not_11_out,
       not_12_out, not_13_out, not_14_out, not_15_out, not_16_out, not_17_out, not_18_out, not_19_out,
       not_20_out, not_21_out, not_22_out, not_23_out, not_24_out, not_25_out, not_26_out, not_27_out,
       not_28_out, not_29_out, not_30_out, not_31_out, not_32_out, not_33_out, not_34_out, not_35_out,
       not_36_out, not_37_out, not_38_out, not_39_out, not_40_out, not_41_out, not_42_out, not_43_out,
       not_44_out, not_45_out, not_46_out, not_47_out, not_48_out, not_49_out, not_50_out, not_51_out,
       not_52_out, not_53_out, not_54_out, not_55_out, not_56_out, not_57_out, not_58_out, not_59_out,
       not_60_out, not_61_out, not_62_out, not_63_out, not_64_out, not_65_out, not_66_out, not_67_out,
       not_68_out, not_69_out, not_70_out, not_71_out, not_72_out, not_73_out, not_74_out, not_75_out,
       not_76_out, not_77_out, not_78_out, not_79_out, not_80_out, not_81_out, not_82_out, not_83_out,
       not_84_out, not_85_out, not_86_out, not_87_out, not_88_out, not_89_out, not_90_out, not_91_out,
       not_92_out, not_93_out, not_94_out, not_95_out, not_96_out, not_97_out, not_98_out, not_99_out,
       not_100_out, not_101_out, not_102_out, not_103_out, not_104_out, not_105_out, not_106_out,
       not_107_out, not_108_out, not_109_out, not_110_out, not_111_out, not_112_out, not_113_out,
       not_114_out, not_115_out, not_116_out, not_117_out, not_118_out, not_119_out, not_120_out,
       not_121_out, not_122_out, not_123_out, not_124_out, not_125_out, not_126_out, not_127_out,
       not_128_out, not_129_out, not_130_out, not_131_out, not_132_out, not_133_out, not_134_out,
       not_135_out, not_136_out, not_137_out, not_138_out, not_139_out, not_140_out, not_141_out,
       not_142_out, not_143_out, not_144_out, not_145_out, not_146_out, not_147_out, not_148_out,
       not_149_out, not_150_out, not_151_out, not_152_out, not_153_out, not_154_out, not_155_out,
       not_156_out, not_157_out, not_158_out, not_159_out, not_160_out, not_161_out, not_162_out,
       not_163_out, not_164_out, not_165_out, not_166_out, not_167_out, not_168_out, not_169_out,
       not_170_out, not_171_out, not_172_out, not_173_out, not_174_out, not_175_out, not_176_out,
       not_177_out, not_178_out, not_179_out, not_180_out, not_181_out, not_182_out, not_183_out,
       not_184_out, not_185_out, not_186_out, not_187_out, not_188_out, not_189_out, not_190_out,
       not_191_out, not_192_out, not_193_out, not_194_out, not_195_out, not_196_out, not_197_out,
       not_198_out, not_199_out, not_200_out, not_201_out, not_202_out, not_203_out, not_204_out,
       not_205_out, not_206_out, not_207_out, not_208_out, not_209_out, not_210_out, not_211_out,
       not_212_out, not_213_out, not_214_out, not_215_out, not_216_out, not_217_out, not_218_out, not_219_out;

  not not_1 (not_1_out, F30);
  not not_2 (not_2_out, F25);
  not not_3 (not_3_out, F14);
  not not_4 (not_4_out, F13);
  not not_5 (not_5_out, F12);
  not not_6 (not_6_out, OP6);
  not not_7 (not_7_out, OP3);
  not not_8 (not_8_out, OP2);
  not not_9 (not_9_out, F30);
  not not_10 (not_10_out, F25);
  not not_11 (not_11_out, OP6);
  not not_12 (not_12_out, OP3);
  not not_13 (not_13_out, OP2);
  not not_14 (not_14_out, F30);
  not not_15 (not_15_out, F25);
  not not_16 (not_16_out, F14);
  not not_17 (not_17_out, F12);
  not not_18 (not_18_out, OP6);
  not not_19 (not_19_out, OP3);
  not not_20 (not_20_out, OP2);
  not not_21 (not_21_out, F14);
  not not_22 (not_22_out, F13);
  not not_23 (not_23_out, F12);
  not not_24 (not_24_out, OP6);
  not not_25 (not_25_out, OP5);
  not not_26 (not_26_out, OP3);
  not not_27 (not_27_out, OP2);
  not not_28 (not_28_out, OP6);
  not not_29 (not_29_out, OP5);
  not not_30 (not_30_out, OP3);
  not not_31 (not_31_out, OP2);
  not not_32 (not_32_out, F13);
  not not_33 (not_33_out, F12);
  not not_34 (not_34_out, OP6);
  not not_35 (not_35_out, OP5);
  not not_36 (not_36_out, OP3);
  not not_37 (not_37_out, OP2);
  not not_38 (not_38_out, F14);
  not not_39 (not_39_out, F12);
  not not_40 (not_40_out, OP6);
  not not_41 (not_41_out, OP5);
  not not_42 (not_42_out, OP3);
  not not_43 (not_43_out, OP2);
  not not_44 (not_44_out, F25);
  not not_45 (not_45_out, F13);
  not not_46 (not_46_out, OP6);
  not not_47 (not_47_out, OP5);
  not not_48 (not_48_out, OP3);
  not not_49 (not_49_out, OP2);
  not not_50 (not_50_out, F14);
  not not_51 (not_51_out, F12);
  not not_52 (not_52_out, OP6);
  not not_53 (not_53_out, OP5);
  not not_54 (not_54_out, OP4);
  not not_55 (not_55_out, OP3);
  not not_56 (not_56_out, OP2);
  not not_57 (not_57_out, F14);
  not not_58 (not_58_out, F12);
  not not_59 (not_59_out, OP6);
  not not_60 (not_60_out, OP4);
  not not_61 (not_61_out, OP3);
  not not_62 (not_62_out, OP2);
  not not_63 (not_63_out, OP3);
  not not_64 (not_64_out, OP2);
  not not_65 (not_65_out, F30);
  not not_66 (not_66_out, F14);
  not not_67 (not_67_out, F13);
  not not_68 (not_68_out, F12);
  not not_69 (not_69_out, OP6);
  not not_70 (not_70_out, OP3);
  not not_71 (not_71_out, OP2);
  not not_72 (not_72_out, F25);
  not not_73 (not_73_out, F14);
  not not_74 (not_74_out, F13);
  not not_75 (not_75_out, F12);
  not not_76 (not_76_out, OP6);
  not not_77 (not_77_out, OP3);
  not not_78 (not_78_out, OP2);
  not not_79 (not_79_out, F30);
  not not_80 (not_80_out, F25);
  not not_81 (not_81_out, OP6);
  not not_82 (not_82_out, OP3);
  not not_83 (not_83_out, OP2);
  not not_84 (not_84_out, F30);
  not not_85 (not_85_out, F25);
  not not_86 (not_86_out, F14);
  not not_87 (not_87_out, F12);
  not not_88 (not_88_out, OP6);
  not not_89 (not_89_out, OP3);
  not not_90 (not_90_out, OP2);
  not not_91 (not_91_out, OP6);
  not not_92 (not_92_out, OP5);
  not not_93 (not_93_out, OP3);
  not not_94 (not_94_out, OP2);
  not not_95 (not_95_out, F14);
  not not_96 (not_96_out, F12);
  not not_97 (not_97_out, OP6);
  not not_98 (not_98_out, OP5);
  not not_99 (not_99_out, OP3);
  not not_100 (not_100_out, OP2);
  not not_101 (not_101_out, F30);
  not not_102 (not_102_out, F25);
  not not_103 (not_103_out, F13);
  not not_104 (not_104_out, OP6);
  not not_105 (not_105_out, OP5);
  not not_106 (not_106_out, OP3);
  not not_107 (not_107_out, OP2);
  not not_108 (not_108_out, OP3);
  not not_109 (not_109_out, OP2);
  not not_110 (not_110_out, F30);
  not not_111 (not_111_out, F14);
  not not_112 (not_112_out, F13);
  not not_113 (not_113_out, F12);
  not not_114 (not_114_out, OP6);
  not not_115 (not_115_out, OP3);
  not not_116 (not_116_out, OP2);
  not not_117 (not_117_out, F30);
  not not_118 (not_118_out, F25);
  not not_119 (not_119_out, F14);
  not not_120 (not_120_out, F13);
  not not_121 (not_121_out, F12);
  not not_122 (not_122_out, OP6);
  not not_123 (not_123_out, OP3);
  not not_124 (not_124_out, OP2);
  not not_125 (not_125_out, F25);
  not not_126 (not_126_out, F14);
  not not_127 (not_127_out, F13);
  not not_128 (not_128_out, F12);
  not not_129 (not_129_out, OP6);
  not not_130 (not_130_out, OP3);
  not not_131 (not_131_out, OP2);
  not not_132 (not_132_out, F30);
  not not_133 (not_133_out, F25);
  not not_134 (not_134_out, OP6);
  not not_135 (not_135_out, OP3);
  not not_136 (not_136_out, OP2);
  not not_137 (not_137_out, F30);
  not not_138 (not_138_out, F25);
  not not_139 (not_139_out, F14);
  not not_140 (not_140_out, OP6);
  not not_141 (not_141_out, OP3);
  not not_142 (not_142_out, OP2);
  not not_143 (not_143_out, F14);
  not not_144 (not_144_out, F13);
  not not_145 (not_145_out, F12);
  not not_146 (not_146_out, OP6);
  not not_147 (not_147_out, OP5);
  not not_148 (not_148_out, OP3);
  not not_149 (not_149_out, OP2);
  not not_150 (not_150_out, OP6);
  not not_151 (not_151_out, OP5);
  not not_152 (not_152_out, OP3);
  not not_153 (not_153_out, OP2);
  not not_154 (not_154_out, F14);
  not not_155 (not_155_out, F12);
  not not_156 (not_156_out, OP6);
  not not_157 (not_157_out, OP5);
  not not_158 (not_158_out, OP4);
  not not_159 (not_159_out, OP3);
  not not_160 (not_160_out, OP2);
  not not_161 (not_161_out, F14);
  not not_162 (not_162_out, F12);
  not not_163 (not_163_out, OP6);
  not not_164 (not_164_out, OP4);
  not not_165 (not_165_out, OP3);
  not not_166 (not_166_out, OP2);
  not not_167 (not_167_out, OP3);
  not not_168 (not_168_out, OP2);
  not not_169 (not_169_out, F30);
  not not_170 (not_170_out, OP6);
  not not_171 (not_171_out, OP3);
  not not_172 (not_172_out, OP2);
  not not_173 (not_173_out, F12);
  not not_174 (not_174_out, OP4);
  not not_175 (not_175_out, OP3);
  not not_176 (not_176_out, OP2);
  not not_177 (not_177_out, F30);
  not not_178 (not_178_out, F25);
  not not_179 (not_179_out, F12);
  not not_180 (not_180_out, OP6);
  not not_181 (not_181_out, OP3);
  not not_182 (not_182_out, OP2);
  not not_183 (not_183_out, F30);
  not not_184 (not_184_out, F25);
  not not_185 (not_185_out, F14);
  not not_186 (not_186_out, F12);
  not not_187 (not_187_out, OP6);
  not not_188 (not_188_out, OP3);
  not not_189 (not_189_out, OP2);
  not not_190 (not_190_out, F30);
  not not_191 (not_191_out, F25);
  not not_192 (not_192_out, F14);
  not not_193 (not_193_out, OP6);
  not not_194 (not_194_out, OP3);
  not not_195 (not_195_out, OP2);
  not not_196 (not_196_out, F12);
  not not_197 (not_197_out, OP6);
  not not_198 (not_198_out, OP5);
  not not_199 (not_199_out, OP3);
  not not_200 (not_200_out, OP2);
  not not_201 (not_201_out, F13);
  not not_202 (not_202_out, F12);
  not not_203 (not_203_out, OP6);
  not not_204 (not_204_out, OP5);
  not not_205 (not_205_out, OP3);
  not not_206 (not_206_out, OP2);
  not not_207 (not_207_out, F14);
  not not_208 (not_208_out, F12);
  not not_209 (not_209_out, OP6);
  not not_210 (not_210_out, OP5);
  not not_211 (not_211_out, OP3);
  not not_212 (not_212_out, OP2);
  not not_213 (not_213_out, F12);
  not not_214 (not_214_out, OP3);
  not not_215 (not_215_out, OP2);
  not not_216 (not_216_out, F12);
  not not_217 (not_217_out, OP4);
  not not_218 (not_218_out, OP3);
  not not_219 (not_219_out, OP2);
  and and_1 (and_1_out, not_1_out, not_2_out, not_3_out, not_4_out, not_5_out, not_6_out, OP5, OP4, not_7_out, not_8_out);
  and and_2 (and_2_out, not_9_out, not_10_out, F14, F13, F12, not_11_out, OP5, OP4, not_12_out, not_13_out);
  and and_3 (and_3_out, not_14_out, not_15_out, not_16_out, F13, not_17_out, not_18_out, OP5, OP4, not_19_out, not_20_out);
  and and_4 (and_4_out, not_21_out, not_22_out, not_23_out, not_24_out, not_25_out, OP4, not_26_out, not_27_out);
  and and_5 (and_5_out, F14, F13, F12, not_28_out, not_29_out, OP4, not_30_out, not_31_out);
  and and_6 (and_6_out, F14, not_32_out, not_33_out, not_34_out, not_35_out, OP4, not_36_out, not_37_out);
  and and_7 (and_7_out, not_38_out, F13, not_39_out, not_40_out, not_41_out, OP4, not_42_out, not_43_out);
  and and_8 (and_8_out, F30, not_44_out, F14, not_45_out, F12, not_46_out, not_47_out, OP4, not_48_out, not_49_out);
  and and_9 (and_9_out, not_50_out, F13, not_51_out, not_52_out, not_53_out, not_54_out, not_55_out, not_56_out);
  and and_10 (and_10_out, not_57_out, F13, not_58_out, not_59_out, OP5, not_60_out, not_61_out, not_62_out);
  and and_11 (and_11_out, F14, F13, F12, OP6, OP5, OP4, not_63_out, not_64_out);
  and and_12 (and_12_out, not_65_out, F25, not_66_out, not_67_out, not_68_out, not_69_out, OP5, OP4, not_70_out, not_71_out);
  and and_13 (and_13_out, F30, not_72_out, not_73_out, not_74_out, not_75_out, not_76_out, OP5, OP4, not_77_out, not_78_out);
  and and_14 (and_14_out, not_79_out, not_80_out, F14, F13, F12, not_81_out, OP5, OP4, not_82_out, not_83_out);
  and and_15 (and_15_out, not_84_out, not_85_out, not_86_out, F13, not_87_out, not_88_out, OP5, OP4, not_89_out, not_90_out);
  and and_16 (and_16_out, F14, F13, F12, not_91_out, not_92_out, OP4, not_93_out, not_94_out);
  and and_17 (and_17_out, not_95_out, F13, not_96_out, not_97_out, not_98_out, OP4, not_99_out, not_100_out);
  and and_18 (and_18_out, not_101_out, not_102_out, F14, not_103_out, F12, not_104_out, not_105_out, OP4, not_106_out, not_107_out);
  and and_19 (and_19_out, F14, F13, F12, OP6, OP5, OP4, not_108_out, not_109_out);
  and and_20 (and_20_out, not_110_out, F25, not_111_out, not_112_out, not_113_out, not_114_out, OP5, OP4, not_115_out, not_116_out);
  and and_21 (and_21_out, not_117_out, not_118_out, not_119_out, not_120_out, not_121_out, not_122_out, OP5, OP4, not_123_out, not_124_out);
  and and_22 (and_22_out, F30, not_125_out, not_126_out, not_127_out, not_128_out, not_129_out, OP5, OP4, not_130_out, not_131_out);
  and and_23 (and_23_out, not_132_out, not_133_out, F14, F13, F12, not_134_out, OP5, OP4, not_135_out, not_136_out);
  and and_24 (and_24_out, not_137_out, not_138_out, not_139_out, F13, F12, not_140_out, OP5, OP4, not_141_out, not_142_out);
  and and_25 (and_25_out, not_143_out, not_144_out, not_145_out, not_146_out, not_147_out, OP4, not_148_out, not_149_out);
  and and_26 (and_26_out, F14, F13, F12, not_150_out, not_151_out, OP4, not_152_out, not_153_out);
  and and_27 (and_27_out, not_154_out, F13, not_155_out, not_156_out, not_157_out, not_158_out, not_159_out, not_160_out);
  and and_28 (and_28_out, not_161_out, F13, not_162_out, not_163_out, OP5, not_164_out, not_165_out, not_166_out);
  and and_29 (and_29_out, F14, F13, F12, OP6, OP5, OP4, not_167_out, not_168_out);
  and and_30 (and_30_out, not_169_out, F25, F14, F13, F12, not_170_out, OP5, OP4, not_171_out, not_172_out);
  and and_31 (and_31_out, F14, F13, not_173_out, OP6, OP5, not_174_out, not_175_out, not_176_out);
  and and_32 (and_32_out, not_177_out, not_178_out, F14, F13, not_179_out, not_180_out, OP5, OP4, not_181_out, not_182_out);
  and and_33 (and_33_out, not_183_out, not_184_out, not_185_out, F13, not_186_out, not_187_out, OP5, OP4, not_188_out, not_189_out);
  and and_34 (and_34_out, not_190_out, not_191_out, not_192_out, F13, F12, not_193_out, OP5, OP4, not_194_out, not_195_out);
  and and_35 (and_35_out, F14, F13, not_196_out, not_197_out, not_198_out, OP4, not_199_out, not_200_out);
  and and_36 (and_36_out, F14, not_201_out, not_202_out, not_203_out, not_204_out, OP4, not_205_out, not_206_out);
  and and_37 (and_37_out, not_207_out, F13, not_208_out, not_209_out, not_210_out, OP4, not_211_out, not_212_out);
  and and_38 (and_38_out, F14, F13, not_213_out, OP6, OP5, OP4, not_214_out, not_215_out);
  and and_39 (and_39_out, F14, F13, not_216_out, OP6, OP5, not_217_out, not_218_out, not_219_out);
  or or_1 (S0, and_1_out, and_2_out, and_3_out, and_4_out, and_5_out, and_6_out, and_7_out, and_8_out, and_9_out, and_10_out, and_11_out, and_12_out);
  or or_2 (S1, and_13_out, and_14_out, and_15_out, and_16_out, and_17_out, and_18_out, and_19_out, and_20_out);
  or or_3 (S2, and_21_out, and_22_out, and_23_out, and_24_out, and_25_out, and_26_out, and_27_out, and_28_out, and_29_out, and_30_out, and_31_out);
  or or_4 (S3, and_32_out, and_33_out, and_34_out, and_35_out, and_36_out, and_37_out, and_38_out, and_39_out);
endmodule

// 控制信号生成
module \控制信号自动生成  (
  input  OP2,
  input  OP3,
  input  OP4,
  input  OP5,
  input  OP6,
  input  F12,
  input  F13,
  input  F14,
  input  F25,
  input  F30,
  output MemToReg,
  output MemWrite,
  output ALU_SRC,
  output RegWrite,
  output ecall,
  output S_Type,
  output BEQ,
  output BNE,
  output JALR,
  output JAL,
  output BLTU,
  output LB,
  output REMU
);

  wire and_3_out, and_4_out, and_5_out, and_6_out, and_7_out, and_8_out, and_9_out, and_10_out, and_11_out,
       and_12_out, and_13_out, and_14_out, and_15_out, and_16_out, and_17_out, and_18_out, and_19_out,
       and_20_out, and_21_out, and_22_out, and_23_out, not_1_out, not_2_out, not_3_out, not_4_out, not_5_out,
       not_6_out, not_7_out, not_8_out, not_9_out, not_10_out, not_11_out, not_12_out, not_13_out,
       not_14_out, not_15_out, not_16_out, not_17_out, not_18_out, not_19_out, not_20_out, not_21_out,
       not_22_out, not_23_out, not_24_out, not_25_out, not_26_out, not_27_out, not_28_out, not_29_out,
       not_30_out, not_31_out, not_32_out, not_33_out, not_34_out, not_35_out, not_36_out, not_37_out,
       not_38_out, not_39_out, not_40_out, not_41_out, not_42_out, not_43_out, not_44_out, not_45_out,
       not_46_out, not_47_out, not_48_out, not_49_out, not_50_out, not_51_out, not_52_out, not_53_out,
       not_54_out, not_55_out, not_56_out, not_57_out, not_58_out, not_59_out, not_60_out, not_61_out,
       not_62_out, not_63_out, not_64_out, not_65_out, not_66_out, not_67_out, not_68_out, not_69_out,
       not_70_out, not_71_out, not_72_out, not_73_out, not_74_out, not_75_out, not_76_out, not_77_out,
       not_78_out, not_79_out, not_80_out, not_81_out, not_82_out, not_83_out, not_84_out, not_85_out,
       not_86_out, not_87_out, not_88_out, not_89_out, not_90_out, not_91_out, not_92_out, not_93_out,
       not_94_out, not_95_out, not_96_out, not_97_out, not_98_out, not_99_out, not_100_out, not_101_out,
       not_102_out, not_103_out, not_104_out, not_105_out, not_106_out, not_107_out, not_108_out,
       not_109_out, not_110_out, not_111_out, not_112_out, not_113_out, not_114_out, not_115_out,
       not_116_out, not_117_out, not_118_out, not_119_out, not_120_out, not_121_out, not_122_out,
       not_123_out, not_124_out, not_125_out, not_126_out, not_127_out, not_128_out, not_129_out,
       not_130_out, not_131_out, not_132_out, not_133_out, not_134_out, not_135_out, not_136_out,
       not_137_out, not_138_out, not_139_out, not_140_out, not_141_out, not_142_out, not_143_out,
       not_144_out, not_145_out, not_146_out, not_147_out, not_148_out, not_149_out, not_150_out,
       not_151_out, not_152_out, not_153_out, not_154_out, not_155_out, not_156_out, not_157_out,
       not_158_out, not_159_out, not_160_out, not_161_out, not_162_out, not_163_out, not_164_out,
       not_165_out, not_166_out, not_167_out, not_168_out, not_169_out, not_170_out, not_171_out,
       not_172_out, not_173_out, not_174_out;

  not not_1 (not_1_out, OP2);
  not not_2 (not_2_out, OP3);
  not not_3 (not_3_out, OP4);
  not not_4 (not_4_out, OP5);
  not not_5 (not_5_out, OP6);
  not not_6 (not_6_out, F12);
  not not_7 (not_7_out, F14);
  not not_8 (not_8_out, OP2);
  not not_9 (not_9_out, OP3);
  not not_10 (not_10_out, OP4);
  not not_11 (not_11_out, OP6);
  not not_12 (not_12_out, F12);
  not not_13 (not_13_out, F14);
  not not_14 (not_14_out, F14);
  not not_15 (not_15_out, F13);
  not not_16 (not_16_out, F12);
  not not_17 (not_17_out, OP6);
  not not_18 (not_18_out, OP5);
  not not_19 (not_19_out, OP3);
  not not_20 (not_20_out, OP2);
  not not_21 (not_21_out, OP6);
  not not_22 (not_22_out, OP5);
  not not_23 (not_23_out, OP3);
  not not_24 (not_24_out, OP2);
  not not_25 (not_25_out, F12);
  not not_26 (not_26_out, OP6);
  not not_27 (not_27_out, OP5);
  not not_28 (not_28_out, OP3);
  not not_29 (not_29_out, OP2);
  not not_30 (not_30_out, F13);
  not not_31 (not_31_out, F12);
  not not_32 (not_32_out, OP6);
  not not_33 (not_33_out, OP5);
  not not_34 (not_34_out, OP3);
  not not_35 (not_35_out, OP2);
  not not_36 (not_36_out, F14);
  not not_37 (not_37_out, F12);
  not not_38 (not_38_out, OP6);
  not not_39 (not_39_out, OP5);
  not not_40 (not_40_out, OP3);
  not not_41 (not_41_out, OP2);
  not not_42 (not_42_out, F30);
  not not_43 (not_43_out, F25);
  not not_44 (not_44_out, F14);
  not not_45 (not_45_out, F13);
  not not_46 (not_46_out, OP6);
  not not_47 (not_47_out, OP5);
  not not_48 (not_48_out, OP3);
  not not_49 (not_49_out, OP2);
  not not_50 (not_50_out, F30);
  not not_51 (not_51_out, F25);
  not not_52 (not_52_out, F13);
  not not_53 (not_53_out, OP6);
  not not_54 (not_54_out, OP5);
  not not_55 (not_55_out, OP3);
  not not_56 (not_56_out, OP2);
  not not_57 (not_57_out, F25);
  not not_58 (not_58_out, F13);
  not not_59 (not_59_out, OP6);
  not not_60 (not_60_out, OP5);
  not not_61 (not_61_out, OP3);
  not not_62 (not_62_out, OP2);
  not not_63 (not_63_out, F14);
  not not_64 (not_64_out, F12);
  not not_65 (not_65_out, OP6);
  not not_66 (not_66_out, OP5);
  not not_67 (not_67_out, OP4);
  not not_68 (not_68_out, OP3);
  not not_69 (not_69_out, OP2);
  not not_70 (not_70_out, F14);
  not not_71 (not_71_out, F12);
  not not_72 (not_72_out, OP6);
  not not_73 (not_73_out, OP4);
  not not_74 (not_74_out, OP3);
  not not_75 (not_75_out, OP2);
  not not_76 (not_76_out, OP2);
  not not_77 (not_77_out, OP3);
  not not_78 (not_78_out, OP5);
  not not_79 (not_79_out, OP6);
  not not_80 (not_80_out, F12);
  not not_81 (not_81_out, F14);
  not not_82 (not_82_out, OP2);
  not not_83 (not_83_out, OP3);
  not not_84 (not_84_out, OP5);
  not not_85 (not_85_out, OP6);
  not not_86 (not_86_out, F12);
  not not_87 (not_87_out, OP2);
  not not_88 (not_88_out, OP3);
  not not_89 (not_89_out, OP5);
  not not_90 (not_90_out, OP6);
  not not_91 (not_91_out, F13);
  not not_92 (not_92_out, F25);
  not not_93 (not_93_out, F30);
  not not_94 (not_94_out, OP2);
  not not_95 (not_95_out, OP3);
  not not_96 (not_96_out, OP6);
  not not_97 (not_97_out, F12);
  not not_98 (not_98_out, F13);
  not not_99 (not_99_out, F14);
  not not_100 (not_100_out, F25);
  not not_101 (not_101_out, OP2);
  not not_102 (not_102_out, OP3);
  not not_103 (not_103_out, OP6);
  not not_104 (not_104_out, F12);
  not not_105 (not_105_out, F13);
  not not_106 (not_106_out, F14);
  not not_107 (not_107_out, F30);
  not not_108 (not_108_out, OP2);
  not not_109 (not_109_out, OP3);
  not not_110 (not_110_out, OP5);
  not not_111 (not_111_out, OP6);
  not not_112 (not_112_out, F25);
  not not_113 (not_113_out, OP2);
  not not_114 (not_114_out, OP3);
  not not_115 (not_115_out, OP5);
  not not_116 (not_116_out, OP6);
  not not_117 (not_117_out, OP2);
  not not_118 (not_118_out, OP3);
  not not_119 (not_119_out, OP6);
  not not_120 (not_120_out, F30);
  not not_121 (not_121_out, OP2);
  not not_122 (not_122_out, OP3);
  not not_123 (not_123_out, OP6);
  not not_124 (not_124_out, F25);
  not not_125 (not_125_out, F30);
  not not_126 (not_126_out, OP4);
  not not_127 (not_127_out, F12);
  not not_128 (not_128_out, F13);
  not not_129 (not_129_out, F14);
  not not_130 (not_130_out, OP4);
  not not_131 (not_131_out, OP2);
  not not_132 (not_132_out, OP3);
  not not_133 (not_133_out, F12);
  not not_134 (not_134_out, F13);
  not not_135 (not_135_out, F14);
  not not_136 (not_136_out, OP2);
  not not_137 (not_137_out, OP3);
  not not_138 (not_138_out, OP4);
  not not_139 (not_139_out, OP6);
  not not_140 (not_140_out, F12);
  not not_141 (not_141_out, F14);
  not not_142 (not_142_out, OP2);
  not not_143 (not_143_out, OP3);
  not not_144 (not_144_out, OP4);
  not not_145 (not_145_out, F12);
  not not_146 (not_146_out, F13);
  not not_147 (not_147_out, F14);
  not not_148 (not_148_out, OP2);
  not not_149 (not_149_out, OP3);
  not not_150 (not_150_out, OP4);
  not not_151 (not_151_out, F13);
  not not_152 (not_152_out, F14);
  not not_153 (not_153_out, OP3);
  not not_154 (not_154_out, OP4);
  not not_155 (not_155_out, F12);
  not not_156 (not_156_out, F13);
  not not_157 (not_157_out, F14);
  not not_158 (not_158_out, OP4);
  not not_159 (not_159_out, OP2);
  not not_160 (not_160_out, OP3);
  not not_161 (not_161_out, OP4);
  not not_162 (not_162_out, F12);
  not not_163 (not_163_out, OP2);
  not not_164 (not_164_out, OP3);
  not not_165 (not_165_out, OP4);
  not not_166 (not_166_out, OP5);
  not not_167 (not_167_out, OP6);
  not not_168 (not_168_out, F12);
  not not_169 (not_169_out, F13);
  not not_170 (not_170_out, F14);
  not not_171 (not_171_out, OP2);
  not not_172 (not_172_out, OP3);
  not not_173 (not_173_out, OP6);
  not not_174 (not_174_out, F30);
  and and_1 (MemToReg, not_1_out, not_2_out, not_3_out, not_4_out, not_5_out, not_6_out, F13, not_7_out);
  and and_2 (MemWrite, not_8_out, not_9_out, not_10_out, OP5, not_11_out, not_12_out, F13, not_13_out);
  and and_3 (and_3_out, not_14_out, not_15_out, not_16_out, not_17_out, not_18_out, OP4, not_19_out, not_20_out);
  and and_4 (and_4_out, F14, F13, F12, not_21_out, not_22_out, OP4, not_23_out, not_24_out);
  and and_5 (and_5_out, F14, F13, not_25_out, not_26_out, not_27_out, OP4, not_28_out, not_29_out);
  and and_6 (and_6_out, F14, not_30_out, not_31_out, not_32_out, not_33_out, OP4, not_34_out, not_35_out);
  and and_7 (and_7_out, not_36_out, F13, not_37_out, not_38_out, not_39_out, OP4, not_40_out, not_41_out);
  and and_8 (and_8_out, not_42_out, not_43_out, not_44_out, not_45_out, F12, not_46_out, not_47_out, OP4, not_48_out, not_49_out);
  and and_9 (and_9_out, not_50_out, not_51_out, F14, not_52_out, F12, not_53_out, not_54_out, OP4, not_55_out, not_56_out);
  and and_10 (and_10_out, F30, not_57_out, F14, not_58_out, F12, not_59_out, not_60_out, OP4, not_61_out, not_62_out);
  and and_11 (and_11_out, not_63_out, F13, not_64_out, not_65_out, not_66_out, not_67_out, not_68_out, not_69_out);
  and and_12 (and_12_out, not_70_out, F13, not_71_out, not_72_out, OP5, not_73_out, not_74_out, not_75_out);
  and and_13 (and_13_out, not_76_out, not_77_out, not_78_out, not_79_out, not_80_out, F13, not_81_out);
  and and_14 (and_14_out, not_82_out, not_83_out, OP4, not_84_out, not_85_out, not_86_out);
  and and_15 (and_15_out, not_87_out, not_88_out, OP4, not_89_out, not_90_out, not_91_out, not_92_out, not_93_out);
  and and_16 (and_16_out, not_94_out, not_95_out, OP4, not_96_out, not_97_out, not_98_out, not_99_out, not_100_out);
  and and_17 (and_17_out, not_101_out, not_102_out, OP4, not_103_out, not_104_out, not_105_out, not_106_out, not_107_out);
  and and_18 (and_18_out, not_108_out, not_109_out, OP4, not_110_out, not_111_out, F14, not_112_out);
  and and_19 (and_19_out, not_113_out, not_114_out, OP4, not_115_out, not_116_out, F13, F14);
  and and_20 (and_20_out, not_117_out, not_118_out, OP4, not_119_out, F12, F13, F14, not_120_out);
  and and_21 (and_21_out, not_121_out, not_122_out, OP4, OP5, not_123_out, F13, not_124_out, not_125_out);
  and and_22 (and_22_out, OP2, not_126_out, OP5, OP6, not_127_out, not_128_out, not_129_out);
  and and_23 (and_23_out, OP2, OP3, not_130_out, OP5, OP6);
  and and_24 (ecall, not_131_out, not_132_out, OP4, OP5, OP6, not_133_out, not_134_out, not_135_out);
  and and_25 (S_Type, not_136_out, not_137_out, not_138_out, OP5, not_139_out, not_140_out, F13, not_141_out);
  and and_26 (BEQ, not_142_out, not_143_out, not_144_out, OP5, OP6, not_145_out, not_146_out, not_147_out);
  and and_27 (BNE, not_148_out, not_149_out, not_150_out, OP5, OP6, F12, not_151_out, not_152_out);
  and and_28 (JALR, OP2, not_153_out, not_154_out, OP5, OP6, not_155_out, not_156_out, not_157_out);
  and and_29 (JAL, OP2, OP3, not_158_out, OP5, OP6);
  and and_30 (BLTU, not_159_out, not_160_out, not_161_out, OP5, OP6, not_162_out, F13, F14);
  and and_31 (LB, not_163_out, not_164_out, not_165_out, not_166_out, not_167_out, not_168_out, not_169_out, not_170_out);
  and and_32 (REMU, not_171_out, not_172_out, OP4, OP5, not_173_out, F12, F13, F14, F25, not_174_out);
  or or_1 (ALU_SRC, and_3_out, and_4_out, and_5_out, and_6_out, and_7_out, and_8_out, and_9_out, and_10_out, and_11_out, and_12_out);
  or or_2 (RegWrite, and_13_out, and_14_out, and_15_out, and_16_out, and_17_out, and_18_out, and_19_out, and_20_out, and_21_out, and_22_out, and_23_out);
endmodule

// ALU
module ALU (
  input  [31:0] X,
  input  [31:0] Y,
  input  [3:0] AluOP,
  output out_4,
  output Equal,
  output out_6,
  output [31:0] Result,
  output [31:0] Result_2
);

  wire [0:0] comparator_1_lt, comparator_2_lt;
  wire [31:0] adder_1_out, AND_out, divider_1_out, divider_1_rem, multiplier_1_cout, multiplier_1_out,
       NOR_out, OR_out, shifter_1_out, shifter_2_out, shifter_3_out, subtractor_1_out, XOR_out;

  assign AND_out = X & Y;  // AND_Gate AND, 32 bits wide
  assign OR_out = X | Y;  // OR_Gate OR, 32 bits wide
  Shifter #(.width(32), .shift("ll")) shifter_1 (.in(X), .\dist (Y[4:0]), .out(shifter_1_out));
  Shifter #(.width(32), .shift("ar")) shifter_2 (.in(X), .\dist (Y[4:0]), .out(shifter_2_out));
  Shifter #(.width(32), .shift("lr")) shifter_3 (.in(X), .\dist (Y[4:0]), .out(shifter_3_out));
  Multiplier #(.width(32)) multiplier_1 (.a(X), .b(Y), .out(multiplier_1_out), .cout(multiplier_1_cout));  // open: cin
  Divider #(.width(32)) divider_1 (.a(X), .b(Y), .out(divider_1_out), .rem(divider_1_rem));  // open: upper
  Adder #(.width(32)) adder_1 (.a(X), .b(Y), .out(adder_1_out));  // open: cin, cout
  Subtractor #(.width(32)) subtractor_1 (.a(X), .b(Y), .out(subtractor_1_out));  // open: bin, bout
  assign XOR_out = X ^ Y;  // XOR_Gate XOR, 32 bits wide
  assign NOR_out = ~(X | Y);  // NOR_Gate NOR, 32 bits wide
  Comparator #(.width(32), .mode("twosComplement")) comparator_1 (
    .a(X), .b(Y), .eq(Equal), .lt(comparator_1_lt[0]));  // open: gt
  Comparator #(.width(32), .mode("unsigned")) comparator_2 (.a(X), .b(Y), .lt(comparator_2_lt[0]));  // open: gt, eq
  Multiplexer #(.select(4), .width(32), .disabled("Z"), .enable("false")) multiplexer_1 (
    .in0(shifter_1_out), .in1(shifter_2_out), .in2(shifter_3_out), .in3(multiplier_1_out),
    .in4(divider_1_out), .in5(adder_1_out), .in6(subtractor_1_out), .in7(AND_out), .in8(OR_out),
    .in9(XOR_out), .in10(NOR_out), .in11({{31{1'b0}}, comparator_1_lt[0]}),
    .in12({{31{1'b0}}, comparator_2_lt[0]}), .in13({32{1'b0}}), .in14({32{1'b0}}), .in15({32{1'b0}}),
    .out(Result), .sel(AluOP));
  Multiplexer #(.select(4), .width(32), .disabled("Z"), .enable("false")) multiplexer_2 (
    .in0({32{1'b0}}), .in1({32{1'b0}}), .in2({32{1'b0}}), .in3(multiplier_1_cout), .in4(divider_1_rem),
    .in5({32{1'b0}}), .in6({32{1'b0}}), .in7({32{1'b0}}), .in8({32{1'b0}}), .in9({32{1'b0}}),
    .in10({32{1'b0}}), .in11({32{1'b0}}), .in12({32{1'b0}}), .in13({32{1'b0}}), .in14({32{1'b0}}),
    .in15({32{1'b0}}), .out(Result_2), .sel(AluOP));
  Multiplexer #(.select(4), .width(1), .disabled("Z"), .enable("false")) multiplexer_3 (
    .in0(1'b0), .in1(1'b0), .in2(1'b0), .in3(1'b0), .in4(1'b0), .in5(1'b0), .in6(1'b0), .in7(1'b0),
    .in8(1'b0), .in9(1'b0), .in10(1'b0), .in11(comparator_1_lt[0]), .in12(comparator_2_lt[0]), .in13(1'b0),
    .in14(1'b0), .in15(1'b0), .out(out_6), .sel(AluOP));
  not not_1 (out_4, out_6);

  // Other names for the same wires on the sheet: Result2[31:0] = Result_2; S[3:0] = AluOP; tunnel = out_6;
  //   tunnel_t = out_4

  // Notes on the sheet:
  //   不要改变此引脚区域内容，也不要改变ALU封装形式
  //   输入引脚
  //   输出引脚
endmodule

module Regifile_DW (
  input  [31:0] Din,
  input  Clk,
  input  WE,
  input  [4:0] R1_num,
  input  [4:0] W_num,
  input  [4:0] R2_num,
  output [31:0] R1,
  output [31:0] R2
);

  // RegisterFile registerfile_1: pin names not known; wires that end beside it: Din, Clk, WE, W_num, R1_num, R2_num, R1, R2
endmodule

module Regfile_UP (
  input  [31:0] Din,
  input  Clk,
  input  WE,
  input  [4:0] R1_num,
  input  [4:0] W_num,
  input  [4:0] R2_num,
  output [31:0] R1,
  output [31:0] R2
);

  // RegisterFile registerfile_1: pin names not known; wires that end beside it: Din, Clk, WE, W_num, R1_num, R2_num, R1, R2
endmodule

module \理想流水线  (
  output RegWrite,
  output MemWrite,
  output [31:0] IF_PC,
  output [31:0] ID_PC,
  output [31:0] EX_PC,
  output [31:0] M_PC,
  output [31:0] WB_PC,
  output [31:0] RDin,
  output [31:0] MDin,
  output [31:0] LedData
);

  wire and_1_out, and_2_out, and_3_out, and_4_out, Beq, Bltu, Bne, Branch, CLK, clock_1_out, comparator_1_eq,
       comparator_2_eq, comparator_2_lt, d_ff_1_q, ecall, ex_mem_1_haltout, ex_mem_1_jalout,
       ex_mem_1_jalrout, ex_mem_1_lbout, ex_mem_1_memtoregout, ex_mem_1_regwritegout, ex_mem_1_remuout,
       ex_mem_1_uretout, Go, halt, id_ex_1_haltout, id_ex_1_jalout, id_ex_1_jalrout, id_ex_1_lbout,
       id_ex_1_memtoregout, id_ex_1_memwriteout, id_ex_1_regwritegout, id_ex_1_remuout, id_ex_1_uretout, IR1,
       IR2, IR3, JAL, JALR, LB, Ledout, nand_1_out, not_1_out, not_2_out, or_2_out, or_3_out, or_4_out,
       rehalt, REMU, RST, tunnel, tunnel_t, URET, W1, W2, W3, \单周期硬布线控制器_1_alu_src , \单周期硬布线控制器_1_beq ,
       \单周期硬布线控制器_1_bltu , \单周期硬布线控制器_1_bne , \单周期硬布线控制器_1_jal , \单周期硬布线控制器_1_jalr , \单周期硬布线控制器_1_lb ,
       \单周期硬布线控制器_1_memtoreg , \单周期硬布线控制器_1_memwrite , \单周期硬布线控制器_1_regwrite , \单周期硬布线控制器_1_remu ,
       \单周期硬布线控制器_1_s_type , \单周期硬布线控制器_1_uret ;
  wire [1:0] LB01;
  wire [3:0] id_ex_1_aluopout, \单周期硬布线控制器_1_alu_op ;
  wire [4:0] ex_mem_1_rwout, id_ex_1_rwout, multiplexer_2_out, multiplexer_3_out, RW_num;
  wire [7:0] multiplexer_9_out;
  wire [11:0] multiplexer_4_out;
  wire [12:0] CNT_num;
  wire [15:0] \LoadUse次数 , \总周期数 , \插入气泡数 , \无条件分支数 , \条件分支成功数 ;
  wire [19:0] shifter_1_out;
  wire [31:0] adder_2_out, adder_3_out, adder_4_out, alu_1_result, alu_1_result_2, and_6_out,
       bit_extender_1_out, bit_extender_2_out, bit_extender_3_out, bit_extender_4_out, bit_extender_5_out,
       BranAddr, EX_IR, ex_mem_1_alurout, ex_mem_1_pc_4out, ex_mem_1_r2out, id_ex_1_alubout, id_ex_1_lbaout,
       id_ex_1_pc_4out, id_ex_1_r1dataout, id_ex_1_r2dataout, ID_IR, if_id_1_pc_4out, IF_IR, JALAddr,
       JALRAddr, LBAddr, MData, MEM_IR, mem_wb_1_memdataout, mem_wb_1_pc_4out, multiplexer_1_out,
       multiplexer_5_out, multiplexer_6_out, multiplexer_7_out, multiplexer_8_out, multiplexer_10_out,
       not_3_out, PC, PC_4, R1Data, R2, ram_1_data, regifile_dw_1_r2, shifter_2_out, WB_IR;

  Button \u_总复位  (.out(RST));
  Button _1 (.out(IR1));
  Button _2 (.out(IR2));
  Button _3 (.out(IR3));
  // Probe on \总周期数 
  // Probe on \总周期数 
  Button \u_继续运行  (.out(Go));
  LED #(.active("true")) led_1 (.in(W1));
  LED #(.active("true")) led_2 (.in(W2));
  LED #(.active("true")) led_3 (.in(W3));
  Hex_Digit_Display hex_digit_display_1 (.value(LedData[31:28]));  // open: dp
  // Probe on IF_PC[19:0]
  // RiscV_Probe riscv_probe_1: pin names not known; wires that end beside it: IF_IR
  Multiplexer #(.select(3), .width(32), .disabled("Z"), .enable("false")) multiplexer_1 (
    .in0(PC_4), .in1(BranAddr), .in2(JALAddr), .in4(JALRAddr), .out(multiplexer_1_out),
    .sel({JALR, JAL, Branch}));  // open: in3, in5, in6, in7
  not not_1 (not_1_out, rehalt);
  Hex_Digit_Display hex_digit_display_2 (.value(LedData[27:24]));  // open: dp
  Hex_Digit_Display hex_digit_display_3 (.value(LedData[23:20]));  // open: dp
  // Probe on ID_PC[19:0]
  // RiscV_Probe riscv_probe_2: pin names not known; wires that end beside it: ID_IR
  Register #(.width(32), .trigger("rising"), .Select("low")) u_PC (
    .D(multiplexer_1_out), .en(not_1_out), .Q(IF_PC), .clk(CLK), .clr(RST));
  Comparator #(.width(32), .mode("twosComplement")) comparator_1 (
    .a(R1Data), .b(32'h22), .eq(comparator_1_eq));  // open: gt, lt
  Register #(.width(32), .trigger("rising"), .Select("low")) register_1 (
    .D(MDin), .en(Ledout), .Q(LedData), .clk(CLK), .clr(RST));
  and and_1 (and_1_out, tunnel_t, Beq);
  and and_2 (and_2_out, ~tunnel_t, Bne);  // AND_Gate
  and and_3 (and_3_out, tunnel, Bltu);
  Hex_Digit_Display hex_digit_display_4 (.value(LedData[19:16]));  // open: dp
  Hex_Digit_Display hex_digit_display_5 (.value(LedData[15:12]));  // open: dp
  and and_4 (and_4_out, ecall, ~comparator_1_eq);  // AND_Gate
  and and_5 (Ledout, ecall, comparator_1_eq);
  or or_1 (Branch, and_1_out, and_2_out, and_3_out);
  Hex_Digit_Display hex_digit_display_6 (.value(LedData[7:4]));  // open: dp
  Hex_Digit_Display hex_digit_display_7 (.value(LedData[11:8]));  // open: dp
  // Probe on EX_PC[19:0]
  // RiscV_Probe riscv_probe_3: pin names not known; wires that end beside it: EX_IR
  // RiscV_Probe riscv_probe_4: pin names not known; wires that end beside it: IF_IR
  Counter #(.width(1), .max('h1), .ongoal("wrap"), .trigger("rising"), .behavior("old")) counter_1 (
    .load(and_4_out), .D(and_4_out), .count(1'b0), .Q(halt), .clk(CLK), .clr(Go));  // open: carry, preset
  Hex_Digit_Display hex_digit_display_8 (.value(LedData[3:0]));  // open: dp
  Adder #(.width(32)) adder_1 (.a(IF_PC), .b(32'h4), .out(PC_4));  // open: cin, cout
  ROM #(.addrWidth(10), .dataWidth(32), .Select("high")) rom_1 (.addr(IF_PC[11:2]), .data(IF_IR));
  // Probe on \总周期数 
  // Probe on M_PC[19:0]
  // RiscV_Probe riscv_probe_5: pin names not known; wires that end beside it: MEM_IR
  IF_ID if_id_1 (
    .PCin(IF_PC), .PCout(ID_PC), .PC_4in(PC_4), .PC_4out(if_id_1_pc_4out), .\指令字in (IF_IR), .\指令字out (ID_IR),
    .clr(RST), .clk(CLK), .abl(rehalt));  // open: PJin, PJout
  // Probe on \总周期数 
  // Probe on \无条件分支数 
  // Probe on \条件分支成功数 
  // Probe on \插入气泡数 
  // Probe on \LoadUse次数 
  // Probe on IF_PC[11:0]
  // Probe on WB_PC[19:0]
  // RiscV_Probe riscv_probe_6: pin names not known; wires that end beside it: WB_IR
  \单周期硬布线控制器  \u_单周期硬布线控制器_1  (
    .Funct({ID_IR[30], ID_IR[25], ID_IR[14:12]}), .OP(ID_IR[6:2]), .ALU_OP(\单周期硬布线控制器_1_alu_op ),
    .MemToReg(\单周期硬布线控制器_1_memtoreg ), .MemWrite(\单周期硬布线控制器_1_memwrite ), .ALU_SRC(\单周期硬布线控制器_1_alu_src ),
    .RegWrite(\单周期硬布线控制器_1_regwrite ), .ecall(ecall), .S_type(\单周期硬布线控制器_1_s_type ),
    .Jalr(\单周期硬布线控制器_1_jalr ), .Beq(\单周期硬布线控制器_1_beq ), .JAL(\单周期硬布线控制器_1_jal ), .Bne(\单周期硬布线控制器_1_bne ),
    .in_3(ID_IR[21]), .uret(\单周期硬布线控制器_1_uret ), .BLTU(\单周期硬布线控制器_1_bltu ), .LB(\单周期硬布线控制器_1_lb ),
    .REMU(\单周期硬布线控制器_1_remu ));
  Multiplexer #(.select(1), .width(5), .disabled("Z"), .enable("false")) multiplexer_2 (
    .in0(ID_IR[19:15]), .in1(5'b10001), .out(multiplexer_2_out), .sel(ecall));
  Multiplexer #(.select(1), .width(5), .disabled("Z"), .enable("false")) multiplexer_3 (
    .in0(ID_IR[24:20]), .in1(5'b01010), .out(multiplexer_3_out), .sel(ecall));
  Multiplexer #(.select(1), .width(12), .disabled("Z"), .enable("false")) multiplexer_4 (
    .in0(ID_IR[31:20]), .in1({ID_IR[31:25], ID_IR[11:7]}), .out(multiplexer_4_out), .sel(\单周期硬布线控制器_1_s_type ));
  assign bit_extender_1_out = {{20{ID_IR[31]}}, ID_IR[31:20]};  // Bit_Extender bit_extender_1
  // Probe on EX_PC[11:0]
  // Probe on ID_PC[11:0]
  assign bit_extender_2_out = {{20{multiplexer_4_out[11]}}, multiplexer_4_out};  // Bit_Extender bit_extender_2
  assign bit_extender_3_out = {{20{ID_IR[31]}}, {ID_IR[31], ID_IR[7], ID_IR[30:25], ID_IR[11:8]}};  // Bit_Extender bit_extender_3
  Shifter #(.width(20), .shift("ll")) shifter_1 (
    .in({ID_IR[31], ID_IR[19:12], ID_IR[20], ID_IR[30:21]}), .\dist (5'b00001), .out(shifter_1_out));
  not not_2 (not_2_out, rehalt);
  Counter #(.width(16), .max('hffff), .ongoal("wrap"), .trigger("rising"), .behavior("new")) counter_2 (
    .count(not_2_out), .Q(\总周期数 ), .clk(CLK));  // open: load, D, carry, clr, preset, down
  // Probe on M_PC[11:0]
  D_Flip_Flop #(.trigger("high"), .Pre_Clr_Positions("LEGACY"), .NegatePresetClear("false"), .enable("true"), .NewFFLayout("false")) d_ff_1 (.Q(d_ff_1_q));  // open: clk, D, Qn, preset, en, reset
  // Probe on 13'hc
  or or_2 (or_2_out, \单周期硬布线控制器_1_lb , RegWrite);
  Shifter #(.width(32), .shift("ll")) shifter_2 (.in(bit_extender_3_out), .\dist (5'b00001), .out(shifter_2_out));
  assign bit_extender_4_out = {{12{shifter_1_out[19]}}, shifter_1_out};  // Bit_Extender bit_extender_4
  Adder #(.width(32)) adder_2 (.a(bit_extender_1_out), .b(R1Data), .out(adder_2_out));  // open: cin, cout
  // Probe on WB_PC[11:0]
  Comparator #(.width(13), .mode("twosComplement")) comparator_2 (
    .a(CNT_num), .b(13'hc), .eq(comparator_2_eq), .lt(comparator_2_lt));  // open: gt
  Clock #(.highDuration(1), .lowDuration(1)) clock_1 (.out(clock_1_out));
  Regifile_DW regifile_dw_1 (
    .Din(RDin), .Clk(CLK), .R1(R1Data), .R2(regifile_dw_1_r2), .WE(or_2_out), .W_num(RW_num),
    .R1_num(multiplexer_2_out), .R2_num(multiplexer_3_out));
  Adder #(.width(32)) adder_3 (.a(shifter_2_out), .b(PC), .out(adder_3_out));  // open: cin, cout
  Adder #(.width(32)) adder_4 (.a(bit_extender_4_out), .b(PC), .out(adder_4_out));  // open: cin, cout
  assign and_6_out = adder_2_out & not_3_out;  // AND_Gate and_6, 32 bits wide
  assign not_3_out = ~32'h1;  // NOT_Gate not_3, 32 bits wide
  Counter #(.width(16), .max('hffff), .ongoal("wrap"), .trigger("rising"), .behavior("new")) counter_3 (
    .count(Branch), .Q(\条件分支成功数 ), .clk(CLK), .clr(RST));  // open: load, D, carry, preset, down
  nand nand_1 (nand_1_out, d_ff_1_q, comparator_2_eq);
  Counter #(.width(13), .max('h1fff), .ongoal("stay"), .trigger("rising"), .behavior("old")) counter_4 (
    .count(comparator_2_lt), .Q(CNT_num), .clk(clock_1_out));  // open: load, D, carry, clr, preset
  Multiplexer #(.select(1), .width(32), .disabled("Z"), .enable("false")) multiplexer_5 (
    .in0(regifile_dw_1_r2), .in1(bit_extender_2_out), .out(multiplexer_5_out), .sel(\单周期硬布线控制器_1_alu_src ));
  or or_3 (or_3_out, JAL, JALR);
  Counter #(.width(16), .max('hffff), .ongoal("wrap"), .trigger("rising"), .behavior("new")) counter_5 (
    .count(or_3_out), .Q(\无条件分支数 ), .clk(CLK), .clr(RST));  // open: load, D, carry, preset, down
  assign CLK = nand_1_out ? clock_1_out : 1'bz;  // Controlled_Buffer controlled_buffer_1
  ID_EX id_ex_1 (
    .REMUin(\单周期硬布线控制器_1_remu ), .LBin(\单周期硬布线控制器_1_lb ), .URETin(\单周期硬布线控制器_1_uret ),
    .JALRin(\单周期硬布线控制器_1_jalr ), .JALin(\单周期硬布线控制器_1_jal ), .BEQin(\单周期硬布线控制器_1_beq ),
    .BLTUin(\单周期硬布线控制器_1_bltu ), .BNEin(\单周期硬布线控制器_1_bne ), .MemToRegin(\单周期硬布线控制器_1_memtoreg ),
    .MemWritein(\单周期硬布线控制器_1_memwrite ), .ALUopin(\单周期硬布线控制器_1_alu_op ), .R1datain(R1Data),
    .R2datain(regifile_dw_1_r2), .RWin(ID_IR[11:7]), .BAin(adder_3_out), .JALAin(adder_4_out),
    .JALRin_2(and_6_out), .LBAin(adder_2_out), .REMUout(id_ex_1_remuout), .LBout(id_ex_1_lbout),
    .URETout(id_ex_1_uretout), .JALRout(id_ex_1_jalrout), .JALout(id_ex_1_jalout), .BEQout(Beq),
    .BLTUout(Bltu), .BNEout(Bne), .MemToRegout(id_ex_1_memtoregout), .MemWriteout(id_ex_1_memwriteout),
    .ALUopout(id_ex_1_aluopout), .R1dataout(id_ex_1_r1dataout), .R2dataout(id_ex_1_r2dataout),
    .RWout(id_ex_1_rwout), .BAout(BranAddr), .JALAout(JALAddr), .JALRout_2(JALRAddr),
    .LBAout(id_ex_1_lbaout), .clr(RST), .clk(CLK), .abl(rehalt), .HALTin(halt), .HALTout(id_ex_1_haltout),
    .PCin(ID_PC), .PCout(EX_PC), .PC_4in(if_id_1_pc_4out), .PC_4out(id_ex_1_pc_4out),
    .ALUBin(multiplexer_5_out), .ALUBout(id_ex_1_alubout), .RegWritein(\单周期硬布线控制器_1_regwrite ),
    .RegWritegout(id_ex_1_regwritegout));  // open: R1Fin, R1Fout, R2Fin, R2Fout, ASBin, ASBout, ECALLin, ECALLout, PJin, PJout
  Pull_Resistor #(.pull(1)) pull_resistor_1 (.node(CLK));
  ALU alu_1 (
    .X(id_ex_1_r1dataout), .Y(id_ex_1_alubout), .AluOP(id_ex_1_aluopout), .Equal(tunnel_t),
    .Result(alu_1_result), .Result_2(alu_1_result_2), .out_6(tunnel));  // open: out_4
  EX_MEM ex_mem_1 (
    .PCin(EX_PC), .PC_4in(id_ex_1_pc_4out), .HALTin(id_ex_1_haltout), .REMUin(id_ex_1_remuout),
    .LBin(id_ex_1_lbout), .URETin(id_ex_1_uretout), .JALRin(id_ex_1_jalrout), .JALin(id_ex_1_jalout),
    .MemToRegin(id_ex_1_memtoregout), .MemWritein(id_ex_1_memwriteout), .ALURin(alu_1_result),
    .RWin(id_ex_1_rwout), .LBAin(id_ex_1_lbaout), .PCout(M_PC), .PC_4out(ex_mem_1_pc_4out),
    .HALTout(ex_mem_1_haltout), .REMUout(ex_mem_1_remuout), .LBout(ex_mem_1_lbout),
    .URETout(ex_mem_1_uretout), .JALRout(ex_mem_1_jalrout), .JALout(ex_mem_1_jalout),
    .MemToRegout(ex_mem_1_memtoregout), .MemWriteout(MemWrite), .ALURout(ex_mem_1_alurout),
    .RWout(ex_mem_1_rwout), .LBAout(LBAddr), .clr(RST), .clk(CLK), .abl(rehalt),
    .R2datain(id_ex_1_r2dataout), .R2dataout(MDin), .R2in(alu_1_result_2), .R2out(ex_mem_1_r2out),
    .RegWritein(id_ex_1_regwritegout), .RegWritegout(ex_mem_1_regwritegout));
  Multiplexer #(.select(1), .width(32), .disabled("Z"), .enable("false")) multiplexer_6 (
    .in0(ex_mem_1_alurout), .in1(LBAddr), .out(multiplexer_6_out), .sel(ex_mem_1_lbout));
  Multiplexer #(.select(1), .width(32), .disabled("Z"), .enable("false")) multiplexer_7 (
    .in0(ex_mem_1_alurout), .in1(ram_1_data), .out(multiplexer_7_out), .sel(ex_mem_1_memtoregout));
  RAM #(.addrWidth(10), .dataWidth(32), .bus("separate"), .Select("high")) ram_1 (
    .addr(multiplexer_6_out[11:2]), .din(MDin), .data(ram_1_data), .str(MemWrite), .clk(CLK), .clr(RST));  // open: sel, ld
  MEM_WB mem_wb_1 (
    .PCin(M_PC), .PC_4in(ex_mem_1_pc_4out), .HALTin(ex_mem_1_haltout), .REMUin(ex_mem_1_remuout),
    .LBin(ex_mem_1_lbout), .URETin(ex_mem_1_uretout), .JALRin(ex_mem_1_jalrout), .JALin(ex_mem_1_jalout),
    .MemDatain(multiplexer_7_out), .R2in(ex_mem_1_r2out), .LB01in(multiplexer_6_out[1:0]),
    .Mdatain(ram_1_data), .RWin(ex_mem_1_rwout), .PCout(WB_PC), .PC_4out(mem_wb_1_pc_4out), .HALTout(rehalt),
    .REMUout(REMU), .LBout(LB), .URETout(URET), .JALRout(JALR), .JALout(JAL),
    .MemDataout(mem_wb_1_memdataout), .R2out(R2), .LB01out(LB01), .Mdataout(MData), .RWout(RW_num),
    .clr(RST), .clk(CLK), .abl(rehalt), .RegWritein(ex_mem_1_regwritegout), .RegWritegout(RegWrite));  // open: go
  Multiplexer #(.select(1), .width(32), .disabled("Z"), .enable("false")) multiplexer_8 (
    .in0(mem_wb_1_memdataout), .in1(mem_wb_1_pc_4out), .out(multiplexer_8_out), .sel(or_4_out));
  or or_4 (or_4_out, JAL, JALR);
  Multiplexer #(.select(2), .width(8), .disabled("Z"), .enable("false")) multiplexer_9 (
    .in0(MData[7:0]), .in1(MData[15:8]), .in2(MData[23:16]), .in3(MData[31:24]), .out(multiplexer_9_out),
    .sel(LB01));
  Multiplexer #(.select(1), .width(32), .disabled("Z"), .enable("false")) multiplexer_10 (
    .in0(multiplexer_8_out), .in1(R2), .out(multiplexer_10_out), .sel(REMU));
  assign bit_extender_5_out = {{24{multiplexer_9_out[7]}}, multiplexer_9_out};  // Bit_Extender bit_extender_5
  Multiplexer #(.select(1), .width(32), .disabled("Z"), .enable("false")) multiplexer_11 (
    .in0(multiplexer_10_out), .in1(bit_extender_5_out), .out(RDin), .sel(LB));

  // Other names for the same wires on the sheet: MEM_PC[31:0] = M_PC; R2Data[31:0] = MDin

  // Notes on the sheet:
  //   中断源
  //   时空图监测，可删除
  //   中断等待指示
  //   数码管输出
  //   指令探针
  //   指令存储器
  //   指令字
  //   contents of rom_1 (hex, n*v repeats v):
  //   413 493 913 993 46413 14e493 296913 39e993 842023 942223 1242423 1342623 a00893 493 913 993 73
  //   JAL
  //   JALR
  //   URET
  //   控制位
  //   Beq
  //   Bne
  //   MemToReg
  //   MemWrite
  //   AluOP
  //   AluSrcB
  //   RegWrite
  //   流水调试日志用
  //   暂停节拍，不能为0
  //   戳工具置1进入计数暂停模式，ctrl+k时钟自动运行到对应节拍暂停
  //   ctrl+k关闭时钟连续运行，将控制位置零，进入单步调试模式调试
  //   用这个时钟源需要去掉电路中的其他时钟源
  //   可计数暂停的时钟源
  //   为方便自动评测，需要输出流水线各段保存的PC值，注意是PC不是PC+4，另外ID段寄存器写入信息，Mem段内存写入信息也要输出
  //   数据存储器
endmodule

module \气泡流水线  (
  output RegWrite,
  output MemWrite,
  output [31:0] IF_PC,
  output [31:0] ID_PC,
  output [31:0] EX_PC,
  output [31:0] M_PC,
  output [31:0] WB_PC,
  output [31:0] RDin,
  output [31:0] MDin,
  output [31:0] LedData
);

  wire and_1_out, and_2_out, and_3_out, and_4_out, and_7_out, and_9_out, Beq, Bltu, Bne, Branch, CLK,
       clock_1_out, comparator_1_eq, comparator_3_eq, comparator_3_lt, d_ff_1_q, ecall, ex_mem_1_haltout,
       ex_mem_1_jalout, ex_mem_1_jalrout, ex_mem_1_lbout, ex_mem_1_memtoregout, ex_mem_1_remuout,
       ex_mem_1_uretout, EXJAL, EXJALR, Go, halt, hazzard, id_ex_1_haltout, id_ex_1_lbout,
       id_ex_1_memtoregout, id_ex_1_memwriteout, id_ex_1_remuout, id_ex_1_uretout, IR1, IR2, IR3, JAL, JALR,
       LB, LBlow7, Ledout, nand_1_out, not_1_out, or_2_out, or_3_out, or_4_out, or_5_out, or_6_out, or_7_out,
       rehalt, REMU, RST, RWE, RWM, tunnel, tunnel_t, URET, W1, W2, W3, \单周期硬布线控制器_1_alu_src ,
       \单周期硬布线控制器_1_beq , \单周期硬布线控制器_1_bltu , \单周期硬布线控制器_1_bne , \单周期硬布线控制器_1_jal , \单周期硬布线控制器_1_jalr ,
       \单周期硬布线控制器_1_lb , \单周期硬布线控制器_1_memtoreg , \单周期硬布线控制器_1_memwrite , \单周期硬布线控制器_1_regwrite ,
       \单周期硬布线控制器_1_remu , \单周期硬布线控制器_1_s_type , \单周期硬布线控制器_1_uret ;
  wire [1:0] LB01;
  wire [3:0] id_ex_1_aluopout, \单周期硬布线控制器_1_alu_op ;
  wire [4:0] EXW, FUNC, MEMW, R1, R2, RW_num;
  wire [7:0] multiplexer_9_out;
  wire [11:0] multiplexer_4_out;
  wire [12:0] CNT_num;
  wire [15:0] \LoadUse次数 , \总周期数 , \插入气泡数 , \无条件分支数 , \条件分支成功数 ;
  wire [19:0] shifter_1_out;
  wire [31:0] adder_2_out, adder_3_out, adder_4_out, alu_1_result, alu_1_result_2, and_8_out,
       bit_extender_1_out, bit_extender_2_out, bit_extender_3_out, bit_extender_4_out, bit_extender_5_out,
       BranAddr, EX_IR, ex_mem_1_alurout, ex_mem_1_pc_4out, ex_mem_1_r2out, id_ex_1_alubout, id_ex_1_lbaout,
       id_ex_1_pc_4out, id_ex_1_r1dataout, id_ex_1_r2dataout, ID_IR, if_id_1_pc_4out, IF_IR, JALAddr,
       JALRAddr, LBAddr, MData, MEM_IR, mem_wb_1_memdataout, mem_wb_1_pc_4out, multiplexer_1_out,
       multiplexer_5_out, multiplexer_6_out, multiplexer_7_out, multiplexer_8_out, multiplexer_10_out,
       not_2_out, PC_4, R1Data, R2Data, ram_1_data, Result2, shifter_2_out, WB_IR;

  Button \u_总复位  (.out(RST));
  Button _1 (.out(IR1));
  Button _2 (.out(IR2));
  Button _3 (.out(IR3));
  // Probe on \总周期数 
  // Probe on \总周期数 
  Button \u_继续运行  (.out(Go));
  LED #(.active("true")) led_1 (.in(W1));
  LED #(.active("true")) led_2 (.in(W2));
  LED #(.active("true")) led_3 (.in(W3));
  Hex_Digit_Display hex_digit_display_1 (.value(LedData[31:28]));  // open: dp
  // Probe on IF_PC[19:0]
  // RiscV_Probe riscv_probe_1: pin names not known; wires that end beside it: IF_IR
  Multiplexer #(.select(3), .width(32), .disabled("Z"), .enable("false")) multiplexer_1 (
    .in0(PC_4), .in1(BranAddr), .in2(JALAddr), .in4(JALRAddr), .out(multiplexer_1_out),
    .sel({EXJALR, EXJAL, Branch}));  // open: in3, in5, in6, in7
  and and_1 (and_1_out, ~hazzard, ~rehalt);  // AND_Gate
  Hex_Digit_Display hex_digit_display_2 (.value(LedData[27:24]));  // open: dp
  Hex_Digit_Display hex_digit_display_3 (.value(LedData[23:20]));  // open: dp
  // Probe on ID_PC[19:0]
  // RiscV_Probe riscv_probe_2: pin names not known; wires that end beside it: {ID_IR[31], FUNC[4], ID_IR[29:26], FUNC[3], ID_IR[24:15], FUNC[2:0], ID_IR[11:0]}
  Register #(.width(32), .trigger("rising"), .Select("low")) PC (
    .D(multiplexer_1_out), .en(and_1_out), .Q(IF_PC), .clk(CLK), .clr(RST));
  Comparator #(.width(32), .mode("twosComplement")) comparator_1 (
    .a(R1Data), .b(32'h22), .eq(comparator_1_eq));  // open: gt, lt
  Register #(.width(32), .trigger("rising"), .Select("low")) register_1 (
    .D(R2Data), .en(Ledout), .Q(LedData), .clk(CLK), .clr(RST));
  and and_2 (and_2_out, tunnel_t, Beq);
  and and_3 (and_3_out, ~tunnel_t, Bne);  // AND_Gate
  and and_4 (and_4_out, tunnel, Bltu);
  Hex_Digit_Display hex_digit_display_4 (.value(LedData[15:12]));  // open: dp
  Hex_Digit_Display hex_digit_display_5 (.value(LedData[19:16]));  // open: dp
  and and_5 (halt, ecall, ~comparator_1_eq);  // AND_Gate
  and and_6 (Ledout, ecall, comparator_1_eq);
  or or_1 (Branch, and_2_out, and_3_out, and_4_out);
  Hex_Digit_Display hex_digit_display_6 (.value(LedData[11:8]));  // open: dp
  Hex_Digit_Display hex_digit_display_7 (.value(LedData[7:4]));  // open: dp
  // Probe on EX_PC[19:0]
  // RiscV_Probe riscv_probe_3: pin names not known; wires that end beside it: EX_IR
  // RiscV_Probe riscv_probe_4: pin names not known; wires that end beside it: IF_IR
  Hex_Digit_Display hex_digit_display_8 (.value(LedData[3:0]));  // open: dp
  Adder #(.width(32)) adder_1 (.a(IF_PC), .b(32'h4), .out(PC_4));  // open: cin, cout
  ROM #(.addrWidth(10), .dataWidth(32), .Select("high")) rom_1 (.addr(IF_PC[11:2]), .data(IF_IR));
  or or_2 (or_2_out, EXJALR, EXJAL, Branch, RST);
  // Probe on \总周期数 
  // Probe on M_PC[19:0]
  // RiscV_Probe riscv_probe_5: pin names not known; wires that end beside it: MEM_IR
  IF_ID if_id_1 (
    .PCin(IF_PC), .PCout(ID_PC), .PC_4in(PC_4), .PC_4out(if_id_1_pc_4out), .\指令字in (IF_IR),
    .\指令字out ({ID_IR[31], FUNC[4], ID_IR[29:26], FUNC[3], ID_IR[24:15], FUNC[2:0], ID_IR[11:0]}),
    .clr(or_2_out), .clk(CLK), .abl(or_3_out));  // open: PJin, PJout
  or or_3 (or_3_out, hazzard, rehalt);
  // Probe on \总周期数 
  // Probe on \无条件分支数 
  // Probe on \条件分支成功数 
  // Probe on \插入气泡数 
  // Probe on \LoadUse次数 
  not not_1 (not_1_out, rehalt);
  Counter #(.width(16), .max('hffff), .ongoal("wrap"), .trigger("rising"), .behavior("new")) counter_1 (
    .count(not_1_out), .Q(\总周期数 ), .clk(CLK));  // open: load, D, carry, clr, preset, down
  // Probe on IF_PC[11:0]
  // Probe on WB_PC[19:0]
  // RiscV_Probe riscv_probe_6: pin names not known; wires that end beside it: WB_IR
  \单周期硬布线控制器  \u_单周期硬布线控制器_1  (
    .Funct(FUNC), .OP(ID_IR[6:2]), .ALU_OP(\单周期硬布线控制器_1_alu_op ), .MemToReg(\单周期硬布线控制器_1_memtoreg ),
    .MemWrite(\单周期硬布线控制器_1_memwrite ), .ALU_SRC(\单周期硬布线控制器_1_alu_src ), .RegWrite(\单周期硬布线控制器_1_regwrite ),
    .ecall(ecall), .S_type(\单周期硬布线控制器_1_s_type ), .Jalr(\单周期硬布线控制器_1_jalr ), .Beq(\单周期硬布线控制器_1_beq ),
    .JAL(\单周期硬布线控制器_1_jal ), .Bne(\单周期硬布线控制器_1_bne ), .in_3(ID_IR[21]), .uret(\单周期硬布线控制器_1_uret ),
    .BLTU(\单周期硬布线控制器_1_bltu ), .LB(\单周期硬布线控制器_1_lb ), .REMU(\单周期硬布线控制器_1_remu ));
  Multiplexer #(.select(1), .width(5), .disabled("Z"), .enable("false")) multiplexer_2 (
    .in0(ID_IR[19:15]), .in1(5'b10001), .out(R1), .sel(ecall));
  Multiplexer #(.select(1), .width(5), .disabled("Z"), .enable("false")) multiplexer_3 (
    .in0(ID_IR[24:20]), .in1(5'b01010), .out(R2), .sel(ecall));
  Multiplexer #(.select(1), .width(12), .disabled("Z"), .enable("false")) multiplexer_4 (
    .in0({ID_IR[31], FUNC[4], ID_IR[29:26], FUNC[3], ID_IR[24:20]}),
    .in1({ID_IR[31], FUNC[4], ID_IR[29:26], FUNC[3], ID_IR[11:7]}), .out(multiplexer_4_out),
    .sel(\单周期硬布线控制器_1_s_type ));
  assign bit_extender_1_out = {{20{ID_IR[31]}}, {ID_IR[31], FUNC[4], ID_IR[29:26], FUNC[3], ID_IR[24:20]}};  // Bit_Extender bit_extender_1
  Comparator #(.width(7), .mode("twosComplement")) comparator_2 (
    .a(ID_IR[6:0]), .b(7'b0000011), .eq(LBlow7));  // open: gt, lt
  // Probe on ID_PC[11:0]
  // Probe on EX_PC[11:0]
  and and_7 (and_7_out, LBlow7, \单周期硬布线控制器_1_lb );
  assign bit_extender_2_out = {{20{multiplexer_4_out[11]}}, multiplexer_4_out};  // Bit_Extender bit_extender_2
  assign bit_extender_3_out = {{20{ID_IR[31]}}, {ID_IR[31], ID_IR[7], FUNC[4], ID_IR[29:26], FUNC[3], ID_IR[11:8]}};  // Bit_Extender bit_extender_3
  Shifter #(.width(20), .shift("ll")) shifter_1 (
    .in({ID_IR[31], ID_IR[19:15], FUNC[2:0], ID_IR[20], FUNC[4], ID_IR[29:26], FUNC[3], ID_IR[24:21]}),
    .\dist (5'b00001), .out(shifter_1_out));
  Counter #(.width(16), .max('hffff), .ongoal("wrap"), .trigger("rising"), .behavior("new")) counter_2 (
    .count(Branch), .Q(\条件分支成功数 ), .clk(CLK), .clr(RST));  // open: load, D, carry, preset, down
  // Probe on M_PC[11:0]
  D_Flip_Flop #(.trigger("high"), .Pre_Clr_Positions("LEGACY"), .NegatePresetClear("false"), .enable("true"), .NewFFLayout("false")) d_ff_1 (.Q(d_ff_1_q));  // open: clk, D, Qn, preset, en, reset
  // Probe on 13'he9
  Shifter #(.width(32), .shift("ll")) shifter_2 (.in(bit_extender_3_out), .\dist (5'b00001), .out(shifter_2_out));
  assign bit_extender_4_out = {{12{shifter_1_out[19]}}, shifter_1_out};  // Bit_Extender bit_extender_4
  Adder #(.width(32)) adder_2 (.a(bit_extender_1_out), .b(R1Data), .out(adder_2_out));  // open: cin, cout
  or or_4 (or_4_out, JAL, JALR);
  Counter #(.width(16), .max('hffff), .ongoal("wrap"), .trigger("rising"), .behavior("new")) counter_3 (
    .count(or_4_out), .Q(\无条件分支数 ), .clk(CLK), .clr(RST));  // open: load, D, carry, preset, down
  // Probe on WB_PC[11:0]
  Comparator #(.width(13), .mode("twosComplement")) comparator_3 (
    .a(CNT_num), .b(13'he9), .eq(comparator_3_eq), .lt(comparator_3_lt));  // open: gt
  Clock #(.highDuration(1), .lowDuration(1)) clock_1 (.out(clock_1_out));
  or or_5 (or_5_out, \单周期硬布线控制器_1_regwrite , and_7_out);
  Regifile_DW regifile_dw_1 (
    .Din(RDin), .Clk(CLK), .R1(R1Data), .R2(R2Data), .WE(RegWrite), .W_num(RW_num), .R1_num(R1), .R2_num(R2));
  Adder #(.width(32)) adder_3 (.a(shifter_2_out), .b(ID_PC), .out(adder_3_out));  // open: cin, cout
  Adder #(.width(32)) adder_4 (.a(bit_extender_4_out), .b(ID_PC), .out(adder_4_out));  // open: cin, cout
  assign and_8_out = adder_2_out & not_2_out;  // AND_Gate and_8, 32 bits wide
  assign not_2_out = ~32'h1;  // NOT_Gate not_2, 32 bits wide
  nand nand_1 (nand_1_out, d_ff_1_q, comparator_3_eq);
  Counter #(.width(13), .max('h1fff), .ongoal("stay"), .trigger("rising"), .behavior("old")) counter_4 (
    .count(comparator_3_lt), .Q(CNT_num), .clk(clock_1_out));  // open: load, D, carry, clr, preset
  Multiplexer #(.select(1), .width(32), .disabled("Z"), .enable("false")) multiplexer_5 (
    .in0(R2Data), .in1(bit_extender_2_out), .out(multiplexer_5_out), .sel(\单周期硬布线控制器_1_alu_src ));
  assign CLK = nand_1_out ? clock_1_out : 1'bz;  // Controlled_Buffer controlled_buffer_1
  ID_EX id_ex_1 (
    .REMUin(\单周期硬布线控制器_1_remu ), .LBin(and_7_out), .URETin(\单周期硬布线控制器_1_uret ), .JALRin(\单周期硬布线控制器_1_jalr ),
    .JALin(\单周期硬布线控制器_1_jal ), .BEQin(\单周期硬布线控制器_1_beq ), .BLTUin(\单周期硬布线控制器_1_bltu ),
    .BNEin(\单周期硬布线控制器_1_bne ), .MemToRegin(\单周期硬布线控制器_1_memtoreg ), .MemWritein(\单周期硬布线控制器_1_memwrite ),
    .ALUopin(\单周期硬布线控制器_1_alu_op ), .R1datain(R1Data), .R2datain(R2Data), .RWin(ID_IR[11:7]),
    .BAin(adder_3_out), .JALAin(adder_4_out), .JALRin_2(and_8_out), .LBAin(adder_2_out),
    .REMUout(id_ex_1_remuout), .LBout(id_ex_1_lbout), .URETout(id_ex_1_uretout), .JALRout(EXJALR),
    .JALout(EXJAL), .BEQout(Beq), .BLTUout(Bltu), .BNEout(Bne), .MemToRegout(id_ex_1_memtoregout),
    .MemWriteout(id_ex_1_memwriteout), .ALUopout(id_ex_1_aluopout), .R1dataout(id_ex_1_r1dataout),
    .R2dataout(id_ex_1_r2dataout), .RWout(EXW), .BAout(BranAddr), .JALAout(JALAddr), .JALRout_2(JALRAddr),
    .LBAout(id_ex_1_lbaout), .clr(or_6_out), .clk(CLK), .abl(rehalt), .HALTin(halt),
    .HALTout(id_ex_1_haltout), .PCin(ID_PC), .PCout(EX_PC), .PC_4in(if_id_1_pc_4out),
    .PC_4out(id_ex_1_pc_4out), .ALUBin(multiplexer_5_out), .ALUBout(id_ex_1_alubout), .RegWritein(or_5_out),
    .RegWritegout(RWE));  // open: R1Fin, R1Fout, R2Fin, R2Fout, ASBin, ASBout, ECALLin, ECALLout, PJin, PJout
  or or_6 (or_6_out, EXJALR, EXJAL, Branch, RST, hazzard);
  and and_9 (and_9_out, ~rehalt, hazzard);  // AND_Gate
  Pull_Resistor #(.pull(1)) pull_resistor_1 (.node(CLK));
  Counter #(.width(16), .max('hffff), .ongoal("wrap"), .trigger("rising"), .behavior("old")) counter_5 (
    .count(and_9_out), .Q(\插入气泡数 ), .clk(CLK), .clr(RST));  // open: load, D, carry, preset
  ALU alu_1 (
    .X(id_ex_1_r1dataout), .Y(id_ex_1_alubout), .AluOP(id_ex_1_aluopout), .Equal(tunnel_t),
    .Result(alu_1_result), .Result_2(alu_1_result_2), .out_6(tunnel));  // open: out_4
  EX_MEM ex_mem_1 (
    .PCin(EX_PC), .PC_4in(id_ex_1_pc_4out), .HALTin(id_ex_1_haltout), .REMUin(id_ex_1_remuout),
    .LBin(id_ex_1_lbout), .URETin(id_ex_1_uretout), .JALRin(EXJALR), .JALin(EXJAL),
    .MemToRegin(id_ex_1_memtoregout), .MemWritein(id_ex_1_memwriteout), .ALURin(alu_1_result), .RWin(EXW),
    .LBAin(id_ex_1_lbaout), .PCout(M_PC), .PC_4out(ex_mem_1_pc_4out), .HALTout(ex_mem_1_haltout),
    .REMUout(ex_mem_1_remuout), .LBout(ex_mem_1_lbout), .URETout(ex_mem_1_uretout),
    .JALRout(ex_mem_1_jalrout), .JALout(ex_mem_1_jalout), .MemToRegout(ex_mem_1_memtoregout),
    .MemWriteout(MemWrite), .ALURout(ex_mem_1_alurout), .RWout(MEMW), .LBAout(LBAddr), .clr(RST), .clk(CLK),
    .abl(rehalt), .R2datain(id_ex_1_r2dataout), .R2dataout(MDin), .R2in(alu_1_result_2),
    .R2out(ex_mem_1_r2out), .RegWritein(RWE), .RegWritegout(RWM));
  Bubble bubble_1 (
    .R1(R1), .EXW(EXW), .MEMW(MEMW), .R2(R2), .hazzard(hazzard), .RWE(RWE), .RWM(RWM), .OP(ID_IR[6:2]),
    .Funct(FUNC));
  Multiplexer #(.select(1), .width(32), .disabled("Z"), .enable("false")) multiplexer_6 (
    .in0(ex_mem_1_alurout), .in1(LBAddr), .out(multiplexer_6_out), .sel(ex_mem_1_lbout));
  Multiplexer #(.select(1), .width(32), .disabled("Z"), .enable("false")) multiplexer_7 (
    .in0(ex_mem_1_alurout), .in1(ram_1_data), .out(multiplexer_7_out), .sel(ex_mem_1_memtoregout));
  RAM #(.addrWidth(10), .dataWidth(32), .bus("separate"), .Select("high")) ram_1 (
    .addr(multiplexer_6_out[11:2]), .din(MDin), .data(ram_1_data), .str(MemWrite), .clk(CLK), .clr(RST));  // open: sel, ld
  MEM_WB mem_wb_1 (
    .PCin(M_PC), .PC_4in(ex_mem_1_pc_4out), .HALTin(ex_mem_1_haltout), .REMUin(ex_mem_1_remuout),
    .LBin(ex_mem_1_lbout), .URETin(ex_mem_1_uretout), .JALRin(ex_mem_1_jalrout), .JALin(ex_mem_1_jalout),
    .MemDatain(multiplexer_7_out), .R2in(ex_mem_1_r2out), .LB01in(multiplexer_6_out[1:0]),
    .Mdatain(ram_1_data), .RWin(MEMW), .PCout(WB_PC), .PC_4out(mem_wb_1_pc_4out), .HALTout(rehalt),
    .REMUout(REMU), .LBout(LB), .URETout(URET), .JALRout(JALR), .JALout(JAL),
    .MemDataout(mem_wb_1_memdataout), .R2out(Result2), .LB01out(LB01), .Mdataout(MData), .RWout(RW_num),
    .clr(RST), .clk(CLK), .abl(rehalt), .RegWritein(RWM), .RegWritegout(RegWrite), .go(Go));
  Multiplexer #(.select(1), .width(32), .disabled("Z"), .enable("false")) multiplexer_8 (
    .in0(mem_wb_1_memdataout), .in1(mem_wb_1_pc_4out), .out(multiplexer_8_out), .sel(or_7_out));
  or or_7 (or_7_out, JAL, JALR);
  Multiplexer #(.select(2), .width(8), .disabled("Z"), .enable("false")) multiplexer_9 (
    .in0(MData[7:0]), .in1(MData[15:8]), .in2(MData[23:16]), .in3(MData[31:24]), .out(multiplexer_9_out),
    .sel(LB01));
  assign bit_extender_5_out = {{24{multiplexer_9_out[7]}}, multiplexer_9_out};  // Bit_Extender bit_extender_5
  Multiplexer #(.select(1), .width(32), .disabled("Z"), .enable("false")) multiplexer_10 (
    .in0(multiplexer_8_out), .in1(Result2), .out(multiplexer_10_out), .sel(REMU));
  Multiplexer #(.select(1), .width(32), .disabled("Z"), .enable("false")) multiplexer_11 (
    .in0(multiplexer_10_out), .in1(bit_extender_5_out), .out(RDin), .sel(LB));

  // Other names for the same wires on the sheet: ID_IR (some bits) = FUNC; OP[4:0] = ID_IR[6:2]; MEM_PC[31:0] = M_PC

  // Notes on the sheet:
  //   中断源
  //   时空图监测，可删除
  //   中断等待指示
  //   数码管输出
  //   指令探针
  //   指令存储器
  //   指令字
  //   contents of rom_1 (hex, n*v repeats v):
  //   100493 100006f 100493 200913 300993 100006f 100493 200913 300993 100006f 100493 200913 300993
  //   100006f 100493 200913 300993 3c8000ef 100413 100493 1f49493 900533 2200893 73 24d493 48463 fedff06f
  //   900533 2200893 73 100493 249493 900533 2200893 73 48463 fedff06f 100493 1f49493 900533 2200893 73
  //   4034d493 900533 2200893 73 4044d493 900533 2200893 73 4044d493 900533 2200893 73 4044d493 900533
  //   2200893 73 4044d493 900533 2200893 73 4044d493 900533 2200893 73 4044d493 900533 2200893 73 4044d493
  //   900533 2200893 73 100413 1f41993 41f9d993 433 c00913 300b13 140413 f47413 800293 100313 499993
  //   89e9b3 1300533 2200893 73 406282b3 fe0294e3 140413 f00f93 1f47433 1c41413 800293 100313 49d993
  //   89e9b3 1300533 2200893 73 406282b3 fe0294e3 1c45413 406b0b33 b0463 f95ff06f 2b3 fff2c293 829293
  //   ff2e293 500533 2200893 73 fff00413 493 84a023 140413 448493 84a023 140413 448493 84a023 140413
  //   448493 84a023 140413 448493 84a023 140413 448493 84a023 140413 448493 84a023 140413 448493 84a023
  //   140413 448493 84a023 140413 448493 84a023 140413 448493 84a023 140413 448493 84a023 140413 448493
  //   84a023 140413 448493 84a023 140413 448493 84a023 140413 448493 84a023 140413 448493 140413 433
  //   3c00493 42983 4aa03 149a2b3 28663 134a023 1442023 ffc48493 fe9412e3 800533 2200893 73 440413 3c00493
  //   fc9416e3 3200893 73 200293 1100493 849493 1148493 900533 2200893 73 2000e13 25484b3 900533 2200893
  //   73 fffe0e13 fe0e16e3 a00893 73 8800493 849493 4848493 8700913 891913 5490913 2997933 1091913
  //   11096913 1200533 2200893 73 a00893 73 313 1000e13 8400493 849493 8348493 400913 891913 490913 849493
  //   8248493 849493 8148493 891913 490913 891913 490913 932023 12484b3 430313 fffe0e13 fe0e18e3 2000e13
  //   313 30483 900533 2200893 73 130313 fffe0e13 fe0e14e3 a00893 73 ff100493 900533 2200893 73 148493
  //   fe9068e3 900533 2200893 73 a00893 73 a00893 73 413 140413 800533 2200893 73 240413 800533 2200893 73
  //   340413 800533 2200893 73 440413 800533 2200893 73 540413 800533 2200893 73 640413 800533 2200893 73
  //   740413 800533 2200893 73 840413 800533 2200893 2200893 73 8067
  //   JAL
  //   JALR
  //   URET
  //   控制位
  //   Beq
  //   Bne
  //   MemToReg
  //   MemWrite
  //   AluOP
  //   AluSrcB
  //   RegWrite
  //   流水调试日志用
  //   暂停节拍，不能为0
  //   戳工具置1进入计数暂停模式，ctrl+k时钟自动运行到对应节拍暂停
  //   ctrl+k关闭时钟连续运行，将控制位置零，进入单步调试模式调试
  //   可计数暂停的时钟源
  //   为方便自动评测，需要输出流水线各段保存的PC值，注意是PC不是PC+4，另外ID段寄存器写入信息，Mem段内存写入信息也要输出
  //   数据存储器
endmodule

module \重定向流水线  (
  output RegWrite,
  output MemWrite,
  output [31:0] IF_PC,
  output [31:0] ID_PC,
  output [31:0] EX_PC,
  output [31:0] M_PC,
  output [31:0] WB_PC,
  output [31:0] RDin,
  output [31:0] MDin,
  output [31:0] LedData
);

  wire and_1_out, and_2_out, and_3_out, and_4_out, and_7_out, and_9_out, Beq, Bltu, Bne, Branch, bubble, CLK,
       clock_1_out, comparator_1_eq, comparator_3_eq, comparator_3_lt, d_ff_1_q, ecall, ex_mem_1_haltout,
       ex_mem_1_jalout, ex_mem_1_jalrout, ex_mem_1_lbout, ex_mem_1_memtoregout, ex_mem_1_remuout,
       ex_mem_1_uretout, EXASB, EXJAL, EXJALR, Go, halt, id_ex_1_lbout, id_ex_1_memwriteout, id_ex_1_remuout,
       id_ex_1_uretout, IR1, IR2, IR3, JAL, JALR, LB, LBlow7, Ledout, LoadUse, MTR, nand_1_out, not_1_out,
       or_2_out, or_3_out, or_4_out, or_5_out, or_6_out, or_7_out, or_8_out, rehalt, REMU, RST, RWE, RWM,
       tunnel, tunnel_t, URET, W1, W2, W3, \单周期硬布线控制器_1_alu_src , \单周期硬布线控制器_1_beq , \单周期硬布线控制器_1_bltu ,
       \单周期硬布线控制器_1_bne , \单周期硬布线控制器_1_ecall , \单周期硬布线控制器_1_jal , \单周期硬布线控制器_1_jalr , \单周期硬布线控制器_1_lb ,
       \单周期硬布线控制器_1_memtoreg , \单周期硬布线控制器_1_memwrite , \单周期硬布线控制器_1_regwrite , \单周期硬布线控制器_1_remu ,
       \单周期硬布线控制器_1_s_type , \单周期硬布线控制器_1_uret ;
  wire [1:0] LB01, R1F, R1F0, R2F, R2F0;
  wire [3:0] id_ex_1_aluopout, \单周期硬布线控制器_1_alu_op ;
  wire [4:0] EXW, FUNC, MEMW, R1, R2, RW_num;
  wire [7:0] multiplexer_13_out;
  wire [11:0] multiplexer_4_out;
  wire [12:0] CNT_num;
  wire [15:0] \LoadUse次数 , \总周期数 , \插入气泡数 , \无条件分支数 , \条件分支成功数 ;
  wire [19:0] shifter_1_out;
  wire [31:0] adder_2_out, adder_3_out, adder_4_out, alu_1_result, alu_1_result_2, ALURES, and_8_out,
       bit_extender_1_out, bit_extender_2_out, bit_extender_3_out, bit_extender_4_out, bit_extender_5_out,
       BranAddr, EX_IR, ex_mem_1_pc_4out, ex_mem_1_r2out, EXALUB, EXMUXR1, EXMUXR2, EXMUXR3, EXR1Data,
       EXR2Data, id_ex_1_lbaout, id_ex_1_pc_4out, ID_IR, if_id_1_pc_4out, IF_IR, JALAddr, JALRAddr, LBAddr,
       MData, MEM_IR, mem_wb_1_memdataout, mem_wb_1_pc_4out, multiplexer_1_out, multiplexer_5_out,
       multiplexer_7_out, multiplexer_10_out, multiplexer_11_out, multiplexer_12_out, multiplexer_14_out,
       not_2_out, PC_4, R1Data, R2Data, ram_1_data, Result2, shifter_2_out, WB_IR;

  Button \u_总复位  (.out(RST));
  Button _1 (.out(IR1));
  Button _2 (.out(IR2));
  Button _3 (.out(IR3));
  // Probe on \总周期数 
  // Probe on \总周期数 
  Button \u_继续运行  (.out(Go));
  LED #(.active("true")) led_1 (.in(W1));
  LED #(.active("true")) led_2 (.in(W2));
  LED #(.active("true")) led_3 (.in(W3));
  Hex_Digit_Display hex_digit_display_1 (.value(LedData[31:28]));  // open: dp
  // Probe on IF_PC[19:0]
  // RiscV_Probe riscv_probe_1: pin names not known; wires that end beside it: IF_IR
  Multiplexer #(.select(3), .width(32), .disabled("Z"), .enable("false")) multiplexer_1 (
    .in0(PC_4), .in1(BranAddr), .in2(JALAddr), .in4(JALRAddr), .out(multiplexer_1_out),
    .sel({EXJALR, EXJAL, Branch}));  // open: in3, in5, in6, in7
  and and_1 (and_1_out, ~LoadUse, ~rehalt);  // AND_Gate
  Hex_Digit_Display hex_digit_display_2 (.value(LedData[23:20]));  // open: dp
  Hex_Digit_Display hex_digit_display_3 (.value(LedData[27:24]));  // open: dp
  // Probe on ID_PC[19:0]
  // RiscV_Probe riscv_probe_2: pin names not known; wires that end beside it: {ID_IR[31], FUNC[4], ID_IR[29:26], FUNC[3], ID_IR[24:15], FUNC[2:0], ID_IR[11:0]}
  Register #(.width(32), .trigger("rising"), .Select("low")) PC (
    .D(multiplexer_1_out), .en(and_1_out), .Q(IF_PC), .clk(CLK), .clr(RST));
  Comparator #(.width(32), .mode("twosComplement")) comparator_1 (
    .a(EXMUXR1), .b(32'h22), .eq(comparator_1_eq));  // open: gt, lt
  Register #(.width(32), .trigger("rising"), .Select("low")) register_1 (
    .D(EXMUXR2), .en(Ledout), .Q(LedData), .clk(CLK), .clr(RST));
  and and_2 (and_2_out, tunnel_t, Beq);
  and and_3 (and_3_out, ~tunnel_t, Bne);  // AND_Gate
  and and_4 (and_4_out, tunnel, Bltu);
  Hex_Digit_Display hex_digit_display_4 (.value(LedData[15:12]));  // open: dp
  Hex_Digit_Display hex_digit_display_5 (.value(LedData[19:16]));  // open: dp
  and and_5 (halt, ecall, ~comparator_1_eq);  // AND_Gate
  and and_6 (Ledout, ecall, comparator_1_eq);
  or or_1 (Branch, and_2_out, and_3_out, and_4_out);
  Hex_Digit_Display hex_digit_display_6 (.value(LedData[7:4]));  // open: dp
  Hex_Digit_Display hex_digit_display_7 (.value(LedData[11:8]));  // open: dp
  // Probe on EX_PC[19:0]
  // RiscV_Probe riscv_probe_3: pin names not known; wires that end beside it: EX_IR
  // RiscV_Probe riscv_probe_4: pin names not known; wires that end beside it: IF_IR
  Hex_Digit_Display hex_digit_display_8 (.value(LedData[3:0]));  // open: dp
  Adder #(.width(32)) adder_1 (.a(IF_PC), .b(32'h4), .out(PC_4));  // open: cin, cout
  ROM #(.addrWidth(10), .dataWidth(32), .Select("high")) rom_1 (.addr(IF_PC[11:2]), .data(IF_IR));
  or or_2 (or_2_out, EXJALR, EXJAL, Branch, RST);
  // Probe on \总周期数 
  // Probe on M_PC[19:0]
  // RiscV_Probe riscv_probe_5: pin names not known; wires that end beside it: MEM_IR
  IF_ID if_id_1 (
    .PCin(IF_PC), .PCout(ID_PC), .PC_4in(PC_4), .PC_4out(if_id_1_pc_4out), .\指令字in (IF_IR),
    .\指令字out ({ID_IR[31], FUNC[4], ID_IR[29:26], FUNC[3], ID_IR[24:15], FUNC[2:0], ID_IR[11:0]}),
    .clr(or_2_out), .clk(CLK), .abl(or_3_out));  // open: PJin, PJout
  or or_3 (or_3_out, LoadUse, rehalt);
  // Probe on \总周期数 
  // Probe on \无条件分支数 
  // Probe on \条件分支成功数 
  // Probe on \插入气泡数 
  // Probe on \LoadUse次数 
  not not_1 (not_1_out, rehalt);
  Counter #(.width(16), .max('hffff), .ongoal("wrap"), .trigger("rising"), .behavior("new")) counter_1 (
    .count(not_1_out), .Q(\总周期数 ), .clk(CLK));  // open: load, D, carry, clr, preset, down
  // Probe on IF_PC[11:0]
  // Probe on WB_PC[19:0]
  // RiscV_Probe riscv_probe_6: pin names not known; wires that end beside it: WB_IR
  \单周期硬布线控制器  \u_单周期硬布线控制器_1  (
    .Funct(FUNC), .OP(ID_IR[6:2]), .ALU_OP(\单周期硬布线控制器_1_alu_op ), .MemToReg(\单周期硬布线控制器_1_memtoreg ),
    .MemWrite(\单周期硬布线控制器_1_memwrite ), .ALU_SRC(\单周期硬布线控制器_1_alu_src ), .RegWrite(\单周期硬布线控制器_1_regwrite ),
    .ecall(\单周期硬布线控制器_1_ecall ), .S_type(\单周期硬布线控制器_1_s_type ), .Jalr(\单周期硬布线控制器_1_jalr ),
    .Beq(\单周期硬布线控制器_1_beq ), .JAL(\单周期硬布线控制器_1_jal ), .Bne(\单周期硬布线控制器_1_bne ), .in_3(ID_IR[21]),
    .uret(\单周期硬布线控制器_1_uret ), .BLTU(\单周期硬布线控制器_1_bltu ), .LB(\单周期硬布线控制器_1_lb ), .REMU(\单周期硬布线控制器_1_remu ));
  Multiplexer #(.select(1), .width(5), .disabled("Z"), .enable("false")) multiplexer_2 (
    .in0(ID_IR[19:15]), .in1(5'b10001), .out(R1), .sel(\单周期硬布线控制器_1_ecall ));
  Multiplexer #(.select(1), .width(5), .disabled("Z"), .enable("false")) multiplexer_3 (
    .in0(ID_IR[24:20]), .in1(5'b01010), .out(R2), .sel(\单周期硬布线控制器_1_ecall ));
  Multiplexer #(.select(1), .width(12), .disabled("Z"), .enable("false")) multiplexer_4 (
    .in0({ID_IR[31], FUNC[4], ID_IR[29:26], FUNC[3], ID_IR[24:20]}),
    .in1({ID_IR[31], FUNC[4], ID_IR[29:26], FUNC[3], ID_IR[11:7]}), .out(multiplexer_4_out),
    .sel(\单周期硬布线控制器_1_s_type ));
  assign bit_extender_1_out = {{20{ID_IR[31]}}, {ID_IR[31], FUNC[4], ID_IR[29:26], FUNC[3], ID_IR[24:20]}};  // Bit_Extender bit_extender_1
  Comparator #(.width(7), .mode("twosComplement")) comparator_2 (
    .a(ID_IR[6:0]), .b(7'b0000011), .eq(LBlow7));  // open: gt, lt
  Counter #(.width(16), .max('hffff), .ongoal("wrap"), .trigger("rising"), .behavior("new")) counter_2 (
    .count(Branch), .Q(\条件分支成功数 ), .clk(CLK), .clr(RST));  // open: load, D, carry, preset, down
  // Probe on EX_PC[11:0]
  // Probe on ID_PC[11:0]
  and and_7 (and_7_out, LBlow7, \单周期硬布线控制器_1_lb );
  assign bit_extender_2_out = {{20{multiplexer_4_out[11]}}, multiplexer_4_out};  // Bit_Extender bit_extender_2
  assign bit_extender_3_out = {{20{ID_IR[31]}}, {ID_IR[31], ID_IR[7], FUNC[4], ID_IR[29:26], FUNC[3], ID_IR[11:8]}};  // Bit_Extender bit_extender_3
  Shifter #(.width(20), .shift("ll")) shifter_1 (
    .in({ID_IR[31], ID_IR[19:15], FUNC[2:0], ID_IR[20], FUNC[4], ID_IR[29:26], FUNC[3], ID_IR[24:21]}),
    .\dist (5'b00001), .out(shifter_1_out));
  // Probe on M_PC[11:0]
  D_Flip_Flop #(.trigger("high"), .Pre_Clr_Positions("LEGACY"), .NegatePresetClear("false"), .enable("true"), .NewFFLayout("false")) d_ff_1 (.Q(d_ff_1_q));  // open: clk, D, Qn, preset, en, reset
  // Probe on 13'h80
  Shifter #(.width(32), .shift("ll")) shifter_2 (.in(bit_extender_3_out), .\dist (5'b00001), .out(shifter_2_out));
  assign bit_extender_4_out = {{12{shifter_1_out[19]}}, shifter_1_out};  // Bit_Extender bit_extender_4
  Adder #(.width(32)) adder_2 (.a(bit_extender_1_out), .b(R1Data), .out(adder_2_out));  // open: cin, cout
  or or_4 (or_4_out, JAL, JALR);
  Counter #(.width(16), .max('hffff), .ongoal("wrap"), .trigger("rising"), .behavior("new")) counter_3 (
    .count(or_4_out), .Q(\无条件分支数 ), .clk(CLK), .clr(RST));  // open: load, D, carry, preset, down
  // Probe on WB_PC[11:0]
  Comparator #(.width(13), .mode("twosComplement")) comparator_3 (
    .a(CNT_num), .b(13'h80), .eq(comparator_3_eq), .lt(comparator_3_lt));  // open: gt
  Clock #(.highDuration(1), .lowDuration(1)) clock_1 (.out(clock_1_out));
  or or_5 (or_5_out, and_7_out, \单周期硬布线控制器_1_memtoreg );
  or or_6 (or_6_out, \单周期硬布线控制器_1_regwrite , and_7_out);
  Regifile_DW regifile_dw_1 (
    .Din(RDin), .Clk(CLK), .R1(R1Data), .R2(R2Data), .WE(RegWrite), .W_num(RW_num), .R1_num(R1), .R2_num(R2));
  Adder #(.width(32)) adder_3 (.a(shifter_2_out), .b(ID_PC), .out(adder_3_out));  // open: cin, cout
  Adder #(.width(32)) adder_4 (.a(bit_extender_4_out), .b(ID_PC), .out(adder_4_out));  // open: cin, cout
  assign and_8_out = adder_2_out & not_2_out;  // AND_Gate and_8, 32 bits wide
  assign not_2_out = ~32'h1;  // NOT_Gate not_2, 32 bits wide
  nand nand_1 (nand_1_out, d_ff_1_q, comparator_3_eq);
  Counter #(.width(13), .max('h1fff), .ongoal("stay"), .trigger("rising"), .behavior("old")) counter_4 (
    .count(comparator_3_lt), .Q(CNT_num), .clk(clock_1_out));  // open: load, D, carry, clr, preset
  Multiplexer #(.select(1), .width(32), .disabled("Z"), .enable("false")) multiplexer_5 (
    .in0(R2Data), .in1(bit_extender_2_out), .out(multiplexer_5_out), .sel(\单周期硬布线控制器_1_alu_src ));
  assign CLK = nand_1_out ? clock_1_out : 1'bz;  // Controlled_Buffer controlled_buffer_1
  ID_EX id_ex_1 (
    .REMUin(\单周期硬布线控制器_1_remu ), .LBin(and_7_out), .URETin(\单周期硬布线控制器_1_uret ), .JALRin(\单周期硬布线控制器_1_jalr ),
    .JALin(\单周期硬布线控制器_1_jal ), .BEQin(\单周期硬布线控制器_1_beq ), .BLTUin(\单周期硬布线控制器_1_bltu ),
    .BNEin(\单周期硬布线控制器_1_bne ), .MemToRegin(or_5_out), .MemWritein(\单周期硬布线控制器_1_memwrite ),
    .ALUopin(\单周期硬布线控制器_1_alu_op ), .R1datain(R1Data), .R2datain(R2Data), .RWin(ID_IR[11:7]),
    .BAin(adder_3_out), .JALAin(adder_4_out), .JALRin_2(and_8_out), .LBAin(adder_2_out),
    .REMUout(id_ex_1_remuout), .LBout(id_ex_1_lbout), .URETout(id_ex_1_uretout), .JALRout(EXJALR),
    .JALout(EXJAL), .BEQout(Beq), .BLTUout(Bltu), .BNEout(Bne), .MemToRegout(MTR),
    .MemWriteout(id_ex_1_memwriteout), .ALUopout(id_ex_1_aluopout), .R1dataout(EXR1Data),
    .R2dataout(EXR2Data), .RWout(EXW), .BAout(BranAddr), .JALAout(JALAddr), .JALRout_2(JALRAddr),
    .LBAout(id_ex_1_lbaout), .clr(or_7_out), .clk(CLK), .abl(rehalt), .PCin(ID_PC), .PCout(EX_PC),
    .PC_4in(if_id_1_pc_4out), .PC_4out(id_ex_1_pc_4out), .ALUBin(multiplexer_5_out), .ALUBout(EXALUB),
    .RegWritein(or_6_out), .RegWritegout(RWE), .R1Fin(R1F0), .R1Fout(R1F), .R2Fin(R2F0), .R2Fout(R2F),
    .ASBin(\单周期硬布线控制器_1_alu_src ), .ASBout(EXASB), .ECALLin(\单周期硬布线控制器_1_ecall ), .ECALLout(ecall));  // open: HALTin, HALTout, PJin, PJout
  or or_7 (or_7_out, EXJALR, EXJAL, Branch, RST, LoadUse);
  and and_9 (and_9_out, ~rehalt, bubble);  // AND_Gate
  Counter #(.width(16), .max('hffff), .ongoal("wrap"), .trigger("rising"), .behavior("new")) counter_5 (
    .count(and_9_out), .Q(\插入气泡数 ), .clk(CLK), .clr(RST));  // open: load, D, carry, preset, down
  Pull_Resistor #(.pull(1)) pull_resistor_1 (.node(CLK));
  Counter #(.width(16), .max('hffff), .ongoal("wrap"), .trigger("rising"), .behavior("new")) counter_6 (
    .count(LoadUse), .Q(\LoadUse次数 ), .clk(CLK), .clr(RST));  // open: load, D, carry, preset, down
  ALU alu_1 (
    .X(EXMUXR1), .Y(EXMUXR3), .AluOP(id_ex_1_aluopout), .Equal(tunnel_t), .Result(alu_1_result),
    .Result_2(alu_1_result_2), .out_6(tunnel));  // open: out_4
  EX_MEM ex_mem_1 (
    .PCin(EX_PC), .PC_4in(id_ex_1_pc_4out), .HALTin(halt), .REMUin(id_ex_1_remuout), .LBin(id_ex_1_lbout),
    .URETin(id_ex_1_uretout), .JALRin(EXJALR), .JALin(EXJAL), .MemToRegin(MTR),
    .MemWritein(id_ex_1_memwriteout), .ALURin(alu_1_result), .RWin(EXW), .LBAin(id_ex_1_lbaout),
    .PCout(M_PC), .PC_4out(ex_mem_1_pc_4out), .HALTout(ex_mem_1_haltout), .REMUout(ex_mem_1_remuout),
    .LBout(ex_mem_1_lbout), .URETout(ex_mem_1_uretout), .JALRout(ex_mem_1_jalrout), .JALout(ex_mem_1_jalout),
    .MemToRegout(ex_mem_1_memtoregout), .MemWriteout(MemWrite), .ALURout(ALURES), .RWout(MEMW),
    .LBAout(LBAddr), .clr(RST), .clk(CLK), .abl(rehalt), .R2datain(EXMUXR2), .R2dataout(MDin),
    .R2in(alu_1_result_2), .R2out(ex_mem_1_r2out), .RegWritein(RWE), .RegWritegout(RWM));
  Multiplexer #(.select(2), .width(32), .disabled("Z"), .enable("false")) multiplexer_6 (
    .in0(EXR1Data), .in1(RDin), .in2(ALURES), .in3({32{1'b0}}), .out(EXMUXR1), .sel(R1F));
  Multiplexer #(.select(2), .width(32), .disabled("Z"), .enable("false")) multiplexer_7 (
    .in0(EXALUB), .in1(RDin), .in2(ALURES), .in3({32{1'b0}}), .out(multiplexer_7_out), .sel(R2F));
  Multiplexer #(.select(2), .width(32), .disabled("Z"), .enable("false")) multiplexer_8 (
    .in0(EXR2Data), .in1(RDin), .in2(ALURES), .in3({32{1'b0}}), .out(EXMUXR2), .sel(R2F));
  Multiplexer #(.select(1), .width(32), .disabled("Z"), .enable("false")) multiplexer_9 (
    .in0(multiplexer_7_out), .in1(EXALUB), .out(EXMUXR3), .sel(EXASB));
  Redirect redirect_1 (
    .R1(R1), .EXW(EXW), .MEMW(MEMW), .R2(R2), .R1F(R1F0), .R2F(R2F0), .LoadUse(LoadUse), .Bubble(bubble),
    .RWE(RWE), .RWM(RWM), .MemToReg(MTR), .OP(ID_IR[6:2]), .Funct(FUNC));
  Multiplexer #(.select(1), .width(32), .disabled("Z"), .enable("false")) multiplexer_10 (
    .in0(ALURES), .in1(LBAddr), .out(multiplexer_10_out), .sel(ex_mem_1_lbout));
  RAM #(.addrWidth(10), .dataWidth(32), .bus("separate"), .Select("high")) ram_1 (
    .addr(multiplexer_10_out[11:2]), .din(MDin), .data(ram_1_data), .str(MemWrite), .clk(CLK), .clr(RST));  // open: sel, ld
  Multiplexer #(.select(1), .width(32), .disabled("Z"), .enable("false")) multiplexer_11 (
    .in0(ALURES), .in1(ram_1_data), .out(multiplexer_11_out), .sel(ex_mem_1_memtoregout));
  MEM_WB mem_wb_1 (
    .PCin(M_PC), .PC_4in(ex_mem_1_pc_4out), .HALTin(ex_mem_1_haltout), .REMUin(ex_mem_1_remuout),
    .LBin(ex_mem_1_lbout), .URETin(ex_mem_1_uretout), .JALRin(ex_mem_1_jalrout), .JALin(ex_mem_1_jalout),
    .MemDatain(multiplexer_11_out), .R2in(ex_mem_1_r2out), .LB01in(multiplexer_10_out[1:0]),
    .Mdatain(ram_1_data), .RWin(MEMW), .PCout(WB_PC), .PC_4out(mem_wb_1_pc_4out), .HALTout(rehalt),
    .REMUout(REMU), .LBout(LB), .URETout(URET), .JALRout(JALR), .JALout(JAL),
    .MemDataout(mem_wb_1_memdataout), .R2out(Result2), .LB01out(LB01), .Mdataout(MData), .RWout(RW_num),
    .clr(RST), .clk(CLK), .abl(rehalt), .RegWritein(RWM), .RegWritegout(RegWrite), .go(Go));
  or or_8 (or_8_out, JAL, JALR);
  Multiplexer #(.select(1), .width(32), .disabled("Z"), .enable("false")) multiplexer_12 (
    .in0(mem_wb_1_memdataout), .in1(mem_wb_1_pc_4out), .out(multiplexer_12_out), .sel(or_8_out));
  Multiplexer #(.select(2), .width(8), .disabled("Z"), .enable("false")) multiplexer_13 (
    .in0(MData[7:0]), .in1(MData[15:8]), .in2(MData[23:16]), .in3(MData[31:24]), .out(multiplexer_13_out),
    .sel(LB01));
  Multiplexer #(.select(1), .width(32), .disabled("Z"), .enable("false")) multiplexer_14 (
    .in0(multiplexer_12_out), .in1(Result2), .out(multiplexer_14_out), .sel(REMU));
  assign bit_extender_5_out = {{24{multiplexer_13_out[7]}}, multiplexer_13_out};  // Bit_Extender bit_extender_5
  Multiplexer #(.select(1), .width(32), .disabled("Z"), .enable("false")) multiplexer_15 (
    .in0(multiplexer_14_out), .in1(bit_extender_5_out), .out(RDin), .sel(LB));

  // Other names for the same wires on the sheet: ID_IR (some bits) = FUNC; OP[4:0] = ID_IR[6:2]; MEM_PC[31:0] = M_PC

  // Notes on the sheet:
  //   中断源
  //   时空图监测，可删除
  //   中断等待指示
  //   数码管输出
  //   指令探针
  //   指令存储器
  //   指令字
  //   contents of rom_1 (hex, n*v repeats v):
  //   100493 100006f 100493 200913 300993 100006f 100493 200913 300993 100006f 100493 200913 300993
  //   100006f 100493 200913 300993 3c8000ef 100413 100493 1f49493 900533 2200893 73 24d493 48463 fedff06f
  //   900533 2200893 73 100493 249493 900533 2200893 73 48463 fedff06f 100493 1f49493 900533 2200893 73
  //   4034d493 900533 2200893 73 4044d493 900533 2200893 73 4044d493 900533 2200893 73 4044d493 900533
  //   2200893 73 4044d493 900533 2200893 73 4044d493 900533 2200893 73 4044d493 900533 2200893 73 4044d493
  //   900533 2200893 73 100413 1f41993 41f9d993 433 c00913 300b13 140413 f47413 800293 100313 499993
  //   89e9b3 1300533 2200893 73 406282b3 fe0294e3 140413 f00f93 1f47433 1c41413 800293 100313 49d993
  //   89e9b3 1300533 2200893 73 406282b3 fe0294e3 1c45413 406b0b33 b0463 f95ff06f 2b3 fff2c293 829293
  //   ff2e293 500533 2200893 73 fff00413 493 84a023 140413 448493 84a023 140413 448493 84a023 140413
  //   448493 84a023 140413 448493 84a023 140413 448493 84a023 140413 448493 84a023 140413 448493 84a023
  //   140413 448493 84a023 140413 448493 84a023 140413 448493 84a023 140413 448493 84a023 140413 448493
  //   84a023 140413 448493 84a023 140413 448493 84a023 140413 448493 84a023 140413 448493 140413 433
  //   3c00493 42983 4aa03 149a2b3 28663 134a023 1442023 ffc48493 fe9412e3 800533 2200893 73 440413 3c00493
  //   fc9416e3 3200893 73 200293 1100493 849493 1148493 900533 2200893 73 2000e13 25484b3 900533 2200893
  //   73 fffe0e13 fe0e16e3 a00893 73 8800493 849493 4848493 8700913 891913 5490913 2997933 1091913
  //   11096913 1200533 2200893 73 a00893 73 313 1000e13 8400493 849493 8348493 400913 891913 490913 849493
  //   8248493 849493 8148493 891913 490913 891913 490913 932023 12484b3 430313 fffe0e13 fe0e18e3 2000e13
  //   313 30483 900533 2200893 73 130313 fffe0e13 fe0e14e3 a00893 73 ff100493 900533 2200893 73 148493
  //   fe9068e3 900533 2200893 73 a00893 73 a00893 73 413 140413 800533 2200893 73 240413 800533 2200893 73
  //   340413 800533 2200893 73 440413 800533 2200893 73 540413 800533 2200893 73 640413 800533 2200893 73
  //   740413 800533 2200893 73 840413 800533 2200893 2200893 73 8067
  //   JAL
  //   JALR
  //   URET
  //   控制位
  //   Beq
  //   Bne
  //   MemToReg
  //   MemWrite
  //   AluOP
  //   AluSrcB
  //   RegWrite
  //   流水调试日志用
  //   暂停节拍，不能为0
  //   戳工具置1进入计数暂停模式，ctrl+k时钟自动运行到对应节拍暂停
  //   ctrl+k关闭时钟连续运行，将控制位置零，进入单步调试模式调试
  //   可计数暂停的时钟源
  //   为方便自动评测，需要输出流水线各段保存的PC值，注意是PC不是PC+4，另外ID段寄存器写入信息，Mem段内存写入信息也要输出
  //   数据存储器
endmodule

module \中断按键参考电路  (
  input  clk,
  input  \中断 ,
  input  \同步清零信号 ,
  output \与中断屏蔽位与 ,
  output \中断等待指示灯 
);

  wire and_1_out, d_ff_1_q, or_2_out;

  or or_1 (\中断等待指示灯 , \与中断屏蔽位与 , d_ff_1_q);
  D_Flip_Flop #(.trigger("rising"), .Pre_Clr_Positions("LEGACY"), .NegatePresetClear("false"), .enable("true"), .NewFFLayout("false")) d_ff_1 (
    .clk(\中断 ), .D(1'b1), .Q(d_ff_1_q), .reset(\与中断屏蔽位与 ));  // open: Qn, preset, en
  or or_2 (or_2_out, d_ff_1_q, \与中断屏蔽位与 );
  and and_1 (and_1_out, or_2_out, ~\同步清零信号 );  // AND_Gate
  D_Flip_Flop #(.trigger("rising"), .Pre_Clr_Positions("LEGACY"), .NegatePresetClear("false"), .enable("true"), .NewFFLayout("false")) IR1 (
    .clk(clk), .D(and_1_out), .Q(\与中断屏蔽位与 ));  // open: Qn, preset, en, reset

  // Notes on the sheet:
  //   中断信号采样参考电路
  //   Reset 
endmodule
module \单周期_单级中断  (
  input  IR1,
  input  IR2,
  input  IR3,
  output RegWrite,
  output MemWrite,
  output [31:0] PC,
  output [31:0] IR,
  output [31:0] RDin,
  output [31:0] MDin,
  output [31:0] LedData
);

  wire and_1_out, and_2_out, and_3_out, and_4_out, and_7_out, Beq, Bltu, Bne, Branch, CLK, clock_1_out, CLR1,
       CLR2, CLR3, comparator_1_eq, comparator_2_eq, comparator_3_eq, comparator_4_eq, comparator_5_eq,
       comparator_7_eq, comparator_7_lt, d_ff_1_qn, d_ff_2_q, decoder_1_out1, decoder_1_out2, decoder_1_out3,
       ecall, Go, halt, INT, IR1_t, IR2_t, IR3_t, IRA, IRB, IRC, IRSig, JAL, JALR, LB, LBlow7, Ledout,
       nand_1_out, not_1_out, not_2_out, or_1_out, or_5_out, or_7_out, REMU, RST, tunnel, tunnel_t, URET, W1,
       W2, W3, \中断按键参考电路_1_与中断屏蔽位与 , \中断按键参考电路_2_与中断屏蔽位与 , \中断按键参考电路_3_与中断屏蔽位与 , \单周期硬布线控制器_1_alu_src ,
       \单周期硬布线控制器_1_lb , \单周期硬布线控制器_1_memtoreg , \单周期硬布线控制器_1_s_type ;
  wire [1:0] IRNum, LB01, register_2_q;
  wire [3:0] \单周期硬布线控制器_1_alu_op ;
  wire [4:0] multiplexer_1_out, multiplexer_2_out;
  wire [7:0] multiplexer_12_out;
  wire [11:0] multiplexer_3_out;
  wire [12:0] CNT_num;
  wire [15:0] \总周期数 ;
  wire [19:0] shifter_1_out;
  wire [31:0] alu_1_result, bit_extender_1_out, bit_extender_2_out, bit_extender_3_out, bit_extender_4_out,
       bit_extender_5_out, BranAddr, JALAddr, JALRAddr, LBAddr, MData, mEPC_q, multiplexer_4_out,
       multiplexer_5_out, multiplexer_7_out, multiplexer_10_out, multiplexer_11_out, multiplexer_13_out,
       NextAddr, not_3_out, OriAddr, PC_4, R1Data, R2, shifter_2_out;
  wire [31:2] multiplexer_6_out;

  Button \u_继续运行  (.out(Go));
  Button _1 (.out(IRA));
  Button _2 (.out(IRB));
  Button _3 (.out(IRC));
  LED #(.active("true")) led_1 (.in(W1));
  LED #(.active("true")) led_2 (.in(W2));
  LED #(.active("true")) led_3 (.in(W3));
  Hex_Digit_Display hex_digit_display_1 (.value(LedData[31:28]));  // open: dp
  Comparator #(.width(16), .mode("twosComplement")) comparator_1 (
    .a(16'h23b), .b(\总周期数 ), .eq(comparator_1_eq));  // open: gt, lt
  Comparator #(.width(16), .mode("twosComplement")) comparator_2 (
    .a(\总周期数 ), .b(16'h1), .eq(comparator_2_eq));  // open: gt, lt
  Comparator #(.width(16), .mode("twosComplement")) comparator_3 (
    .a(\总周期数 ), .b(16'h4), .eq(comparator_3_eq));  // open: gt, lt
  Comparator #(.width(16), .mode("twosComplement")) comparator_4 (
    .a(\总周期数 ), .b(16'h7), .eq(comparator_4_eq));  // open: gt, lt
  not not_1 (not_1_out, halt);
  Comparator #(.width(32), .mode("twosComplement")) comparator_5 (
    .a(R1Data), .b(32'h22), .eq(comparator_5_eq));  // open: gt, lt
  Register #(.width(32), .trigger("rising"), .Select("low")) register_1 (
    .D(MDin), .en(Ledout), .Q(LedData), .clk(CLK), .clr(RST));
  and and_1 (and_1_out, tunnel_t, Beq);
  and and_2 (and_2_out, ~tunnel_t, Bne);  // AND_Gate
  and and_3 (and_3_out, tunnel, Bltu);
  Hex_Digit_Display hex_digit_display_2 (.value(LedData[27:24]));  // open: dp
  Hex_Digit_Display hex_digit_display_3 (.value(LedData[23:20]));  // open: dp
  or or_1 (or_1_out, comparator_1_eq, comparator_2_eq);
  assign IRA = or_1_out ? ~CLK : 1'bz;  // Controlled_Inverter controlled_inverter_1
  assign IRB = comparator_3_eq ? ~CLK : 1'bz;  // Controlled_Inverter controlled_inverter_2
  assign IRC = comparator_4_eq ? ~CLK : 1'bz;  // Controlled_Inverter controlled_inverter_3
  Register #(.width(32), .trigger("rising"), .Select("low")) u_PC (
    .D(NextAddr), .en(not_1_out), .Q(PC), .clk(CLK), .clr(RST));
  or or_2 (Branch, and_1_out, and_2_out, and_3_out);
  Hex_Digit_Display hex_digit_display_4 (.value(LedData[19:16]));  // open: dp
  Hex_Digit_Display hex_digit_display_5 (.value(LedData[15:12]));  // open: dp
  Pull_Resistor #(.pull(0)) pull_resistor_1 (.node(IRA));
  Pull_Resistor #(.pull(0)) pull_resistor_2 (.node(IRB));
  Pull_Resistor #(.pull(0)) pull_resistor_3 (.node(IRC));
  Adder #(.width(32)) adder_1 (.a(PC), .b(32'h4), .out(PC_4));  // open: cin, cout
  and and_4 (and_4_out, ecall, ~comparator_5_eq);  // AND_Gate
  and and_5 (Ledout, ecall, comparator_5_eq);
  not not_2 (not_2_out, halt);
  Counter #(.width(16), .max('hffff), .ongoal("wrap"), .trigger("rising"), .behavior("new")) counter_1 (
    .count(not_2_out), .Q(\总周期数 ), .clk(CLK));  // open: load, D, carry, clr, preset, down
  Hex_Digit_Display hex_digit_display_6 (.value(LedData[7:4]));  // open: dp
  Hex_Digit_Display hex_digit_display_7 (.value(LedData[11:8]));  // open: dp
  // Probe on \总周期数 
  // RiscV_Probe riscv_probe_1: pin names not known; wires that end beside it: IR
  ROM #(.addrWidth(10), .dataWidth(32), .Select("high")) rom_1 (.addr(PC[11:2]), .data(IR));
  Counter #(.width(1), .max('h1), .ongoal("wrap"), .trigger("rising"), .behavior("old")) counter_2 (
    .load(and_4_out), .D(and_4_out), .count(1'b0), .Q(halt), .clk(CLK), .clr(Go));  // open: carry, preset
  Hex_Digit_Display hex_digit_display_8 (.value(LedData[3:0]));  // open: dp
  and and_6 (LB, LBlow7, \单周期硬布线控制器_1_lb );
  \单周期硬布线控制器  \u_单周期硬布线控制器_1  (
    .Funct({IR[30], IR[25], IR[14:12]}), .OP(IR[6:2]), .ALU_OP(\单周期硬布线控制器_1_alu_op ),
    .MemToReg(\单周期硬布线控制器_1_memtoreg ), .MemWrite(MemWrite), .ALU_SRC(\单周期硬布线控制器_1_alu_src ),
    .RegWrite(RegWrite), .ecall(ecall), .S_type(\单周期硬布线控制器_1_s_type ), .Jalr(JALR), .Beq(Beq), .JAL(JAL),
    .Bne(Bne), .in_3(IR[21]), .uret(URET), .BLTU(Bltu), .LB(\单周期硬布线控制器_1_lb ), .REMU(REMU));
  Multiplexer #(.select(1), .width(5), .disabled("Z"), .enable("false")) multiplexer_1 (
    .in0(IR[19:15]), .in1(5'b10001), .out(multiplexer_1_out), .sel(ecall));
  Multiplexer #(.select(1), .width(5), .disabled("Z"), .enable("false")) multiplexer_2 (
    .in0(IR[24:20]), .in1(5'b01010), .out(multiplexer_2_out), .sel(ecall));
  Multiplexer #(.select(1), .width(12), .disabled("Z"), .enable("false")) multiplexer_3 (
    .in0(IR[31:20]), .in1({IR[31:25], IR[11:7]}), .out(multiplexer_3_out), .sel(\单周期硬布线控制器_1_s_type ));
  assign bit_extender_1_out = {{20{IR[31]}}, IR[31:20]};  // Bit_Extender bit_extender_1
  Comparator #(.width(7), .mode("twosComplement")) comparator_6 (
    .a(IR[6:0]), .b(7'b0000011), .eq(LBlow7));  // open: gt, lt
  \中断按键参考电路  \u_中断按键参考电路_1  (.\与中断屏蔽位与 (\中断按键参考电路_1_与中断屏蔽位与 ), .\同步清零信号 (CLR1), .\中断等待指示灯 (W1), .\中断 (IRA), .clk(CLK));
  \中断按键参考电路  \u_中断按键参考电路_2  (.\与中断屏蔽位与 (\中断按键参考电路_2_与中断屏蔽位与 ), .\同步清零信号 (CLR2), .\中断等待指示灯 (W2), .\中断 (IRB), .clk(CLK));
  \中断按键参考电路  \u_中断按键参考电路_3  (.\与中断屏蔽位与 (\中断按键参考电路_3_与中断屏蔽位与 ), .\同步清零信号 (CLR3), .\中断等待指示灯 (W3), .\中断 (IRC), .clk(CLK));
  or or_3 (IR1_t, IR1, IRA);
  assign bit_extender_2_out = {{20{multiplexer_3_out[11]}}, multiplexer_3_out};  // Bit_Extender bit_extender_2
  assign bit_extender_3_out = {{20{IR[31]}}, {IR[31], IR[7], IR[30:25], IR[11:8]}};  // Bit_Extender bit_extender_3
  Shifter #(.width(20), .shift("ll")) shifter_1 (
    .in({IR[31], IR[19:12], IR[20], IR[30:21]}), .\dist (5'b00001), .out(shifter_1_out));
  Priority_Encoder #(.select(2), .disabled("Z")) priority_encoder_1 (
    .in1(\中断按键参考电路_1_与中断屏蔽位与 ), .in2(\中断按键参考电路_2_与中断屏蔽位与 ), .in3(\中断按键参考电路_3_与中断屏蔽位与 ), .out(IRNum),
    .gs(IRSig));  // open: in0, en_out, en_in
  D_Flip_Flop #(.trigger("rising"), .Pre_Clr_Positions("LEGACY"), .NegatePresetClear("false"), .enable("true"), .NewFFLayout("true")) d_ff_1 (
    .clk(CLK), .D(and_7_out), .Qn(d_ff_1_qn));  // open: Q, preset, en, reset
  and and_7 (and_7_out, ~URET, IRSig);  // AND_Gate
  or or_4 (IR2_t, IR2, IRB);
  or or_5 (or_5_out, LB, RegWrite);
  Shifter #(.width(32), .shift("ll")) shifter_2 (.in(bit_extender_3_out), .\dist (5'b00001), .out(shifter_2_out));
  assign bit_extender_4_out = {{12{shifter_1_out[19]}}, shifter_1_out};  // Bit_Extender bit_extender_4
  Adder #(.width(32)) adder_2 (.a(bit_extender_1_out), .b(R1Data), .out(LBAddr));  // open: cin, cout
  and and_8 (INT, d_ff_1_qn, IRSig);
  Regfile_UP regfile_up_1 (
    .Din(RDin), .Clk(CLK), .R1(R1Data), .R2(MDin), .WE(or_5_out), .W_num(IR[11:7]),
    .R1_num(multiplexer_1_out), .R2_num(multiplexer_2_out));
  Adder #(.width(32)) adder_3 (.a(shifter_2_out), .b(PC), .out(BranAddr));  // open: cin, cout
  Adder #(.width(32)) adder_4 (.a(bit_extender_4_out), .b(PC), .out(JALAddr));  // open: cin, cout
  assign JALRAddr = LBAddr & not_3_out;  // AND_Gate and_9, 32 bits wide
  assign not_3_out = ~32'h1;  // NOT_Gate not_3, 32 bits wide
  or or_6 (IR3_t, IR3, IRC);
  Multiplexer #(.select(1), .width(32), .disabled("Z"), .enable("false")) multiplexer_4 (
    .in0(MDin), .in1(bit_extender_2_out), .out(multiplexer_4_out), .sel(\单周期硬布线控制器_1_alu_src ));
  Register #(.width(2), .trigger("rising"), .Select("low")) register_2 (
    .D(IRNum), .en(INT), .Q(register_2_q), .clk(CLK), .clr(RST));
  ALU alu_1 (
    .X(R1Data), .Y(multiplexer_4_out), .AluOP(\单周期硬布线控制器_1_alu_op ), .Equal(tunnel_t), .Result(alu_1_result),
    .Result_2(R2), .out_6(tunnel));  // open: out_4
  Decoder #(.select(2), .tristate("false"), .disabled("Z"), .enable("false")) decoder_1 (
    .out1(decoder_1_out1), .out2(decoder_1_out2), .out3(decoder_1_out3), .sel(register_2_q));  // open: out0
  and and_10 (CLR1, decoder_1_out1, URET);
  and and_11 (CLR2, decoder_1_out2, URET);
  Register #(.width(32), .trigger("rising"), .Select("low")) mEPC (
    .D(OriAddr), .en(INT), .Q(mEPC_q), .clk(CLK), .clr(RST));
  Multiplexer #(.select(2), .width(32), .disabled("Z"), .enable("false")) multiplexer_5 (
    .in1(32'h30ac), .in2(32'h3150), .in3(32'h31f4), .out(multiplexer_5_out), .sel(IRNum));  // open: in0
  Multiplexer #(.select(1), .width(32), .disabled("Z"), .enable("false")) multiplexer_6 (
    .in0(alu_1_result), .in1(LBAddr), .out({multiplexer_6_out, LB01}), .sel(LB));
  and and_12 (CLR3, decoder_1_out3, URET);
  Multiplexer #(.select(1), .width(32), .disabled("Z"), .enable("false")) multiplexer_7 (
    .in0(OriAddr), .in1(mEPC_q), .out(multiplexer_7_out), .sel(URET));
  Multiplexer #(.select(1), .width(32), .disabled("Z"), .enable("false")) multiplexer_8 (
    .in0(multiplexer_7_out), .in1(multiplexer_5_out), .out(NextAddr), .sel(INT));
  RAM #(.addrWidth(10), .dataWidth(32), .bus("separate"), .Select("high")) ram_1 (
    .addr(multiplexer_6_out[11:2]), .din(MDin), .data(MData), .str(MemWrite), .clk(CLK), .clr(RST));  // open: sel, ld
  Multiplexer #(.select(3), .width(32), .disabled("Z"), .enable("false")) multiplexer_9 (
    .in0(PC_4), .in1(BranAddr), .in2(JALAddr), .in4(JALRAddr), .out(OriAddr), .sel({JALR, JAL, Branch}));  // open: in3, in5, in6, in7
  Multiplexer #(.select(1), .width(32), .disabled("Z"), .enable("false")) multiplexer_10 (
    .in0(alu_1_result), .in1(MData), .out(multiplexer_10_out), .sel(\单周期硬布线控制器_1_memtoreg ));
  D_Flip_Flop #(.trigger("high"), .Pre_Clr_Positions("LEGACY"), .NegatePresetClear("false"), .enable("true"), .NewFFLayout("false")) d_ff_2 (.Q(d_ff_2_q));  // open: clk, D, Qn, preset, en, reset
  // Probe on 13'hc
  Multiplexer #(.select(1), .width(32), .disabled("Z"), .enable("false")) multiplexer_11 (
    .in0(multiplexer_10_out), .in1(PC_4), .out(multiplexer_11_out), .sel(or_7_out));
  or or_7 (or_7_out, JAL, JALR);
  Multiplexer #(.select(2), .width(8), .disabled("Z"), .enable("false")) multiplexer_12 (
    .in0(MData[7:0]), .in1(MData[15:8]), .in2(MData[23:16]), .in3(MData[31:24]), .out(multiplexer_12_out),
    .sel(LB01));
  assign bit_extender_5_out = {{24{multiplexer_12_out[7]}}, multiplexer_12_out};  // Bit_Extender bit_extender_5
  Comparator #(.width(13), .mode("twosComplement")) comparator_7 (
    .a(CNT_num), .b(13'hc), .eq(comparator_7_eq), .lt(comparator_7_lt));  // open: gt
  Clock #(.highDuration(1), .lowDuration(1)) clock_1 (.out(clock_1_out));
  Multiplexer #(.select(1), .width(32), .disabled("Z"), .enable("false")) multiplexer_13 (
    .in0(multiplexer_11_out), .in1(R2), .out(multiplexer_13_out), .sel(REMU));
  Counter #(.width(13), .max('h1fff), .ongoal("stay"), .trigger("rising"), .behavior("old")) counter_3 (
    .count(comparator_7_lt), .Q(CNT_num), .clk(clock_1_out));  // open: load, D, carry, clr, preset
  Multiplexer #(.select(1), .width(32), .disabled("Z"), .enable("false")) multiplexer_14 (
    .in0(multiplexer_13_out), .in1(bit_extender_5_out), .out(RDin), .sel(LB));
  nand nand_1 (nand_1_out, d_ff_2_q, comparator_7_eq);
  assign CLK = nand_1_out ? clock_1_out : 1'bz;  // Controlled_Buffer controlled_buffer_1
  Pull_Resistor #(.pull(1)) pull_resistor_4 (.node(CLK));

  // Other names for the same wires on the sheet: R2Data[31:0] = MDin

  // Notes on the sheet:
  //   中断源
  //   中断等待指示
  //   总复位信号应将除ROM以外所有存储组件全部清零
  //   单级中断测试信号模拟器
  //   数码管输出
  //   数码管输出应该用寄存器锁存，否则显示数据只能一闪而过
  //   指令探针
  //   指令存储器
  //   contents of rom_1 (hex, n*v repeats v):
  //   7d000113 100413 1f41993 41f9d993 433 c00913 800b13 140413 f47413 800293 100313 499993 89e9b3 1300533
  //   2200893 73 406282b3 fe0294e3 140413 f00f93 1f47433 1c41413 800293 100313 49d993 89e9b3 1300533
  //   2200893 73 406282b3 fe0294e3 1c45413 406b0b33 b0463 f95ff06f 2b3 fff2c293 1029293 fff2e293 500533
  //   2200893 73 f5dff06f 1112023 410113 a12023 410113 812023 410113 1312023 410113 1412023 410113 1512023
  //   410113 1612023 410113 100b13 300a13 100a93 1600433 441413 14469b3 1300533 2200893 73 fe0416e3
  //   415a0a33 fe0a10e3 ffc10113 12b03 ffc10113 12a83 ffc10113 12a03 ffc10113 12983 ffc10113 12403
  //   ffc10113 12503 ffc10113 12883 200073 1112023 410113 a12023 410113 812023 410113 1312023 410113
  //   1412023 410113 1512023 410113 1612023 410113 200b13 300a13 100a93 1600433 441413 14469b3 1300533
  //   2200893 73 fe0416e3 415a0a33 fe0a10e3 ffc10113 12b03 ffc10113 12a83 ffc10113 12a03 ffc10113 12983
  //   ffc10113 12403 ffc10113 12503 ffc10113 12883 200073 1112023 410113 a12023 410113 812023 410113
  //   1312023 410113 1412023 410113 1512023 410113 1612023 410113 300b13 300a13 100a93 1600433 441413
  //   14469b3 1300533 2200893 73 fe0416e3 415a0a33 fe0a10e3 ffc10113 12b03 ffc10113 12a83 ffc10113 12a03
  //   ffc10113 12983 ffc10113 12403 ffc10113 12503 ffc10113 12883 200073
  //   指令字
  //   JAL
  //   JALR
  //   URET
  //   Beq
  //   Bne
  //   MemToReg
  //   MemWrite
  //   AluOP
  //   AluSrcB
  //   RegWrite
  //   为方便自动评测，需要输出PC，IR，寄存器堆写如数据RDin
  //   RAM写使能MemWrite、RAM写入数据MDin等信号
  //   数据存储器
  //   控制位
  //   暂停节拍，不能为0
  //   戳工具置1进入计数暂停模式，ctrl+k时钟自动运行到对应节拍暂停
  //   ctrl+k关闭时钟连续运行，将控制位置零，进入单步调试模式调试
  //   可计数暂停的时钟源
endmodule

module \单周期_多级中断  (
  input  IR1,
  input  IR2,
  input  IR3,
  output RegWrite,
  output MemWrite,
  output [31:0] PC,
  output [31:0] IR,
  output [31:0] RDin,
  output [31:0] MDin,
  output [31:0] LedData
);

  wire and_1_out, and_2_out, and_3_out, and_4_out, Beq, Bltu, Bne, Branch, CLK, clock_1_out, CLR1, CLR2,
       CLR3, comparator_1_eq, comparator_2_eq, comparator_3_eq, comparator_4_eq, comparator_5_eq,
       comparator_6_eq, comparator_8_eq, comparator_9_eq, comparator_10_eq, comparator_11_eq,
       comparator_11_lt, comparator_12_gt, CSRRCI, CSRRSI, d_ff_1_q, decoder_1_out1, decoder_1_out2,
       decoder_1_out3, ecall, Go, halt, IR1_t, IR2_t, IR3_t, IRA, IRB, IRC, IREn, IRSig, JAL, JALR, LB,
       LBlow7, Ledout, nand_1_out, not_1_out, not_2_out, or_1_out, or_2_out, or_7_out, or_8_out, or_9_out,
       or_11_out, register_2_q, REMU, RST, tunnel, tunnel_t, URET, W1, W2, W3, \中断按键参考电路_1_与中断屏蔽位与 ,
       \中断按键参考电路_2_与中断屏蔽位与 , \中断按键参考电路_3_与中断屏蔽位与 , \单周期硬布线控制器_1_alu_src , \单周期硬布线控制器_1_lb ,
       \单周期硬布线控制器_1_memtoreg , \单周期硬布线控制器_1_s_type ;
  wire [1:0] IRNum, LB01, multiplexer_15_out, multiplexer_17_out, multiplexer_19_out, register_4_q,
       register_5_q, reIRNum;
  wire [3:0] \单周期硬布线控制器_1_alu_op ;
  wire [4:0] multiplexer_1_out, multiplexer_2_out;
  wire [7:0] multiplexer_12_out;
  wire [11:0] multiplexer_3_out;
  wire [12:0] CNT_num;
  wire [15:0] \总周期数 ;
  wire [19:0] shifter_1_out;
  wire [31:0] alu_1_result, bit_extender_1_out, bit_extender_2_out, bit_extender_3_out, bit_extender_4_out,
       bit_extender_5_out, BranAddr, EPC2_q, EPC3_q, IRAddr, JALAddr, JALRAddr, LBAddr, MData,
       multiplexer_4_out, multiplexer_7_out, multiplexer_8_out, multiplexer_10_out, multiplexer_11_out,
       multiplexer_13_out, multiplexer_16_out, multiplexer_18_out, multiplexer_20_out, NextAddr, not_3_out,
       OriAddr, PC_4, R1Data, R2, shifter_2_out;
  wire [31:2] multiplexer_6_out;

  Button \u_继续运行  (.out(Go));
  Button _1 (.out(IRA));
  Button _2 (.out(IRB));
  Button _3 (.out(IRC));
  LED #(.active("true")) led_1 (.in(W1));
  LED #(.active("true")) led_2 (.in(W2));
  LED #(.active("true")) led_3 (.in(W3));
  Hex_Digit_Display hex_digit_display_1 (.value(LedData[31:28]));  // open: dp
  Comparator #(.width(16), .mode("twosComplement")) comparator_1 (
    .a(\总周期数 ), .b(16'h7), .eq(comparator_1_eq));  // open: gt, lt
  Comparator #(.width(16), .mode("twosComplement")) comparator_2 (
    .a(\总周期数 ), .b(16'h241), .eq(comparator_2_eq));  // open: gt, lt
  Comparator #(.width(32), .mode("twosComplement")) comparator_3 (
    .a(R1Data), .b(32'h22), .eq(comparator_3_eq));  // open: gt, lt
  Register #(.width(32), .trigger("rising"), .Select("low")) register_1 (
    .D(MDin), .en(Ledout), .Q(LedData), .clk(CLK), .clr(RST));
  and and_1 (and_1_out, tunnel_t, Beq);
  and and_2 (and_2_out, ~tunnel_t, Bne);  // AND_Gate
  and and_3 (and_3_out, tunnel, Bltu);
  Hex_Digit_Display hex_digit_display_2 (.value(LedData[23:20]));  // open: dp
  Hex_Digit_Display hex_digit_display_3 (.value(LedData[27:24]));  // open: dp
  Comparator #(.width(16), .mode("twosComplement")) comparator_4 (
    .a(16'h258), .b(\总周期数 ), .eq(comparator_4_eq));  // open: gt, lt
  or or_1 (or_1_out, comparator_4_eq, comparator_5_eq);
  Comparator #(.width(16), .mode("twosComplement")) comparator_5 (
    .a(\总周期数 ), .b(16'h1), .eq(comparator_5_eq));  // open: gt, lt
  Comparator #(.width(16), .mode("twosComplement")) comparator_6 (
    .a(\总周期数 ), .b(16'h4), .eq(comparator_6_eq));  // open: gt, lt
  or or_2 (or_2_out, comparator_1_eq, comparator_2_eq);
  or or_3 (Branch, and_1_out, and_2_out, and_3_out);
  Hex_Digit_Display hex_digit_display_4 (.value(LedData[19:16]));  // open: dp
  Hex_Digit_Display hex_digit_display_5 (.value(LedData[15:12]));  // open: dp
  Pull_Resistor #(.pull(0)) pull_resistor_1 (.node(IRA));
  assign IRA = or_1_out ? ~CLK : 1'bz;  // Controlled_Inverter controlled_inverter_1
  Pull_Resistor #(.pull(0)) pull_resistor_2 (.node(IRB));
  assign IRB = comparator_6_eq ? ~CLK : 1'bz;  // Controlled_Inverter controlled_inverter_2
  Pull_Resistor #(.pull(0)) pull_resistor_3 (.node(IRC));
  assign IRC = or_2_out ? ~CLK : 1'bz;  // Controlled_Inverter controlled_inverter_3
  and and_4 (and_4_out, ecall, ~comparator_3_eq);  // AND_Gate
  and and_5 (Ledout, ecall, comparator_3_eq);
  not not_1 (not_1_out, halt);
  Counter #(.width(16), .max('hffff), .ongoal("wrap"), .trigger("rising"), .behavior("new")) counter_1 (
    .count(not_1_out), .Q(\总周期数 ), .clk(CLK));  // open: load, D, carry, clr, preset, down
  Hex_Digit_Display hex_digit_display_6 (.value(LedData[11:8]));  // open: dp
  Hex_Digit_Display hex_digit_display_7 (.value(LedData[7:4]));  // open: dp
  // Probe on \总周期数 
  Counter #(.width(1), .max('h1), .ongoal("wrap"), .trigger("rising"), .behavior("old")) counter_2 (
    .load(and_4_out), .D(and_4_out), .count(1'b0), .Q(halt), .clk(CLK), .clr(Go));  // open: carry, preset
  Hex_Digit_Display hex_digit_display_8 (.value(LedData[3:0]));  // open: dp
  not not_2 (not_2_out, halt);
  \中断按键参考电路  \u_中断按键参考电路_1  (.\与中断屏蔽位与 (\中断按键参考电路_1_与中断屏蔽位与 ), .\同步清零信号 (CLR1), .\中断等待指示灯 (W1), .\中断 (IRA), .clk(CLK));
  \中断按键参考电路  \u_中断按键参考电路_2  (.\与中断屏蔽位与 (\中断按键参考电路_2_与中断屏蔽位与 ), .\同步清零信号 (CLR2), .\中断等待指示灯 (W2), .\中断 (IRB), .clk(CLK));
  \中断按键参考电路  \u_中断按键参考电路_3  (.\与中断屏蔽位与 (\中断按键参考电路_3_与中断屏蔽位与 ), .\同步清零信号 (CLR3), .\中断等待指示灯 (W3), .\中断 (IRC), .clk(CLK));
  or or_4 (IR1_t, IR1, IRA);
  Register #(.width(32), .trigger("rising"), .Select("low")) u_PC (
    .D(NextAddr), .en(not_2_out), .Q(PC), .clk(CLK), .clr(RST));
  or or_5 (IR2_t, IR2, IRB);
  Priority_Encoder #(.select(2), .disabled("Z")) priority_encoder_1 (
    .in0(1'b1), .in1(\中断按键参考电路_1_与中断屏蔽位与 ), .in2(\中断按键参考电路_2_与中断屏蔽位与 ), .in3(\中断按键参考电路_3_与中断屏蔽位与 ),
    .out(IRNum));  // open: gs, en_out, en_in
  // RiscV_Probe riscv_probe_1: pin names not known; wires that end beside it: IR
  Adder #(.width(32)) adder_1 (.a(PC), .b(32'h4), .out(PC_4));  // open: cin, cout
  or or_6 (IR3_t, IR3, IRC);
  and and_6 (LB, LBlow7, \单周期硬布线控制器_1_lb );
  ROM #(.addrWidth(10), .dataWidth(32), .Select("high")) rom_1 (.addr(PC[11:2]), .data(IR));
  Decoder #(.select(2), .tristate("false"), .disabled("Z"), .enable("false")) decoder_1 (
    .out1(decoder_1_out1), .out2(decoder_1_out2), .out3(decoder_1_out3), .sel(IRNum));  // open: out0
  and and_7 (CLR1, decoder_1_out1, URET);
  and and_8 (CLR2, decoder_1_out2, URET);
  and and_9 (CLR3, decoder_1_out3, URET);
  \单周期硬布线控制器  \u_单周期硬布线控制器_1  (
    .Funct({IR[30], IR[25], IR[14:12]}), .OP(IR[6:2]), .ALU_OP(\单周期硬布线控制器_1_alu_op ),
    .MemToReg(\单周期硬布线控制器_1_memtoreg ), .MemWrite(MemWrite), .ALU_SRC(\单周期硬布线控制器_1_alu_src ),
    .RegWrite(RegWrite), .ecall(ecall), .S_type(\单周期硬布线控制器_1_s_type ), .Jalr(JALR), .Beq(Beq), .JAL(JAL),
    .Bne(Bne), .in_3(IR[21]), .uret(URET), .BLTU(Bltu), .LB(\单周期硬布线控制器_1_lb ), .REMU(REMU));
  Multiplexer #(.select(1), .width(5), .disabled("Z"), .enable("false")) multiplexer_1 (
    .in0(IR[19:15]), .in1(5'b10001), .out(multiplexer_1_out), .sel(ecall));
  Multiplexer #(.select(1), .width(5), .disabled("Z"), .enable("false")) multiplexer_2 (
    .in0(IR[24:20]), .in1(5'b01010), .out(multiplexer_2_out), .sel(ecall));
  Multiplexer #(.select(1), .width(12), .disabled("Z"), .enable("false")) multiplexer_3 (
    .in0(IR[31:20]), .in1({IR[31:25], IR[11:7]}), .out(multiplexer_3_out), .sel(\单周期硬布线控制器_1_s_type ));
  assign bit_extender_1_out = {{20{IR[31]}}, {IR[31], IR[7], IR[30:25], IR[11:8]}};  // Bit_Extender bit_extender_1
  Shifter #(.width(20), .shift("ll")) shifter_1 (
    .in({IR[31], IR[19:12], IR[20], IR[30:21]}), .\dist (5'b00001), .out(shifter_1_out));
  assign bit_extender_2_out = {{20{IR[31]}}, IR[31:20]};  // Bit_Extender bit_extender_2
  Comparator #(.width(7), .mode("twosComplement")) comparator_7 (
    .a(IR[6:0]), .b(7'b0000011), .eq(LBlow7));  // open: gt, lt
  Comparator #(.width(3), .mode("twosComplement")) comparator_8 (
    .a(IR[14:12]), .b(3'b111), .eq(comparator_8_eq));  // open: gt, lt
  Comparator #(.width(3), .mode("twosComplement")) comparator_9 (
    .a(IR[14:12]), .b(3'b110), .eq(comparator_9_eq));  // open: gt, lt
  Comparator #(.width(5), .mode("twosComplement")) comparator_10 (
    .a(IR[6:2]), .b(5'b11100), .eq(comparator_10_eq));  // open: gt, lt
  or or_7 (or_7_out, LB, RegWrite);
  assign bit_extender_3_out = {{20{multiplexer_3_out[11]}}, multiplexer_3_out};  // Bit_Extender bit_extender_3
  Shifter #(.width(32), .shift("ll")) shifter_2 (.in(bit_extender_1_out), .\dist (5'b00001), .out(shifter_2_out));
  assign bit_extender_4_out = {{12{shifter_1_out[19]}}, shifter_1_out};  // Bit_Extender bit_extender_4
  Adder #(.width(32)) adder_2 (.a(bit_extender_2_out), .b(R1Data), .out(LBAddr));  // open: cin, cout
  and and_10 (CSRRCI, comparator_8_eq, comparator_10_eq);
  and and_11 (CSRRSI, comparator_9_eq, comparator_10_eq);
  Regfile_UP regfile_up_1 (
    .Din(RDin), .Clk(CLK), .R1(R1Data), .R2(MDin), .WE(or_7_out), .W_num(IR[11:7]),
    .R1_num(multiplexer_1_out), .R2_num(multiplexer_2_out));
  Adder #(.width(32)) adder_3 (.a(shifter_2_out), .b(PC), .out(BranAddr));  // open: cin, cout
  Adder #(.width(32)) adder_4 (.a(bit_extender_4_out), .b(PC), .out(JALAddr));  // open: cin, cout
  assign not_3_out = ~32'h1;  // NOT_Gate not_3, 32 bits wide
  Multiplexer #(.select(1), .width(32), .disabled("Z"), .enable("false")) multiplexer_4 (
    .in0(MDin), .in1(bit_extender_3_out), .out(multiplexer_4_out), .sel(\单周期硬布线控制器_1_alu_src ));
  assign JALRAddr = LBAddr & not_3_out;  // AND_Gate and_12, 32 bits wide
  Multiplexer #(.select(3), .width(32), .disabled("Z"), .enable("false")) multiplexer_5 (
    .in0(PC_4), .in1(BranAddr), .in2(JALAddr), .in4(JALRAddr), .out(OriAddr), .sel({JALR, JAL, Branch}));  // open: in3, in5, in6, in7
  ALU alu_1 (
    .X(R1Data), .Y(multiplexer_4_out), .AluOP(\单周期硬布线控制器_1_alu_op ), .Equal(tunnel_t), .Result(alu_1_result),
    .Result_2(R2), .out_6(tunnel));  // open: out_4
  D_Flip_Flop #(.trigger("high"), .Pre_Clr_Positions("LEGACY"), .NegatePresetClear("false"), .enable("true"), .NewFFLayout("false")) d_ff_1 (.Q(d_ff_1_q));  // open: clk, D, Qn, preset, en, reset
  // Probe on 13'hc
  Comparator #(.width(13), .mode("twosComplement")) comparator_11 (
    .a(CNT_num), .b(13'hc), .eq(comparator_11_eq), .lt(comparator_11_lt));  // open: gt
  Clock #(.highDuration(1), .lowDuration(1)) clock_1 (.out(clock_1_out));
  Multiplexer #(.select(1), .width(32), .disabled("Z"), .enable("false")) multiplexer_6 (
    .in0(alu_1_result), .in1(LBAddr), .out({multiplexer_6_out, LB01}), .sel(LB));
  Multiplexer #(.select(2), .width(32), .disabled("Z"), .enable("false")) multiplexer_7 (
    .in0(OriAddr), .in1(32'h30ac), .in2(32'h3158), .in3(32'h3204), .out(multiplexer_7_out), .sel(IRNum));
  or or_8 (or_8_out, IRSig, URET, CSRRSI, CSRRCI);
  or or_9 (or_9_out, CSRRCI, IRSig);
  Counter #(.width(13), .max('h1fff), .ongoal("stay"), .trigger("rising"), .behavior("old")) counter_3 (
    .count(comparator_11_lt), .Q(CNT_num), .clk(clock_1_out));  // open: load, D, carry, clr, preset
  Multiplexer #(.select(1), .width(32), .disabled("Z"), .enable("false")) multiplexer_8 (
    .in0(OriAddr), .in1(multiplexer_7_out), .out(multiplexer_8_out), .sel(IRSig));
  Register #(.width(1), .trigger("rising"), .Select("low")) register_2 (
    .D(or_9_out), .en(or_8_out), .Q(register_2_q), .clk(CLK));  // open: clr
  Comparator #(.width(2), .mode("unsigned")) comparator_12 (
    .a(IRNum), .b(reIRNum), .gt(comparator_12_gt));  // open: eq, lt
  nand nand_1 (nand_1_out, d_ff_1_q, comparator_11_eq);
  Multiplexer #(.select(1), .width(32), .disabled("Z"), .enable("false")) multiplexer_9 (
    .in0(multiplexer_8_out), .in1(IRAddr), .out(NextAddr), .sel(URET));
  and and_13 (IRSig, ~register_2_q, comparator_12_gt);  // AND_Gate
  assign CLK = nand_1_out ? clock_1_out : 1'bz;  // Controlled_Buffer controlled_buffer_1
  Pull_Resistor #(.pull(1)) pull_resistor_4 (.node(CLK));
  RAM #(.addrWidth(10), .dataWidth(32), .bus("separate"), .Select("high")) ram_1 (
    .addr(multiplexer_6_out[11:2]), .din(MDin), .data(MData), .str(MemWrite), .clk(CLK), .clr(RST));  // open: sel, ld
  or or_10 (IREn, URET, IRSig);
  Multiplexer #(.select(1), .width(32), .disabled("Z"), .enable("false")) multiplexer_10 (
    .in0(alu_1_result), .in1(MData), .out(multiplexer_10_out), .sel(\单周期硬布线控制器_1_memtoreg ));
  Multiplexer #(.select(1), .width(32), .disabled("Z"), .enable("false")) multiplexer_11 (
    .in0(multiplexer_10_out), .in1(PC_4), .out(multiplexer_11_out), .sel(or_11_out));
  or or_11 (or_11_out, JAL, JALR);
  Multiplexer #(.select(2), .width(8), .disabled("Z"), .enable("false")) multiplexer_12 (
    .in0(MData[7:0]), .in1(MData[15:8]), .in2(MData[23:16]), .in3(MData[31:24]), .out(multiplexer_12_out),
    .sel(LB01));
  Multiplexer #(.select(1), .width(32), .disabled("Z"), .enable("false")) multiplexer_13 (
    .in0(multiplexer_11_out), .in1(R2), .out(multiplexer_13_out), .sel(REMU));
  assign bit_extender_5_out = {{24{multiplexer_12_out[7]}}, multiplexer_12_out};  // Bit_Extender bit_extender_5
  Multiplexer #(.select(1), .width(32), .disabled("Z"), .enable("false")) multiplexer_14 (
    .in0(multiplexer_13_out), .in1(bit_extender_5_out), .out(RDin), .sel(LB));
  Multiplexer #(.select(1), .width(2), .disabled("Z"), .enable("false")) multiplexer_15 (
    .in0(IRNum), .in1(register_4_q), .out(multiplexer_15_out), .sel(URET));
  Multiplexer #(.select(1), .width(32), .disabled("Z"), .enable("false")) multiplexer_16 (
    .in0(OriAddr), .in1(EPC2_q), .out(multiplexer_16_out), .sel(URET));
  Register #(.width(2), .trigger("rising"), .Select("low")) register_3 (
    .D(multiplexer_15_out), .en(IREn), .Q(reIRNum), .clk(CLK));  // open: clr
  Register #(.width(32), .trigger("rising"), .Select("low")) EPC1 (
    .D(multiplexer_16_out), .en(IREn), .Q(IRAddr), .clk(CLK));  // open: clr
  Multiplexer #(.select(1), .width(2), .disabled("Z"), .enable("false")) multiplexer_17 (
    .in0(reIRNum), .in1(register_5_q), .out(multiplexer_17_out), .sel(URET));
  Register #(.width(2), .trigger("rising"), .Select("low")) register_4 (
    .D(multiplexer_17_out), .en(IREn), .Q(register_4_q), .clk(CLK));  // open: clr
  Multiplexer #(.select(1), .width(32), .disabled("Z"), .enable("false")) multiplexer_18 (
    .in0(IRAddr), .in1(EPC3_q), .out(multiplexer_18_out), .sel(URET));
  Register #(.width(32), .trigger("rising"), .Select("low")) EPC2 (
    .D(multiplexer_18_out), .en(IREn), .Q(EPC2_q), .clk(CLK));  // open: clr
  Multiplexer #(.select(1), .width(2), .disabled("Z"), .enable("false")) multiplexer_19 (
    .in0(register_4_q), .in1(2'b00), .out(multiplexer_19_out), .sel(URET));
  Multiplexer #(.select(1), .width(32), .disabled("Z"), .enable("false")) multiplexer_20 (
    .in0(EPC2_q), .in1({32{1'b0}}), .out(multiplexer_20_out), .sel(URET));
  Register #(.width(2), .trigger("rising"), .Select("low")) register_5 (
    .D(multiplexer_19_out), .en(IREn), .Q(register_5_q), .clk(CLK));  // open: clr
  Register #(.width(32), .trigger("rising"), .Select("low")) EPC3 (
    .D(multiplexer_20_out), .en(IREn), .Q(EPC3_q), .clk(CLK));  // open: clr

  // Other names for the same wires on the sheet: R2Data[31:0] = MDin

  // Notes on the sheet:
  //   中断源
  //   中断等待指示
  //   总复位信号应将除ROM以外所有存储组件全部清零
  //   多级中断测试信号模拟器
  //   数码管输出
  //   数码管输出应该用寄存器锁存，否则显示数据只能一闪而过
  //   指令探针
  //   指令存储器
  //   指令字
  //   contents of rom_1 (hex, n*v repeats v):
  //   7d000113 100413 1f41993 41f9d993 433 c00913 800b13 140413 f47413 800293 100313 499993 89e9b3 1300533
  //   2200893 73 406282b3 fe0294e3 140413 f00f93 1f47433 1c41413 800293 100313 49d993 89e9b3 1300533
  //   2200893 73 406282b3 fe0294e3 1c45413 406b0b33 b0463 f95ff06f 2b3 fff2c293 1029293 fff2e293 500533
  //   2200893 73 f5dff06f 1112023 410113 a12023 410113 812023 410113 1312023 410113 1412023 410113 1512023
  //   410113 1612023 410113 40e073 100b13 300a13 100a93 1600433 441413 14469b3 1300533 2200893 73 fe0416e3
  //   415a0a33 fe0a10e3 40f073 ffc10113 12b03 ffc10113 12a83 ffc10113 12a03 ffc10113 12983 ffc10113 12403
  //   ffc10113 12503 ffc10113 12883 200073 1112023 410113 a12023 410113 812023 410113 1312023 410113
  //   1412023 410113 1512023 410113 1612023 410113 40e073 200b13 300a13 100a93 1600433 441413 14469b3
  //   1300533 2200893 73 fe0416e3 415a0a33 fe0a10e3 40f073 ffc10113 12b03 ffc10113 12a83 ffc10113 12a03
  //   ffc10113 12983 ffc10113 12403 ffc10113 12503 ffc10113 12883 200073 1112023 410113 a12023 410113
  //   812023 410113 1312023 410113 1412023 410113 1512023 410113 1612023 410113 40e073 300b13 300a13
  //   100a93 1600433 441413 14469b3 1300533 2200893 73 fe0416e3 415a0a33 fe0a10e3 40f073 ffc10113 12b03
  //   ffc10113 12a83 ffc10113 12a03 ffc10113 12983 ffc10113 12403 ffc10113 12503 ffc10113 12883 200073
  //   JAL
  //   JALR
  //   URET
  //   Beq
  //   Bne
  //   MemToReg
  //   MemWrite
  //   AluOP
  //   AluSrcB
  //   RegWrite
  //   为方便自动评测，需要输出PC，IR，寄存器堆写如数据RDin
  //   RAM写使能MemWrite、RAM写入数据MDin等信号
  //   控制位
  //   暂停节拍，不能为0
  //   戳工具置1进入计数暂停模式，ctrl+k时钟自动运行到对应节拍暂停
  //   ctrl+k关闭时钟连续运行，将控制位置零，进入单步调试模式调试
  //   数据存储器
  //   可计数暂停的时钟源
endmodule

module \分支预测  (
  output RegWrite,
  output MemWrite,
  output [31:0] IF_PC,
  output [31:0] ID_PC,
  output [31:0] EX_PC,
  output [31:0] M_PC,
  output [31:0] WB_PC,
  output [31:0] RDin,
  output [31:0] MDin,
  output [31:0] LedData
);

  wire and_1_out, and_2_out, and_4_out, and_7_out, and_8_out, and_9_out, Beq, Bltu, Bne, Branch, bubble, CLK,
       clock_1_out, comparator_2_eq, comparator_2_lt, comparator_3_eq, comparator_4_eq, d_ff_1_q, ecall,
       EX_Branch, EX_Branched, ex_mem_1_haltout, ex_mem_1_jalout, ex_mem_1_jalrout, ex_mem_1_lbout,
       ex_mem_1_memtoregout, ex_mem_1_remuout, ex_mem_1_uretout, EX_PJ, EXASB, EXJAL, EXJALR, Fail, Go, halt,
       id_ex_1_lbout, id_ex_1_memwriteout, id_ex_1_remuout, id_ex_1_uretout, if_id_1_pjout, IR1, IR2, IR3,
       JAL, JALR, LB, LBlow7, Ledout, LoadUse, MTR, nand_1_out, not_1_out, or_1_out, or_2_out, or_3_out,
       or_6_out, or_7_out, or_8_out, or_9_out, or_10_out, or_12_out, PJ, rehalt, REMU, RST, RWE, RWM, tunnel,
       tunnel_t, URET, W1, W2, W3, \单周期硬布线控制器_1_alu_src , \单周期硬布线控制器_1_beq , \单周期硬布线控制器_1_bltu ,
       \单周期硬布线控制器_1_bne , \单周期硬布线控制器_1_ecall , \单周期硬布线控制器_1_jal , \单周期硬布线控制器_1_jalr , \单周期硬布线控制器_1_lb ,
       \单周期硬布线控制器_1_memtoreg , \单周期硬布线控制器_1_memwrite , \单周期硬布线控制器_1_regwrite , \单周期硬布线控制器_1_remu ,
       \单周期硬布线控制器_1_s_type , \单周期硬布线控制器_1_uret ;
  wire [1:0] LB01, R1F, R1F0, R2F, R2F0;
  wire [3:0] id_ex_1_aluopout, \单周期硬布线控制器_1_alu_op ;
  wire [4:0] EXW, FUNC, MEMW, R1, R2, RW_num;
  wire [7:0] multiplexer_16_out;
  wire [11:0] multiplexer_7_out;
  wire [12:0] CNT_num;
  wire [15:0] \LoadUse次数 , \总周期数 , \插入气泡数 , \无条件分支数 , \条件分支成功数 ;
  wire [19:0] shifter_1_out;
  wire [31:0] adder_2_out, adder_3_out, adder_4_out, alu_1_result, alu_1_result_2, ALURES, and_3_out,
       bit_extender_1_out, bit_extender_2_out, bit_extender_3_out, bit_extender_4_out, bit_extender_5_out,
       BranAddr, btb_1_jumpaddr, EX_IR, ex_mem_1_pc_4out, ex_mem_1_r2out, EX_PC_4, EXALUB, EXMUXR1, EXMUXR2,
       EXMUXR3, EXR1Data, EXR2Data, id_ex_1_lbaout, ID_IR, if_id_1_pc_4out, IF_IR, JALAddr, JALRAddr, LBAddr,
       MData, MEM_IR, mem_wb_1_memdataout, mem_wb_1_pc_4out, multiplexer_2_out, multiplexer_8_out,
       multiplexer_10_out, multiplexer_11_out, multiplexer_13_out, multiplexer_14_out, multiplexer_15_out,
       multiplexer_17_out, NextAddr, not_2_out, OriAddr, PC_4, R1Data, R2Data, ram_1_data, Result2,
       shifter_2_out, WB_IR;

  Button \u_总复位  (.out(RST));
  Button _1 (.out(IR1));
  Button _2 (.out(IR2));
  Button _3 (.out(IR3));
  // Probe on \总周期数 
  // Probe on \总周期数 
  Button \u_继续运行  (.out(Go));
  LED #(.active("true")) led_1 (.in(W1));
  LED #(.active("true")) led_2 (.in(W2));
  LED #(.active("true")) led_3 (.in(W3));
  Hex_Digit_Display hex_digit_display_1 (.value(LedData[31:28]));  // open: dp
  // Probe on IF_PC[19:0]
  // RiscV_Probe riscv_probe_1: pin names not known; wires that end beside it: IF_IR
  and and_1 (and_1_out, ~LoadUse, ~rehalt);  // AND_Gate
  Hex_Digit_Display hex_digit_display_2 (.value(LedData[27:24]));  // open: dp
  Hex_Digit_Display hex_digit_display_3 (.value(LedData[23:20]));  // open: dp
  // Probe on ID_PC[19:0]
  // RiscV_Probe riscv_probe_2: pin names not known; wires that end beside it: {ID_IR[31], FUNC[4], ID_IR[29:26], FUNC[3], ID_IR[24:15], FUNC[2:0], ID_IR[11:0]}
  Register #(.width(32), .trigger("rising"), .Select("low")) PC (
    .D(NextAddr), .en(and_1_out), .Q(IF_PC), .clk(CLK), .clr(RST));
  Hex_Digit_Display hex_digit_display_4 (.value(LedData[15:12]));  // open: dp
  Hex_Digit_Display hex_digit_display_5 (.value(LedData[19:16]));  // open: dp
  Hex_Digit_Display hex_digit_display_6 (.value(LedData[11:8]));  // open: dp
  Hex_Digit_Display hex_digit_display_7 (.value(LedData[7:4]));  // open: dp
  // Probe on EX_PC[19:0]
  // RiscV_Probe riscv_probe_3: pin names not known; wires that end beside it: EX_IR
  // RiscV_Probe riscv_probe_4: pin names not known; wires that end beside it: IF_IR
  Hex_Digit_Display hex_digit_display_8 (.value(LedData[3:0]));  // open: dp
  Adder #(.width(32)) adder_1 (.a(IF_PC), .b(32'h4), .out(PC_4));  // open: cin, cout
  ROM #(.addrWidth(10), .dataWidth(32), .Select("high")) rom_1 (.addr(IF_PC[11:2]), .data(IF_IR));
  or or_1 (or_1_out, Fail, RST);
  not not_1 (not_1_out, rehalt);
  // Probe on \总周期数 
  // Probe on M_PC[19:0]
  // RiscV_Probe riscv_probe_5: pin names not known; wires that end beside it: MEM_IR
  IF_ID if_id_1 (
    .PCin(IF_PC), .PCout(ID_PC), .PC_4in(PC_4), .PC_4out(if_id_1_pc_4out), .\指令字in (IF_IR),
    .\指令字out ({ID_IR[31], FUNC[4], ID_IR[29:26], FUNC[3], ID_IR[24:15], FUNC[2:0], ID_IR[11:0]}),
    .clr(or_1_out), .clk(CLK), .abl(or_2_out), .PJin(PJ), .PJout(if_id_1_pjout));
  or or_2 (or_2_out, LoadUse, rehalt);
  Counter #(.width(16), .max('hffff), .ongoal("wrap"), .trigger("rising"), .behavior("new")) counter_1 (
    .count(not_1_out), .Q(\总周期数 ), .clk(CLK));  // open: load, D, carry, clr, preset, down
  or or_3 (or_3_out, Beq, Bltu, Bne);
  // Probe on \总周期数 
  // Probe on \无条件分支数 
  // Probe on \条件分支成功数 
  // Probe on \插入气泡数 
  // Probe on \LoadUse次数 
  Multiplexer #(.select(2), .width(32), .disabled("Z"), .enable("false")) multiplexer_1 (
    .in0(EXR1Data), .in1(RDin), .in2(ALURES), .in3({32{1'b0}}), .out(EXMUXR1), .sel(R1F));
  Multiplexer #(.select(2), .width(32), .disabled("Z"), .enable("false")) multiplexer_2 (
    .in0(EXALUB), .in1(RDin), .in2(ALURES), .in3({32{1'b0}}), .out(multiplexer_2_out), .sel(R2F));
  Multiplexer #(.select(2), .width(32), .disabled("Z"), .enable("false")) multiplexer_3 (
    .in0(EXR2Data), .in1(RDin), .in2(ALURES), .in3({32{1'b0}}), .out(EXMUXR2), .sel(R2F));
  Multiplexer #(.select(1), .width(32), .disabled("Z"), .enable("false")) multiplexer_4 (
    .in0(multiplexer_2_out), .in1(EXALUB), .out(EXMUXR3), .sel(EXASB));
  Counter #(.width(16), .max('hffff), .ongoal("wrap"), .trigger("rising"), .behavior("new")) counter_2 (
    .count(Branch), .Q(\条件分支成功数 ), .clk(CLK), .clr(RST));  // open: load, D, carry, preset, down
  or or_4 (EX_Branch, or_3_out, EXJALR, EXJAL);
  or or_5 (EX_Branched, Branch, EXJALR, EXJAL);
  // Probe on IF_PC[11:0]
  // Probe on WB_PC[19:0]
  // RiscV_Probe riscv_probe_6: pin names not known; wires that end beside it: WB_IR
  \单周期硬布线控制器  \u_单周期硬布线控制器_1  (
    .Funct(FUNC), .OP(ID_IR[6:2]), .ALU_OP(\单周期硬布线控制器_1_alu_op ), .MemToReg(\单周期硬布线控制器_1_memtoreg ),
    .MemWrite(\单周期硬布线控制器_1_memwrite ), .ALU_SRC(\单周期硬布线控制器_1_alu_src ), .RegWrite(\单周期硬布线控制器_1_regwrite ),
    .ecall(\单周期硬布线控制器_1_ecall ), .S_type(\单周期硬布线控制器_1_s_type ), .Jalr(\单周期硬布线控制器_1_jalr ),
    .Beq(\单周期硬布线控制器_1_beq ), .JAL(\单周期硬布线控制器_1_jal ), .Bne(\单周期硬布线控制器_1_bne ), .in_3(ID_IR[21]),
    .uret(\单周期硬布线控制器_1_uret ), .BLTU(\单周期硬布线控制器_1_bltu ), .LB(\单周期硬布线控制器_1_lb ), .REMU(\单周期硬布线控制器_1_remu ));
  Multiplexer #(.select(1), .width(5), .disabled("Z"), .enable("false")) multiplexer_5 (
    .in0(ID_IR[19:15]), .in1(5'b10001), .out(R1), .sel(\单周期硬布线控制器_1_ecall ));
  Multiplexer #(.select(1), .width(5), .disabled("Z"), .enable("false")) multiplexer_6 (
    .in0(ID_IR[24:20]), .in1(5'b01010), .out(R2), .sel(\单周期硬布线控制器_1_ecall ));
  Multiplexer #(.select(1), .width(12), .disabled("Z"), .enable("false")) multiplexer_7 (
    .in0({ID_IR[31], FUNC[4], ID_IR[29:26], FUNC[3], ID_IR[24:20]}),
    .in1({ID_IR[31], FUNC[4], ID_IR[29:26], FUNC[3], ID_IR[11:7]}), .out(multiplexer_7_out),
    .sel(\单周期硬布线控制器_1_s_type ));
  assign bit_extender_1_out = {{20{ID_IR[31]}}, {ID_IR[31], FUNC[4], ID_IR[29:26], FUNC[3], ID_IR[24:20]}};  // Bit_Extender bit_extender_1
  Comparator #(.width(7), .mode("twosComplement")) comparator_1 (
    .a(ID_IR[6:0]), .b(7'b0000011), .eq(LBlow7));  // open: gt, lt
  // Probe on EX_PC[11:0]
  // Probe on ID_PC[11:0]
  and and_2 (and_2_out, LBlow7, \单周期硬布线控制器_1_lb );
  assign bit_extender_2_out = {{20{multiplexer_7_out[11]}}, multiplexer_7_out};  // Bit_Extender bit_extender_2
  assign bit_extender_3_out = {{20{ID_IR[31]}}, {ID_IR[31], ID_IR[7], FUNC[4], ID_IR[29:26], FUNC[3], ID_IR[11:8]}};  // Bit_Extender bit_extender_3
  Shifter #(.width(20), .shift("ll")) shifter_1 (
    .in({ID_IR[31], ID_IR[19:15], FUNC[2:0], ID_IR[20], FUNC[4], ID_IR[29:26], FUNC[3], ID_IR[24:21]}),
    .\dist (5'b00001), .out(shifter_1_out));
  or or_6 (or_6_out, JAL, JALR);
  Counter #(.width(16), .max('hffff), .ongoal("wrap"), .trigger("rising"), .behavior("new")) counter_3 (
    .count(or_6_out), .Q(\无条件分支数 ), .clk(CLK), .clr(RST));  // open: load, D, carry, preset, down
  // Probe on M_PC[11:0]
  D_Flip_Flop #(.trigger("high"), .Pre_Clr_Positions("LEGACY"), .NegatePresetClear("false"), .enable("true"), .NewFFLayout("false")) d_ff_1 (.Q(d_ff_1_q));  // open: clk, D, Qn, preset, en, reset
  // Probe on 13'h14
  Shifter #(.width(32), .shift("ll")) shifter_2 (.in(bit_extender_3_out), .\dist (5'b00001), .out(shifter_2_out));
  assign bit_extender_4_out = {{12{shifter_1_out[19]}}, shifter_1_out};  // Bit_Extender bit_extender_4
  Adder #(.width(32)) adder_2 (.a(bit_extender_1_out), .b(R1Data), .out(adder_2_out));  // open: cin, cout
  Redirect redirect_1 (
    .R1(R1), .EXW(EXW), .MEMW(MEMW), .R2(R2), .R1F(R1F0), .R2F(R2F0), .LoadUse(LoadUse), .Bubble(bubble),
    .RWE(RWE), .RWM(RWM), .MemToReg(MTR), .OP(ID_IR[6:2]), .Funct(FUNC));
  or or_7 (or_7_out, Branch, EXJAL, EXJALR);
  // Probe on WB_PC[11:0]
  Comparator #(.width(13), .mode("twosComplement")) comparator_2 (
    .a(CNT_num), .b(13'h14), .eq(comparator_2_eq), .lt(comparator_2_lt));  // open: gt
  Clock #(.highDuration(1), .lowDuration(1)) clock_1 (.out(clock_1_out));
  or or_8 (or_8_out, and_2_out, \单周期硬布线控制器_1_memtoreg );
  or or_9 (or_9_out, \单周期硬布线控制器_1_regwrite , and_2_out);
  Regifile_DW regifile_dw_1 (
    .Din(RDin), .Clk(CLK), .R1(R1Data), .R2(R2Data), .WE(RegWrite), .W_num(RW_num), .R1_num(R1), .R2_num(R2));
  Adder #(.width(32)) adder_3 (.a(shifter_2_out), .b(ID_PC), .out(adder_3_out));  // open: cin, cout
  Adder #(.width(32)) adder_4 (.a(bit_extender_4_out), .b(ID_PC), .out(adder_4_out));  // open: cin, cout
  assign and_3_out = adder_2_out & not_2_out;  // AND_Gate and_3, 32 bits wide
  assign not_2_out = ~32'h1;  // NOT_Gate not_2, 32 bits wide
  and and_4 (and_4_out, ~rehalt, bubble);  // AND_Gate
  Comparator #(.width(1), .mode("twosComplement")) comparator_3 (
    .a(EX_PJ), .b(or_7_out), .eq(comparator_3_eq));  // open: gt, lt
  not not_3 (Fail, comparator_3_eq);
  nand nand_1 (nand_1_out, d_ff_1_q, comparator_2_eq);
  Counter #(.width(13), .max('h1fff), .ongoal("stay"), .trigger("rising"), .behavior("old")) counter_4 (
    .count(comparator_2_lt), .Q(CNT_num), .clk(clock_1_out));  // open: load, D, carry, clr, preset
  Multiplexer #(.select(1), .width(32), .disabled("Z"), .enable("false")) multiplexer_8 (
    .in0(R2Data), .in1(bit_extender_2_out), .out(multiplexer_8_out), .sel(\单周期硬布线控制器_1_alu_src ));
  Counter #(.width(16), .max('hffff), .ongoal("wrap"), .trigger("rising"), .behavior("new")) counter_5 (
    .count(and_4_out), .Q(\插入气泡数 ), .clk(CLK), .clr(RST));  // open: load, D, carry, preset, down
  assign CLK = nand_1_out ? clock_1_out : 1'bz;  // Controlled_Buffer controlled_buffer_1
  ID_EX id_ex_1 (
    .REMUin(\单周期硬布线控制器_1_remu ), .LBin(and_2_out), .URETin(\单周期硬布线控制器_1_uret ), .JALRin(\单周期硬布线控制器_1_jalr ),
    .JALin(\单周期硬布线控制器_1_jal ), .BEQin(\单周期硬布线控制器_1_beq ), .BLTUin(\单周期硬布线控制器_1_bltu ),
    .BNEin(\单周期硬布线控制器_1_bne ), .MemToRegin(or_8_out), .MemWritein(\单周期硬布线控制器_1_memwrite ),
    .ALUopin(\单周期硬布线控制器_1_alu_op ), .R1datain(R1Data), .R2datain(R2Data), .RWin(ID_IR[11:7]),
    .BAin(adder_3_out), .JALAin(adder_4_out), .JALRin_2(and_3_out), .LBAin(adder_2_out),
    .REMUout(id_ex_1_remuout), .LBout(id_ex_1_lbout), .URETout(id_ex_1_uretout), .JALRout(EXJALR),
    .JALout(EXJAL), .BEQout(Beq), .BLTUout(Bltu), .BNEout(Bne), .MemToRegout(MTR),
    .MemWriteout(id_ex_1_memwriteout), .ALUopout(id_ex_1_aluopout), .R1dataout(EXR1Data),
    .R2dataout(EXR2Data), .RWout(EXW), .BAout(BranAddr), .JALAout(JALAddr), .JALRout_2(JALRAddr),
    .LBAout(id_ex_1_lbaout), .clr(or_10_out), .clk(CLK), .abl(rehalt), .PCin(ID_PC), .PCout(EX_PC),
    .PC_4in(if_id_1_pc_4out), .PC_4out(EX_PC_4), .ALUBin(multiplexer_8_out), .ALUBout(EXALUB),
    .RegWritein(or_9_out), .RegWritegout(RWE), .R1Fin(R1F0), .R1Fout(R1F), .R2Fin(R2F0), .R2Fout(R2F),
    .ASBin(\单周期硬布线控制器_1_alu_src ), .ASBout(EXASB), .ECALLin(\单周期硬布线控制器_1_ecall ), .ECALLout(ecall),
    .PJin(if_id_1_pjout), .PJout(EX_PJ));  // open: HALTin, HALTout
  or or_10 (or_10_out, Fail, RST, LoadUse);
  Pull_Resistor #(.pull(1)) pull_resistor_1 (.node(CLK));
  Counter #(.width(16), .max('hffff), .ongoal("wrap"), .trigger("rising"), .behavior("new")) counter_6 (
    .count(LoadUse), .Q(\LoadUse次数 ), .clk(CLK), .clr(RST));  // open: load, D, carry, preset, down
  Multiplexer #(.select(3), .width(32), .disabled("Z"), .enable("false")) multiplexer_9 (
    .in0(PC_4), .in1(BranAddr), .in2(JALAddr), .in4(JALRAddr), .out(OriAddr), .sel({EXJALR, EXJAL, Branch}));  // open: in3, in5, in6, in7
  Comparator #(.width(32), .mode("twosComplement")) comparator_4 (
    .a(EXMUXR1), .b(32'h22), .eq(comparator_4_eq));  // open: gt, lt
  Register #(.width(32), .trigger("rising"), .Select("low")) register_1 (
    .D(EXMUXR2), .en(Ledout), .Q(LedData), .clk(CLK), .clr(RST));
  BTB btb_1 (
    .CLK(CLK), .EX_Branch(EX_Branch), .PC(IF_PC), .EX_PC(EX_PC), .EX_BranchAddr(OriAddr),
    .EX_Branched(EX_Branched), .JumpAddr(btb_1_jumpaddr), .PJ(PJ));
  ALU alu_1 (
    .X(EXMUXR1), .Y(EXMUXR3), .AluOP(id_ex_1_aluopout), .Equal(tunnel_t), .Result(alu_1_result),
    .Result_2(alu_1_result_2), .out_6(tunnel));  // open: out_4
  and and_5 (halt, ecall, ~comparator_4_eq);  // AND_Gate
  and and_6 (Ledout, ecall, comparator_4_eq);
  Multiplexer #(.select(1), .width(32), .disabled("Z"), .enable("false")) multiplexer_10 (
    .in0(PC_4), .in1(btb_1_jumpaddr), .out(multiplexer_10_out), .sel(PJ));
  Multiplexer #(.select(1), .width(32), .disabled("Z"), .enable("false")) multiplexer_11 (
    .in0(EX_PC_4), .in1(OriAddr), .out(multiplexer_11_out), .sel(EX_Branched));
  EX_MEM ex_mem_1 (
    .PCin(EX_PC), .PC_4in(EX_PC_4), .HALTin(halt), .REMUin(id_ex_1_remuout), .LBin(id_ex_1_lbout),
    .URETin(id_ex_1_uretout), .JALRin(EXJALR), .JALin(EXJAL), .MemToRegin(MTR),
    .MemWritein(id_ex_1_memwriteout), .ALURin(alu_1_result), .RWin(EXW), .LBAin(id_ex_1_lbaout),
    .PCout(M_PC), .PC_4out(ex_mem_1_pc_4out), .HALTout(ex_mem_1_haltout), .REMUout(ex_mem_1_remuout),
    .LBout(ex_mem_1_lbout), .URETout(ex_mem_1_uretout), .JALRout(ex_mem_1_jalrout), .JALout(ex_mem_1_jalout),
    .MemToRegout(ex_mem_1_memtoregout), .MemWriteout(MemWrite), .ALURout(ALURES), .RWout(MEMW),
    .LBAout(LBAddr), .clr(RST), .clk(CLK), .abl(rehalt), .R2datain(EXMUXR2), .R2dataout(MDin),
    .R2in(alu_1_result_2), .R2out(ex_mem_1_r2out), .RegWritein(RWE), .RegWritegout(RWM));
  Multiplexer #(.select(1), .width(32), .disabled("Z"), .enable("false")) multiplexer_12 (
    .in0(multiplexer_10_out), .in1(multiplexer_11_out), .out(NextAddr), .sel(Fail));
  and and_7 (and_7_out, tunnel_t, Beq);
  and and_8 (and_8_out, ~tunnel_t, Bne);  // AND_Gate
  or or_11 (Branch, and_7_out, and_8_out, and_9_out);
  and and_9 (and_9_out, tunnel, Bltu);
  Multiplexer #(.select(1), .width(32), .disabled("Z"), .enable("false")) multiplexer_13 (
    .in0(ALURES), .in1(LBAddr), .out(multiplexer_13_out), .sel(ex_mem_1_lbout));
  RAM #(.addrWidth(10), .dataWidth(32), .bus("separate"), .Select("high")) ram_1 (
    .addr(multiplexer_13_out[11:2]), .din(MDin), .data(ram_1_data), .str(MemWrite), .clk(CLK), .clr(RST));  // open: sel, ld
  Multiplexer #(.select(1), .width(32), .disabled("Z"), .enable("false")) multiplexer_14 (
    .in0(ALURES), .in1(ram_1_data), .out(multiplexer_14_out), .sel(ex_mem_1_memtoregout));
  MEM_WB mem_wb_1 (
    .PCin(M_PC), .PC_4in(ex_mem_1_pc_4out), .HALTin(ex_mem_1_haltout), .REMUin(ex_mem_1_remuout),
    .LBin(ex_mem_1_lbout), .URETin(ex_mem_1_uretout), .JALRin(ex_mem_1_jalrout), .JALin(ex_mem_1_jalout),
    .MemDatain(multiplexer_14_out), .R2in(ex_mem_1_r2out), .LB01in(multiplexer_13_out[1:0]),
    .Mdatain(ram_1_data), .RWin(MEMW), .PCout(WB_PC), .PC_4out(mem_wb_1_pc_4out), .HALTout(rehalt),
    .REMUout(REMU), .LBout(LB), .URETout(URET), .JALRout(JALR), .JALout(JAL),
    .MemDataout(mem_wb_1_memdataout), .R2out(Result2), .LB01out(LB01), .Mdataout(MData), .RWout(RW_num),
    .clr(RST), .clk(CLK), .abl(rehalt), .RegWritein(RWM), .RegWritegout(RegWrite), .go(Go));
  or or_12 (or_12_out, JAL, JALR);
  Multiplexer #(.select(1), .width(32), .disabled("Z"), .enable("false")) multiplexer_15 (
    .in0(mem_wb_1_memdataout), .in1(mem_wb_1_pc_4out), .out(multiplexer_15_out), .sel(or_12_out));
  Multiplexer #(.select(2), .width(8), .disabled("Z"), .enable("false")) multiplexer_16 (
    .in0(MData[7:0]), .in1(MData[15:8]), .in2(MData[23:16]), .in3(MData[31:24]), .out(multiplexer_16_out),
    .sel(LB01));
  Multiplexer #(.select(1), .width(32), .disabled("Z"), .enable("false")) multiplexer_17 (
    .in0(multiplexer_15_out), .in1(Result2), .out(multiplexer_17_out), .sel(REMU));
  assign bit_extender_5_out = {{24{multiplexer_16_out[7]}}, multiplexer_16_out};  // Bit_Extender bit_extender_5
  Multiplexer #(.select(1), .width(32), .disabled("Z"), .enable("false")) multiplexer_18 (
    .in0(multiplexer_17_out), .in1(bit_extender_5_out), .out(RDin), .sel(LB));

  // Other names for the same wires on the sheet: ID_IR (some bits) = FUNC; OP[4:0] = ID_IR[6:2]; MEM_PC[31:0] = M_PC

  // Notes on the sheet:
  //   中断源
  //   时空图监测，可删除
  //   中断等待指示
  //   数码管输出
  //   指令探针
  //   指令存储器
  //   指令字
  //   contents of rom_1 (hex, n*v repeats v):
  //   100493 100006f 100493 200913 300993 100006f 100493 200913 300993 100006f 100493 200913 300993
  //   100006f 100493 200913 300993 3c8000ef 100413 100493 1f49493 900533 2200893 73 24d493 48463 fedff06f
  //   900533 2200893 73 100493 249493 900533 2200893 73 48463 fedff06f 100493 1f49493 900533 2200893 73
  //   4034d493 900533 2200893 73 4044d493 900533 2200893 73 4044d493 900533 2200893 73 4044d493 900533
  //   2200893 73 4044d493 900533 2200893 73 4044d493 900533 2200893 73 4044d493 900533 2200893 73 4044d493
  //   900533 2200893 73 100413 1f41993 41f9d993 433 c00913 300b13 140413 f47413 800293 100313 499993
  //   89e9b3 1300533 2200893 73 406282b3 fe0294e3 140413 f00f93 1f47433 1c41413 800293 100313 49d993
  //   89e9b3 1300533 2200893 73 406282b3 fe0294e3 1c45413 406b0b33 b0463 f95ff06f 2b3 fff2c293 829293
  //   ff2e293 500533 2200893 73 fff00413 493 84a023 140413 448493 84a023 140413 448493 84a023 140413
  //   448493 84a023 140413 448493 84a023 140413 448493 84a023 140413 448493 84a023 140413 448493 84a023
  //   140413 448493 84a023 140413 448493 84a023 140413 448493 84a023 140413 448493 84a023 140413 448493
  //   84a023 140413 448493 84a023 140413 448493 84a023 140413 448493 84a023 140413 448493 140413 433
  //   3c00493 42983 4aa03 149a2b3 28663 134a023 1442023 ffc48493 fe9412e3 800533 2200893 73 440413 3c00493
  //   fc9416e3 3200893 73 200293 1100493 849493 1148493 900533 2200893 73 2000e13 25484b3 900533 2200893
  //   73 fffe0e13 fe0e16e3 a00893 73 8800493 849493 4848493 8700913 891913 5490913 2997933 1091913
  //   11096913 1200533 2200893 73 a00893 73 313 1000e13 8400493 849493 8348493 400913 891913 490913 849493
  //   8248493 849493 8148493 891913 490913 891913 490913 932023 12484b3 430313 fffe0e13 fe0e18e3 2000e13
  //   313 30483 900533 2200893 73 130313 fffe0e13 fe0e14e3 a00893 73 ff100493 900533 2200893 73 148493
  //   fe9068e3 900533 2200893 73 a00893 73 a00893 73 413 140413 800533 2200893 73 240413 800533 2200893 73
  //   340413 800533 2200893 73 440413 800533 2200893 73 540413 800533 2200893 73 640413 800533 2200893 73
  //   740413 800533 2200893 73 840413 800533 2200893 2200893 73 8067
  //   JAL
  //   JALR
  //   URET
  //   控制位
  //   Beq
  //   Bne
  //   MemToReg
  //   MemWrite
  //   AluOP
  //   AluSrcB
  //   RegWrite
  //   流水调试日志用
  //   暂停节拍，不能为0
  //   戳工具置1进入计数暂停模式，ctrl+k时钟自动运行到对应节拍暂停
  //   ctrl+k关闭时钟连续运行，将控制位置零，进入单步调试模式调试
  //   可计数暂停的时钟源
  //   为方便自动评测，需要输出流水线各段保存的PC值，注意是PC不是PC+4，另外ID段寄存器写入信息，Mem段内存写入信息也要输出
  //   数据存储器
endmodule

module \流水中断_单级  (
  input  IR1,
  input  IR2,
  input  IR3,
  output RegWrite,
  output MemWrite,
  output [31:0] IF_PC,
  output [31:0] ID_PC,
  output [31:0] EX_PC,
  output [31:0] M_PC,
  output [31:0] WB_PC,
  output [31:0] RDin,
  output [31:0] MDin,
  output [31:0] LedData
);

  wire and_1_out, and_2_out, and_3_out, and_4_out, and_7_out, and_8_out, and_9_out, and_14_out, and_16_out,
       and_17_out, and_18_out, Beq, Bltu, Bne, Branch, bubble, CLK, clock_1_out, CLR1, CLR2, CLR3,
       comparator_1_eq, comparator_3_eq, comparator_3_lt, comparator_4_eq, comparator_5_eq, comparator_6_eq,
       comparator_7_eq, d_ff_1_qn, d_ff_2_q, decoder_1_out1, decoder_1_out2, decoder_1_out3, ecall,
       ex_mem_1_haltout, ex_mem_1_jalout, ex_mem_1_jalrout, ex_mem_1_lbout, ex_mem_1_memtoregout,
       ex_mem_1_remuout, ex_mem_1_uretout, EXASB, EXJAL, EXJALR, Go, halt, id_ex_1_lbout,
       id_ex_1_memwriteout, id_ex_1_remuout, id_ex_1_uretout, INT, IR1_t, IR2_t, IR3_t, IRA, IRB, IRC, IRSig,
       JAL, JALR, LB, LBlow7, Ledout, LoadUse, MTR, nand_1_out, not_1_out, or_1_out, or_3_out, or_4_out,
       or_5_out, or_6_out, or_7_out, or_8_out, or_11_out, or_13_out, or_14_out, or_15_out, rehalt, REMU, RST,
       RWE, RWM, tunnel, tunnel_t, URET, W1, W2, W3, \中断按键参考电路_1_与中断屏蔽位与 , \中断按键参考电路_2_与中断屏蔽位与 ,
       \中断按键参考电路_3_与中断屏蔽位与 , \单周期硬布线控制器_1_alu_src , \单周期硬布线控制器_1_beq , \单周期硬布线控制器_1_bltu , \单周期硬布线控制器_1_bne ,
       \单周期硬布线控制器_1_ecall , \单周期硬布线控制器_1_jal , \单周期硬布线控制器_1_jalr , \单周期硬布线控制器_1_lb , \单周期硬布线控制器_1_memtoreg ,
       \单周期硬布线控制器_1_memwrite , \单周期硬布线控制器_1_regwrite , \单周期硬布线控制器_1_remu , \单周期硬布线控制器_1_s_type ,
       \单周期硬布线控制器_1_uret ;
  wire [1:0] IRNum, LB01, R1F, R1F0, R2F, R2F0, register_2_q;
  wire [3:0] id_ex_1_aluopout, \单周期硬布线控制器_1_alu_op ;
  wire [4:0] EXW, FUNC, MEMW, R1, R2, RW_num;
  wire [7:0] multiplexer_16_out;
  wire [11:0] multiplexer_3_out;
  wire [12:0] CNT_num;
  wire [15:0] \LoadUse次数 , \总周期数 , \插入气泡数 , \无条件分支数 , \条件分支成功数 ;
  wire [19:0] shifter_1_out;
  wire [31:0] adder_2_out, adder_3_out, adder_4_out, alu_1_result, alu_1_result_2, ALURES, and_11_out,
       bit_extender_1_out, bit_extender_2_out, bit_extender_3_out, bit_extender_4_out, bit_extender_5_out,
       BranAddr, EX_IR, ex_mem_1_pc_4out, ex_mem_1_r2out, EXALUB, EXMUXR1, EXMUXR2, EXMUXR3, EXR1Data,
       EXR2Data, id_ex_1_lbaout, id_ex_1_pc_4out, ID_IR, if_id_1_pc_4out, IF_IR, JALAddr, JALRAddr, LBAddr,
       MData, MEM_IR, mem_wb_1_memdataout, mem_wb_1_pc_4out, mEPC_q, multiplexer_4_out, multiplexer_5_out,
       multiplexer_6_out, multiplexer_10_out, multiplexer_13_out, multiplexer_14_out, multiplexer_15_out,
       multiplexer_17_out, NextAddr, not_2_out, OriAddr, PC_4, R1Data, R2Data, ram_1_data, Result2,
       shifter_2_out, WB_IR;

  Button \u_总复位  (.out(RST));
  Button _1 (.out(IRA));
  Button _2 (.out(IRB));
  Button _3 (.out(IRC));
  // Probe on \总周期数 
  // Probe on \总周期数 
  Button \u_继续运行  (.out(Go));
  LED #(.active("true")) led_1 (.in(W1));
  LED #(.active("true")) led_2 (.in(W2));
  LED #(.active("true")) led_3 (.in(W3));
  Hex_Digit_Display hex_digit_display_1 (.value(LedData[31:28]));  // open: dp
  // Probe on IF_PC[19:0]
  // RiscV_Probe riscv_probe_1: pin names not known; wires that end beside it: IF_IR
  or or_1 (or_1_out, and_1_out, Go);
  and and_1 (and_1_out, ~LoadUse, ~rehalt);  // AND_Gate
  Hex_Digit_Display hex_digit_display_2 (.value(LedData[27:24]));  // open: dp
  Hex_Digit_Display hex_digit_display_3 (.value(LedData[23:20]));  // open: dp
  // Probe on ID_PC[19:0]
  // RiscV_Probe riscv_probe_2: pin names not known; wires that end beside it: {ID_IR[31], FUNC[4], ID_IR[29:26], FUNC[3], ID_IR[24:15], FUNC[2:0], ID_IR[11:0]}
  Register #(.width(32), .trigger("rising"), .Select("low")) PC (
    .D(NextAddr), .en(or_1_out), .Q(IF_PC), .clk(CLK), .clr(RST));
  Comparator #(.width(32), .mode("twosComplement")) comparator_1 (
    .a(EXMUXR1), .b(32'h22), .eq(comparator_1_eq));  // open: gt, lt
  Register #(.width(32), .trigger("rising"), .Select("low")) register_1 (
    .D(EXMUXR2), .en(Ledout), .Q(LedData), .clk(CLK), .clr(RST));
  and and_2 (and_2_out, tunnel_t, Beq);
  and and_3 (and_3_out, ~tunnel_t, Bne);  // AND_Gate
  and and_4 (and_4_out, tunnel, Bltu);
  Hex_Digit_Display hex_digit_display_4 (.value(LedData[15:12]));  // open: dp
  Hex_Digit_Display hex_digit_display_5 (.value(LedData[19:16]));  // open: dp
  and and_5 (halt, ecall, ~comparator_1_eq);  // AND_Gate
  and and_6 (Ledout, ecall, comparator_1_eq);
  or or_2 (Branch, and_2_out, and_3_out, and_4_out);
  Hex_Digit_Display hex_digit_display_6 (.value(LedData[7:4]));  // open: dp
  Hex_Digit_Display hex_digit_display_7 (.value(LedData[11:8]));  // open: dp
  // Probe on EX_PC[19:0]
  // RiscV_Probe riscv_probe_3: pin names not known; wires that end beside it: EX_IR
  // RiscV_Probe riscv_probe_4: pin names not known; wires that end beside it: IF_IR
  Hex_Digit_Display hex_digit_display_8 (.value(LedData[3:0]));  // open: dp
  Adder #(.width(32)) adder_1 (.a(IF_PC), .b(32'h4), .out(PC_4));  // open: cin, cout
  ROM #(.addrWidth(10), .dataWidth(32), .Select("high")) rom_1 (.addr(IF_PC[11:2]), .data(IF_IR));
  or or_3 (or_3_out, URET, EXJALR, EXJAL, Branch, RST, INT);
  // Probe on \总周期数 
  // Probe on M_PC[19:0]
  // RiscV_Probe riscv_probe_5: pin names not known; wires that end beside it: MEM_IR
  IF_ID if_id_1 (
    .PCin(IF_PC), .PCout(ID_PC), .PC_4in(PC_4), .PC_4out(if_id_1_pc_4out), .\指令字in (IF_IR),
    .\指令字out ({ID_IR[31], FUNC[4], ID_IR[29:26], FUNC[3], ID_IR[24:15], FUNC[2:0], ID_IR[11:0]}),
    .clr(or_3_out), .clk(CLK), .abl(or_4_out));  // open: PJin, PJout
  or or_4 (or_4_out, LoadUse, and_7_out);
  and and_7 (and_7_out, rehalt, ~Go);  // AND_Gate
  // Probe on \总周期数 
  // Probe on \无条件分支数 
  // Probe on \条件分支成功数 
  // Probe on \插入气泡数 
  // Probe on \LoadUse次数 
  not not_1 (not_1_out, rehalt);
  Counter #(.width(16), .max('hffff), .ongoal("wrap"), .trigger("rising"), .behavior("new")) counter_1 (
    .count(not_1_out), .Q(\总周期数 ), .clk(CLK));  // open: load, D, carry, clr, preset, down
  \中断按键参考电路  \u_中断按键参考电路_1  (.\与中断屏蔽位与 (\中断按键参考电路_1_与中断屏蔽位与 ), .\同步清零信号 (CLR1), .\中断等待指示灯 (W1), .\中断 (IRA), .clk(CLK));
  \中断按键参考电路  \u_中断按键参考电路_2  (.\与中断屏蔽位与 (\中断按键参考电路_2_与中断屏蔽位与 ), .\同步清零信号 (CLR2), .\中断等待指示灯 (W2), .\中断 (IRB), .clk(CLK));
  \中断按键参考电路  \u_中断按键参考电路_3  (.\与中断屏蔽位与 (\中断按键参考电路_3_与中断屏蔽位与 ), .\同步清零信号 (CLR3), .\中断等待指示灯 (W3), .\中断 (IRC), .clk(CLK));
  and and_8 (and_8_out, ~URET, IRSig);  // AND_Gate
  // Probe on IF_PC[11:0]
  // Probe on WB_PC[19:0]
  // RiscV_Probe riscv_probe_6: pin names not known; wires that end beside it: WB_IR
  \单周期硬布线控制器  \u_单周期硬布线控制器_1  (
    .Funct(FUNC), .OP(ID_IR[6:2]), .ALU_OP(\单周期硬布线控制器_1_alu_op ), .MemToReg(\单周期硬布线控制器_1_memtoreg ),
    .MemWrite(\单周期硬布线控制器_1_memwrite ), .ALU_SRC(\单周期硬布线控制器_1_alu_src ), .RegWrite(\单周期硬布线控制器_1_regwrite ),
    .ecall(\单周期硬布线控制器_1_ecall ), .S_type(\单周期硬布线控制器_1_s_type ), .Jalr(\单周期硬布线控制器_1_jalr ),
    .Beq(\单周期硬布线控制器_1_beq ), .JAL(\单周期硬布线控制器_1_jal ), .Bne(\单周期硬布线控制器_1_bne ), .in_3(ID_IR[21]),
    .uret(\单周期硬布线控制器_1_uret ), .BLTU(\单周期硬布线控制器_1_bltu ), .LB(\单周期硬布线控制器_1_lb ), .REMU(\单周期硬布线控制器_1_remu ));
  Multiplexer #(.select(1), .width(5), .disabled("Z"), .enable("false")) multiplexer_1 (
    .in0(ID_IR[19:15]), .in1(5'b10001), .out(R1), .sel(\单周期硬布线控制器_1_ecall ));
  Multiplexer #(.select(1), .width(5), .disabled("Z"), .enable("false")) multiplexer_2 (
    .in0(ID_IR[24:20]), .in1(5'b01010), .out(R2), .sel(\单周期硬布线控制器_1_ecall ));
  Multiplexer #(.select(1), .width(12), .disabled("Z"), .enable("false")) multiplexer_3 (
    .in0({ID_IR[31], FUNC[4], ID_IR[29:26], FUNC[3], ID_IR[24:20]}),
    .in1({ID_IR[31], FUNC[4], ID_IR[29:26], FUNC[3], ID_IR[11:7]}), .out(multiplexer_3_out),
    .sel(\单周期硬布线控制器_1_s_type ));
  assign bit_extender_1_out = {{20{ID_IR[31]}}, {ID_IR[31], FUNC[4], ID_IR[29:26], FUNC[3], ID_IR[24:20]}};  // Bit_Extender bit_extender_1
  Comparator #(.width(7), .mode("twosComplement")) comparator_2 (
    .a(ID_IR[6:0]), .b(7'b0000011), .eq(LBlow7));  // open: gt, lt
  Counter #(.width(16), .max('hffff), .ongoal("wrap"), .trigger("rising"), .behavior("new")) counter_2 (
    .count(Branch), .Q(\条件分支成功数 ), .clk(CLK), .clr(RST));  // open: load, D, carry, preset, down
  Priority_Encoder #(.select(2), .disabled("Z")) priority_encoder_1 (
    .in1(\中断按键参考电路_1_与中断屏蔽位与 ), .in2(\中断按键参考电路_2_与中断屏蔽位与 ), .in3(\中断按键参考电路_3_与中断屏蔽位与 ), .out(IRNum),
    .gs(IRSig));  // open: in0, en_out, en_in
  D_Flip_Flop #(.trigger("rising"), .Pre_Clr_Positions("LEGACY"), .NegatePresetClear("false"), .enable("true"), .NewFFLayout("true")) d_ff_1 (
    .clk(CLK), .D(and_8_out), .Qn(d_ff_1_qn));  // open: Q, preset, en, reset
  // Probe on ID_PC[11:0]
  // Probe on EX_PC[11:0]
  and and_9 (and_9_out, LBlow7, \单周期硬布线控制器_1_lb );
  assign bit_extender_2_out = {{20{multiplexer_3_out[11]}}, multiplexer_3_out};  // Bit_Extender bit_extender_2
  assign bit_extender_3_out = {{20{ID_IR[31]}}, {ID_IR[31], ID_IR[7], FUNC[4], ID_IR[29:26], FUNC[3], ID_IR[11:8]}};  // Bit_Extender bit_extender_3
  Shifter #(.width(20), .shift("ll")) shifter_1 (
    .in({ID_IR[31], ID_IR[19:15], FUNC[2:0], ID_IR[20], FUNC[4], ID_IR[29:26], FUNC[3], ID_IR[24:21]}),
    .\dist (5'b00001), .out(shifter_1_out));
  and and_10 (INT, d_ff_1_qn, IRSig);
  // Probe on M_PC[11:0]
  D_Flip_Flop #(.trigger("high"), .Pre_Clr_Positions("LEGACY"), .NegatePresetClear("false"), .enable("true"), .NewFFLayout("false")) d_ff_2 (.Q(d_ff_2_q));  // open: clk, D, Qn, preset, en, reset
  // Probe on 13'h80
  Shifter #(.width(32), .shift("ll")) shifter_2 (.in(bit_extender_3_out), .\dist (5'b00001), .out(shifter_2_out));
  assign bit_extender_4_out = {{12{shifter_1_out[19]}}, shifter_1_out};  // Bit_Extender bit_extender_4
  Adder #(.width(32)) adder_2 (.a(bit_extender_1_out), .b(R1Data), .out(adder_2_out));  // open: cin, cout
  or or_5 (or_5_out, JAL, JALR);
  Counter #(.width(16), .max('hffff), .ongoal("wrap"), .trigger("rising"), .behavior("new")) counter_3 (
    .count(or_5_out), .Q(\无条件分支数 ), .clk(CLK), .clr(RST));  // open: load, D, carry, preset, down
  // Probe on WB_PC[11:0]
  Comparator #(.width(13), .mode("twosComplement")) comparator_3 (
    .a(CNT_num), .b(13'h80), .eq(comparator_3_eq), .lt(comparator_3_lt));  // open: gt
  Clock #(.highDuration(1), .lowDuration(1)) clock_1 (.out(clock_1_out));
  or or_6 (or_6_out, and_9_out, \单周期硬布线控制器_1_memtoreg );
  or or_7 (or_7_out, \单周期硬布线控制器_1_regwrite , and_9_out);
  Regifile_DW regifile_dw_1 (
    .Din(RDin), .Clk(CLK), .R1(R1Data), .R2(R2Data), .WE(RegWrite), .W_num(RW_num), .R1_num(R1), .R2_num(R2));
  Adder #(.width(32)) adder_3 (.a(shifter_2_out), .b(ID_PC), .out(adder_3_out));  // open: cin, cout
  Adder #(.width(32)) adder_4 (.a(bit_extender_4_out), .b(ID_PC), .out(adder_4_out));  // open: cin, cout
  assign and_11_out = adder_2_out & not_2_out;  // AND_Gate and_11, 32 bits wide
  assign not_2_out = ~32'h1;  // NOT_Gate not_2, 32 bits wide
  Register #(.width(2), .trigger("rising"), .Select("low")) register_2 (
    .D(IRNum), .en(INT), .Q(register_2_q), .clk(CLK), .clr(RST));
  nand nand_1 (nand_1_out, d_ff_2_q, comparator_3_eq);
  Counter #(.width(13), .max('h1fff), .ongoal("stay"), .trigger("rising"), .behavior("old")) counter_4 (
    .count(comparator_3_lt), .Q(CNT_num), .clk(clock_1_out));  // open: load, D, carry, clr, preset
  Multiplexer #(.select(1), .width(32), .disabled("Z"), .enable("false")) multiplexer_4 (
    .in0(R2Data), .in1(bit_extender_2_out), .out(multiplexer_4_out), .sel(\单周期硬布线控制器_1_alu_src ));
  or or_8 (or_8_out, INT, EXJALR, EXJAL, Branch, RST, LoadUse, URET);
  Decoder #(.select(2), .tristate("false"), .disabled("Z"), .enable("false")) decoder_1 (
    .out1(decoder_1_out1), .out2(decoder_1_out2), .out3(decoder_1_out3), .sel(register_2_q));  // open: out0
  and and_12 (CLR1, decoder_1_out1, URET);
  and and_13 (CLR2, decoder_1_out2, URET);
  Multiplexer #(.select(1), .width(32), .disabled("Z"), .enable("false")) multiplexer_5 (
    .in0(OriAddr), .in1(mEPC_q), .out(multiplexer_5_out), .sel(URET));
  Register #(.width(32), .trigger("rising"), .Select("low")) mEPC (
    .D(OriAddr), .en(INT), .Q(mEPC_q), .clk(CLK), .clr(RST));
  Multiplexer #(.select(2), .width(32), .disabled("Z"), .enable("false")) multiplexer_6 (
    .in1(32'h30ac), .in2(32'h3150), .in3(32'h31f4), .out(multiplexer_6_out), .sel(IRNum));  // open: in0
  assign CLK = nand_1_out ? clock_1_out : 1'bz;  // Controlled_Buffer controlled_buffer_1
  ID_EX id_ex_1 (
    .REMUin(\单周期硬布线控制器_1_remu ), .LBin(and_9_out), .URETin(\单周期硬布线控制器_1_uret ), .JALRin(\单周期硬布线控制器_1_jalr ),
    .JALin(\单周期硬布线控制器_1_jal ), .BEQin(\单周期硬布线控制器_1_beq ), .BLTUin(\单周期硬布线控制器_1_bltu ),
    .BNEin(\单周期硬布线控制器_1_bne ), .MemToRegin(or_6_out), .MemWritein(\单周期硬布线控制器_1_memwrite ),
    .ALUopin(\单周期硬布线控制器_1_alu_op ), .R1datain(R1Data), .R2datain(R2Data), .RWin(ID_IR[11:7]),
    .BAin(adder_3_out), .JALAin(adder_4_out), .JALRin_2(and_11_out), .LBAin(adder_2_out),
    .REMUout(id_ex_1_remuout), .LBout(id_ex_1_lbout), .URETout(id_ex_1_uretout), .JALRout(EXJALR),
    .JALout(EXJAL), .BEQout(Beq), .BLTUout(Bltu), .BNEout(Bne), .MemToRegout(MTR),
    .MemWriteout(id_ex_1_memwriteout), .ALUopout(id_ex_1_aluopout), .R1dataout(EXR1Data),
    .R2dataout(EXR2Data), .RWout(EXW), .BAout(BranAddr), .JALAout(JALAddr), .JALRout_2(JALRAddr),
    .LBAout(id_ex_1_lbaout), .clr(or_8_out), .clk(CLK), .abl(and_16_out), .PCin(ID_PC), .PCout(EX_PC),
    .PC_4in(if_id_1_pc_4out), .PC_4out(id_ex_1_pc_4out), .ALUBin(multiplexer_4_out), .ALUBout(EXALUB),
    .RegWritein(or_7_out), .RegWritegout(RWE), .R1Fin(R1F0), .R1Fout(R1F), .R2Fin(R2F0), .R2Fout(R2F),
    .ASBin(\单周期硬布线控制器_1_alu_src ), .ASBout(EXASB), .ECALLin(\单周期硬布线控制器_1_ecall ), .ECALLout(ecall));  // open: HALTin, HALTout, PJin, PJout
  and and_14 (and_14_out, ~rehalt, bubble);  // AND_Gate
  Counter #(.width(16), .max('hffff), .ongoal("wrap"), .trigger("rising"), .behavior("new")) counter_5 (
    .count(and_14_out), .Q(\插入气泡数 ), .clk(CLK), .clr(RST));  // open: load, D, carry, preset, down
  and and_15 (CLR3, decoder_1_out3, URET);
  Multiplexer #(.select(1), .width(32), .disabled("Z"), .enable("false")) multiplexer_7 (
    .in0(multiplexer_5_out), .in1(multiplexer_6_out), .out(NextAddr), .sel(INT));
  Pull_Resistor #(.pull(1)) pull_resistor_1 (.node(CLK));
  and and_16 (and_16_out, rehalt, ~Go);  // AND_Gate
  Counter #(.width(16), .max('hffff), .ongoal("wrap"), .trigger("rising"), .behavior("new")) counter_6 (
    .count(LoadUse), .Q(\LoadUse次数 ), .clk(CLK), .clr(RST));  // open: load, D, carry, preset, down
  or or_9 (IR1_t, IR1, IRA);
  Multiplexer #(.select(3), .width(32), .disabled("Z"), .enable("false")) multiplexer_8 (
    .in0(PC_4), .in1(BranAddr), .in2(JALAddr), .in4(JALRAddr), .out(OriAddr), .sel({JALR, JAL, Branch}));  // open: in3, in5, in6, in7
  or or_10 (IR2_t, IR2, IRB);
  ALU alu_1 (
    .X(EXMUXR1), .Y(EXMUXR3), .AluOP(id_ex_1_aluopout), .Equal(tunnel_t), .Result(alu_1_result),
    .Result_2(alu_1_result_2), .out_6(tunnel));  // open: out_4
  or or_11 (or_11_out, INT, URET, RST);
  or or_12 (IR3_t, IR3, IRC);
  EX_MEM ex_mem_1 (
    .PCin(EX_PC), .PC_4in(id_ex_1_pc_4out), .HALTin(halt), .REMUin(id_ex_1_remuout), .LBin(id_ex_1_lbout),
    .URETin(id_ex_1_uretout), .JALRin(EXJALR), .JALin(EXJAL), .MemToRegin(MTR),
    .MemWritein(id_ex_1_memwriteout), .ALURin(alu_1_result), .RWin(EXW), .LBAin(id_ex_1_lbaout),
    .PCout(M_PC), .PC_4out(ex_mem_1_pc_4out), .HALTout(ex_mem_1_haltout), .REMUout(ex_mem_1_remuout),
    .LBout(ex_mem_1_lbout), .URETout(ex_mem_1_uretout), .JALRout(ex_mem_1_jalrout), .JALout(ex_mem_1_jalout),
    .MemToRegout(ex_mem_1_memtoregout), .MemWriteout(MemWrite), .ALURout(ALURES), .RWout(MEMW),
    .LBAout(LBAddr), .clr(or_11_out), .clk(CLK), .abl(and_17_out), .R2datain(EXMUXR2), .R2dataout(MDin),
    .R2in(alu_1_result_2), .R2out(ex_mem_1_r2out), .RegWritein(RWE), .RegWritegout(RWM));
  and and_17 (and_17_out, rehalt, ~Go);  // AND_Gate
  Multiplexer #(.select(2), .width(32), .disabled("Z"), .enable("false")) multiplexer_9 (
    .in0(EXR1Data), .in1(RDin), .in2(ALURES), .in3({32{1'b0}}), .out(EXMUXR1), .sel(R1F));
  Multiplexer #(.select(2), .width(32), .disabled("Z"), .enable("false")) multiplexer_10 (
    .in0(EXALUB), .in1(RDin), .in2(ALURES), .in3({32{1'b0}}), .out(multiplexer_10_out), .sel(R2F));
  Multiplexer #(.select(2), .width(32), .disabled("Z"), .enable("false")) multiplexer_11 (
    .in0(EXR2Data), .in1(RDin), .in2(ALURES), .in3({32{1'b0}}), .out(EXMUXR2), .sel(R2F));
  Multiplexer #(.select(1), .width(32), .disabled("Z"), .enable("false")) multiplexer_12 (
    .in0(multiplexer_10_out), .in1(EXALUB), .out(EXMUXR3), .sel(EXASB));
  Redirect redirect_1 (
    .R1(R1), .EXW(EXW), .MEMW(MEMW), .R2(R2), .R1F(R1F0), .R2F(R2F0), .LoadUse(LoadUse), .Bubble(bubble),
    .RWE(RWE), .RWM(RWM), .MemToReg(MTR), .OP(ID_IR[6:2]), .Funct(FUNC));
  Multiplexer #(.select(1), .width(32), .disabled("Z"), .enable("false")) multiplexer_13 (
    .in0(ALURES), .in1(LBAddr), .out(multiplexer_13_out), .sel(ex_mem_1_lbout));
  RAM #(.addrWidth(10), .dataWidth(32), .bus("separate"), .Select("high")) ram_1 (
    .addr(multiplexer_13_out[11:2]), .din(MDin), .data(ram_1_data), .str(MemWrite), .clk(CLK), .clr(RST));  // open: sel, ld
  Multiplexer #(.select(1), .width(32), .disabled("Z"), .enable("false")) multiplexer_14 (
    .in0(ALURES), .in1(ram_1_data), .out(multiplexer_14_out), .sel(ex_mem_1_memtoregout));
  or or_13 (or_13_out, INT, RST);
  MEM_WB mem_wb_1 (
    .PCin(M_PC), .PC_4in(ex_mem_1_pc_4out), .HALTin(ex_mem_1_haltout), .REMUin(ex_mem_1_remuout),
    .LBin(ex_mem_1_lbout), .URETin(ex_mem_1_uretout), .JALRin(ex_mem_1_jalrout), .JALin(ex_mem_1_jalout),
    .MemDatain(multiplexer_14_out), .R2in(ex_mem_1_r2out), .LB01in(multiplexer_13_out[1:0]),
    .Mdatain(ram_1_data), .RWin(MEMW), .PCout(WB_PC), .PC_4out(mem_wb_1_pc_4out), .HALTout(rehalt),
    .REMUout(REMU), .LBout(LB), .URETout(URET), .JALRout(JALR), .JALout(JAL),
    .MemDataout(mem_wb_1_memdataout), .R2out(Result2), .LB01out(LB01), .Mdataout(MData), .RWout(RW_num),
    .clr(or_13_out), .clk(CLK), .abl(and_18_out), .RegWritein(RWM), .RegWritegout(RegWrite));  // open: go
  and and_18 (and_18_out, rehalt, ~Go);  // AND_Gate
  or or_14 (or_14_out, JAL, JALR);
  Multiplexer #(.select(1), .width(32), .disabled("Z"), .enable("false")) multiplexer_15 (
    .in0(mem_wb_1_memdataout), .in1(mem_wb_1_pc_4out), .out(multiplexer_15_out), .sel(or_14_out));
  Multiplexer #(.select(2), .width(8), .disabled("Z"), .enable("false")) multiplexer_16 (
    .in0(MData[7:0]), .in1(MData[15:8]), .in2(MData[23:16]), .in3(MData[31:24]), .out(multiplexer_16_out),
    .sel(LB01));
  Multiplexer #(.select(1), .width(32), .disabled("Z"), .enable("false")) multiplexer_17 (
    .in0(multiplexer_15_out), .in1(Result2), .out(multiplexer_17_out), .sel(REMU));
  assign bit_extender_5_out = {{24{multiplexer_16_out[7]}}, multiplexer_16_out};  // Bit_Extender bit_extender_5
  Comparator #(.width(16), .mode("twosComplement")) comparator_4 (
    .a(16'h23b), .b(\总周期数 ), .eq(comparator_4_eq));  // open: gt, lt
  or or_15 (or_15_out, comparator_4_eq, comparator_5_eq);
  Comparator #(.width(16), .mode("twosComplement")) comparator_5 (
    .a(\总周期数 ), .b(16'h1), .eq(comparator_5_eq));  // open: gt, lt
  Comparator #(.width(16), .mode("twosComplement")) comparator_6 (
    .a(\总周期数 ), .b(16'h4), .eq(comparator_6_eq));  // open: gt, lt
  Comparator #(.width(16), .mode("twosComplement")) comparator_7 (
    .a(\总周期数 ), .b(16'h7), .eq(comparator_7_eq));  // open: gt, lt
  Multiplexer #(.select(1), .width(32), .disabled("Z"), .enable("false")) multiplexer_18 (
    .in0(multiplexer_17_out), .in1(bit_extender_5_out), .out(RDin), .sel(LB));
  Pull_Resistor #(.pull(0)) pull_resistor_2 (.node(IRA));
  assign IRA = or_15_out ? ~CLK : 1'bz;  // Controlled_Inverter controlled_inverter_1
  Pull_Resistor #(.pull(0)) pull_resistor_3 (.node(IRB));
  assign IRB = comparator_6_eq ? ~CLK : 1'bz;  // Controlled_Inverter controlled_inverter_2
  Pull_Resistor #(.pull(0)) pull_resistor_4 (.node(IRC));
  assign IRC = comparator_7_eq ? ~CLK : 1'bz;  // Controlled_Inverter controlled_inverter_3

  // Other names for the same wires on the sheet: ID_IR (some bits) = FUNC; OP[4:0] = ID_IR[6:2]; MEM_PC[31:0] = M_PC

  // Notes on the sheet:
  //   中断源
  //   时空图监测，可删除
  //   中断等待指示
  //   数码管输出
  //   指令探针
  //   指令存储器
  //   指令字
  //   contents of rom_1 (hex, n*v repeats v):
  //   7d000113 100413 1f41993 41f9d993 433 c00913 800b13 140413 f47413 800293 100313 499993 89e9b3 1300533
  //   2200893 73 406282b3 fe0294e3 140413 f00f93 1f47433 1c41413 800293 100313 49d993 89e9b3 1300533
  //   2200893 73 406282b3 fe0294e3 1c45413 406b0b33 b0463 f95ff06f 2b3 fff2c293 1029293 fff2e293 500533
  //   2200893 73 f5dff06f 1112023 410113 a12023 410113 812023 410113 1312023 410113 1412023 410113 1512023
  //   410113 1612023 410113 100b13 300a13 100a93 1600433 441413 14469b3 1300533 2200893 73 fe0416e3
  //   415a0a33 fe0a10e3 ffc10113 12b03 ffc10113 12a83 ffc10113 12a03 ffc10113 12983 ffc10113 12403
  //   ffc10113 12503 ffc10113 12883 200073 1112023 410113 a12023 410113 812023 410113 1312023 410113
  //   1412023 410113 1512023 410113 1612023 410113 200b13 300a13 100a93 1600433 441413 14469b3 1300533
  //   2200893 73 fe0416e3 415a0a33 fe0a10e3 ffc10113 12b03 ffc10113 12a83 ffc10113 12a03 ffc10113 12983
  //   ffc10113 12403 ffc10113 12503 ffc10113 12883 200073 1112023 410113 a12023 410113 812023 410113
  //   1312023 410113 1412023 410113 1512023 410113 1612023 410113 300b13 300a13 100a93 1600433 441413
  //   14469b3 1300533 2200893 73 fe0416e3 415a0a33 fe0a10e3 ffc10113 12b03 ffc10113 12a83 ffc10113 12a03
  //   ffc10113 12983 ffc10113 12403 ffc10113 12503 ffc10113 12883 200073
  //   JAL
  //   JALR
  //   URET
  //   控制位
  //   Beq
  //   Bne
  //   MemToReg
  //   MemWrite
  //   AluOP
  //   AluSrcB
  //   RegWrite
  //   流水调试日志用
  //   暂停节拍，不能为0
  //   戳工具置1进入计数暂停模式，ctrl+k时钟自动运行到对应节拍暂停
  //   ctrl+k关闭时钟连续运行，将控制位置零，进入单步调试模式调试
  //   可计数暂停的时钟源
  //   为方便自动评测，需要输出流水线各段保存的PC值，注意是PC不是PC+4，另外ID段寄存器写入信息，Mem段内存写入信息也要输出
  //   数据存储器
  //   单级中断测试信号模拟器
endmodule

module \封装正确性测试  (
);

  wire IR1, IR2, IR3, MemW, RegW;
  wire [31:0] EX_PC, ID_PC, IF_PC, IR, LED, MDin, MDinr, MEM_PC, PC, RDin, RDinr, WB_PC;

  \单周期RISC_V  \u_单周期risc_v_1  (
    .IR1(IR1), .IR2(IR2), .IR3(IR3), .RegWrite(RegW), .MemWrite(MemW), .PC(PC), .IR(IR), .RDin(RDin),
    .MDin(MDin), .LedData(LED));
  \气泡流水线  \u_气泡流水线_1  (
    .RegWrite(RegW), .MemWrite(MemW), .IF_PC(IF_PC), .ID_PC(ID_PC), .EX_PC(EX_PC), .M_PC(MEM_PC),
    .WB_PC(WB_PC), .RDin(RDinr), .MDin(MDinr), .LedData(LED));
  \单周期_单级中断  \u_单周期_单级中断_1  (
    .IR1(IR1), .IR2(IR2), .IR3(IR3), .RegWrite(RegW), .MemWrite(MemW), .PC(PC), .IR(IR), .RDin(RDin),
    .MDin(MDin), .LedData(LED));
  \理想流水线  \u_理想流水线_1  (
    .RegWrite(RegW), .MemWrite(MemW), .IF_PC(IF_PC), .ID_PC(ID_PC), .EX_PC(EX_PC), .M_PC(MEM_PC),
    .WB_PC(WB_PC), .RDin(RDinr), .MDin(MDinr), .LedData(LED));
  \重定向流水线  \u_重定向流水线_1  (
    .RegWrite(RegW), .MemWrite(MemW), .IF_PC(IF_PC), .ID_PC(ID_PC), .EX_PC(EX_PC), .M_PC(MEM_PC),
    .WB_PC(WB_PC), .RDin(RDinr), .MDin(MDinr), .LedData(LED));
  \单周期_多级中断  \u_单周期_多级中断_1  (
    .IR1(IR1), .IR2(IR2), .IR3(IR3), .RegWrite(RegW), .MemWrite(MemW), .PC(PC), .IR(IR), .RDin(RDin),
    .MDin(MDin), .LedData(LED));

  // Notes on the sheet:
  //   单周期封装测试
  //   气泡流水封装测试
  //   单周期+单级中断封装测试
  //   请检查上面封装有无位宽不匹配，引脚标签是否和连接的标签相对应，否则无法在educoder平台上正确测试
  //   理想流水封装测试
  //   重定向流水封装测试
  //   单周期+多级中断封装测试
endmodule

module IF_ID (
  input  [31:0] PCin,
  input  [31:0] PC_4in,
  input  PJin,
  input  [31:0] \指令字in ,
  input  clr,
  input  clk,
  input  abl,
  output [31:0] PCout,
  output [31:0] PC_4out,
  output PJout,
  output [31:0] \指令字out 
);

  wire multiplexer_3_out, not_1_out;
  wire [31:0] multiplexer_1_out, multiplexer_2_out, multiplexer_4_out;

  Multiplexer #(.select(1), .width(32), .disabled("Z"), .enable("false")) multiplexer_1 (
    .in0(PCin), .in1({32{1'b0}}), .out(multiplexer_1_out), .sel(clr));
  Multiplexer #(.select(1), .width(32), .disabled("Z"), .enable("false")) multiplexer_2 (
    .in0(PC_4in), .in1({32{1'b0}}), .out(multiplexer_2_out), .sel(clr));
  Multiplexer #(.select(1), .width(1), .disabled("Z"), .enable("false")) multiplexer_3 (
    .in0(PJin), .in1(1'b0), .out(multiplexer_3_out), .sel(clr));
  Multiplexer #(.select(1), .width(32), .disabled("Z"), .enable("false")) multiplexer_4 (
    .in0(\指令字in ), .in1({32{1'b0}}), .out(multiplexer_4_out), .sel(clr));
  not not_1 (not_1_out, abl);
  Register #(.width(32), .trigger("rising"), .Select("low")) register_1 (
    .D(multiplexer_1_out), .en(not_1_out), .Q(PCout), .clk(clk));  // open: clr
  Register #(.width(32), .trigger("rising"), .Select("low")) register_2 (
    .D(multiplexer_2_out), .en(not_1_out), .Q(PC_4out), .clk(clk));  // open: clr
  Register #(.width(1), .trigger("rising"), .Select("low")) register_3 (
    .D(multiplexer_3_out), .en(not_1_out), .Q(PJout), .clk(clk));  // open: clr
  Register #(.width(32), .trigger("rising"), .Select("low")) register_4 (
    .D(multiplexer_4_out), .en(not_1_out), .Q(\指令字out ), .clk(clk));  // open: clr
endmodule

module ID_EX (
  input  [31:0] PCin,
  input  [31:0] PC_4in,
  input  HALTin,
  input  PJin,
  input  ECALLin,
  input  REMUin,
  input  LBin,
  input  URETin,
  input  JALRin,
  input  JALin,
  input  BEQin,
  input  BLTUin,
  input  BNEin,
  input  RegWritein,
  input  MemToRegin,
  input  MemWritein,
  input  [3:0] ALUopin,
  input  [1:0] R1Fin,
  input  [1:0] R2Fin,
  input  ASBin,
  input  [31:0] R1datain,
  input  [31:0] R2datain,
  input  [31:0] ALUBin,
  input  [4:0] RWin,
  input  [31:0] BAin,
  input  [31:0] JALAin,
  input  [31:0] JALRin_2,
  input  [31:0] LBAin,
  input  clr,
  input  clk,
  input  abl,
  output [31:0] PCout,
  output [31:0] PC_4out,
  output HALTout,
  output PJout,
  output ECALLout,
  output REMUout,
  output LBout,
  output URETout,
  output JALRout,
  output JALout,
  output BEQout,
  output BLTUout,
  output BNEout,
  output RegWritegout,
  output MemToRegout,
  output MemWriteout,
  output [3:0] ALUopout,
  output [1:0] R1Fout,
  output [1:0] R2Fout,
  output ASBout,
  output [31:0] R1dataout,
  output [31:0] R2dataout,
  output [31:0] ALUBout,
  output [4:0] RWout,
  output [31:0] BAout,
  output [31:0] JALAout,
  output [31:0] JALRout_2,
  output [31:0] LBAout
);

  wire multiplexer_3_out, multiplexer_4_out, multiplexer_5_out, multiplexer_6_out, multiplexer_7_out,
       multiplexer_8_out, multiplexer_9_out, multiplexer_10_out, multiplexer_11_out, multiplexer_12_out,
       multiplexer_13_out, multiplexer_14_out, multiplexer_15_out, multiplexer_16_out, multiplexer_20_out,
       not_1_out;
  wire [1:0] multiplexer_18_out, multiplexer_19_out;
  wire [3:0] multiplexer_17_out;
  wire [4:0] multiplexer_24_out;
  wire [31:0] multiplexer_1_out, multiplexer_2_out, multiplexer_21_out, multiplexer_22_out,
       multiplexer_23_out, multiplexer_25_out, multiplexer_26_out, multiplexer_27_out, multiplexer_28_out;

  Multiplexer #(.select(1), .width(32), .disabled("Z"), .enable("false")) multiplexer_1 (
    .in0(PCin), .in1({32{1'b0}}), .out(multiplexer_1_out), .sel(clr));
  Multiplexer #(.select(1), .width(32), .disabled("Z"), .enable("false")) multiplexer_2 (
    .in0(PC_4in), .in1({32{1'b0}}), .out(multiplexer_2_out), .sel(clr));
  Multiplexer #(.select(1), .width(1), .disabled("Z"), .enable("false")) multiplexer_3 (
    .in0(HALTin), .in1(1'b0), .out(multiplexer_3_out), .sel(clr));
  Multiplexer #(.select(1), .width(1), .disabled("Z"), .enable("false")) multiplexer_4 (
    .in0(PJin), .in1(1'b0), .out(multiplexer_4_out), .sel(clr));
  Multiplexer #(.select(1), .width(1), .disabled("Z"), .enable("false")) multiplexer_5 (
    .in0(ECALLin), .in1(1'b0), .out(multiplexer_5_out), .sel(clr));
  Multiplexer #(.select(1), .width(1), .disabled("Z"), .enable("false")) multiplexer_6 (
    .in0(REMUin), .in1(1'b0), .out(multiplexer_6_out), .sel(clr));
  Multiplexer #(.select(1), .width(1), .disabled("Z"), .enable("false")) multiplexer_7 (
    .in0(LBin), .in1(1'b0), .out(multiplexer_7_out), .sel(clr));
  Multiplexer #(.select(1), .width(1), .disabled("Z"), .enable("false")) multiplexer_8 (
    .in0(URETin), .in1(1'b0), .out(multiplexer_8_out), .sel(clr));
  Multiplexer #(.select(1), .width(1), .disabled("Z"), .enable("false")) multiplexer_9 (
    .in0(JALRin), .in1(1'b0), .out(multiplexer_9_out), .sel(clr));
  Multiplexer #(.select(1), .width(1), .disabled("Z"), .enable("false")) multiplexer_10 (
    .in0(JALin), .in1(1'b0), .out(multiplexer_10_out), .sel(clr));
  Multiplexer #(.select(1), .width(1), .disabled("Z"), .enable("false")) multiplexer_11 (
    .in0(BEQin), .in1(1'b0), .out(multiplexer_11_out), .sel(clr));
  Multiplexer #(.select(1), .width(1), .disabled("Z"), .enable("false")) multiplexer_12 (
    .in0(BLTUin), .in1(1'b0), .out(multiplexer_12_out), .sel(clr));
  Multiplexer #(.select(1), .width(1), .disabled("Z"), .enable("false")) multiplexer_13 (
    .in0(BNEin), .in1(1'b0), .out(multiplexer_13_out), .sel(clr));
  Multiplexer #(.select(1), .width(1), .disabled("Z"), .enable("false")) multiplexer_14 (
    .in0(RegWritein), .in1(1'b0), .out(multiplexer_14_out), .sel(clr));
  Multiplexer #(.select(1), .width(1), .disabled("Z"), .enable("false")) multiplexer_15 (
    .in0(MemToRegin), .in1(1'b0), .out(multiplexer_15_out), .sel(clr));
  Multiplexer #(.select(1), .width(1), .disabled("Z"), .enable("false")) multiplexer_16 (
    .in0(MemWritein), .in1(1'b0), .out(multiplexer_16_out), .sel(clr));
  Multiplexer #(.select(1), .width(4), .disabled("Z"), .enable("false")) multiplexer_17 (
    .in0(ALUopin), .in1(4'b0000), .out(multiplexer_17_out), .sel(clr));
  Multiplexer #(.select(1), .width(2), .disabled("Z"), .enable("false")) multiplexer_18 (
    .in0(R1Fin), .in1(2'b00), .out(multiplexer_18_out), .sel(clr));
  Multiplexer #(.select(1), .width(2), .disabled("Z"), .enable("false")) multiplexer_19 (
    .in0(R2Fin), .in1(2'b00), .out(multiplexer_19_out), .sel(clr));
  Multiplexer #(.select(1), .width(1), .disabled("Z"), .enable("false")) multiplexer_20 (
    .in0(ASBin), .in1(1'b0), .out(multiplexer_20_out), .sel(clr));
  Multiplexer #(.select(1), .width(32), .disabled("Z"), .enable("false")) multiplexer_21 (
    .in0(R1datain), .in1({32{1'b0}}), .out(multiplexer_21_out), .sel(clr));
  Multiplexer #(.select(1), .width(32), .disabled("Z"), .enable("false")) multiplexer_22 (
    .in0(R2datain), .in1({32{1'b0}}), .out(multiplexer_22_out), .sel(clr));
  Multiplexer #(.select(1), .width(32), .disabled("Z"), .enable("false")) multiplexer_23 (
    .in0(ALUBin), .in1({32{1'b0}}), .out(multiplexer_23_out), .sel(clr));
  Multiplexer #(.select(1), .width(5), .disabled("Z"), .enable("false")) multiplexer_24 (
    .in0(RWin), .in1({5{1'b0}}), .out(multiplexer_24_out), .sel(clr));
  Multiplexer #(.select(1), .width(32), .disabled("Z"), .enable("false")) multiplexer_25 (
    .in0(BAin), .in1({32{1'b0}}), .out(multiplexer_25_out), .sel(clr));
  Multiplexer #(.select(1), .width(32), .disabled("Z"), .enable("false")) multiplexer_26 (
    .in0(JALAin), .in1({32{1'b0}}), .out(multiplexer_26_out), .sel(clr));
  Multiplexer #(.select(1), .width(32), .disabled("Z"), .enable("false")) multiplexer_27 (
    .in0(JALRin_2), .in1({32{1'b0}}), .out(multiplexer_27_out), .sel(clr));
  Multiplexer #(.select(1), .width(32), .disabled("Z"), .enable("false")) multiplexer_28 (
    .in0(LBAin), .in1({32{1'b0}}), .out(multiplexer_28_out), .sel(clr));
  not not_1 (not_1_out, abl);
  Register #(.width(32), .trigger("rising"), .Select("low")) register_1 (
    .D(multiplexer_1_out), .en(not_1_out), .Q(PCout), .clk(clk));  // open: clr
  Register #(.width(32), .trigger("rising"), .Select("low")) register_2 (
    .D(multiplexer_2_out), .en(not_1_out), .Q(PC_4out), .clk(clk));  // open: clr
  Register #(.width(1), .trigger("rising"), .Select("low")) register_3 (
    .D(multiplexer_3_out), .en(not_1_out), .Q(HALTout), .clk(clk));  // open: clr
  Register #(.width(1), .trigger("rising"), .Select("low")) register_4 (
    .D(multiplexer_4_out), .en(not_1_out), .Q(PJout), .clk(clk));  // open: clr
  Register #(.width(1), .trigger("rising"), .Select("low")) register_5 (
    .D(multiplexer_5_out), .en(not_1_out), .Q(ECALLout), .clk(clk));  // open: clr
  Register #(.width(1), .trigger("rising"), .Select("low")) register_6 (
    .D(multiplexer_6_out), .en(not_1_out), .Q(REMUout), .clk(clk));  // open: clr
  Register #(.width(1), .trigger("rising"), .Select("low")) register_7 (
    .D(multiplexer_7_out), .en(not_1_out), .Q(LBout), .clk(clk));  // open: clr
  Register #(.width(1), .trigger("rising"), .Select("low")) register_8 (
    .D(multiplexer_8_out), .en(not_1_out), .Q(URETout), .clk(clk));  // open: clr
  Register #(.width(1), .trigger("rising"), .Select("low")) register_9 (
    .D(multiplexer_9_out), .en(not_1_out), .Q(JALRout), .clk(clk));  // open: clr
  Register #(.width(1), .trigger("rising"), .Select("low")) register_10 (
    .D(multiplexer_10_out), .en(not_1_out), .Q(JALout), .clk(clk));  // open: clr
  Register #(.width(1), .trigger("rising"), .Select("low")) register_11 (
    .D(multiplexer_11_out), .en(not_1_out), .Q(BEQout), .clk(clk));  // open: clr
  Register #(.width(1), .trigger("rising"), .Select("low")) register_12 (
    .D(multiplexer_12_out), .en(not_1_out), .Q(BLTUout), .clk(clk));  // open: clr
  Register #(.width(1), .trigger("rising"), .Select("low")) register_13 (
    .D(multiplexer_13_out), .en(not_1_out), .Q(BNEout), .clk(clk));  // open: clr
  Register #(.width(1), .trigger("rising"), .Select("low")) register_14 (
    .D(multiplexer_14_out), .en(not_1_out), .Q(RegWritegout), .clk(clk));  // open: clr
  Register #(.width(1), .trigger("rising"), .Select("low")) register_15 (
    .D(multiplexer_15_out), .en(not_1_out), .Q(MemToRegout), .clk(clk));  // open: clr
  Register #(.width(1), .trigger("rising"), .Select("low")) register_16 (
    .D(multiplexer_16_out), .en(not_1_out), .Q(MemWriteout), .clk(clk));  // open: clr
  Register #(.width(4), .trigger("rising"), .Select("low")) register_17 (
    .D(multiplexer_17_out), .en(not_1_out), .Q(ALUopout), .clk(clk));  // open: clr
  Register #(.width(2), .trigger("rising"), .Select("low")) register_18 (
    .D(multiplexer_18_out), .en(not_1_out), .Q(R1Fout), .clk(clk));  // open: clr
  Register #(.width(2), .trigger("rising"), .Select("low")) register_19 (
    .D(multiplexer_19_out), .en(not_1_out), .Q(R2Fout), .clk(clk));  // open: clr
  Register #(.width(1), .trigger("rising"), .Select("low")) register_20 (
    .D(multiplexer_20_out), .en(not_1_out), .Q(ASBout), .clk(clk));  // open: clr
  Register #(.width(32), .trigger("rising"), .Select("low")) register_21 (
    .D(multiplexer_21_out), .en(not_1_out), .Q(R1dataout), .clk(clk));  // open: clr
  Register #(.width(32), .trigger("rising"), .Select("low")) register_22 (
    .D(multiplexer_22_out), .en(not_1_out), .Q(R2dataout), .clk(clk));  // open: clr
  Register #(.width(32), .trigger("rising"), .Select("low")) register_23 (
    .D(multiplexer_23_out), .en(not_1_out), .Q(ALUBout), .clk(clk));  // open: clr
  Register #(.width(5), .trigger("rising"), .Select("low")) register_24 (
    .D(multiplexer_24_out), .en(not_1_out), .Q(RWout), .clk(clk));  // open: clr
  Register #(.width(32), .trigger("rising"), .Select("low")) register_25 (
    .D(multiplexer_25_out), .en(not_1_out), .Q(BAout), .clk(clk));  // open: clr
  Register #(.width(32), .trigger("rising"), .Select("low")) register_26 (
    .D(multiplexer_26_out), .en(not_1_out), .Q(JALAout), .clk(clk));  // open: clr
  Register #(.width(32), .trigger("rising"), .Select("low")) register_27 (
    .D(multiplexer_27_out), .en(not_1_out), .Q(JALRout_2), .clk(clk));  // open: clr
  Register #(.width(32), .trigger("rising"), .Select("low")) register_28 (
    .D(multiplexer_28_out), .en(not_1_out), .Q(LBAout), .clk(clk));  // open: clr
endmodule

module EX_MEM (
  input  [31:0] PCin,
  input  [31:0] PC_4in,
  input  HALTin,
  input  REMUin,
  input  LBin,
  input  URETin,
  input  JALRin,
  input  JALin,
  input  RegWritein,
  input  MemToRegin,
  input  MemWritein,
  input  [31:0] R2datain,
  input  [31:0] R2in,
  input  [31:0] ALURin,
  input  [4:0] RWin,
  input  [31:0] LBAin,
  input  clr,
  input  clk,
  input  abl,
  output [31:0] PCout,
  output [31:0] PC_4out,
  output HALTout,
  output REMUout,
  output LBout,
  output URETout,
  output JALRout,
  output JALout,
  output RegWritegout,
  output MemToRegout,
  output MemWriteout,
  output [31:0] R2dataout,
  output [31:0] R2out,
  output [31:0] ALURout,
  output [4:0] RWout,
  output [31:0] LBAout
);

  wire multiplexer_3_out, multiplexer_4_out, multiplexer_5_out, multiplexer_6_out, multiplexer_7_out,
       multiplexer_8_out, multiplexer_9_out, multiplexer_10_out, multiplexer_11_out, not_1_out;
  wire [4:0] multiplexer_15_out;
  wire [31:0] multiplexer_1_out, multiplexer_2_out, multiplexer_12_out, multiplexer_13_out,
       multiplexer_14_out, multiplexer_16_out;

  Multiplexer #(.select(1), .width(32), .disabled("Z"), .enable("false")) multiplexer_1 (
    .in0(PCin), .in1({32{1'b0}}), .out(multiplexer_1_out), .sel(clr));
  Multiplexer #(.select(1), .width(32), .disabled("Z"), .enable("false")) multiplexer_2 (
    .in0(PC_4in), .in1({32{1'b0}}), .out(multiplexer_2_out), .sel(clr));
  Multiplexer #(.select(1), .width(1), .disabled("Z"), .enable("false")) multiplexer_3 (
    .in0(HALTin), .in1(1'b0), .out(multiplexer_3_out), .sel(clr));
  Multiplexer #(.select(1), .width(1), .disabled("Z"), .enable("false")) multiplexer_4 (
    .in0(REMUin), .in1(1'b0), .out(multiplexer_4_out), .sel(clr));
  Multiplexer #(.select(1), .width(1), .disabled("Z"), .enable("false")) multiplexer_5 (
    .in0(LBin), .in1(1'b0), .out(multiplexer_5_out), .sel(clr));
  Multiplexer #(.select(1), .width(1), .disabled("Z"), .enable("false")) multiplexer_6 (
    .in0(URETin), .in1(1'b0), .out(multiplexer_6_out), .sel(clr));
  Multiplexer #(.select(1), .width(1), .disabled("Z"), .enable("false")) multiplexer_7 (
    .in0(JALRin), .in1(1'b0), .out(multiplexer_7_out), .sel(clr));
  Multiplexer #(.select(1), .width(1), .disabled("Z"), .enable("false")) multiplexer_8 (
    .in0(JALin), .in1(1'b0), .out(multiplexer_8_out), .sel(clr));
  Multiplexer #(.select(1), .width(1), .disabled("Z"), .enable("false")) multiplexer_9 (
    .in0(RegWritein), .in1(1'b0), .out(multiplexer_9_out), .sel(clr));
  Multiplexer #(.select(1), .width(1), .disabled("Z"), .enable("false")) multiplexer_10 (
    .in0(MemToRegin), .in1(1'b0), .out(multiplexer_10_out), .sel(clr));
  Multiplexer #(.select(1), .width(1), .disabled("Z"), .enable("false")) multiplexer_11 (
    .in0(MemWritein), .in1(1'b0), .out(multiplexer_11_out), .sel(clr));
  Multiplexer #(.select(1), .width(32), .disabled("Z"), .enable("false")) multiplexer_12 (
    .in0(R2datain), .in1({32{1'b0}}), .out(multiplexer_12_out), .sel(clr));
  Multiplexer #(.select(1), .width(32), .disabled("Z"), .enable("false")) multiplexer_13 (
    .in0(R2in), .in1({32{1'b0}}), .out(multiplexer_13_out), .sel(clr));
  Multiplexer #(.select(1), .width(32), .disabled("Z"), .enable("false")) multiplexer_14 (
    .in0(ALURin), .in1({32{1'b0}}), .out(multiplexer_14_out), .sel(clr));
  Multiplexer #(.select(1), .width(5), .disabled("Z"), .enable("false")) multiplexer_15 (
    .in0(RWin), .in1({5{1'b0}}), .out(multiplexer_15_out), .sel(clr));
  Multiplexer #(.select(1), .width(32), .disabled("Z"), .enable("false")) multiplexer_16 (
    .in0(LBAin), .in1({32{1'b0}}), .out(multiplexer_16_out), .sel(clr));
  not not_1 (not_1_out, abl);
  Register #(.width(32), .trigger("rising"), .Select("low")) register_1 (
    .D(multiplexer_1_out), .en(not_1_out), .Q(PCout), .clk(clk));  // open: clr
  Register #(.width(32), .trigger("rising"), .Select("low")) register_2 (
    .D(multiplexer_2_out), .en(not_1_out), .Q(PC_4out), .clk(clk));  // open: clr
  Register #(.width(1), .trigger("rising"), .Select("low")) register_3 (
    .D(multiplexer_3_out), .en(not_1_out), .Q(HALTout), .clk(clk));  // open: clr
  Register #(.width(1), .trigger("rising"), .Select("low")) register_4 (
    .D(multiplexer_4_out), .en(not_1_out), .Q(REMUout), .clk(clk));  // open: clr
  Register #(.width(1), .trigger("rising"), .Select("low")) register_5 (
    .D(multiplexer_5_out), .en(not_1_out), .Q(LBout), .clk(clk));  // open: clr
  Register #(.width(1), .trigger("rising"), .Select("low")) register_6 (
    .D(multiplexer_6_out), .en(not_1_out), .Q(URETout), .clk(clk));  // open: clr
  Register #(.width(1), .trigger("rising"), .Select("low")) register_7 (
    .D(multiplexer_7_out), .en(not_1_out), .Q(JALRout), .clk(clk));  // open: clr
  Register #(.width(1), .trigger("rising"), .Select("low")) register_8 (
    .D(multiplexer_8_out), .en(not_1_out), .Q(JALout), .clk(clk));  // open: clr
  Register #(.width(1), .trigger("rising"), .Select("low")) register_9 (
    .D(multiplexer_9_out), .en(not_1_out), .Q(RegWritegout), .clk(clk));  // open: clr
  Register #(.width(1), .trigger("rising"), .Select("low")) register_10 (
    .D(multiplexer_10_out), .en(not_1_out), .Q(MemToRegout), .clk(clk));  // open: clr
  Register #(.width(1), .trigger("rising"), .Select("low")) register_11 (
    .D(multiplexer_11_out), .en(not_1_out), .Q(MemWriteout), .clk(clk));  // open: clr
  Register #(.width(32), .trigger("rising"), .Select("low")) register_12 (
    .D(multiplexer_12_out), .en(not_1_out), .Q(R2dataout), .clk(clk));  // open: clr
  Register #(.width(32), .trigger("rising"), .Select("low")) register_13 (
    .D(multiplexer_13_out), .en(not_1_out), .Q(R2out), .clk(clk));  // open: clr
  Register #(.width(32), .trigger("rising"), .Select("low")) register_14 (
    .D(multiplexer_14_out), .en(not_1_out), .Q(ALURout), .clk(clk));  // open: clr
  Register #(.width(5), .trigger("rising"), .Select("low")) register_15 (
    .D(multiplexer_15_out), .en(not_1_out), .Q(RWout), .clk(clk));  // open: clr
  Register #(.width(32), .trigger("rising"), .Select("low")) register_16 (
    .D(multiplexer_16_out), .en(not_1_out), .Q(LBAout), .clk(clk));  // open: clr
endmodule

module MEM_WB (
  input  [31:0] PCin,
  input  [31:0] PC_4in,
  input  HALTin,
  input  go,
  input  REMUin,
  input  LBin,
  input  URETin,
  input  JALRin,
  input  JALin,
  input  RegWritein,
  input  [31:0] MemDatain,
  input  [31:0] R2in,
  input  [1:0] LB01in,
  input  [31:0] Mdatain,
  input  [4:0] RWin,
  input  clr,
  input  clk,
  input  abl,
  output [31:0] PCout,
  output [31:0] PC_4out,
  output HALTout,
  output REMUout,
  output LBout,
  output URETout,
  output JALRout,
  output JALout,
  output RegWritegout,
  output [31:0] MemDataout,
  output [31:0] R2out,
  output [1:0] LB01out,
  output [31:0] Mdataout,
  output [4:0] RWout
);

  wire multiplexer_3_out, multiplexer_4_out, multiplexer_5_out, multiplexer_6_out, multiplexer_7_out,
       multiplexer_8_out, multiplexer_9_out, not_1_out;
  wire [1:0] multiplexer_12_out;
  wire [4:0] multiplexer_14_out;
  wire [31:0] multiplexer_1_out, multiplexer_2_out, multiplexer_10_out, multiplexer_11_out,
       multiplexer_13_out;

  Multiplexer #(.select(1), .width(32), .disabled("Z"), .enable("false")) multiplexer_1 (
    .in0(PCin), .in1({32{1'b0}}), .out(multiplexer_1_out), .sel(clr));
  Multiplexer #(.select(1), .width(32), .disabled("Z"), .enable("false")) multiplexer_2 (
    .in0(PC_4in), .in1({32{1'b0}}), .out(multiplexer_2_out), .sel(clr));
  Multiplexer #(.select(1), .width(1), .disabled("Z"), .enable("false")) multiplexer_3 (
    .in0(HALTin), .in1(1'b0), .out(multiplexer_3_out), .sel(clr));
  Multiplexer #(.select(1), .width(1), .disabled("Z"), .enable("false")) multiplexer_4 (
    .in0(REMUin), .in1(1'b0), .out(multiplexer_4_out), .sel(clr));
  Multiplexer #(.select(1), .width(1), .disabled("Z"), .enable("false")) multiplexer_5 (
    .in0(LBin), .in1(1'b0), .out(multiplexer_5_out), .sel(clr));
  Multiplexer #(.select(1), .width(1), .disabled("Z"), .enable("false")) multiplexer_6 (
    .in0(URETin), .in1(1'b0), .out(multiplexer_6_out), .sel(clr));
  Multiplexer #(.select(1), .width(1), .disabled("Z"), .enable("false")) multiplexer_7 (
    .in0(JALRin), .in1(1'b0), .out(multiplexer_7_out), .sel(clr));
  Multiplexer #(.select(1), .width(1), .disabled("Z"), .enable("false")) multiplexer_8 (
    .in0(JALin), .in1(1'b0), .out(multiplexer_8_out), .sel(clr));
  Multiplexer #(.select(1), .width(1), .disabled("Z"), .enable("false")) multiplexer_9 (
    .in0(RegWritein), .in1(1'b0), .out(multiplexer_9_out), .sel(clr));
  Multiplexer #(.select(1), .width(32), .disabled("Z"), .enable("false")) multiplexer_10 (
    .in0(MemDatain), .in1({32{1'b0}}), .out(multiplexer_10_out), .sel(clr));
  Multiplexer #(.select(1), .width(32), .disabled("Z"), .enable("false")) multiplexer_11 (
    .in0(R2in), .in1({32{1'b0}}), .out(multiplexer_11_out), .sel(clr));
  Multiplexer #(.select(1), .width(2), .disabled("Z"), .enable("false")) multiplexer_12 (
    .in0(LB01in), .in1(2'b00), .out(multiplexer_12_out), .sel(clr));
  Multiplexer #(.select(1), .width(32), .disabled("Z"), .enable("false")) multiplexer_13 (
    .in0(Mdatain), .in1({32{1'b0}}), .out(multiplexer_13_out), .sel(clr));
  Multiplexer #(.select(1), .width(5), .disabled("Z"), .enable("false")) multiplexer_14 (
    .in0(RWin), .in1({5{1'b0}}), .out(multiplexer_14_out), .sel(clr));
  not not_1 (not_1_out, abl);
  Register #(.width(32), .trigger("rising"), .Select("low")) register_1 (
    .D(multiplexer_1_out), .en(not_1_out), .Q(PCout), .clk(clk));  // open: clr
  Register #(.width(32), .trigger("rising"), .Select("low")) register_2 (
    .D(multiplexer_2_out), .en(not_1_out), .Q(PC_4out), .clk(clk));  // open: clr
  Register #(.width(1), .trigger("rising"), .Select("low")) register_3 (
    .D(multiplexer_3_out), .en(not_1_out), .Q(HALTout), .clk(clk), .clr(go));
  Register #(.width(1), .trigger("rising"), .Select("low")) register_4 (
    .D(multiplexer_4_out), .en(not_1_out), .Q(REMUout), .clk(clk));  // open: clr
  Register #(.width(1), .trigger("rising"), .Select("low")) register_5 (
    .D(multiplexer_5_out), .en(not_1_out), .Q(LBout), .clk(clk));  // open: clr
  Register #(.width(1), .trigger("rising"), .Select("low")) register_6 (
    .D(multiplexer_6_out), .en(not_1_out), .Q(URETout), .clk(clk));  // open: clr
  Register #(.width(1), .trigger("rising"), .Select("low")) register_7 (
    .D(multiplexer_7_out), .en(not_1_out), .Q(JALRout), .clk(clk));  // open: clr
  Register #(.width(1), .trigger("rising"), .Select("low")) register_8 (
    .D(multiplexer_8_out), .en(not_1_out), .Q(JALout), .clk(clk));  // open: clr
  Register #(.width(1), .trigger("rising"), .Select("low")) register_9 (
    .D(multiplexer_9_out), .en(not_1_out), .Q(RegWritegout), .clk(clk));  // open: clr
  Register #(.width(32), .trigger("rising"), .Select("low")) register_10 (
    .D(multiplexer_10_out), .en(not_1_out), .Q(MemDataout), .clk(clk));  // open: clr
  Register #(.width(32), .trigger("rising"), .Select("low")) register_11 (
    .D(multiplexer_11_out), .en(not_1_out), .Q(R2out), .clk(clk));  // open: clr
  Register #(.width(2), .trigger("rising"), .Select("low")) register_12 (
    .D(multiplexer_12_out), .en(not_1_out), .Q(LB01out), .clk(clk));  // open: clr
  Register #(.width(32), .trigger("rising"), .Select("low")) register_13 (
    .D(multiplexer_13_out), .en(not_1_out), .Q(Mdataout), .clk(clk));  // open: clr
  Register #(.width(5), .trigger("rising"), .Select("low")) register_14 (
    .D(multiplexer_14_out), .en(not_1_out), .Q(RWout), .clk(clk));  // open: clr
endmodule
module RegUseCon (
  input  OP2,
  input  OP3,
  input  OP4,
  input  OP5,
  input  OP6,
  input  F12,
  input  F13,
  input  F14,
  input  F25,
  input  F30,
  output R1Used,
  output R2USed
);

  wire and_1_out, and_2_out, and_3_out, and_4_out, and_5_out, and_6_out, and_7_out, and_8_out, and_9_out,
       and_10_out, and_11_out, and_12_out, and_13_out, and_14_out, and_15_out, and_16_out, and_17_out,
       and_18_out, and_19_out, and_20_out, and_21_out, and_22_out, and_23_out, and_24_out, and_25_out,
       and_26_out, and_27_out, and_28_out, and_29_out, and_30_out, and_31_out, and_32_out, and_33_out,
       and_34_out, and_35_out, and_36_out, and_37_out, and_38_out, and_39_out, and_40_out, and_41_out,
       not_1_out, not_2_out, not_3_out, not_4_out, not_5_out, not_6_out, not_7_out, not_8_out, not_9_out,
       not_10_out, not_11_out, not_12_out, not_13_out, not_14_out, not_15_out, not_16_out, not_17_out,
       not_18_out, not_19_out, not_20_out, not_21_out, not_22_out, not_23_out, not_24_out, not_25_out,
       not_26_out, not_27_out, not_28_out, not_29_out, not_30_out, not_31_out, not_32_out, not_33_out,
       not_34_out, not_35_out, not_36_out, not_37_out, not_38_out, not_39_out, not_40_out, not_41_out,
       not_42_out, not_43_out, not_44_out, not_45_out, not_46_out, not_47_out, not_48_out, not_49_out,
       not_50_out, not_51_out, not_52_out, not_53_out, not_54_out, not_55_out, not_56_out, not_57_out,
       not_58_out, not_59_out, not_60_out, not_61_out, not_62_out, not_63_out, not_64_out, not_65_out,
       not_66_out, not_67_out, not_68_out, not_69_out, not_70_out, not_71_out, not_72_out, not_73_out,
       not_74_out, not_75_out, not_76_out, not_77_out, not_78_out, not_79_out, not_80_out, not_81_out,
       not_82_out, not_83_out, not_84_out, not_85_out, not_86_out, not_87_out, not_88_out, not_89_out,
       not_90_out, not_91_out, not_92_out, not_93_out, not_94_out, not_95_out, not_96_out, not_97_out,
       not_98_out, not_99_out, not_100_out, not_101_out, not_102_out, not_103_out, not_104_out, not_105_out,
       not_106_out, not_107_out, not_108_out, not_109_out, not_110_out, not_111_out, not_112_out,
       not_113_out, not_114_out, not_115_out, not_116_out, not_117_out, not_118_out, not_119_out,
       not_120_out, not_121_out, not_122_out, not_123_out, not_124_out, not_125_out, not_126_out,
       not_127_out, not_128_out, not_129_out, not_130_out, not_131_out, not_132_out, not_133_out,
       not_134_out, not_135_out, not_136_out, not_137_out, not_138_out, not_139_out, not_140_out,
       not_141_out, not_142_out, not_143_out, not_144_out, not_145_out, not_146_out, not_147_out,
       not_148_out, not_149_out, not_150_out, not_151_out, not_152_out, not_153_out, not_154_out,
       not_155_out, not_156_out, not_157_out, not_158_out, not_159_out, not_160_out, not_161_out,
       not_162_out, not_163_out, not_164_out, not_165_out, not_166_out, not_167_out, not_168_out,
       not_169_out, not_170_out, not_171_out, not_172_out, not_173_out, not_174_out, not_175_out,
       not_176_out, not_177_out, not_178_out, not_179_out, not_180_out, not_181_out, not_182_out,
       not_183_out, not_184_out, not_185_out, not_186_out, not_187_out, not_188_out, not_189_out,
       not_190_out, not_191_out, not_192_out, not_193_out, not_194_out, not_195_out, not_196_out,
       not_197_out, not_198_out, not_199_out, not_200_out, not_201_out, not_202_out, not_203_out,
       not_204_out, not_205_out, not_206_out, not_207_out, not_208_out, not_209_out, not_210_out,
       not_211_out, not_212_out, not_213_out, not_214_out, not_215_out, not_216_out, not_217_out,
       not_218_out, not_219_out, not_220_out, not_221_out, not_222_out, not_223_out, not_224_out,
       not_225_out, not_226_out, not_227_out, not_228_out, not_229_out, not_230_out, not_231_out,
       not_232_out, not_233_out, not_234_out, not_235_out, not_236_out;

  not not_1 (not_1_out, F30);
  not not_2 (not_2_out, F25);
  not not_3 (not_3_out, F14);
  not not_4 (not_4_out, F13);
  not not_5 (not_5_out, F12);
  not not_6 (not_6_out, OP6);
  not not_7 (not_7_out, OP3);
  not not_8 (not_8_out, OP2);
  not not_9 (not_9_out, F25);
  not not_10 (not_10_out, F14);
  not not_11 (not_11_out, F13);
  not not_12 (not_12_out, F12);
  not not_13 (not_13_out, OP6);
  not not_14 (not_14_out, OP3);
  not not_15 (not_15_out, OP2);
  not not_16 (not_16_out, F30);
  not not_17 (not_17_out, F25);
  not not_18 (not_18_out, OP6);
  not not_19 (not_19_out, OP3);
  not not_20 (not_20_out, OP2);
  not not_21 (not_21_out, F30);
  not not_22 (not_22_out, F25);
  not not_23 (not_23_out, F12);
  not not_24 (not_24_out, OP6);
  not not_25 (not_25_out, OP3);
  not not_26 (not_26_out, OP2);
  not not_27 (not_27_out, F30);
  not not_28 (not_28_out, F25);
  not not_29 (not_29_out, F14);
  not not_30 (not_30_out, F12);
  not not_31 (not_31_out, OP6);
  not not_32 (not_32_out, OP3);
  not not_33 (not_33_out, OP2);
  not not_34 (not_34_out, F30);
  not not_35 (not_35_out, F25);
  not not_36 (not_36_out, F14);
  not not_37 (not_37_out, OP6);
  not not_38 (not_38_out, OP3);
  not not_39 (not_39_out, OP2);
  not not_40 (not_40_out, F14);
  not not_41 (not_41_out, F13);
  not not_42 (not_42_out, F12);
  not not_43 (not_43_out, OP6);
  not not_44 (not_44_out, OP5);
  not not_45 (not_45_out, OP3);
  not not_46 (not_46_out, OP2);
  not not_47 (not_47_out, OP6);
  not not_48 (not_48_out, OP5);
  not not_49 (not_49_out, OP3);
  not not_50 (not_50_out, OP2);
  not not_51 (not_51_out, F12);
  not not_52 (not_52_out, OP6);
  not not_53 (not_53_out, OP5);
  not not_54 (not_54_out, OP3);
  not not_55 (not_55_out, OP2);
  not not_56 (not_56_out, F13);
  not not_57 (not_57_out, F12);
  not not_58 (not_58_out, OP6);
  not not_59 (not_59_out, OP5);
  not not_60 (not_60_out, OP3);
  not not_61 (not_61_out, OP2);
  not not_62 (not_62_out, F14);
  not not_63 (not_63_out, F12);
  not not_64 (not_64_out, OP6);
  not not_65 (not_65_out, OP5);
  not not_66 (not_66_out, OP3);
  not not_67 (not_67_out, OP2);
  not not_68 (not_68_out, F30);
  not not_69 (not_69_out, F25);
  not not_70 (not_70_out, F14);
  not not_71 (not_71_out, F13);
  not not_72 (not_72_out, OP6);
  not not_73 (not_73_out, OP5);
  not not_74 (not_74_out, OP3);
  not not_75 (not_75_out, OP2);
  not not_76 (not_76_out, F30);
  not not_77 (not_77_out, F25);
  not not_78 (not_78_out, F13);
  not not_79 (not_79_out, OP6);
  not not_80 (not_80_out, OP5);
  not not_81 (not_81_out, OP3);
  not not_82 (not_82_out, OP2);
  not not_83 (not_83_out, F25);
  not not_84 (not_84_out, F13);
  not not_85 (not_85_out, OP6);
  not not_86 (not_86_out, OP5);
  not not_87 (not_87_out, OP3);
  not not_88 (not_88_out, OP2);
  not not_89 (not_89_out, F14);
  not not_90 (not_90_out, F12);
  not not_91 (not_91_out, OP6);
  not not_92 (not_92_out, OP5);
  not not_93 (not_93_out, OP4);
  not not_94 (not_94_out, OP3);
  not not_95 (not_95_out, OP2);
  not not_96 (not_96_out, F14);
  not not_97 (not_97_out, F12);
  not not_98 (not_98_out, OP6);
  not not_99 (not_99_out, OP4);
  not not_100 (not_100_out, OP3);
  not not_101 (not_101_out, OP2);
  not not_102 (not_102_out, F14);
  not not_103 (not_103_out, F13);
  not not_104 (not_104_out, F12);
  not not_105 (not_105_out, OP3);
  not not_106 (not_106_out, OP2);
  not not_107 (not_107_out, F14);
  not not_108 (not_108_out, F13);
  not not_109 (not_109_out, F12);
  not not_110 (not_110_out, OP4);
  not not_111 (not_111_out, OP3);
  not not_112 (not_112_out, OP2);
  not not_113 (not_113_out, F14);
  not not_114 (not_114_out, F13);
  not not_115 (not_115_out, OP4);
  not not_116 (not_116_out, OP3);
  not not_117 (not_117_out, OP2);
  not not_118 (not_118_out, F14);
  not not_119 (not_119_out, F13);
  not not_120 (not_120_out, F12);
  not not_121 (not_121_out, OP4);
  not not_122 (not_122_out, OP3);
  not not_123 (not_123_out, F12);
  not not_124 (not_124_out, OP3);
  not not_125 (not_125_out, OP2);
  not not_126 (not_126_out, OP3);
  not not_127 (not_127_out, OP2);
  not not_128 (not_128_out, F14);
  not not_129 (not_129_out, F13);
  not not_130 (not_130_out, F12);
  not not_131 (not_131_out, OP3);
  not not_132 (not_132_out, OP2);
  not not_133 (not_133_out, F30);
  not not_134 (not_134_out, F14);
  not not_135 (not_135_out, F13);
  not not_136 (not_136_out, F12);
  not not_137 (not_137_out, OP6);
  not not_138 (not_138_out, OP3);
  not not_139 (not_139_out, OP2);
  not not_140 (not_140_out, F30);
  not not_141 (not_141_out, OP6);
  not not_142 (not_142_out, OP3);
  not not_143 (not_143_out, OP2);
  not not_144 (not_144_out, F14);
  not not_145 (not_145_out, F13);
  not not_146 (not_146_out, F12);
  not not_147 (not_147_out, OP6);
  not not_148 (not_148_out, OP5);
  not not_149 (not_149_out, OP4);
  not not_150 (not_150_out, OP3);
  not not_151 (not_151_out, OP2);
  not not_152 (not_152_out, F12);
  not not_153 (not_153_out, OP4);
  not not_154 (not_154_out, OP3);
  not not_155 (not_155_out, OP2);
  not not_156 (not_156_out, F30);
  not not_157 (not_157_out, F25);
  not not_158 (not_158_out, F14);
  not not_159 (not_159_out, F13);
  not not_160 (not_160_out, F12);
  not not_161 (not_161_out, OP6);
  not not_162 (not_162_out, OP3);
  not not_163 (not_163_out, OP2);
  not not_164 (not_164_out, F25);
  not not_165 (not_165_out, F14);
  not not_166 (not_166_out, F13);
  not not_167 (not_167_out, F12);
  not not_168 (not_168_out, OP6);
  not not_169 (not_169_out, OP3);
  not not_170 (not_170_out, OP2);
  not not_171 (not_171_out, F30);
  not not_172 (not_172_out, F25);
  not not_173 (not_173_out, OP6);
  not not_174 (not_174_out, OP3);
  not not_175 (not_175_out, OP2);
  not not_176 (not_176_out, F30);
  not not_177 (not_177_out, F25);
  not not_178 (not_178_out, F12);
  not not_179 (not_179_out, OP6);
  not not_180 (not_180_out, OP3);
  not not_181 (not_181_out, OP2);
  not not_182 (not_182_out, F30);
  not not_183 (not_183_out, F25);
  not not_184 (not_184_out, F14);
  not not_185 (not_185_out, F12);
  not not_186 (not_186_out, OP6);
  not not_187 (not_187_out, OP3);
  not not_188 (not_188_out, OP2);
  not not_189 (not_189_out, F30);
  not not_190 (not_190_out, F25);
  not not_191 (not_191_out, F14);
  not not_192 (not_192_out, OP6);
  not not_193 (not_193_out, OP3);
  not not_194 (not_194_out, OP2);
  not not_195 (not_195_out, F14);
  not not_196 (not_196_out, F12);
  not not_197 (not_197_out, OP6);
  not not_198 (not_198_out, OP4);
  not not_199 (not_199_out, OP3);
  not not_200 (not_200_out, OP2);
  not not_201 (not_201_out, F14);
  not not_202 (not_202_out, F13);
  not not_203 (not_203_out, F12);
  not not_204 (not_204_out, OP3);
  not not_205 (not_205_out, OP2);
  not not_206 (not_206_out, F14);
  not not_207 (not_207_out, F13);
  not not_208 (not_208_out, F12);
  not not_209 (not_209_out, OP4);
  not not_210 (not_210_out, OP3);
  not not_211 (not_211_out, OP2);
  not not_212 (not_212_out, F14);
  not not_213 (not_213_out, F13);
  not not_214 (not_214_out, OP4);
  not not_215 (not_215_out, OP3);
  not not_216 (not_216_out, OP2);
  not not_217 (not_217_out, F14);
  not not_218 (not_218_out, F13);
  not not_219 (not_219_out, F12);
  not not_220 (not_220_out, OP3);
  not not_221 (not_221_out, OP2);
  not not_222 (not_222_out, F30);
  not not_223 (not_223_out, F14);
  not not_224 (not_224_out, F13);
  not not_225 (not_225_out, F12);
  not not_226 (not_226_out, OP6);
  not not_227 (not_227_out, OP3);
  not not_228 (not_228_out, OP2);
  not not_229 (not_229_out, F30);
  not not_230 (not_230_out, OP6);
  not not_231 (not_231_out, OP3);
  not not_232 (not_232_out, OP2);
  not not_233 (not_233_out, F12);
  not not_234 (not_234_out, OP4);
  not not_235 (not_235_out, OP3);
  not not_236 (not_236_out, OP2);
  and and_1 (and_1_out, not_1_out, not_2_out, not_3_out, not_4_out, not_5_out, not_6_out, OP5, OP4, not_7_out, not_8_out);
  and and_2 (and_2_out, F30, not_9_out, not_10_out, not_11_out, not_12_out, not_13_out, OP5, OP4, not_14_out, not_15_out);
  and and_3 (and_3_out, not_16_out, not_17_out, F14, F13, F12, not_18_out, OP5, OP4, not_19_out, not_20_out);
  and and_4 (and_4_out, not_21_out, not_22_out, F14, F13, not_23_out, not_24_out, OP5, OP4, not_25_out, not_26_out);
  and and_5 (and_5_out, not_27_out, not_28_out, not_29_out, F13, not_30_out, not_31_out, OP5, OP4, not_32_out, not_33_out);
  and and_6 (and_6_out, not_34_out, not_35_out, not_36_out, F13, F12, not_37_out, OP5, OP4, not_38_out, not_39_out);
  and and_7 (and_7_out, not_40_out, not_41_out, not_42_out, not_43_out, not_44_out, OP4, not_45_out, not_46_out);
  and and_8 (and_8_out, F14, F13, F12, not_47_out, not_48_out, OP4, not_49_out, not_50_out);
  and and_9 (and_9_out, F14, F13, not_51_out, not_52_out, not_53_out, OP4, not_54_out, not_55_out);
  and and_10 (and_10_out, F14, not_56_out, not_57_out, not_58_out, not_59_out, OP4, not_60_out, not_61_out);
  and and_11 (and_11_out, not_62_out, F13, not_63_out, not_64_out, not_65_out, OP4, not_66_out, not_67_out);
  and and_12 (and_12_out, not_68_out, not_69_out, not_70_out, not_71_out, F12, not_72_out, not_73_out, OP4, not_74_out, not_75_out);
  and and_13 (and_13_out, not_76_out, not_77_out, F14, not_78_out, F12, not_79_out, not_80_out, OP4, not_81_out, not_82_out);
  and and_14 (and_14_out, F30, not_83_out, F14, not_84_out, F12, not_85_out, not_86_out, OP4, not_87_out, not_88_out);
  and and_15 (and_15_out, not_89_out, F13, not_90_out, not_91_out, not_92_out, not_93_out, not_94_out, not_95_out);
  and and_16 (and_16_out, not_96_out, F13, not_97_out, not_98_out, OP5, not_99_out, not_100_out, not_101_out);
  and and_17 (and_17_out, not_102_out, not_103_out, not_104_out, OP6, OP5, OP4, not_105_out, not_106_out);
  and and_18 (and_18_out, not_107_out, not_108_out, not_109_out, OP6, OP5, not_110_out, not_111_out, not_112_out);
  and and_19 (and_19_out, not_113_out, not_114_out, F12, OP6, OP5, not_115_out, not_116_out, not_117_out);
  and and_20 (and_20_out, not_118_out, not_119_out, not_120_out, OP6, OP5, not_121_out, not_122_out, OP2);
  and and_21 (and_21_out, F14, F13, not_123_out, OP6, OP5, OP4, not_124_out, not_125_out);
  and and_22 (and_22_out, F14, F13, F12, OP6, OP5, OP4, not_126_out, not_127_out);
  and and_23 (and_23_out, not_128_out, not_129_out, not_130_out, OP6, OP5, OP4, not_131_out, not_132_out);
  and and_24 (and_24_out, not_133_out, F25, not_134_out, not_135_out, not_136_out, not_137_out, OP5, OP4, not_138_out, not_139_out);
  and and_25 (and_25_out, not_140_out, F25, F14, F13, F12, not_141_out, OP5, OP4, not_142_out, not_143_out);
  and and_26 (and_26_out, not_144_out, not_145_out, not_146_out, not_147_out, not_148_out, not_149_out, not_150_out, not_151_out);
  and and_27 (and_27_out, F14, F13, not_152_out, OP6, OP5, not_153_out, not_154_out, not_155_out);
  and and_28 (and_28_out, not_156_out, not_157_out, not_158_out, not_159_out, not_160_out, not_161_out, OP5, OP4, not_162_out, not_163_out);
  and and_29 (and_29_out, F30, not_164_out, not_165_out, not_166_out, not_167_out, not_168_out, OP5, OP4, not_169_out, not_170_out);
  and and_30 (and_30_out, not_171_out, not_172_out, F14, F13, F12, not_173_out, OP5, OP4, not_174_out, not_175_out);
  and and_31 (and_31_out, not_176_out, not_177_out, F14, F13, not_178_out, not_179_out, OP5, OP4, not_180_out, not_181_out);
  and and_32 (and_32_out, not_182_out, not_183_out, not_184_out, F13, not_185_out, not_186_out, OP5, OP4, not_187_out, not_188_out);
  and and_33 (and_33_out, not_189_out, not_190_out, not_191_out, F13, F12, not_192_out, OP5, OP4, not_193_out, not_194_out);
  and and_34 (and_34_out, not_195_out, F13, not_196_out, not_197_out, OP5, not_198_out, not_199_out, not_200_out);
  and and_35 (and_35_out, not_201_out, not_202_out, not_203_out, OP6, OP5, OP4, not_204_out, not_205_out);
  and and_36 (and_36_out, not_206_out, not_207_out, not_208_out, OP6, OP5, not_209_out, not_210_out, not_211_out);
  and and_37 (and_37_out, not_212_out, not_213_out, F12, OP6, OP5, not_214_out, not_215_out, not_216_out);
  and and_38 (and_38_out, not_217_out, not_218_out, not_219_out, OP6, OP5, OP4, not_220_out, not_221_out);
  and and_39 (and_39_out, not_222_out, F25, not_223_out, not_224_out, not_225_out, not_226_out, OP5, OP4, not_227_out, not_228_out);
  and and_40 (and_40_out, not_229_out, F25, F14, F13, F12, not_230_out, OP5, OP4, not_231_out, not_232_out);
  and and_41 (and_41_out, F14, F13, not_233_out, OP6, OP5, not_234_out, not_235_out, not_236_out);
  or or_1 (R2USed, and_28_out, and_29_out, and_30_out, and_31_out, and_32_out, and_33_out, and_34_out, and_35_out, and_36_out, and_37_out, and_38_out, and_39_out, and_40_out, and_41_out);
  or or_2 (R1Used, and_1_out, and_2_out, and_3_out, and_4_out, and_5_out, and_6_out, and_7_out, and_8_out, and_9_out, and_10_out, and_11_out, and_12_out, and_13_out, and_14_out, and_15_out, and_16_out, and_17_out, and_18_out, and_19_out, and_20_out, and_21_out, and_22_out, and_23_out, and_24_out, and_25_out, and_26_out, and_27_out);
endmodule

module Bubble (
  input  RWE,
  input  RWM,
  input  [4:0] R1,
  input  [4:0] EXW,
  input  [4:0] MEMW,
  input  [4:0] R2,
  input  [4:0] OP,
  input  [4:0] Funct,
  output hazzard
);

  wire and_1_out, and_2_out, and_3_out, and_4_out, comparator_1_eq, comparator_2_eq, comparator_3_eq,
       comparator_4_eq, comparator_5_eq, comparator_6_eq, comparator_7_eq, comparator_8_eq, not_1_out,
       not_2_out, not_3_out, not_4_out, regusecon_1_r1used, regusecon_1_r2used;

  not not_1 (not_1_out, comparator_1_eq);
  Comparator #(.width(5), .mode("twosComplement")) comparator_1 (
    .a(R1), .b({5{1'b0}}), .eq(comparator_1_eq));  // open: gt, lt
  Comparator #(.width(5), .mode("twosComplement")) comparator_2 (
    .a(R1), .b(EXW), .eq(comparator_2_eq));  // open: gt, lt
  Comparator #(.width(5), .mode("twosComplement")) comparator_3 (
    .a(R1), .b({5{1'b0}}), .eq(comparator_3_eq));  // open: gt, lt
  not not_2 (not_2_out, comparator_3_eq);
  Comparator #(.width(5), .mode("twosComplement")) comparator_4 (
    .a(R1), .b(MEMW), .eq(comparator_4_eq));  // open: gt, lt
  Comparator #(.width(5), .mode("twosComplement")) comparator_5 (
    .a(R2), .b({5{1'b0}}), .eq(comparator_5_eq));  // open: gt, lt
  not not_3 (not_3_out, comparator_5_eq);
  Comparator #(.width(5), .mode("twosComplement")) comparator_6 (
    .a(R2), .b(EXW), .eq(comparator_6_eq));  // open: gt, lt
  Comparator #(.width(5), .mode("twosComplement")) comparator_7 (
    .a(R2), .b({5{1'b0}}), .eq(comparator_7_eq));  // open: gt, lt
  not not_4 (not_4_out, comparator_7_eq);
  Comparator #(.width(5), .mode("twosComplement")) comparator_8 (
    .a(R2), .b(MEMW), .eq(comparator_8_eq));  // open: gt, lt
  RegUseCon regusecon_1 (
    .OP2(OP[0]), .OP3(OP[1]), .OP4(OP[2]), .OP5(OP[3]), .OP6(OP[4]), .F12(Funct[0]), .F13(Funct[1]),
    .F14(Funct[2]), .F25(Funct[3]), .F30(Funct[4]), .R1Used(regusecon_1_r1used), .R2USed(regusecon_1_r2used));
  and and_1 (and_1_out, not_1_out, RWE, regusecon_1_r1used, comparator_2_eq);
  and and_2 (and_2_out, not_2_out, RWM, regusecon_1_r1used, comparator_4_eq);
  and and_3 (and_3_out, not_3_out, RWE, regusecon_1_r2used, comparator_6_eq);
  and and_4 (and_4_out, not_4_out, RWM, regusecon_1_r2used, comparator_8_eq);
  or or_1 (hazzard, and_1_out, and_2_out, and_3_out, and_4_out);
endmodule

module Redirect (
  input  RWE,
  input  RWM,
  input  MemToReg,
  input  [4:0] R1,
  input  [4:0] R2,
  input  [4:0] EXW,
  input  [4:0] MEMW,
  input  [4:0] OP,
  input  [4:0] Funct,
  output [1:0] R1F,
  output [1:0] R2F,
  output Bubble,
  output LoadUse
);

  wire and_1_out, and_2_out, and_3_out, and_4_out, and_5_out, and_6_out, and_7_out, and_8_out,
       comparator_1_eq, comparator_2_eq, comparator_3_eq, comparator_4_eq, comparator_5_eq, comparator_6_eq,
       comparator_7_eq, comparator_8_eq, not_1_out, not_2_out, not_3_out, not_4_out, or_2_out, or_3_out,
       regusecon_1_r1used, regusecon_1_r2used;

  Comparator #(.width(5), .mode("twosComplement")) comparator_1 (
    .a(R1), .b({5{1'b0}}), .eq(comparator_1_eq));  // open: gt, lt
  not not_1 (not_1_out, comparator_1_eq);
  Comparator #(.width(5), .mode("twosComplement")) comparator_2 (
    .a(R1), .b(MEMW), .eq(comparator_2_eq));  // open: gt, lt
  not not_2 (not_2_out, comparator_3_eq);
  Comparator #(.width(5), .mode("twosComplement")) comparator_3 (
    .a(R1), .b({5{1'b0}}), .eq(comparator_3_eq));  // open: gt, lt
  Comparator #(.width(5), .mode("twosComplement")) comparator_4 (
    .a(R1), .b(EXW), .eq(comparator_4_eq));  // open: gt, lt
  not not_3 (not_3_out, comparator_5_eq);
  Comparator #(.width(5), .mode("twosComplement")) comparator_5 (
    .a(R2), .b({5{1'b0}}), .eq(comparator_5_eq));  // open: gt, lt
  Comparator #(.width(5), .mode("twosComplement")) comparator_6 (
    .a(R2), .b(MEMW), .eq(comparator_6_eq));  // open: gt, lt
  not not_4 (not_4_out, comparator_7_eq);
  Comparator #(.width(5), .mode("twosComplement")) comparator_7 (
    .a(R2), .b({5{1'b0}}), .eq(comparator_7_eq));  // open: gt, lt
  Comparator #(.width(5), .mode("twosComplement")) comparator_8 (
    .a(R2), .b(EXW), .eq(comparator_8_eq));  // open: gt, lt
  RegUseCon regusecon_1 (
    .OP2(OP[0]), .OP3(OP[1]), .OP4(OP[2]), .OP5(OP[3]), .OP6(OP[4]), .F12(Funct[0]), .F13(Funct[1]),
    .F14(Funct[2]), .F25(Funct[3]), .F30(Funct[4]), .R1Used(regusecon_1_r1used), .R2USed(regusecon_1_r2used));
  and and_1 (and_1_out, not_1_out, RWM, regusecon_1_r1used, comparator_2_eq);
  and and_2 (and_2_out, not_2_out, RWE, regusecon_1_r1used, comparator_4_eq);
  and and_3 (and_3_out, not_3_out, RWM, regusecon_1_r2used, comparator_6_eq);
  and and_4 (and_4_out, not_4_out, RWE, regusecon_1_r2used, comparator_8_eq);
  and and_5 (and_5_out, not_2_out, comparator_4_eq, MemToReg, regusecon_1_r1used);
  and and_6 (and_6_out, not_4_out, comparator_8_eq, MemToReg, regusecon_1_r2used);
  or or_1 (LoadUse, and_5_out, and_6_out);
  Priority_Encoder #(.select(2), .disabled("Z")) priority_encoder_1 (
    .in0(1'b1), .in1(and_1_out), .in2(and_2_out), .out(R1F));  // open: in3, gs, en_out, en_in
  Priority_Encoder #(.select(2), .disabled("Z")) priority_encoder_2 (
    .in0(1'b1), .in1(and_3_out), .in2(and_4_out), .out(R2F));  // open: in3, gs, en_out, en_in
  or or_2 (or_2_out, and_1_out, and_2_out);
  or or_3 (or_3_out, and_3_out, and_4_out);
  and and_7 (and_7_out, or_2_out, regusecon_1_r1used);
  or or_4 (Bubble, and_7_out, and_8_out);
  and and_8 (and_8_out, or_3_out, regusecon_1_r2used);
endmodule

module \Max3_归并比较  (
  input  [15:0] Y,
  input  [15:0] X,
  input  [2:0] Y_num,
  input  [2:0] X_num,
  output [15:0] MAX,
  output [2:0] Max_num
);

  wire comparator_1_eq, comparator_1_gt, or_1_out;

  Multiplexer #(.select(1), .width(16), .disabled("Z"), .enable("false")) multiplexer_1 (
    .in0(Y), .in1(X), .out(MAX), .sel(or_1_out));
  Comparator #(.width(16), .mode("unsigned")) comparator_1 (
    .a(X), .b(Y), .gt(comparator_1_gt), .eq(comparator_1_eq));  // open: lt
  or or_1 (or_1_out, comparator_1_gt, comparator_1_eq);
  Multiplexer #(.select(1), .width(3), .disabled("Z"), .enable("false")) multiplexer_2 (
    .in0(Y_num), .in1(X_num), .out(Max_num), .sel(or_1_out));

  // Notes on the sheet:
  //   输出两个输入中的较大值，并输出较大值的3位编号
endmodule

module BTB (
  input  CLK,
  input  EX_Branch,
  input  [31:0] PC,
  input  [31:0] EX_PC,
  input  [31:0] EX_BranchAddr,
  input  EX_Branched,
  output [31:0] JumpAddr,
  output PJ
);

  wire A0, A1, A2, A3, A4, A5, A6, A7, and_17_out, comparator_1_eq, comparator_2_eq, comparator_3_eq,
       comparator_4_eq, comparator_5_eq, comparator_6_eq, comparator_7_eq, comparator_8_eq, comparator_9_eq,
       comparator_10_eq, comparator_11_eq, comparator_12_eq, comparator_13_eq, comparator_14_eq,
       comparator_15_eq, comparator_16_eq, decoder_1_out0, decoder_1_out1, decoder_1_out2, decoder_1_out3,
       decoder_1_out4, decoder_1_out5, decoder_1_out6, decoder_1_out7, decoder_2_out0, decoder_2_out1,
       decoder_2_out2, decoder_2_out3, decoder_2_out4, decoder_2_out5, decoder_2_out6, decoder_2_out7,
       EX_Hit, EX_Miss, IF_Hit, IF_Miss, L0, L1, L2, L3, L4, L5, L6, L7, M0, M1, M2, M3, M4, M5, M6, M7,
       not_3_out, not_4_out, not_5_out, not_6_out, not_7_out, not_8_out, not_9_out, not_10_out, or_3_out,
       or_4_out, or_5_out, or_6_out, or_7_out, or_8_out, or_9_out, or_10_out, or_11_out, or_12_out,
       or_13_out, or_14_out, or_15_out, or_16_out, or_17_out, or_18_out, priority_encoder_1_gs, V0, V1, V2,
       V3, V4, V5, V6, V7, W0, W1, W2, W3, W4, W5, W6, W7;
  wire [0:0] controlled_buffer_1_out, controlled_buffer_2_out, controlled_buffer_3_out,
       controlled_buffer_4_out, controlled_buffer_5_out, controlled_buffer_6_out, controlled_buffer_7_out,
       controlled_buffer_8_out;
  wire [1:0] adder_1_out, adder_2_out, adder_3_out, adder_4_out, adder_5_out, adder_6_out, adder_7_out,
       adder_8_out, multiplexer_1_out, multiplexer_2_out, multiplexer_3_out, multiplexer_4_out,
       multiplexer_5_out, multiplexer_6_out, multiplexer_7_out, multiplexer_8_out, multiplexer_9_out,
       multiplexer_10_out, multiplexer_11_out, multiplexer_12_out, multiplexer_13_out, multiplexer_14_out,
       multiplexer_15_out, multiplexer_16_out, multiplexer_17_out, multiplexer_18_out, multiplexer_19_out,
       multiplexer_20_out, multiplexer_21_out, multiplexer_22_out, multiplexer_23_out, multiplexer_24_out,
       multiplexer_25_out, multiplexer_26_out, multiplexer_27_out, multiplexer_28_out, multiplexer_29_out,
       multiplexer_30_out, multiplexer_31_out, multiplexer_32_out, multiplexer_33_out, multiplexer_34_out,
       multiplexer_35_out, multiplexer_36_out, multiplexer_37_out, multiplexer_38_out, multiplexer_39_out,
       multiplexer_40_out, Predict0, Predict1, Predict2, Predict3, Predict4, Predict5, Predict6, Predict7;
  wire [2:0] \max3_归并比较_1_max_num , \max3_归并比较_2_max_num , \max3_归并比较_3_max_num , \max3_归并比较_4_max_num ,
       \max3_归并比较_5_max_num , \max3_归并比较_6_max_num , \max3_归并比较_7_max_num , priority_encoder_1_out;
  wire [15:0] C0, C1, C2, C3, C4, C5, C6, C7, \max3_归并比较_1_max , \max3_归并比较_2_max , \max3_归并比较_3_max ,
       \max3_归并比较_4_max , \max3_归并比较_5_max , \max3_归并比较_7_max ;
  wire [31:0] Tag0, Tag1, Tag2, Tag3, Tag4, Tag5, Tag6, Tag7, \分支目标地址_2_q , \分支目标地址_3_q , \分支目标地址_4_q ,
       \分支目标地址_5_q , \分支目标地址_6_q , \分支目标地址_7_q , \分支目标地址_8_q , \分支目标地址_q ;

  Pull_Resistor #(.pull(0)) pull_resistor_1 (.node(PJ));
  assign {PJ, controlled_buffer_1_out[0]} = L0 ? Predict0 : 2'bz;  // Controlled_Buffer controlled_buffer_1
  assign {PJ, controlled_buffer_2_out[0]} = L1 ? Predict1 : 2'bz;  // Controlled_Buffer controlled_buffer_2
  assign {PJ, controlled_buffer_3_out[0]} = L2 ? Predict2 : 2'bz;  // Controlled_Buffer controlled_buffer_3
  assign {PJ, controlled_buffer_4_out[0]} = L3 ? Predict3 : 2'bz;  // Controlled_Buffer controlled_buffer_4
  assign {PJ, controlled_buffer_5_out[0]} = L4 ? Predict4 : 2'bz;  // Controlled_Buffer controlled_buffer_5
  assign {PJ, controlled_buffer_6_out[0]} = L5 ? Predict5 : 2'bz;  // Controlled_Buffer controlled_buffer_6
  assign {PJ, controlled_buffer_7_out[0]} = L6 ? Predict6 : 2'bz;  // Controlled_Buffer controlled_buffer_7
  assign {PJ, controlled_buffer_8_out[0]} = L7 ? Predict7 : 2'bz;  // Controlled_Buffer controlled_buffer_8
  Multiplexer #(.select(1), .width(2), .disabled("Z"), .enable("false")) multiplexer_1 (
    .in0(2'b00), .in1(2'b01), .out(multiplexer_1_out), .sel(EX_Branched));
  Multiplexer #(.select(1), .width(2), .disabled("Z"), .enable("false")) multiplexer_2 (
    .in0(2'b11), .in1(2'b01), .out(multiplexer_2_out), .sel(EX_Branched));
  Multiplexer #(.select(1), .width(2), .disabled("Z"), .enable("false")) multiplexer_3 (
    .in0(2'b01), .in1(2'b00), .out(multiplexer_3_out), .sel(EX_Branched));
  Multiplexer #(.select(1), .width(2), .disabled("Z"), .enable("false")) multiplexer_4 (
    .in0(2'b01), .in1(2'b11), .out(multiplexer_4_out), .sel(EX_Branched));
  Multiplexer #(.select(1), .width(2), .disabled("Z"), .enable("false")) multiplexer_5 (
    .in0(2'b00), .in1(2'b01), .out(multiplexer_5_out), .sel(EX_Branched));
  Multiplexer #(.select(1), .width(2), .disabled("Z"), .enable("false")) multiplexer_6 (
    .in0(2'b11), .in1(2'b01), .out(multiplexer_6_out), .sel(EX_Branched));
  Multiplexer #(.select(1), .width(2), .disabled("Z"), .enable("false")) multiplexer_7 (
    .in0(2'b01), .in1(2'b00), .out(multiplexer_7_out), .sel(EX_Branched));
  Multiplexer #(.select(1), .width(2), .disabled("Z"), .enable("false")) multiplexer_8 (
    .in0(2'b01), .in1(2'b11), .out(multiplexer_8_out), .sel(EX_Branched));
  Multiplexer #(.select(1), .width(2), .disabled("Z"), .enable("false")) multiplexer_9 (
    .in0(2'b00), .in1(2'b01), .out(multiplexer_9_out), .sel(EX_Branched));
  Multiplexer #(.select(1), .width(2), .disabled("Z"), .enable("false")) multiplexer_10 (
    .in0(2'b11), .in1(2'b01), .out(multiplexer_10_out), .sel(EX_Branched));
  Multiplexer #(.select(1), .width(2), .disabled("Z"), .enable("false")) multiplexer_11 (
    .in0(2'b01), .in1(2'b00), .out(multiplexer_11_out), .sel(EX_Branched));
  Multiplexer #(.select(1), .width(2), .disabled("Z"), .enable("false")) multiplexer_12 (
    .in0(2'b01), .in1(2'b11), .out(multiplexer_12_out), .sel(EX_Branched));
  Multiplexer #(.select(1), .width(2), .disabled("Z"), .enable("false")) multiplexer_13 (
    .in0(2'b00), .in1(2'b01), .out(multiplexer_13_out), .sel(EX_Branched));
  Multiplexer #(.select(1), .width(2), .disabled("Z"), .enable("false")) multiplexer_14 (
    .in0(2'b11), .in1(2'b01), .out(multiplexer_14_out), .sel(EX_Branched));
  Multiplexer #(.select(1), .width(2), .disabled("Z"), .enable("false")) multiplexer_15 (
    .in0(2'b01), .in1(2'b00), .out(multiplexer_15_out), .sel(EX_Branched));
  Multiplexer #(.select(1), .width(2), .disabled("Z"), .enable("false")) multiplexer_16 (
    .in0(2'b01), .in1(2'b11), .out(multiplexer_16_out), .sel(EX_Branched));
  Multiplexer #(.select(1), .width(2), .disabled("Z"), .enable("false")) multiplexer_17 (
    .in0(2'b00), .in1(2'b01), .out(multiplexer_17_out), .sel(EX_Branched));
  Multiplexer #(.select(1), .width(2), .disabled("Z"), .enable("false")) multiplexer_18 (
    .in0(2'b11), .in1(2'b01), .out(multiplexer_18_out), .sel(EX_Branched));
  Multiplexer #(.select(1), .width(2), .disabled("Z"), .enable("false")) multiplexer_19 (
    .in0(2'b01), .in1(2'b00), .out(multiplexer_19_out), .sel(EX_Branched));
  Multiplexer #(.select(1), .width(2), .disabled("Z"), .enable("false")) multiplexer_20 (
    .in0(2'b01), .in1(2'b11), .out(multiplexer_20_out), .sel(EX_Branched));
  Multiplexer #(.select(1), .width(2), .disabled("Z"), .enable("false")) multiplexer_21 (
    .in0(2'b00), .in1(2'b01), .out(multiplexer_21_out), .sel(EX_Branched));
  Multiplexer #(.select(1), .width(2), .disabled("Z"), .enable("false")) multiplexer_22 (
    .in0(2'b11), .in1(2'b01), .out(multiplexer_22_out), .sel(EX_Branched));
  Multiplexer #(.select(1), .width(2), .disabled("Z"), .enable("false")) multiplexer_23 (
    .in0(2'b01), .in1(2'b00), .out(multiplexer_23_out), .sel(EX_Branched));
  Multiplexer #(.select(1), .width(2), .disabled("Z"), .enable("false")) multiplexer_24 (
    .in0(2'b01), .in1(2'b11), .out(multiplexer_24_out), .sel(EX_Branched));
  Multiplexer #(.select(1), .width(2), .disabled("Z"), .enable("false")) multiplexer_25 (
    .in0(2'b00), .in1(2'b01), .out(multiplexer_25_out), .sel(EX_Branched));
  Multiplexer #(.select(1), .width(2), .disabled("Z"), .enable("false")) multiplexer_26 (
    .in0(2'b11), .in1(2'b01), .out(multiplexer_26_out), .sel(EX_Branched));
  Multiplexer #(.select(1), .width(2), .disabled("Z"), .enable("false")) multiplexer_27 (
    .in0(2'b01), .in1(2'b00), .out(multiplexer_27_out), .sel(EX_Branched));
  Multiplexer #(.select(1), .width(2), .disabled("Z"), .enable("false")) multiplexer_28 (
    .in0(2'b01), .in1(2'b11), .out(multiplexer_28_out), .sel(EX_Branched));
  Multiplexer #(.select(1), .width(2), .disabled("Z"), .enable("false")) multiplexer_29 (
    .in0(2'b00), .in1(2'b01), .out(multiplexer_29_out), .sel(EX_Branched));
  Multiplexer #(.select(1), .width(2), .disabled("Z"), .enable("false")) multiplexer_30 (
    .in0(2'b11), .in1(2'b01), .out(multiplexer_30_out), .sel(EX_Branched));
  Multiplexer #(.select(1), .width(2), .disabled("Z"), .enable("false")) multiplexer_31 (
    .in0(2'b01), .in1(2'b00), .out(multiplexer_31_out), .sel(EX_Branched));
  Multiplexer #(.select(1), .width(2), .disabled("Z"), .enable("false")) multiplexer_32 (
    .in0(2'b01), .in1(2'b11), .out(multiplexer_32_out), .sel(EX_Branched));
  Multiplexer #(.select(2), .width(2), .disabled("Z"), .enable("false")) multiplexer_33 (
    .in0(multiplexer_1_out), .in1(multiplexer_2_out), .in2(multiplexer_3_out), .in3(multiplexer_4_out),
    .out(multiplexer_33_out), .sel(Predict0));
  Adder #(.width(2)) adder_1 (.a(multiplexer_33_out), .b(Predict0), .out(adder_1_out));  // open: cin, cout
  Multiplexer #(.select(2), .width(2), .disabled("Z"), .enable("false")) multiplexer_34 (
    .in0(multiplexer_5_out), .in1(multiplexer_6_out), .in2(multiplexer_7_out), .in3(multiplexer_8_out),
    .out(multiplexer_34_out), .sel(Predict1));
  Adder #(.width(2)) adder_2 (.a(multiplexer_34_out), .b(Predict1), .out(adder_2_out));  // open: cin, cout
  Multiplexer #(.select(2), .width(2), .disabled("Z"), .enable("false")) multiplexer_35 (
    .in0(multiplexer_9_out), .in1(multiplexer_10_out), .in2(multiplexer_11_out), .in3(multiplexer_12_out),
    .out(multiplexer_35_out), .sel(Predict2));
  Adder #(.width(2)) adder_3 (.a(multiplexer_35_out), .b(Predict2), .out(adder_3_out));  // open: cin, cout
  Multiplexer #(.select(2), .width(2), .disabled("Z"), .enable("false")) multiplexer_36 (
    .in0(multiplexer_13_out), .in1(multiplexer_14_out), .in2(multiplexer_15_out), .in3(multiplexer_16_out),
    .out(multiplexer_36_out), .sel(Predict3));
  Adder #(.width(2)) adder_4 (.a(multiplexer_36_out), .b(Predict3), .out(adder_4_out));  // open: cin, cout
  Multiplexer #(.select(2), .width(2), .disabled("Z"), .enable("false")) multiplexer_37 (
    .in0(multiplexer_17_out), .in1(multiplexer_18_out), .in2(multiplexer_19_out), .in3(multiplexer_20_out),
    .out(multiplexer_37_out), .sel(Predict4));
  Adder #(.width(2)) adder_5 (.a(multiplexer_37_out), .b(Predict4), .out(adder_5_out));  // open: cin, cout
  Multiplexer #(.select(2), .width(2), .disabled("Z"), .enable("false")) multiplexer_38 (
    .in0(multiplexer_21_out), .in1(multiplexer_22_out), .in2(multiplexer_23_out), .in3(multiplexer_24_out),
    .out(multiplexer_38_out), .sel(Predict5));
  Adder #(.width(2)) adder_6 (.a(multiplexer_38_out), .b(Predict5), .out(adder_6_out));  // open: cin, cout
  Multiplexer #(.select(2), .width(2), .disabled("Z"), .enable("false")) multiplexer_39 (
    .in0(multiplexer_25_out), .in1(multiplexer_26_out), .in2(multiplexer_27_out), .in3(multiplexer_28_out),
    .out(multiplexer_39_out), .sel(Predict6));
  Adder #(.width(2)) adder_7 (.a(multiplexer_39_out), .b(Predict6), .out(adder_7_out));  // open: cin, cout
  Multiplexer #(.select(2), .width(2), .disabled("Z"), .enable("false")) multiplexer_40 (
    .in0(multiplexer_29_out), .in1(multiplexer_30_out), .in2(multiplexer_31_out), .in3(multiplexer_32_out),
    .out(multiplexer_40_out), .sel(Predict7));
  Adder #(.width(2)) adder_8 (.a(multiplexer_40_out), .b(Predict7), .out(adder_8_out));  // open: cin, cout
  Register #(.width(2), .trigger("rising"), .Select("low")) register_1 (
    .D(adder_1_out), .en(M0), .Q(Predict0), .clk(CLK));  // open: clr
  Register #(.width(2), .trigger("rising"), .Select("low")) register_2 (
    .D(adder_2_out), .en(M1), .Q(Predict1), .clk(CLK));  // open: clr
  Register #(.width(2), .trigger("rising"), .Select("low")) register_3 (
    .D(adder_3_out), .en(M2), .Q(Predict2), .clk(CLK));  // open: clr
  Register #(.width(2), .trigger("rising"), .Select("low")) register_4 (
    .D(adder_4_out), .en(M3), .Q(Predict3), .clk(CLK));  // open: clr
  Register #(.width(2), .trigger("rising"), .Select("low")) register_5 (
    .D(adder_5_out), .en(M4), .Q(Predict4), .clk(CLK));  // open: clr
  Register #(.width(2), .trigger("rising"), .Select("low")) register_6 (
    .D(adder_6_out), .en(M5), .Q(Predict5), .clk(CLK));  // open: clr
  Register #(.width(2), .trigger("rising"), .Select("low")) register_7 (
    .D(adder_7_out), .en(M6), .Q(Predict6), .clk(CLK));  // open: clr
  Register #(.width(2), .trigger("rising"), .Select("low")) register_8 (
    .D(adder_8_out), .en(M7), .Q(Predict7), .clk(CLK));  // open: clr
  Comparator #(.width(32), .mode("twosComplement")) comparator_1 (
    .a(PC), .b(Tag0), .eq(comparator_1_eq));  // open: gt, lt
  Comparator #(.width(32), .mode("twosComplement")) comparator_2 (
    .a(PC), .b(Tag1), .eq(comparator_2_eq));  // open: gt, lt
  Comparator #(.width(32), .mode("twosComplement")) comparator_3 (
    .a(PC), .b(Tag2), .eq(comparator_3_eq));  // open: gt, lt
  Comparator #(.width(32), .mode("twosComplement")) comparator_4 (
    .a(PC), .b(Tag3), .eq(comparator_4_eq));  // open: gt, lt
  Comparator #(.width(32), .mode("twosComplement")) comparator_5 (
    .a(PC), .b(Tag4), .eq(comparator_5_eq));  // open: gt, lt
  Comparator #(.width(32), .mode("twosComplement")) comparator_6 (
    .a(PC), .b(Tag5), .eq(comparator_6_eq));  // open: gt, lt
  Comparator #(.width(32), .mode("twosComplement")) comparator_7 (
    .a(PC), .b(Tag6), .eq(comparator_7_eq));  // open: gt, lt
  Comparator #(.width(32), .mode("twosComplement")) comparator_8 (
    .a(PC), .b(Tag7), .eq(comparator_8_eq));  // open: gt, lt
  and and_1 (L0, comparator_1_eq, V0);
  and and_2 (L1, comparator_2_eq, V1);
  and and_3 (L2, comparator_3_eq, V2);
  and and_4 (L3, comparator_4_eq, V3);
  and and_5 (L4, comparator_5_eq, V4);
  and and_6 (L5, comparator_6_eq, V5);
  and and_7 (L6, comparator_7_eq, V6);
  and and_8 (L7, comparator_8_eq, V7);
  Register #(.width(1), .trigger("rising"), .Select("low")) VALID (.D(1'b1), .en(W0), .Q(V0), .clk(CLK));  // open: clr
  Register #(.width(1), .trigger("rising"), .Select("low")) VALID_2 (
    .D(1'b1), .en(W1), .Q(V1), .clk(CLK));  // open: clr
  Register #(.width(1), .trigger("rising"), .Select("low")) VALID_3 (
    .D(1'b1), .en(W2), .Q(V2), .clk(CLK));  // open: clr
  Register #(.width(1), .trigger("rising"), .Select("low")) VALID_4 (
    .D(1'b1), .en(W3), .Q(V3), .clk(CLK));  // open: clr
  Register #(.width(1), .trigger("rising"), .Select("low")) VALID_5 (
    .D(1'b1), .en(W4), .Q(V4), .clk(CLK));  // open: clr
  Register #(.width(1), .trigger("rising"), .Select("low")) VALID_6 (
    .D(1'b1), .en(W5), .Q(V5), .clk(CLK));  // open: clr
  Register #(.width(1), .trigger("rising"), .Select("low")) VALID_7 (
    .D(1'b1), .en(W6), .Q(V6), .clk(CLK));  // open: clr
  Register #(.width(1), .trigger("rising"), .Select("low")) VALID_8 (
    .D(1'b1), .en(W7), .Q(V7), .clk(CLK));  // open: clr
  or or_1 (IF_Hit, L0, L1, L2, L3, L4, L5, L6, L7);
  Register #(.width(32), .trigger("rising"), .Select("low")) \u_分支指令地址  (
    .D(EX_PC), .en(W0), .Q(Tag0), .clk(CLK));  // open: clr
  Register #(.width(32), .trigger("rising"), .Select("low")) \u_分支指令地址_2  (
    .D(EX_PC), .en(W1), .Q(Tag1), .clk(CLK));  // open: clr
  Register #(.width(32), .trigger("rising"), .Select("low")) \u_分支指令地址_3  (
    .D(EX_PC), .en(W2), .Q(Tag2), .clk(CLK));  // open: clr
  Register #(.width(32), .trigger("rising"), .Select("low")) \u_分支指令地址_4  (
    .D(EX_PC), .en(W3), .Q(Tag3), .clk(CLK));  // open: clr
  Register #(.width(32), .trigger("rising"), .Select("low")) \u_分支指令地址_5  (
    .D(EX_PC), .en(W4), .Q(Tag4), .clk(CLK));  // open: clr
  Register #(.width(32), .trigger("rising"), .Select("low")) \u_分支指令地址_6  (
    .D(EX_PC), .en(W5), .Q(Tag5), .clk(CLK));  // open: clr
  Register #(.width(32), .trigger("rising"), .Select("low")) \u_分支指令地址_7  (
    .D(EX_PC), .en(W6), .Q(Tag6), .clk(CLK));  // open: clr
  Register #(.width(32), .trigger("rising"), .Select("low")) \u_分支指令地址_8  (
    .D(EX_PC), .en(W7), .Q(Tag7), .clk(CLK));  // open: clr
  not not_1 (IF_Miss, IF_Hit);
  Counter #(.width(16), .max('hffff), .ongoal("wrap"), .trigger("rising"), .behavior("old")) \u_置换标记  (
    .count(A0), .Q(C0), .clk(CLK), .clr(L0));  // open: load, D, carry, preset
  Counter #(.width(16), .max('hffff), .ongoal("wrap"), .trigger("rising"), .behavior("old")) \u_置换标记_2  (
    .count(A1), .Q(C1), .clk(CLK), .clr(L1));  // open: load, D, carry, preset
  Counter #(.width(16), .max('hffff), .ongoal("wrap"), .trigger("rising"), .behavior("old")) \u_置换标记_3  (
    .count(A2), .Q(C2), .clk(CLK), .clr(L2));  // open: load, D, carry, preset
  Counter #(.width(16), .max('hffff), .ongoal("wrap"), .trigger("rising"), .behavior("old")) \u_置换标记_4  (
    .count(A3), .Q(C3), .clk(CLK), .clr(L3));  // open: load, D, carry, preset
  Counter #(.width(16), .max('hffff), .ongoal("wrap"), .trigger("rising"), .behavior("old")) \u_置换标记_5  (
    .count(A4), .Q(C4), .clk(CLK), .clr(L4));  // open: load, D, carry, preset
  Counter #(.width(16), .max('hffff), .ongoal("wrap"), .trigger("rising"), .behavior("old")) \u_置换标记_6  (
    .count(A5), .Q(C5), .clk(CLK), .clr(L5));  // open: load, D, carry, preset
  Counter #(.width(16), .max('hffff), .ongoal("wrap"), .trigger("rising"), .behavior("old")) \u_置换标记_7  (
    .count(A6), .Q(C6), .clk(CLK), .clr(L6));  // open: load, D, carry, preset
  Counter #(.width(16), .max('hffff), .ongoal("wrap"), .trigger("rising"), .behavior("old")) \u_置换标记_8  (
    .count(A7), .Q(C7), .clk(CLK), .clr(L7));  // open: load, D, carry, preset
  Comparator #(.width(32), .mode("twosComplement")) comparator_9 (
    .a(EX_PC), .b(Tag0), .eq(comparator_9_eq));  // open: gt, lt
  Comparator #(.width(32), .mode("twosComplement")) comparator_10 (
    .a(EX_PC), .b(Tag1), .eq(comparator_10_eq));  // open: gt, lt
  Comparator #(.width(32), .mode("twosComplement")) comparator_11 (
    .a(EX_PC), .b(Tag2), .eq(comparator_11_eq));  // open: gt, lt
  Comparator #(.width(32), .mode("twosComplement")) comparator_12 (
    .a(EX_PC), .b(Tag3), .eq(comparator_12_eq));  // open: gt, lt
  Comparator #(.width(32), .mode("twosComplement")) comparator_13 (
    .a(EX_PC), .b(Tag4), .eq(comparator_13_eq));  // open: gt, lt
  Comparator #(.width(32), .mode("twosComplement")) comparator_14 (
    .a(EX_PC), .b(Tag5), .eq(comparator_14_eq));  // open: gt, lt
  Comparator #(.width(32), .mode("twosComplement")) comparator_15 (
    .a(EX_PC), .b(Tag6), .eq(comparator_15_eq));  // open: gt, lt
  Comparator #(.width(32), .mode("twosComplement")) comparator_16 (
    .a(EX_PC), .b(Tag7), .eq(comparator_16_eq));  // open: gt, lt
  and and_9 (M0, comparator_9_eq, V0);
  and and_10 (M1, comparator_10_eq, V1);
  and and_11 (M2, comparator_11_eq, V2);
  and and_12 (M3, comparator_12_eq, V3);
  and and_13 (M4, comparator_13_eq, V4);
  and and_14 (M5, comparator_14_eq, V5);
  and and_15 (M6, comparator_15_eq, V6);
  and and_16 (M7, comparator_16_eq, V7);
  assign JumpAddr = L0 ? \分支目标地址_q  : 32'bz;  // Controlled_Buffer controlled_buffer_9
  Register #(.width(32), .trigger("rising"), .Select("low")) \u_分支目标地址  (
    .D(EX_BranchAddr), .en(W0), .Q(\分支目标地址_q ), .clk(CLK));  // open: clr
  Register #(.width(32), .trigger("rising"), .Select("low")) \u_分支目标地址_2  (
    .D(EX_BranchAddr), .en(W1), .Q(\分支目标地址_2_q ), .clk(CLK));  // open: clr
  assign JumpAddr = L1 ? \分支目标地址_2_q  : 32'bz;  // Controlled_Buffer controlled_buffer_10
  assign JumpAddr = L2 ? \分支目标地址_3_q  : 32'bz;  // Controlled_Buffer controlled_buffer_11
  Register #(.width(32), .trigger("rising"), .Select("low")) \u_分支目标地址_3  (
    .D(EX_BranchAddr), .en(W2), .Q(\分支目标地址_3_q ), .clk(CLK));  // open: clr
  assign JumpAddr = L3 ? \分支目标地址_4_q  : 32'bz;  // Controlled_Buffer controlled_buffer_12
  Register #(.width(32), .trigger("rising"), .Select("low")) \u_分支目标地址_4  (
    .D(EX_BranchAddr), .en(W3), .Q(\分支目标地址_4_q ), .clk(CLK));  // open: clr
  assign JumpAddr = L4 ? \分支目标地址_5_q  : 32'bz;  // Controlled_Buffer controlled_buffer_13
  Register #(.width(32), .trigger("rising"), .Select("low")) \u_分支目标地址_5  (
    .D(EX_BranchAddr), .en(W4), .Q(\分支目标地址_5_q ), .clk(CLK));  // open: clr
  Register #(.width(32), .trigger("rising"), .Select("low")) \u_分支目标地址_6  (
    .D(EX_BranchAddr), .en(W5), .Q(\分支目标地址_6_q ), .clk(CLK));  // open: clr
  assign JumpAddr = L5 ? \分支目标地址_6_q  : 32'bz;  // Controlled_Buffer controlled_buffer_14
  assign JumpAddr = L6 ? \分支目标地址_7_q  : 32'bz;  // Controlled_Buffer controlled_buffer_15
  Register #(.width(32), .trigger("rising"), .Select("low")) \u_分支目标地址_7  (
    .D(EX_BranchAddr), .en(W6), .Q(\分支目标地址_7_q ), .clk(CLK));  // open: clr
  Register #(.width(32), .trigger("rising"), .Select("low")) \u_分支目标地址_8  (
    .D(EX_BranchAddr), .en(W7), .Q(\分支目标地址_8_q ), .clk(CLK));  // open: clr
  assign JumpAddr = L7 ? \分支目标地址_8_q  : 32'bz;  // Controlled_Buffer controlled_buffer_16
  or or_2 (EX_Hit, M0, M1, M2, M3, M4, M5, M6, M7);
  not not_2 (EX_Miss, EX_Hit);
  not not_3 (not_3_out, V0);
  not not_4 (not_4_out, V1);
  not not_5 (not_5_out, V2);
  not not_6 (not_6_out, V3);
  not not_7 (not_7_out, V4);
  not not_8 (not_8_out, V5);
  not not_9 (not_9_out, V6);
  not not_10 (not_10_out, V7);
  \Max3_归并比较  \max3_归并比较_1  (
    .Y(C1), .X(C0), .Y_num(3'b001), .X_num(3'b000), .MAX(\max3_归并比较_1_max ), .Max_num(\max3_归并比较_1_max_num ));
  \Max3_归并比较  \max3_归并比较_2  (
    .Y(C3), .X(C2), .Y_num(3'b011), .X_num(3'b010), .MAX(\max3_归并比较_2_max ), .Max_num(\max3_归并比较_2_max_num ));
  \Max3_归并比较  \max3_归并比较_3  (
    .Y(C5), .X(C4), .Y_num(3'b101), .X_num(3'b100), .MAX(\max3_归并比较_3_max ), .Max_num(\max3_归并比较_3_max_num ));
  \Max3_归并比较  \max3_归并比较_4  (
    .Y(C7), .X(C6), .Y_num(3'b111), .X_num(3'b110), .MAX(\max3_归并比较_4_max ), .Max_num(\max3_归并比较_4_max_num ));
  Priority_Encoder #(.select(3), .disabled("Z")) priority_encoder_1 (
    .in0(not_3_out), .in1(not_4_out), .in2(not_5_out), .in3(not_6_out), .in4(not_7_out), .in5(not_8_out),
    .in6(not_9_out), .in7(not_10_out), .out(priority_encoder_1_out), .gs(priority_encoder_1_gs));  // open: en_out, en_in
  \Max3_归并比较  \max3_归并比较_5  (
    .Y(\max3_归并比较_2_max ), .X(\max3_归并比较_1_max ), .Y_num(\max3_归并比较_2_max_num ),
    .X_num(\max3_归并比较_1_max_num ), .MAX(\max3_归并比较_5_max ), .Max_num(\max3_归并比较_5_max_num ));
  \Max3_归并比较  \max3_归并比较_6  (
    .Y(\max3_归并比较_7_max ), .X(\max3_归并比较_5_max ), .Y_num(\max3_归并比较_7_max_num ),
    .X_num(\max3_归并比较_5_max_num ), .Max_num(\max3_归并比较_6_max_num ));  // open: MAX
  \Max3_归并比较  \max3_归并比较_7  (
    .Y(\max3_归并比较_4_max ), .X(\max3_归并比较_3_max ), .Y_num(\max3_归并比较_4_max_num ),
    .X_num(\max3_归并比较_3_max_num ), .MAX(\max3_归并比较_7_max ), .Max_num(\max3_归并比较_7_max_num ));
  and and_17 (and_17_out, V0, V1, V2, V3, V4, V5, V6, V7);
  or or_3 (or_3_out, L1, L2, L3, L4, L5, L6, L7, W1, W2, W3, W4, W5, W6, W7);
  or or_4 (or_4_out, L0, L2, L3, L4, L5, L6, L7, W0, W2, W3, W4, W5, W6, W7);
  or or_5 (or_5_out, L0, L1, L3, L4, L5, L6, L7, W0, W1, W3, W4, W5, W6, W7);
  or or_6 (or_6_out, L0, L1, L2, L4, L5, L6, L7, W0, W1, W2, W4, W5, W6, W7);
  or or_7 (or_7_out, L0, L1, L2, L3, L5, L6, L7, W0, W1, W2, W3, W5, W6, W7);
  or or_8 (or_8_out, L0, L1, L2, L3, L4, L6, L7, W0, W1, W2, W3, W4, W6, W7);
  or or_9 (or_9_out, L0, L1, L2, L3, L4, L5, L7, W0, W1, W2, W3, W4, W5, W7);
  or or_10 (or_10_out, L0, L1, L2, L3, L4, L5, L6, W0, W1, W2, W3, W4, W5, W6);
  Decoder #(.select(3), .tristate("false"), .disabled(0), .enable("true")) decoder_1 (
    .out0(decoder_1_out0), .out1(decoder_1_out1), .out2(decoder_1_out2), .out3(decoder_1_out3),
    .out4(decoder_1_out4), .out5(decoder_1_out5), .out6(decoder_1_out6), .out7(decoder_1_out7),
    .sel(priority_encoder_1_out), .en(priority_encoder_1_gs));
  and and_18 (A0, or_3_out, V0);
  and and_19 (A1, or_4_out, V1);
  and and_20 (A2, or_5_out, V2);
  and and_21 (A3, or_6_out, V3);
  and and_22 (A4, or_7_out, V4);
  and and_23 (A5, or_8_out, V5);
  and and_24 (A6, or_9_out, V6);
  and and_25 (A7, or_10_out, V7);
  Decoder #(.select(3), .tristate("false"), .disabled(0), .enable("true")) decoder_2 (
    .out0(decoder_2_out0), .out1(decoder_2_out1), .out2(decoder_2_out2), .out3(decoder_2_out3),
    .out4(decoder_2_out4), .out5(decoder_2_out5), .out6(decoder_2_out6), .out7(decoder_2_out7),
    .sel(\max3_归并比较_6_max_num ), .en(and_17_out));
  or or_11 (or_11_out, decoder_1_out0, decoder_2_out0);
  or or_12 (or_12_out, decoder_1_out1, decoder_2_out1);
  or or_13 (or_13_out, decoder_1_out2, decoder_2_out2);
  or or_14 (or_14_out, decoder_1_out3, decoder_2_out3);
  or or_15 (or_15_out, decoder_1_out4, decoder_2_out4);
  or or_16 (or_16_out, decoder_1_out5, decoder_2_out5);
  or or_17 (or_17_out, decoder_1_out6, decoder_2_out6);
  or or_18 (or_18_out, decoder_1_out7, decoder_2_out7);
  and and_26 (W0, EX_Miss, or_11_out, EX_Branch);
  and and_27 (W1, EX_Miss, or_12_out, EX_Branch);
  and and_28 (W2, EX_Miss, or_13_out, EX_Branch);
  and and_29 (W3, EX_Miss, or_14_out, EX_Branch);
  and and_30 (W4, EX_Miss, or_15_out, EX_Branch);
  and and_31 (W5, EX_Miss, or_16_out, EX_Branch);
  and and_32 (W6, EX_Miss, or_17_out, EX_Branch);
  and and_33 (W7, EX_Miss, or_18_out, EX_Branch);

  // Other names for the same wires on the sheet: Tag[31:0] = EX_PC
endmodule
