// Logisim project 实验1-CS2003-U202015375-汪宇飞.circ as structural Verilog: 5 circuits, main circuit 一位二级制全加器
module \一位二级制全加器  (
  input  Ai,
  input  Bi,
  input  Ci_1,
  output Si,
  output Ci
);

  wire nand_1_out, nand_2_out, xor_1_out;

  xor xor_1 (xor_1_out, Ai, Bi);
  nand nand_1 (nand_1_out, xor_1_out, Ci_1);
  nand nand_2 (nand_2_out, Bi, Ai);
  xor xor_2 (Si, xor_1_out, Ci_1);
  nand nand_3 (Ci, nand_1_out, nand_2_out);
endmodule

module \一位二进制半加器  (
  input  A,
  input  B,
  output C,
  output S
);

  and and_1 (C, A, B);
  or or_1 (S, A, B);
endmodule

module \串行进位并行加法器  (
  input  A0,
  input  B0,
  input  C0,
  input  A1,
  input  B1,
  input  A2,
  input  B2,
  input  A3,
  input  B3,
  output S0,
  output S1,
  output S2,
  output S3,
  output C4
);

  wire \一位二级制全加器_1_ci , \一位二级制全加器_2_ci , \一位二级制全加器_3_ci ;

  \一位二级制全加器  \u_一位二级制全加器_1  (.Ai(A0), .Bi(B0), .Ci_1(C0), .Si(S0), .Ci(\一位二级制全加器_1_ci ));
  \一位二级制全加器  \u_一位二级制全加器_2  (.Ai(A1), .Bi(B1), .Ci_1(\一位二级制全加器_1_ci ), .Si(S1), .Ci(\一位二级制全加器_2_ci ));
  \一位二级制全加器  \u_一位二级制全加器_3  (.Ai(A2), .Bi(B2), .Ci_1(\一位二级制全加器_2_ci ), .Si(S2), .Ci(\一位二级制全加器_3_ci ));
  \一位二级制全加器  \u_一位二级制全加器_4  (.Ai(A3), .Bi(B3), .Ci_1(\一位二级制全加器_3_ci ), .Si(S3), .Ci(C4));
endmodule

module \先行进位并行加法器  (
  input  C0,
  input  A0,
  input  B0,
  input  A1,
  input  B1,
  input  A2,
  input  B2,
  input  A3,
  input  B3,
  output S0,
  output S1,
  output S2,
  output S3,
  output C4
);

  wire and_1_out, and_2_out, and_3_out, and_4_out, and_5_out, and_6_out, and_7_out, and_8_out, or_1_out,
       or_2_out, or_3_out, xor_1_out, xor_2_out, xor_3_out, xor_4_out, xor_5_out, xor_6_out, xor_7_out,
       xor_8_out;

  and and_1 (and_1_out, A0, B0);
  and and_2 (and_2_out, A1, B1);
  and and_3 (and_3_out, A2, B2);
  and and_4 (and_4_out, A3, B3);
  xor xor_1 (xor_1_out, A0, B0);
  xor xor_2 (xor_2_out, A1, B1);
  xor xor_3 (xor_3_out, A2, B2);
  xor xor_4 (xor_4_out, A3, B3);
  and and_5 (and_5_out, C0, xor_1_out);
  and and_6 (and_6_out, or_1_out, xor_2_out);
  and and_7 (and_7_out, or_2_out, xor_3_out);
  and and_8 (and_8_out, or_3_out, xor_4_out);
  or or_1 (or_1_out, and_5_out, and_1_out);
  or or_2 (or_2_out, and_6_out, and_2_out);
  or or_3 (or_3_out, and_7_out, and_3_out);
  or or_4 (C4, and_8_out, and_4_out);
  xor xor_5 (xor_5_out, A0, B0);
  xor xor_6 (xor_6_out, A1, B1);
  xor xor_7 (xor_7_out, A2, B2);
  xor xor_8 (xor_8_out, A3, B3);
  xor xor_9 (S0, C0, xor_5_out);
  xor xor_10 (S1, or_1_out, xor_6_out);
  xor xor_11 (S2, or_2_out, xor_7_out);
  xor xor_12 (S3, or_3_out, xor_8_out);
endmodule

module \先行进位并行加法器测试电路  (
  input  in_1,
  input  in_2,
  input  in_3,
  input  in_4,
  input  in_5,
  input  in_6,
  input  in_7,
  input  in_8,
  input  in_9,
  output out_10,
  output out_11,
  output out_12,
  output out_13,
  output out_14
);

  \先行进位并行加法器  \u_先行进位并行加法器_1  (
    .C0(in_5), .A0(in_1), .B0(in_6), .A1(in_2), .B1(in_7), .A2(in_3), .B2(in_8), .A3(in_4), .B3(in_9),
    .S0(out_10), .S1(out_11), .S2(out_12), .S3(out_13), .C4(out_14));
endmodule
