// Logisim project 实验2-CS2003-U202015375-汪宇飞.circ as structural Verilog: 10 circuits, main circuit 四位二进制可逆计数器
module \四位二进制可逆计数器  (
  input  CLR,
  input  LD,
  input  D,
  input  C,
  input  B,
  input  A,
  input  CPU,
  input  CPD,
  output QD,
  output QC,
  output QB,
  output QA
);

  wire and_1_out, and_2_out, and_3_out, and_4_out, and_5_out, and_6_out, and_7_out, and_8_out, and_9_out,
       and_10_out, and_11_out, and_12_out, and_13_out, and_14_out, d_ff_1_qn, d_ff_2_qn, d_ff_3_qn,
       d_ff_4_qn, not_1_out, not_2_out, not_3_out, not_4_out, not_5_out, or_1_out, or_2_out, or_3_out,
       or_4_out, or_5_out, or_6_out, or_7_out, or_8_out;

  not not_1 (not_1_out, LD);
  not not_2 (not_2_out, D);
  not not_3 (not_3_out, C);
  not not_4 (not_4_out, B);
  not not_5 (not_5_out, A);
  and and_1 (and_1_out, not_1_out, D);
  and and_2 (and_2_out, not_2_out, not_1_out);
  and and_3 (and_3_out, not_1_out, C);
  and and_4 (and_4_out, not_3_out, not_1_out);
  and and_5 (and_5_out, not_1_out, B);
  and and_6 (and_6_out, not_4_out, not_1_out);
  and and_7 (and_7_out, not_1_out, A);
  and and_8 (and_8_out, not_5_out, not_1_out);
  or or_1 (or_1_out, CLR, and_2_out);
  or or_2 (or_2_out, CLR, and_4_out);
  or or_3 (or_3_out, CLR, and_6_out);
  or or_4 (or_4_out, CLR, and_8_out);
  and and_9 (and_9_out, d_ff_2_qn, and_11_out);
  and and_10 (and_10_out, QC, and_12_out);
  and and_11 (and_11_out, d_ff_3_qn, and_13_out);
  and and_12 (and_12_out, QB, and_14_out);
  and and_13 (and_13_out, CPD, d_ff_4_qn);
  and and_14 (and_14_out, CPU, QA);
  or or_5 (or_5_out, and_9_out, and_10_out);
  or or_6 (or_6_out, and_11_out, and_12_out);
  or or_7 (or_7_out, and_13_out, and_14_out);
  or or_8 (or_8_out, CPU, CPD);
  D_Flip_Flop #(.trigger("falling"), .Pre_Clr_Positions("ABOVE_BELOW"), .NegatePresetClear("false"), .enable("false"), .NewFFLayout("true")) d_ff_1 (
    .clk(or_5_out), .D(d_ff_1_qn), .Q(QD), .Qn(d_ff_1_qn), .preset(and_1_out), .reset(or_1_out));
  D_Flip_Flop #(.trigger("falling"), .Pre_Clr_Positions("ABOVE_BELOW"), .NegatePresetClear("false"), .enable("false"), .NewFFLayout("true")) d_ff_2 (
    .clk(or_6_out), .D(d_ff_2_qn), .Q(QC), .Qn(d_ff_2_qn), .preset(and_3_out), .reset(or_2_out));
  D_Flip_Flop #(.trigger("falling"), .Pre_Clr_Positions("ABOVE_BELOW"), .NegatePresetClear("false"), .enable("false"), .NewFFLayout("true")) d_ff_3 (
    .clk(or_7_out), .D(d_ff_3_qn), .Q(QB), .Qn(d_ff_3_qn), .preset(and_5_out), .reset(or_3_out));
  D_Flip_Flop #(.trigger("falling"), .Pre_Clr_Positions("ABOVE_BELOW"), .NegatePresetClear("false"), .enable("false"), .NewFFLayout("true")) d_ff_4 (
    .clk(or_8_out), .D(d_ff_4_qn), .Q(QA), .Qn(d_ff_4_qn), .preset(and_7_out), .reset(or_4_out));
endmodule

module \四位二进制可逆计数器测试电路  (
  input  in_1,
  input  in_2,
  input  in_3,
  input  in_4,
  input  in_5,
  output out_6,
  output out_7,
  output out_8,
  output out_9
);

  wire button_1_out, button_2_out, button_3_out;

  Button button_1 (.out(button_1_out));
  Button button_2 (.out(button_2_out));
  Button button_3 (.out(button_3_out));
  \四位二进制可逆计数器  \u_四位二进制可逆计数器_1  (
    .D(in_1), .C(in_2), .B(in_3), .A(in_4), .QD(out_6), .CLR(button_3_out), .QC(out_7), .QB(out_8),
    .QA(out_9), .LD(in_5), .CPU(button_1_out), .CPD(button_2_out));
endmodule

module \先行进位并行加法器  (
  input  C0,
  input  A0,
  input  B0,
  input  A1,
  input  B1,
  input  A2,
  input  B2,
  input  A3,
  input  B3,
  output S0,
  output S1,
  output S2,
  output S3,
  output C4
);

  wire and_1_out, and_2_out, and_3_out, and_4_out, and_5_out, and_6_out, and_7_out, and_8_out, or_1_out,
       or_2_out, or_3_out, xor_1_out, xor_2_out, xor_3_out, xor_4_out, xor_5_out, xor_6_out, xor_7_out,
       xor_8_out;

  and and_1 (and_1_out, A0, B0);
  and and_2 (and_2_out, A1, B1);
  and and_3 (and_3_out, A2, B2);
  and and_4 (and_4_out, A3, B3);
  xor xor_1 (xor_1_out, A0, B0);
  xor xor_2 (xor_2_out, A1, B1);
  xor xor_3 (xor_3_out, A2, B2);
  xor xor_4 (xor_4_out, A3, B3);
  and and_5 (and_5_out, C0, xor_1_out);
  and and_6 (and_6_out, or_1_out, xor_2_out);
  and and_7 (and_7_out, or_2_out, xor_3_out);
  and and_8 (and_8_out, or_3_out, xor_4_out);
  or or_1 (or_1_out, and_5_out, and_1_out);
  or or_2 (or_2_out, and_6_out, and_2_out);
  or or_3 (or_3_out, and_7_out, and_3_out);
  or or_4 (C4, and_8_out, and_4_out);
  xor xor_5 (xor_5_out, A0, B0);
  xor xor_6 (xor_6_out, A1, B1);
  xor xor_7 (xor_7_out, A2, B2);
  xor xor_8 (xor_8_out, A3, B3);
  xor xor_9 (S0, C0, xor_5_out);
  xor xor_10 (S1, or_1_out, xor_6_out);
  xor xor_11 (S2, or_2_out, xor_7_out);
  xor xor_12 (S3, or_3_out, xor_8_out);
endmodule

module \二进制转8421码电路  (
  input  QD,
  input  QC,
  input  QB,
  input  QA,
  output A7,
  output A0,
  output A1,
  output A2,
  output A3,
  output A6,
  output A5,
  output A4
);

  wire and_1_out, or_1_out;

  \先行进位并行加法器  \u_先行进位并行加法器_1  (
    .C0(1'b0), .A0(QA), .B0(1'b0), .A1(QB), .B1(and_1_out), .A2(QC), .B2(and_1_out), .A3(QD), .B3(1'b0),
    .S0(A0), .S1(A1), .S2(A2), .S3(A3), .C4(A4));
  or or_1 (or_1_out, QC, QB);
  and and_1 (and_1_out, QD, or_1_out);

  assign A5 = 1'b0;
  assign A6 = 1'b0;
  assign A7 = 1'b0;
endmodule

module \二进制转8421码测试电路  (
  input  in_1,
  input  in_2,
  input  in_3,
  input  in_4,
  output out_5,
  output out_6,
  output out_7,
  output out_8,
  output out_9,
  output out_10,
  output out_11,
  output out_12
);

  \二进制转8421码电路  \u_二进制转8421码电路_1  (
    .QD(in_1), .QC(in_2), .QB(in_3), .QA(in_4), .A7(out_5), .A6(out_7), .A5(out_9), .A4(out_11), .A0(out_12),
    .A1(out_10), .A2(out_8), .A3(out_6));
endmodule

module \显示电路  (
  input  A0,
  input  A1,
  input  A2,
  input  A3,
  output a,
  output b,
  output c,
  output d,
  output e,
  output f,
  output g
);

  wire and_1_out, and_2_out, and_3_out, and_4_out, and_5_out, and_6_out, and_7_out, and_8_out, and_9_out,
       and_10_out, and_11_out, and_12_out, and_13_out, and_14_out, and_15_out, and_16_out, and_17_out,
       and_18_out, and_19_out, and_20_out, and_21_out, not_1_out, not_2_out, not_3_out, not_4_out;

  not not_1 (not_1_out, A0);
  not not_2 (not_2_out, A1);
  not not_3 (not_3_out, A2);
  not not_4 (not_4_out, A3);
  and and_1 (and_1_out, not_1_out, not_2_out, not_3_out);
  and and_2 (and_2_out, A1, not_3_out, not_4_out);
  and and_3 (and_3_out, A0, A2, not_4_out);
  and and_4 (and_4_out, A0, not_2_out, A3);
  and and_5 (and_5_out, not_3_out, not_4_out);
  and and_6 (and_6_out, not_2_out, not_1_out);
  and and_7 (and_7_out, not_2_out, not_3_out);
  and and_8 (and_8_out, not_4_out, A0, A1);
  and and_9 (and_9_out, not_4_out, A2);
  and and_10 (and_10_out, not_3_out, not_2_out);
  and and_11 (and_11_out, A0, not_3_out);
  and and_12 (and_12_out, A0, not_2_out, A2);
  and and_13 (and_13_out, not_1_out, not_3_out);
  and and_14 (and_14_out, A0, A1, not_3_out);
  and and_15 (and_15_out, not_1_out, A1, A2);
  and and_16 (and_16_out, not_1_out, A1);
  and and_17 (and_17_out, not_2_out, A2);
  and and_18 (and_18_out, not_2_out, not_3_out, A3);
  and and_19 (and_19_out, not_1_out, A2);
  and and_20 (and_20_out, A3, not_3_out);
  and and_21 (and_21_out, not_3_out, A1);
  or or_1 (a, and_1_out, and_2_out, and_3_out, and_4_out);
  or or_2 (b, and_5_out, and_6_out, and_7_out, and_8_out);
  or or_3 (c, and_9_out, and_10_out, and_11_out);
  or or_4 (d, and_12_out, and_13_out, and_14_out, and_15_out);
  or or_5 (e, and_13_out, and_16_out);
  or or_6 (f, and_6_out, and_17_out, and_18_out, and_19_out);
  or or_7 (g, and_17_out, and_20_out, and_21_out, and_16_out);
endmodule

module \显示电路测试电路  (
  input  in_1,
  input  in_2,
  input  in_3,
  input  in_4
);

  wire \二进制转8421码电路_1_a0 , \二进制转8421码电路_1_a1 , \二进制转8421码电路_1_a2 , \二进制转8421码电路_1_a3 , \二进制转8421码电路_1_a4 ,
       \二进制转8421码电路_1_a5 , \二进制转8421码电路_1_a6 , \二进制转8421码电路_1_a7 , \显示电路_1_a , \显示电路_1_b , \显示电路_1_c ,
       \显示电路_1_d , \显示电路_1_e , \显示电路_1_f , \显示电路_1_g , \显示电路_2_a , \显示电路_2_b , \显示电路_2_c , \显示电路_2_d ,
       \显示电路_2_e , \显示电路_2_f , \显示电路_2_g ;

  _7_Segment_Display #(.active("true")) u_7_segment_display_1 (
    .g(\显示电路_1_g ), .f(\显示电路_1_f ), .a(\显示电路_1_a ), .b(\显示电路_1_b ), .e(\显示电路_1_e ), .d(\显示电路_1_d ),
    .c(\显示电路_1_c ), .dp(1'b0));
  \显示电路  \u_显示电路_1  (
    .A0(\二进制转8421码电路_1_a4 ), .A1(\二进制转8421码电路_1_a5 ), .A2(\二进制转8421码电路_1_a6 ), .A3(\二进制转8421码电路_1_a7 ),
    .a(\显示电路_1_a ), .b(\显示电路_1_b ), .c(\显示电路_1_c ), .d(\显示电路_1_d ), .e(\显示电路_1_e ), .f(\显示电路_1_f ),
    .g(\显示电路_1_g ));
  \二进制转8421码电路  \u_二进制转8421码电路_1  (
    .QD(in_1), .QC(in_2), .QB(in_3), .QA(in_4), .A7(\二进制转8421码电路_1_a7 ), .A6(\二进制转8421码电路_1_a6 ),
    .A5(\二进制转8421码电路_1_a5 ), .A4(\二进制转8421码电路_1_a4 ), .A0(\二进制转8421码电路_1_a0 ), .A1(\二进制转8421码电路_1_a1 ),
    .A2(\二进制转8421码电路_1_a2 ), .A3(\二进制转8421码电路_1_a3 ));
  _7_Segment_Display #(.active("true")) u_7_segment_display_2 (
    .g(\显示电路_2_g ), .f(\显示电路_2_f ), .a(\显示电路_2_a ), .b(\显示电路_2_b ), .e(\显示电路_2_e ), .d(\显示电路_2_d ),
    .c(\显示电路_2_c ), .dp(1'b0));
  \显示电路  \u_显示电路_2  (
    .A0(\二进制转8421码电路_1_a0 ), .A1(\二进制转8421码电路_1_a1 ), .A2(\二进制转8421码电路_1_a2 ), .A3(\二进制转8421码电路_1_a3 ),
    .a(\显示电路_2_a ), .b(\显示电路_2_b ), .c(\显示电路_2_c ), .d(\显示电路_2_d ), .e(\显示电路_2_e ), .f(\显示电路_2_f ),
    .g(\显示电路_2_g ));
endmodule

module \报警电路  (
  input  CPU,
  input  CPD,
  input  A,
  input  B,
  input  C,
  input  D,
  output CPU_2,
  output CPD_2,
  output alarm
);

  wire and_1_out, not_1_out, or_1_out;

  and and_1 (and_1_out, A, B, C, D);
  or or_1 (or_1_out, A, B, C, D);
  and and_2 (CPU_2, CPU, not_1_out);
  not not_1 (not_1_out, and_1_out);
  and and_3 (CPD_2, CPD, or_1_out);
  and and_4 (alarm, CPU, and_1_out);
endmodule

module \小型实验室门禁系统  (
  input  CPU,
  input  CPD,
  input  CLR,
  output a0,
  output b0,
  output c0,
  output d0,
  output e0,
  output f0,
  output g0,
  output a1,
  output b1,
  output c1,
  output d1,
  output e1,
  output f1,
  output g1,
  output alarm
);

  wire \二进制转8421码电路_1_a0 , \二进制转8421码电路_1_a1 , \二进制转8421码电路_1_a2 , \二进制转8421码电路_1_a3 , \二进制转8421码电路_1_a4 ,
       \二进制转8421码电路_1_a5 , \二进制转8421码电路_1_a6 , \二进制转8421码电路_1_a7 , \四位二进制可逆计数器_1_qa , \四位二进制可逆计数器_1_qb ,
       \四位二进制可逆计数器_1_qc , \四位二进制可逆计数器_1_qd , \报警电路_1_cpd_2 , \报警电路_1_cpu_2 ;

  \报警电路  \u_报警电路_1  (
    .CPU(CPU), .CPD(CPD), .A(\四位二进制可逆计数器_1_qa ), .B(\四位二进制可逆计数器_1_qb ), .C(\四位二进制可逆计数器_1_qc ),
    .D(\四位二进制可逆计数器_1_qd ), .CPU_2(\报警电路_1_cpu_2 ), .CPD_2(\报警电路_1_cpd_2 ), .alarm(alarm));
  \显示电路  \u_显示电路_1  (
    .A0(\二进制转8421码电路_1_a4 ), .A1(\二进制转8421码电路_1_a5 ), .A2(\二进制转8421码电路_1_a6 ), .A3(\二进制转8421码电路_1_a7 ),
    .a(a0), .b(b0), .c(c0), .d(d0), .e(e0), .f(f0), .g(g0));
  \二进制转8421码电路  \u_二进制转8421码电路_1  (
    .QD(\四位二进制可逆计数器_1_qd ), .QC(\四位二进制可逆计数器_1_qc ), .QB(\四位二进制可逆计数器_1_qb ), .QA(\四位二进制可逆计数器_1_qa ),
    .A7(\二进制转8421码电路_1_a7 ), .A6(\二进制转8421码电路_1_a6 ), .A5(\二进制转8421码电路_1_a5 ), .A4(\二进制转8421码电路_1_a4 ),
    .A0(\二进制转8421码电路_1_a0 ), .A1(\二进制转8421码电路_1_a1 ), .A2(\二进制转8421码电路_1_a2 ), .A3(\二进制转8421码电路_1_a3 ));
  \四位二进制可逆计数器  \u_四位二进制可逆计数器_1  (
    .D(1'b0), .C(1'b0), .B(1'b0), .A(1'b0), .QD(\四位二进制可逆计数器_1_qd ), .CLR(CLR), .QC(\四位二进制可逆计数器_1_qc ),
    .QB(\四位二进制可逆计数器_1_qb ), .QA(\四位二进制可逆计数器_1_qa ), .LD(1'b1), .CPU(\报警电路_1_cpu_2 ), .CPD(\报警电路_1_cpd_2 ));
  \显示电路  \u_显示电路_2  (
    .A0(\二进制转8421码电路_1_a0 ), .A1(\二进制转8421码电路_1_a1 ), .A2(\二进制转8421码电路_1_a2 ), .A3(\二进制转8421码电路_1_a3 ),
    .a(a1), .b(b1), .c(c1), .d(d1), .e(e1), .f(f1), .g(g1));
endmodule

module \小型门禁系统测试电路  (
);

  wire button_1_out, button_2_out, button_3_out, \小型实验室门禁系统_1_a0 , \小型实验室门禁系统_1_a1 , \小型实验室门禁系统_1_alarm ,
       \小型实验室门禁系统_1_b0 , \小型实验室门禁系统_1_b1 , \小型实验室门禁系统_1_c0 , \小型实验室门禁系统_1_c1 , \小型实验室门禁系统_1_d0 ,
       \小型实验室门禁系统_1_d1 , \小型实验室门禁系统_1_e0 , \小型实验室门禁系统_1_e1 , \小型实验室门禁系统_1_f0 , \小型实验室门禁系统_1_f1 ,
       \小型实验室门禁系统_1_g0 , \小型实验室门禁系统_1_g1 ;

  Button button_1 (.out(button_1_out));
  Button button_2 (.out(button_2_out));
  Button button_3 (.out(button_3_out));
  _7_Segment_Display #(.active("true")) u_7_segment_display_1 (
    .g(\小型实验室门禁系统_1_g0 ), .f(\小型实验室门禁系统_1_f0 ), .a(\小型实验室门禁系统_1_a0 ), .b(\小型实验室门禁系统_1_b0 ),
    .e(\小型实验室门禁系统_1_e0 ), .d(\小型实验室门禁系统_1_d0 ), .c(\小型实验室门禁系统_1_c0 ), .dp(1'b0));
  \小型实验室门禁系统  \u_小型实验室门禁系统_1  (
    .CPU(button_1_out), .CPD(button_3_out), .CLR(button_2_out), .a0(\小型实验室门禁系统_1_a0 ), .b0(\小型实验室门禁系统_1_b0 ),
    .c0(\小型实验室门禁系统_1_c0 ), .d0(\小型实验室门禁系统_1_d0 ), .e0(\小型实验室门禁系统_1_e0 ), .f0(\小型实验室门禁系统_1_f0 ),
    .g0(\小型实验室门禁系统_1_g0 ), .a1(\小型实验室门禁系统_1_a1 ), .b1(\小型实验室门禁系统_1_b1 ), .c1(\小型实验室门禁系统_1_c1 ),
    .d1(\小型实验室门禁系统_1_d1 ), .e1(\小型实验室门禁系统_1_e1 ), .f1(\小型实验室门禁系统_1_f1 ), .g1(\小型实验室门禁系统_1_g1 ),
    .alarm(\小型实验室门禁系统_1_alarm ));
  _7_Segment_Display #(.active("true")) u_7_segment_display_2 (
    .g(\小型实验室门禁系统_1_g1 ), .f(\小型实验室门禁系统_1_f1 ), .a(\小型实验室门禁系统_1_a1 ), .b(\小型实验室门禁系统_1_b1 ),
    .e(\小型实验室门禁系统_1_e1 ), .d(\小型实验室门禁系统_1_d1 ), .c(\小型实验室门禁系统_1_c1 ), .dp(1'b0));
  // Buzzer #(.freq_measure("Hz"), .vol_width(7)) buzzer_1: pin names not known; wires that end beside it: \小型实验室门禁系统_1_g0 , \小型实验室门禁系统_1_alarm 
endmodule
