// Logisim project 实验5-CS2003-U202015375-汪宇飞.circ as structural Verilog: 14 circuits, main circuit 六十进制计数器
module \四位二进制可逆计数器  (
  input  D,
  input  C,
  input  B,
  input  A,
  input  LD,
  input  CPu,
  input  CPd,
  input  CLR,
  output QD,
  output QC,
  output QB,
  output QA
);

  wire and_1_out, and_2_out, and_3_out, and_4_out, and_5_out, and_6_out, and_7_out, and_8_out, and_9_out,
       and_10_out, and_11_out, and_12_out, and_13_out, and_14_out, and_15_out, and_16_out, d_ff_1_qn,
       d_ff_2_qn, d_ff_3_qn, d_ff_4_qn, not_1_out, not_2_out, not_3_out, not_4_out, not_5_out, or_1_out,
       or_2_out, or_3_out, or_4_out, or_5_out, or_6_out, or_7_out, or_8_out;

  not not_1 (not_1_out, D);
  not not_2 (not_2_out, C);
  not not_3 (not_3_out, B);
  not not_4 (not_4_out, A);
  not not_5 (not_5_out, LD);
  and and_1 (and_1_out, D, not_5_out);
  and and_2 (and_2_out, not_1_out, not_5_out);
  and and_3 (and_3_out, C, not_5_out);
  and and_4 (and_4_out, not_2_out, not_5_out);
  and and_5 (and_5_out, B, not_5_out);
  and and_6 (and_6_out, not_3_out, not_5_out);
  and and_7 (and_7_out, A, not_5_out);
  and and_8 (and_8_out, not_4_out, not_5_out);
  and and_9 (and_9_out, QA, QB, QC, CPu);
  and and_10 (and_10_out, d_ff_4_qn, CPd, d_ff_3_qn, d_ff_2_qn);
  or or_1 (or_1_out, and_9_out, and_10_out);
  and and_11 (and_11_out, CPu, QB, QA);
  or or_2 (or_2_out, and_11_out, and_12_out);
  and and_12 (and_12_out, CPd, d_ff_3_qn, d_ff_4_qn);
  and and_13 (and_13_out, QA, CPu);
  or or_3 (or_3_out, and_13_out, and_14_out);
  and and_14 (and_14_out, d_ff_4_qn, CPd);
  and and_15 (and_15_out, CPu, 1'b1);
  or or_4 (or_4_out, and_15_out, and_16_out);
  and and_16 (and_16_out, CPd, 1'b1);
  D_Flip_Flop #(.trigger("falling"), .Pre_Clr_Positions("ABOVE_BELOW"), .NegatePresetClear("false"), .enable("false"), .NewFFLayout("true")) d_ff_1 (
    .clk(or_1_out), .D(d_ff_1_qn), .Q(QD), .Qn(d_ff_1_qn), .preset(and_1_out), .reset(or_5_out));
  or or_5 (or_5_out, and_2_out, CLR);
  D_Flip_Flop #(.trigger("falling"), .Pre_Clr_Positions("ABOVE_BELOW"), .NegatePresetClear("false"), .enable("false"), .NewFFLayout("true")) d_ff_2 (
    .clk(or_2_out), .D(d_ff_2_qn), .Q(QC), .Qn(d_ff_2_qn), .preset(and_3_out), .reset(or_6_out));
  or or_6 (or_6_out, CLR, and_4_out);
  D_Flip_Flop #(.trigger("falling"), .Pre_Clr_Positions("ABOVE_BELOW"), .NegatePresetClear("false"), .enable("false"), .NewFFLayout("true")) d_ff_3 (
    .clk(or_3_out), .D(d_ff_3_qn), .Q(QB), .Qn(d_ff_3_qn), .preset(and_5_out), .reset(or_7_out));
  or or_7 (or_7_out, and_6_out, CLR);
  D_Flip_Flop #(.trigger("falling"), .Pre_Clr_Positions("ABOVE_BELOW"), .NegatePresetClear("false"), .enable("false"), .NewFFLayout("true")) d_ff_4 (
    .clk(or_4_out), .D(d_ff_4_qn), .Q(QA), .Qn(d_ff_4_qn), .preset(and_7_out), .reset(or_8_out));
  or or_8 (or_8_out, CLR, and_8_out);
endmodule

module \六十进制计数器  (
  input  CPU,
  input  CPD,
  input  CLR,
  input  Adj,
  output Q0D,
  output Q0C,
  output Q0B,
  output Q0A,
  output Q1D,
  output Q1C,
  output Q1B,
  output Q1A,
  output Qcc
);

  wire and_1_out, and_2_out, and_3_out, and_4_out, and_5_out, buffer_1_out, buffer_2_out, not_1_out,
       not_2_out, not_3_out, not_4_out, or_1_out, or_2_out, or_3_out, or_4_out, or_5_out;

  or or_1 (or_1_out, Q0A, Q0B, Q0C, Q0D);
  or or_2 (or_2_out, or_1_out, or_4_out);
  not not_1 (not_1_out, Adj);
  and and_1 (and_1_out, or_2_out, CPD, Adj);
  or or_3 (or_3_out, and_5_out, CLR, and_3_out);
  \四位二进制可逆计数器  \u_四位二进制可逆计数器_1  (
    .D(1'b1), .C(1'b0), .B(1'b0), .A(1'b1), .QD(Q0D), .QC(Q0C), .QB(Q0B), .QA(Q0A), .LD(not_2_out),
    .CPu(CPU), .CPd(and_1_out), .CLR(or_3_out));
  not not_2 (not_2_out, and_2_out);
  and and_2 (and_2_out, Q0A, Q0B, Q0C, Q0D);
  not not_3 (not_3_out, Q0A);
  buf buffer_1 (buffer_1_out, Q0B);
  not not_4 (not_4_out, Q0C);
  buf buffer_2 (buffer_2_out, Q0D);
  and and_3 (and_3_out, not_3_out, buffer_1_out, not_4_out, buffer_2_out);
  or or_4 (or_4_out, Q1A, Q1B, Q1C, Q1D);
  and and_4 (and_4_out, or_4_out, and_2_out);
  or or_5 (or_5_out, and_5_out, CLR);
  \四位二进制可逆计数器  \u_四位二进制可逆计数器_2  (
    .D(1'b1), .C(1'b1), .B(1'b1), .A(1'b1), .QD(Q1D), .QC(Q1C), .QB(Q1B), .QA(Q1A), .LD(1'b1),
    .CPu(and_3_out), .CPd(and_4_out), .CLR(or_5_out));
  and and_5 (and_5_out, Q1B, Q1C);
  and and_6 (Qcc, and_5_out, not_1_out);
endmodule

module \六十进制计数器测试电路  (
  input  in_1,
  output out_2,
  output out_3,
  output out_4,
  output out_5
);

  wire button_1_out, button_2_out, button_3_out, button_4_out, clock_1_out, \六十进制计数器_1_qcc ;
  wire [3:0] \六十进制计数器_1_q0a , \六十进制计数器_1_q1a ;

  Clock #(.highDuration(1), .lowDuration(1)) clock_1 (.out(clock_1_out));
  Button button_1 (.out(button_1_out));
  Hex_Digit_Display hex_digit_display_1 (.value(\六十进制计数器_1_q1a ), .dp(1'b0));
  Hex_Digit_Display hex_digit_display_2 (.value(\六十进制计数器_1_q0a ), .dp(1'b0));
  \六十进制计数器  \u_六十进制计数器_1  (
    .CPU(clock_1_out), .CPD(button_1_out), .CLR(button_3_out), .Adj(in_1), .Qcc(\六十进制计数器_1_qcc ),
    .Q0D(\六十进制计数器_1_q0a [3]), .Q0C(\六十进制计数器_1_q0a [2]), .Q0B(\六十进制计数器_1_q0a [1]), .Q0A(\六十进制计数器_1_q0a [0]),
    .Q1D(\六十进制计数器_1_q1a [3]), .Q1C(\六十进制计数器_1_q1a [2]), .Q1B(\六十进制计数器_1_q1a [1]), .Q1A(\六十进制计数器_1_q1a [0]));
  Button button_2 (.out(button_2_out));
  Button button_3 (.out(button_3_out));
  Button button_4 (.out(button_4_out));
  \四位二进制可逆计数器  \u_四位二进制可逆计数器_1  (
    .D(1'b1), .C(1'b1), .B(1'b1), .A(1'b1), .QD(out_2), .QC(out_3), .QB(out_4), .QA(out_5), .LD(1'b1),
    .CPu(\六十进制计数器_1_qcc ), .CPd(button_2_out), .CLR(button_4_out));
endmodule

module \十二进制计数器  (
  input  CPU,
  input  CPD,
  input  CLR,
  input  Adj,
  output Q0D,
  output Q0C,
  output Q0B,
  output Q0A,
  output Q1D,
  output Q1C,
  output Q1B,
  output Q1A,
  output Qcc
);

  wire and_1_out, and_2_out, and_3_out, and_4_out, and_5_out, buffer_1_out, buffer_2_out, buffer_3_out,
       buffer_4_out, not_1_out, not_2_out, not_3_out, not_4_out, not_5_out, not_6_out, not_7_out, not_8_out,
       not_9_out, not_10_out, or_1_out, or_2_out, or_3_out, or_4_out, or_5_out;

  or or_1 (or_1_out, Q0A, Q0B, Q0C, Q0D);
  or or_2 (or_2_out, or_1_out, or_4_out);
  not not_1 (not_1_out, Adj);
  and and_1 (and_1_out, or_2_out, CPD, Adj);
  or or_3 (or_3_out, and_5_out, CLR, and_3_out);
  \四位二进制可逆计数器  \u_四位二进制可逆计数器_1  (
    .D(1'b1), .C(1'b0), .B(1'b0), .A(1'b1), .QD(Q0D), .QC(Q0C), .QB(Q0B), .QA(Q0A), .LD(not_2_out),
    .CPu(CPU), .CPd(and_1_out), .CLR(or_3_out));
  not not_2 (not_2_out, and_2_out);
  not not_3 (not_3_out, Q0D);
  not not_4 (not_4_out, Q0C);
  buf buffer_1 (buffer_1_out, Q0B);
  not not_5 (not_5_out, Q0A);
  and and_2 (and_2_out, Q0A, Q0B, Q0C, Q0D);
  not not_6 (not_6_out, Q0A);
  buf buffer_2 (buffer_2_out, Q0B);
  not not_7 (not_7_out, Q0C);
  buf buffer_3 (buffer_3_out, Q0D);
  and and_3 (and_3_out, not_6_out, buffer_2_out, not_7_out, buffer_3_out);
  or or_4 (or_4_out, Q1A, Q1B, Q1C, Q1D);
  and and_4 (and_4_out, or_4_out, and_2_out);
  or or_5 (or_5_out, and_5_out, CLR);
  \四位二进制可逆计数器  \u_四位二进制可逆计数器_2  (
    .D(1'b1), .C(1'b1), .B(1'b1), .A(1'b1), .QD(Q1D), .QC(Q1C), .QB(Q1B), .QA(Q1A), .LD(1'b1),
    .CPu(and_3_out), .CPd(and_4_out), .CLR(or_5_out));
  not not_8 (not_8_out, Q1D);
  not not_9 (not_9_out, Q1C);
  not not_10 (not_10_out, Q1B);
  buf buffer_4 (buffer_4_out, Q1A);
  and and_5 (and_5_out, not_3_out, not_4_out, buffer_1_out, not_5_out, not_8_out, not_9_out, not_10_out, buffer_4_out);
  and and_6 (Qcc, and_5_out, not_1_out);
endmodule

module \二十四机制计数器  (
  input  CPU,
  input  CPD,
  input  CLR,
  input  Adj,
  output Q0D,
  output Q0C,
  output Q0B,
  output Q0A,
  output Q1D,
  output Q1C,
  output Q1B,
  output Q1A,
  output Qcc
);

  wire and_1_out, and_2_out, and_3_out, and_4_out, and_5_out, buffer_1_out, buffer_2_out, buffer_3_out,
       buffer_4_out, not_1_out, not_2_out, not_3_out, not_4_out, not_5_out, not_6_out, not_7_out, not_8_out,
       not_9_out, not_10_out, or_1_out, or_2_out, or_3_out, or_4_out, or_5_out;

  or or_1 (or_1_out, Q0A, Q0B, Q0C, Q0D);
  or or_2 (or_2_out, or_1_out, or_4_out);
  not not_1 (not_1_out, Adj);
  and and_1 (and_1_out, or_2_out, CPD, Adj);
  or or_3 (or_3_out, and_5_out, CLR, and_3_out);
  \四位二进制可逆计数器  \u_四位二进制可逆计数器_1  (
    .D(1'b1), .C(1'b0), .B(1'b0), .A(1'b1), .QD(Q0D), .QC(Q0C), .QB(Q0B), .QA(Q0A), .LD(not_2_out),
    .CPu(CPU), .CPd(and_1_out), .CLR(or_3_out));
  not not_2 (not_2_out, and_2_out);
  not not_3 (not_3_out, Q0D);
  buf buffer_1 (buffer_1_out, Q0C);
  not not_4 (not_4_out, Q0B);
  not not_5 (not_5_out, Q0A);
  and and_2 (and_2_out, Q0A, Q0B, Q0C, Q0D);
  not not_6 (not_6_out, Q0A);
  buf buffer_2 (buffer_2_out, Q0B);
  not not_7 (not_7_out, Q0C);
  buf buffer_3 (buffer_3_out, Q0D);
  and and_3 (and_3_out, not_6_out, buffer_2_out, not_7_out, buffer_3_out);
  or or_4 (or_4_out, Q1A, Q1B, Q1C, Q1D);
  and and_4 (and_4_out, or_4_out, and_2_out);
  or or_5 (or_5_out, and_5_out, CLR);
  \四位二进制可逆计数器  \u_四位二进制可逆计数器_2  (
    .D(1'b1), .C(1'b1), .B(1'b1), .A(1'b1), .QD(Q1D), .QC(Q1C), .QB(Q1B), .QA(Q1A), .LD(1'b1),
    .CPu(and_3_out), .CPd(and_4_out), .CLR(or_5_out));
  not not_8 (not_8_out, Q1D);
  not not_9 (not_9_out, Q1C);
  buf buffer_4 (buffer_4_out, Q1B);
  not not_10 (not_10_out, Q1A);
  and and_5 (and_5_out, not_3_out, buffer_1_out, not_4_out, not_5_out, not_8_out, not_9_out, buffer_4_out, not_10_out);
  and and_6 (Qcc, and_5_out, not_1_out);
endmodule

module \十二进制计数器或二十四进制的计数器电路  (
  input  CPU,
  input  Adj,
  input  CPD,
  input  CLR,
  input  SET,
  output Q1D,
  output Q1C,
  output Q1B,
  output Q1A,
  output Q0D,
  output Q0C,
  output Q0B,
  output Q0A,
  output Qcc
);

  wire \二十四机制计数器_1_q0a , \二十四机制计数器_1_q0b , \二十四机制计数器_1_q0c , \二十四机制计数器_1_q0d , \二十四机制计数器_1_q1a ,
       \二十四机制计数器_1_q1b , \二十四机制计数器_1_q1c , \二十四机制计数器_1_q1d , \二十四机制计数器_1_qcc , \十二进制计数器_1_q0a ,
       \十二进制计数器_1_q0b , \十二进制计数器_1_q0c , \十二进制计数器_1_q0d , \十二进制计数器_1_q1a , \十二进制计数器_1_q1b , \十二进制计数器_1_q1c ,
       \十二进制计数器_1_q1d , \十二进制计数器_1_qcc ;

  \十二进制计数器  \u_十二进制计数器_1  (
    .CPU(CPU), .CPD(CPD), .CLR(CLR), .Adj(Adj), .Qcc(\十二进制计数器_1_qcc ), .Q0D(\十二进制计数器_1_q0d ),
    .Q0C(\十二进制计数器_1_q0c ), .Q0B(\十二进制计数器_1_q0b ), .Q0A(\十二进制计数器_1_q0a ), .Q1D(\十二进制计数器_1_q1d ),
    .Q1C(\十二进制计数器_1_q1c ), .Q1B(\十二进制计数器_1_q1b ), .Q1A(\十二进制计数器_1_q1a ));
  \二十四机制计数器  \u_二十四机制计数器_1  (
    .Q0D(\二十四机制计数器_1_q0d ), .Q0C(\二十四机制计数器_1_q0c ), .Q0B(\二十四机制计数器_1_q0b ), .Q0A(\二十四机制计数器_1_q0a ),
    .Q1D(\二十四机制计数器_1_q1d ), .Q1C(\二十四机制计数器_1_q1c ), .Q1B(\二十四机制计数器_1_q1b ), .Q1A(\二十四机制计数器_1_q1a ),
    .Qcc(\二十四机制计数器_1_qcc ), .CPU(CPU), .CPD(CPD), .CLR(CLR), .Adj(Adj));
  Multiplexer #(.select(1), .width(1), .disabled("Z"), .enable("false")) multiplexer_1 (
    .in0(\十二进制计数器_1_q1d ), .in1(\二十四机制计数器_1_q1d ), .out(Q1D), .sel(SET));
  Multiplexer #(.select(1), .width(1), .disabled("Z"), .enable("false")) multiplexer_2 (
    .in0(\十二进制计数器_1_q1c ), .in1(\二十四机制计数器_1_q1c ), .out(Q1C), .sel(SET));
  Multiplexer #(.select(1), .width(1), .disabled("Z"), .enable("false")) multiplexer_3 (
    .in0(\十二进制计数器_1_q1b ), .in1(\二十四机制计数器_1_q1b ), .out(Q1B), .sel(SET));
  Multiplexer #(.select(1), .width(1), .disabled("Z"), .enable("false")) multiplexer_4 (
    .in0(\十二进制计数器_1_q1a ), .in1(\二十四机制计数器_1_q1a ), .out(Q1A), .sel(SET));
  Multiplexer #(.select(1), .width(1), .disabled("Z"), .enable("false")) multiplexer_5 (
    .in0(\十二进制计数器_1_q0d ), .in1(\二十四机制计数器_1_q0d ), .out(Q0D), .sel(SET));
  Multiplexer #(.select(1), .width(1), .disabled("Z"), .enable("false")) multiplexer_6 (
    .in0(\十二进制计数器_1_q0c ), .in1(\二十四机制计数器_1_q0c ), .out(Q0C), .sel(SET));
  Multiplexer #(.select(1), .width(1), .disabled("Z"), .enable("false")) multiplexer_7 (
    .in0(\十二进制计数器_1_q0b ), .in1(\二十四机制计数器_1_q0b ), .out(Q0B), .sel(SET));
  Multiplexer #(.select(1), .width(1), .disabled("Z"), .enable("false")) multiplexer_8 (
    .in0(\十二进制计数器_1_q0a ), .in1(\二十四机制计数器_1_q0a ), .out(Q0A), .sel(SET));
  Multiplexer #(.select(1), .width(1), .disabled("Z"), .enable("false")) multiplexer_9 (
    .in0(\十二进制计数器_1_qcc ), .in1(\二十四机制计数器_1_qcc ), .out(Qcc), .sel(SET));
endmodule

module \十二进制计数器或二十四进制的计数器测试电路  (
  input  in_1,
  input  in_2
);

  wire button_1_out, button_2_out, button_3_out, button_4_out, button_5_out, \十二进制计数器或二十四进制的计数器电路_1_qcc ;
  wire [3:0] \十二进制计数器或二十四进制的计数器电路_1_q0a , \十二进制计数器或二十四进制的计数器电路_1_q1a , \四位二进制可逆计数器_1_qa ;

  Button button_1 (.out(button_1_out));
  Button button_2 (.out(button_2_out));
  Hex_Digit_Display hex_digit_display_1 (.value(\十二进制计数器或二十四进制的计数器电路_1_q1a ), .dp(1'b0));
  Hex_Digit_Display hex_digit_display_2 (.value(\十二进制计数器或二十四进制的计数器电路_1_q0a ), .dp(1'b0));
  \十二进制计数器或二十四进制的计数器电路  \u_十二进制计数器或二十四进制的计数器电路_1  (
    .SET(in_2), .CPU(button_1_out), .CPD(button_2_out), .CLR(button_3_out), .Adj(in_1),
    .Qcc(\十二进制计数器或二十四进制的计数器电路_1_qcc ), .Q0D(\十二进制计数器或二十四进制的计数器电路_1_q0a [3]),
    .Q0C(\十二进制计数器或二十四进制的计数器电路_1_q0a [2]), .Q0B(\十二进制计数器或二十四进制的计数器电路_1_q0a [1]),
    .Q0A(\十二进制计数器或二十四进制的计数器电路_1_q0a [0]), .Q1D(\十二进制计数器或二十四进制的计数器电路_1_q1a [3]),
    .Q1C(\十二进制计数器或二十四进制的计数器电路_1_q1a [2]), .Q1B(\十二进制计数器或二十四进制的计数器电路_1_q1a [1]),
    .Q1A(\十二进制计数器或二十四进制的计数器电路_1_q1a [0]));
  Button button_3 (.out(button_3_out));
  Button button_4 (.out(button_4_out));
  Button button_5 (.out(button_5_out));
  Hex_Digit_Display hex_digit_display_3 (.value(\四位二进制可逆计数器_1_qa ), .dp(1'b0));
  \四位二进制可逆计数器  \u_四位二进制可逆计数器_1  (
    .D(1'b1), .C(1'b1), .B(1'b1), .A(1'b1), .QD(\四位二进制可逆计数器_1_qa [3]), .QC(\四位二进制可逆计数器_1_qa [2]),
    .QB(\四位二进制可逆计数器_1_qa [1]), .QA(\四位二进制可逆计数器_1_qa [0]), .LD(1'b1), .CPu(\十二进制计数器或二十四进制的计数器电路_1_qcc ),
    .CPd(button_4_out), .CLR(button_5_out));
endmodule

module \上下午文字显示的电路  (
  input  AM_FM,
  input  TT,
  output [4:0] out_3,
  output [4:0] out_4,
  output [4:0] out_5,
  output [4:0] out_6
);

  wire [19:0] multiplexer_1_out;

  Multiplexer #(.select(1), .width(20), .disabled("Z"), .enable("false")) multiplexer_1 (
    .in0(20'hfca1), .in1(20'h87e90), .out(multiplexer_1_out), .sel(AM_FM));
  Multiplexer #(.select(1), .width(20), .disabled("Z"), .enable("false")) multiplexer_2 (
    .in0({20{1'b0}}), .in1(multiplexer_1_out), .out({out_6, out_5, out_4, out_3}), .sel(TT));
endmodule

module \上下午文字显示测试电路  (
  input  in_1,
  input  in_2
);

  wire [4:0] \上下午文字显示的电路_1_out_3 , \上下午文字显示的电路_1_out_4 , \上下午文字显示的电路_1_out_5 , \上下午文字显示的电路_1_out_6 ;

  DotMatrix #(.inputtype("column"), .matrixcols(4), .matrixrows(5), .persist(0), .dotshape("square")) dotmatrix_1 (
    .col0(\上下午文字显示的电路_1_out_6 ), .col1(\上下午文字显示的电路_1_out_5 ), .col2(\上下午文字显示的电路_1_out_4 ),
    .col3(\上下午文字显示的电路_1_out_3 ));
  \上下午文字显示的电路  \u_上下午文字显示的电路_1  (
    .AM_FM(in_1), .TT(in_2), .out_3(\上下午文字显示的电路_1_out_3 ), .out_4(\上下午文字显示的电路_1_out_4 ),
    .out_5(\上下午文字显示的电路_1_out_5 ), .out_6(\上下午文字显示的电路_1_out_6 ));
endmodule

module \电子钟整点报时电路  (
  input  CPU,
  input  in_2,
  input  ADJ,
  input  CPD,
  input  CLR,
  output [3:0] out_6,
  output [3:0] out_7,
  output [3:0] out_8,
  output [3:0] out_9,
  output [3:0] out_10,
  output [3:0] out_11,
  output out_12
);

  wire \六十进制计数器_1_qcc , \六十进制计数器_2_qcc ;

  \六十进制计数器  \u_六十进制计数器_1  (
    .CPU(CPU), .CPD(CPD), .CLR(CLR), .Adj(ADJ), .Qcc(\六十进制计数器_1_qcc ), .Q0D(out_7[3]), .Q0C(out_7[2]),
    .Q0B(out_7[1]), .Q0A(out_7[0]), .Q1D(out_6[3]), .Q1C(out_6[2]), .Q1B(out_6[1]), .Q1A(out_6[0]));
  \六十进制计数器  \u_六十进制计数器_2  (
    .CPU(\六十进制计数器_1_qcc ), .CPD(CPD), .CLR(CLR), .Adj(ADJ), .Qcc(\六十进制计数器_2_qcc ), .Q0D(out_9[3]),
    .Q0C(out_9[2]), .Q0B(out_9[1]), .Q0A(out_9[0]), .Q1D(out_8[3]), .Q1C(out_8[2]), .Q1B(out_8[1]),
    .Q1A(out_8[0]));
  \十二进制计数器或二十四进制的计数器电路  \u_十二进制计数器或二十四进制的计数器电路_1  (
    .SET(in_2), .CPU(\六十进制计数器_2_qcc ), .CPD(CPD), .CLR(CLR), .Adj(ADJ), .Q0D(out_11[3]), .Q0C(out_11[2]),
    .Q0B(out_11[1]), .Q0A(out_11[0]), .Q1D(out_10[3]), .Q1C(out_10[2]), .Q1B(out_10[1]), .Q1A(out_10[0]));  // open: Qcc
  and and_1 (out_12, out_6[2], out_6[0], out_8[2], out_8[0], out_9[3], out_9[0]);
endmodule

module \电子钟整点报时电路测试电路  (
  input  in_1,
  input  in_2
);

  wire button_1_out, button_2_out, clock_1_out, \电子钟整点报时电路_1_out_12 ;
  wire [3:0] \电子钟整点报时电路_1_out_6 , \电子钟整点报时电路_1_out_7 , \电子钟整点报时电路_1_out_8 , \电子钟整点报时电路_1_out_9 ,
       \电子钟整点报时电路_1_out_10 , \电子钟整点报时电路_1_out_11 ;

  Hex_Digit_Display hex_digit_display_1 (.value(\电子钟整点报时电路_1_out_11 ), .dp(1'b0));
  Hex_Digit_Display hex_digit_display_2 (.value(\电子钟整点报时电路_1_out_10 ), .dp(1'b0));
  Clock #(.highDuration(1), .lowDuration(1)) clock_1 (.out(clock_1_out));
  Button button_1 (.out(button_1_out));
  Hex_Digit_Display hex_digit_display_3 (.value(\电子钟整点报时电路_1_out_8 ), .dp(1'b0));
  \电子钟整点报时电路  \u_电子钟整点报时电路_1  (
    .CPU(clock_1_out), .ADJ(in_1), .CPD(button_1_out), .CLR(button_2_out), .out_12(\电子钟整点报时电路_1_out_12 ),
    .in_2(in_2), .out_6(\电子钟整点报时电路_1_out_6 ), .out_7(\电子钟整点报时电路_1_out_7 ), .out_8(\电子钟整点报时电路_1_out_8 ),
    .out_9(\电子钟整点报时电路_1_out_9 ), .out_10(\电子钟整点报时电路_1_out_10 ), .out_11(\电子钟整点报时电路_1_out_11 ));
  Hex_Digit_Display hex_digit_display_4 (.value(\电子钟整点报时电路_1_out_6 ), .dp(1'b0));
  Hex_Digit_Display hex_digit_display_5 (.value(\电子钟整点报时电路_1_out_9 ), .dp(1'b0));
  Hex_Digit_Display hex_digit_display_6 (.value(\电子钟整点报时电路_1_out_7 ), .dp(1'b0));
  LED #(.active("true")) led_1 (.in(\电子钟整点报时电路_1_out_12 ));
  Button button_2 (.out(button_2_out));
endmodule

module \秒脉冲产生电路  (
  input  in_1,
  output out_2
);

  wire \四位二进制可逆计数器_1_qa , \四位二进制可逆计数器_1_qb , \四位二进制可逆计数器_1_qc ;

  \四位二进制可逆计数器  \u_四位二进制可逆计数器_1  (
    .D(1'b1), .C(1'b1), .B(1'b1), .A(1'b1), .QC(\四位二进制可逆计数器_1_qc ), .QB(\四位二进制可逆计数器_1_qb ),
    .QA(\四位二进制可逆计数器_1_qa ), .LD(1'b1), .CPu(in_1), .CPd(1'b0), .CLR(1'b0));  // open: QD
  and and_1 (out_2, in_1, \四位二进制可逆计数器_1_qc , \四位二进制可逆计数器_1_qb , \四位二进制可逆计数器_1_qa );
endmodule

module \多功能数字钟  (
  input  in_1,
  input  Adj0,
  input  Adj1,
  input  CLR,
  input  CPD,
  input  SET,
  input  CPU,
  output [3:0] out_8,
  output [3:0] out_9,
  output [4:0] out_10,
  output [4:0] out_11,
  output [4:0] out_12,
  output [4:0] out_13,
  output [3:0] out_14,
  output [3:0] out_15,
  output [3:0] out_16,
  output [3:0] out_17,
  output LED
);

  wire and_1_out, and_2_out, and_4_out, and_5_out, and_6_out, comparator_1_eq, comparator_2_eq,
       multiplexer_1_out, multiplexer_2_out, multiplexer_3_out, multiplexer_5_out, multiplexer_6_out,
       not_1_out, not_2_out, or_1_out, or_2_out, or_3_out, t_ff_1_q, \六十进制计数器_1_qcc , \六十进制计数器_2_qcc ,
       \十二进制计数器或二十四进制的计数器电路_1_qcc , \秒脉冲产生电路_1_out_2 ;
  wire [3:0] \十二进制计数器或二十四进制的计数器电路_1_q0a , \十二进制计数器或二十四进制的计数器电路_1_q1a ;

  \秒脉冲产生电路  \u_秒脉冲产生电路_1  (.in_1(in_1), .out_2(\秒脉冲产生电路_1_out_2 ));
  and and_1 (and_1_out, Adj0, Adj1);
  and and_2 (and_2_out, Adj0, not_1_out);
  not not_1 (not_1_out, Adj1);
  \六十进制计数器  \u_六十进制计数器_1  (
    .CPU(\秒脉冲产生电路_1_out_2 ), .CPD(1'b0), .CLR(CLR), .Adj(1'b0), .Qcc(\六十进制计数器_1_qcc ), .Q0D(out_15[3]),
    .Q0C(out_15[2]), .Q0B(out_15[1]), .Q0A(out_15[0]), .Q1D(out_14[3]), .Q1C(out_14[2]), .Q1B(out_14[1]),
    .Q1A(out_14[0]));
  Multiplexer #(.select(1), .width(1), .disabled("Z"), .enable("false")) multiplexer_1 (
    .in0(1'b0), .in1(CPD), .out(multiplexer_1_out), .sel(and_1_out));
  Multiplexer #(.select(1), .width(1), .disabled("Z"), .enable("false")) multiplexer_2 (
    .in0(\六十进制计数器_1_qcc ), .in1(CPU), .out(multiplexer_2_out), .sel(and_1_out));
  \六十进制计数器  \u_六十进制计数器_2  (
    .CPU(multiplexer_2_out), .CPD(multiplexer_1_out), .CLR(CLR), .Adj(and_1_out), .Qcc(\六十进制计数器_2_qcc ),
    .Q0D(out_17[3]), .Q0C(out_17[2]), .Q0B(out_17[1]), .Q0A(out_17[0]), .Q1D(out_16[3]), .Q1C(out_16[2]),
    .Q1B(out_16[1]), .Q1A(out_16[0]));
  and and_3 (LED, out_17[3], out_17[0], out_16[2], \秒脉冲产生电路_1_out_2 , out_16[0], out_14[2], out_14[0]);
  Multiplexer #(.select(1), .width(1), .disabled("Z"), .enable("false")) multiplexer_3 (
    .in0(\六十进制计数器_2_qcc ), .in1(1'b0), .out(multiplexer_3_out), .sel(and_1_out));
  Multiplexer #(.select(1), .width(4), .disabled("Z"), .enable("false")) multiplexer_4 (
    .in0(4'b0001), .in1(\十二进制计数器或二十四进制的计数器电路_1_q1a ), .out(out_8), .sel(or_1_out));
  Multiplexer #(.select(1), .width(1), .disabled("Z"), .enable("false")) multiplexer_5 (
    .in0(multiplexer_3_out), .in1(CPU), .out(multiplexer_5_out), .sel(and_2_out));
  Multiplexer #(.select(1), .width(1), .disabled("Z"), .enable("false")) multiplexer_6 (
    .in0(1'b0), .in1(CPD), .out(multiplexer_6_out), .sel(and_2_out));
  Multiplexer #(.select(1), .width(4), .disabled("Z"), .enable("false")) multiplexer_7 (
    .in0(4'b0010), .in1(\十二进制计数器或二十四进制的计数器电路_1_q0a ), .out(out_9), .sel(or_1_out));
  \十二进制计数器或二十四进制的计数器电路  \u_十二进制计数器或二十四进制的计数器电路_1  (
    .SET(SET), .CPU(multiplexer_5_out), .CPD(multiplexer_6_out), .CLR(CLR), .Adj(and_2_out),
    .Qcc(\十二进制计数器或二十四进制的计数器电路_1_qcc ), .Q0D(\十二进制计数器或二十四进制的计数器电路_1_q0a [3]),
    .Q0C(\十二进制计数器或二十四进制的计数器电路_1_q0a [2]), .Q0B(\十二进制计数器或二十四进制的计数器电路_1_q0a [1]),
    .Q0A(\十二进制计数器或二十四进制的计数器电路_1_q0a [0]), .Q1D(\十二进制计数器或二十四进制的计数器电路_1_q1a [3]),
    .Q1C(\十二进制计数器或二十四进制的计数器电路_1_q1a [2]), .Q1B(\十二进制计数器或二十四进制的计数器电路_1_q1a [1]),
    .Q1A(\十二进制计数器或二十四进制的计数器电路_1_q1a [0]));
  Comparator #(.width(4), .mode("twosComplement")) comparator_1 (
    .a(\十二进制计数器或二十四进制的计数器电路_1_q1a ), .b(4'b0001), .eq(comparator_1_eq));  // open: gt, lt
  Comparator #(.width(4), .mode("twosComplement")) comparator_2 (
    .a(4'b0001), .b(\十二进制计数器或二十四进制的计数器电路_1_q0a ), .eq(comparator_2_eq));  // open: gt, lt
  or or_1 (or_1_out, or_2_out, SET);
  or or_2 (or_2_out, \十二进制计数器或二十四进制的计数器电路_1_q1a [3], \十二进制计数器或二十四进制的计数器电路_1_q1a [2], \十二进制计数器或二十四进制的计数器电路_1_q1a [1], \十二进制计数器或二十四进制的计数器电路_1_q1a [0], \十二进制计数器或二十四进制的计数器电路_1_q0a [3], \十二进制计数器或二十四进制的计数器电路_1_q0a [2], \十二进制计数器或二十四进制的计数器电路_1_q0a [1], \十二进制计数器或二十四进制的计数器电路_1_q0a [0]);
  and and_4 (and_4_out, comparator_1_eq, comparator_2_eq);
  and and_5 (and_5_out, and_4_out, multiplexer_5_out);
  and and_6 (and_6_out, t_ff_1_q, or_2_out, CPD);
  or or_3 (or_3_out, and_5_out, and_6_out, \十二进制计数器或二十四进制的计数器电路_1_qcc );
  \上下午文字显示的电路  \u_上下午文字显示的电路_1  (
    .AM_FM(t_ff_1_q), .TT(not_2_out), .out_3(out_13), .out_4(out_12), .out_5(out_11), .out_6(out_10));
  T_Flip_Flop #(.trigger("rising"), .Pre_Clr_Positions("ABOVE_BELOW"), .NegatePresetClear("false"), .enable("false"), .NewFFLayout("true")) t_ff_1 (
    .clk(or_3_out), .T(1'b1), .Q(t_ff_1_q), .preset(1'b0), .reset(CLR));  // open: Qn
  not not_2 (not_2_out, SET);
endmodule

module \多功能数字钟测试电路  (
  input  in_1,
  input  in_2,
  input  in_3
);

  wire button_1_out, button_2_out, button_3_out, clock_1_out, \多功能数字钟_1_led ;
  wire [3:0] \多功能数字钟_1_out_8 , \多功能数字钟_1_out_9 , \多功能数字钟_1_out_14 , \多功能数字钟_1_out_15 , \多功能数字钟_1_out_16 ,
       \多功能数字钟_1_out_17 ;
  wire [4:0] \多功能数字钟_1_out_10 , \多功能数字钟_1_out_11 , \多功能数字钟_1_out_12 , \多功能数字钟_1_out_13 ;

  DotMatrix #(.inputtype("column"), .matrixcols(4), .matrixrows(5), .persist(0), .dotshape("square")) dotmatrix_1 (
    .col0(\多功能数字钟_1_out_10 ), .col1(\多功能数字钟_1_out_11 ), .col2(\多功能数字钟_1_out_12 ), .col3(\多功能数字钟_1_out_13 ));
  Clock #(.highDuration(1), .lowDuration(1)) clock_1 (.out(clock_1_out));
  Hex_Digit_Display hex_digit_display_1 (.value(\多功能数字钟_1_out_8 ), .dp(1'b0));
  \多功能数字钟  \u_多功能数字钟_1  (
    .in_1(clock_1_out), .Adj0(in_1), .Adj1(in_2), .CLR(button_3_out), .CPD(button_1_out), .CPU(button_2_out),
    .LED(\多功能数字钟_1_led ), .out_14(\多功能数字钟_1_out_14 ), .out_15(\多功能数字钟_1_out_15 ), .out_16(\多功能数字钟_1_out_16 ),
    .out_17(\多功能数字钟_1_out_17 ), .out_8(\多功能数字钟_1_out_8 ), .out_9(\多功能数字钟_1_out_9 ),
    .out_10(\多功能数字钟_1_out_10 ), .out_11(\多功能数字钟_1_out_11 ), .out_12(\多功能数字钟_1_out_12 ),
    .out_13(\多功能数字钟_1_out_13 ), .SET(in_3));
  Button button_1 (.out(button_1_out));
  Button button_2 (.out(button_2_out));
  Hex_Digit_Display hex_digit_display_2 (.value(\多功能数字钟_1_out_16 ), .dp(1'b0));
  Hex_Digit_Display hex_digit_display_3 (.value(\多功能数字钟_1_out_9 ), .dp(1'b0));
  Hex_Digit_Display hex_digit_display_4 (.value(\多功能数字钟_1_out_17 ), .dp(1'b0));
  LED #(.active("true")) led_1 (.in(\多功能数字钟_1_led ));
  Button button_3 (.out(button_3_out));
  Hex_Digit_Display hex_digit_display_5 (.value(\多功能数字钟_1_out_14 ), .dp(1'b0));
  Hex_Digit_Display hex_digit_display_6 (.value(\多功能数字钟_1_out_15 ), .dp(1'b0));
endmodule
