// Logisim project 实验6-CS2003-U202015375-汪宇飞.circ as structural Verilog: 7 circuits, main circuit sqrX
module sqrX (
  input  [31:0] a,
  input  [31:0] b,
  input  [31:0] c,
  input  [31:0] d,
  output [31:0] a_prime,
  output [31:0] b_prime,
  output [31:0] c_prime,
  output [31:0] d_prime
);

  wire [31:0] multiplier_1_out, multiplier_2_out, multiplier_3_out, multiplier_4_out, multiplier_5_out,
       multiplier_6_out, multiplier_7_out;

  Multiplier #(.width(32)) multiplier_1 (.a(a), .b(a), .out(multiplier_1_out), .cin({32{1'b0}}));  // open: cout
  Multiplier #(.width(32)) multiplier_2 (.a(b), .b(c), .out(multiplier_2_out), .cin({32{1'b0}}));  // open: cout
  Multiplier #(.width(32)) multiplier_3 (.a(a), .b(b), .out(multiplier_3_out), .cin({32{1'b0}}));  // open: cout
  Multiplier #(.width(32)) multiplier_4 (.a(b), .b(d), .out(multiplier_4_out), .cin({32{1'b0}}));  // open: cout
  Multiplier #(.width(32)) multiplier_5 (.a(a), .b(c), .out(multiplier_5_out), .cin({32{1'b0}}));  // open: cout
  Multiplier #(.width(32)) multiplier_6 (.a(d), .b(c), .out(multiplier_6_out), .cin({32{1'b0}}));  // open: cout
  Multiplier #(.width(32)) multiplier_7 (.a(d), .b(d), .out(multiplier_7_out), .cin({32{1'b0}}));  // open: cout
  Adder #(.width(32)) adder_1 (.a(multiplier_1_out), .b(multiplier_2_out), .out(a_prime), .cin(1'b0));  // open: cout
  Adder #(.width(32)) adder_2 (.a(multiplier_3_out), .b(multiplier_4_out), .out(b_prime), .cin(1'b0));  // open: cout
  Adder #(.width(32)) adder_3 (.a(multiplier_5_out), .b(multiplier_6_out), .out(c_prime), .cin(1'b0));  // open: cout
  Adder #(.width(32)) adder_4 (.a(multiplier_2_out), .b(multiplier_7_out), .out(d_prime), .cin(1'b0));  // open: cout
endmodule

module sqrX_A (
  input  [31:0] a,
  input  [31:0] b,
  input  [31:0] c,
  input  [31:0] d,
  output [31:0] a_prime,
  output [31:0] b_prime,
  output [31:0] c_prime,
  output [31:0] d_prime
);

  wire [31:0] adder_1_out, adder_2_out, multiplier_1_out, multiplier_2_out, multiplier_3_out,
       multiplier_4_out, multiplier_5_out, multiplier_6_out, multiplier_7_out;

  Multiplier #(.width(32)) multiplier_1 (.a(a), .b(a), .out(multiplier_1_out), .cin({32{1'b0}}));  // open: cout
  Multiplier #(.width(32)) multiplier_2 (.a(b), .b(c), .out(multiplier_2_out), .cin({32{1'b0}}));  // open: cout
  Multiplier #(.width(32)) multiplier_3 (.a(a), .b(b), .out(multiplier_3_out), .cin({32{1'b0}}));  // open: cout
  Multiplier #(.width(32)) multiplier_4 (.a(b), .b(d), .out(multiplier_4_out), .cin({32{1'b0}}));  // open: cout
  Multiplier #(.width(32)) multiplier_5 (.a(a), .b(c), .out(multiplier_5_out), .cin({32{1'b0}}));  // open: cout
  Multiplier #(.width(32)) multiplier_6 (.a(d), .b(c), .out(multiplier_6_out), .cin({32{1'b0}}));  // open: cout
  Multiplier #(.width(32)) multiplier_7 (.a(d), .b(d), .out(multiplier_7_out), .cin({32{1'b0}}));  // open: cout
  Adder #(.width(32)) adder_1 (
    .a(multiplier_1_out), .b(multiplier_2_out), .out(adder_1_out), .cin(1'b0));  // open: cout
  Adder #(.width(32)) adder_2 (
    .a(multiplier_5_out), .b(multiplier_6_out), .out(adder_2_out), .cin(1'b0));  // open: cout
  Adder #(.width(32)) adder_3 (.a(multiplier_3_out), .b(multiplier_4_out), .out(a_prime), .cin(1'b0));  // open: cout
  Adder #(.width(32)) adder_4 (.a(adder_1_out), .b(a_prime), .out(b_prime), .cin(1'b0));  // open: cout
  Adder #(.width(32)) adder_5 (.a(multiplier_2_out), .b(multiplier_7_out), .out(c_prime), .cin(1'b0));  // open: cout
  Adder #(.width(32)) adder_6 (.a(c_prime), .b(adder_2_out), .out(d_prime), .cin(1'b0));  // open: cout
endmodule

module \矩阵快速幂算法迭代模块  (
  input  start,
  input  clr,
  input  n_i_1,
  input  clk,
  output [31:0] Fi
);

  wire [31:0] multiplexer_1_out, multiplexer_2_out, multiplexer_3_out, multiplexer_4_out, multiplexer_5_out,
       multiplexer_6_out, multiplexer_7_out, multiplexer_8_out, register_1_q, register_3_q, register_4_q,
       sqrx_1_a_prime, sqrx_1_b_prime, sqrx_1_c_prime, sqrx_1_d_prime, sqrx_a_1_a_prime, sqrx_a_1_b_prime,
       sqrx_a_1_c_prime, sqrx_a_1_d_prime;

  Multiplexer #(.select(1), .width(32), .disabled("Z"), .enable("false")) multiplexer_1 (
    .in0({32{1'b0}}), .in1(multiplexer_5_out), .out(multiplexer_1_out), .sel(start));
  Multiplexer #(.select(1), .width(32), .disabled("Z"), .enable("false")) multiplexer_2 (
    .in0(32'h1), .in1(multiplexer_6_out), .out(multiplexer_2_out), .sel(start));
  Multiplexer #(.select(1), .width(32), .disabled("Z"), .enable("false")) multiplexer_3 (
    .in0(32'h1), .in1(multiplexer_7_out), .out(multiplexer_3_out), .sel(start));
  Multiplexer #(.select(1), .width(32), .disabled("Z"), .enable("false")) multiplexer_4 (
    .in0(32'h1), .in1(multiplexer_8_out), .out(multiplexer_4_out), .sel(start));
  Register #(.width(32), .trigger("rising"), .Select("low")) register_1 (
    .D(multiplexer_1_out), .en(1'b1), .Q(register_1_q), .clk(clk), .clr(clr), .cs(1'b0), .preset(1'b0));
  Register #(.width(32), .trigger("rising"), .Select("low")) register_2 (
    .D(multiplexer_2_out), .en(1'b1), .Q(Fi), .clk(clk), .clr(clr), .cs(1'b0), .preset(1'b0));
  Register #(.width(32), .trigger("rising"), .Select("low")) register_3 (
    .D(multiplexer_3_out), .en(1'b1), .Q(register_3_q), .clk(clk), .clr(clr), .cs(1'b0), .preset(1'b0));
  Register #(.width(32), .trigger("rising"), .Select("low")) register_4 (
    .D(multiplexer_4_out), .en(1'b1), .Q(register_4_q), .clk(clk), .clr(clr), .cs(1'b0), .preset(1'b0));
  sqrX sqrx_1 (
    .a(register_1_q), .b(Fi), .c(register_3_q), .d(register_4_q), .a_prime(sqrx_1_a_prime),
    .b_prime(sqrx_1_b_prime), .c_prime(sqrx_1_c_prime), .d_prime(sqrx_1_d_prime));
  sqrX_A sqrx_a_1 (
    .a(register_1_q), .b(Fi), .c(register_3_q), .d(register_4_q), .a_prime(sqrx_a_1_a_prime),
    .b_prime(sqrx_a_1_b_prime), .c_prime(sqrx_a_1_c_prime), .d_prime(sqrx_a_1_d_prime));
  Multiplexer #(.select(1), .width(32), .disabled("Z"), .enable("false")) multiplexer_5 (
    .in0(sqrx_1_a_prime), .in1(sqrx_a_1_a_prime), .out(multiplexer_5_out), .sel(n_i_1));
  Multiplexer #(.select(1), .width(32), .disabled("Z"), .enable("false")) multiplexer_6 (
    .in0(sqrx_1_b_prime), .in1(sqrx_a_1_b_prime), .out(multiplexer_6_out), .sel(n_i_1));
  Multiplexer #(.select(1), .width(32), .disabled("Z"), .enable("false")) multiplexer_7 (
    .in0(sqrx_1_c_prime), .in1(sqrx_a_1_c_prime), .out(multiplexer_7_out), .sel(n_i_1));
  Multiplexer #(.select(1), .width(32), .disabled("Z"), .enable("false")) multiplexer_8 (
    .in0(sqrx_1_d_prime), .in1(sqrx_a_1_d_prime), .out(multiplexer_8_out), .sel(n_i_1));
endmodule

module \Fibonacci数显示模块  (
  input  [31:0] in_1,
  output [3:0] out_2,
  output [3:0] out_3,
  output [3:0] out_4,
  output [3:0] out_5,
  output [3:0] out_6,
  output [3:0] out_7,
  output [3:0] out_8,
  output [3:0] out_9,
  output [3:0] out_10,
  output [3:0] out_11
);

  wire [31:0] divider_1_rem, divider_2_rem, divider_3_rem, divider_4_rem, divider_5_rem, divider_6_rem,
       divider_7_rem, divider_8_rem;
  wire [31:4] divider_1_out, divider_2_out, divider_3_out, divider_4_out, divider_5_out, divider_6_out,
       divider_7_out, divider_8_out, divider_9_out, divider_9_rem;

  Divider #(.width(32)) divider_1 (
    .a(in_1), .b(32'h3b9aca00), .out({divider_1_out, out_2}), .upper({32{1'b0}}), .rem(divider_1_rem));
  Divider #(.width(32)) divider_2 (
    .a(divider_1_rem), .b(32'h5f5e100), .out({divider_2_out, out_3}), .upper({32{1'b0}}), .rem(divider_2_rem));
  Divider #(.width(32)) divider_3 (
    .a(divider_2_rem), .b(32'h989680), .out({divider_3_out, out_4}), .upper({32{1'b0}}), .rem(divider_3_rem));
  Divider #(.width(32)) divider_4 (
    .a(divider_3_rem), .b(32'hf4240), .out({divider_4_out, out_5}), .upper({32{1'b0}}), .rem(divider_4_rem));
  Divider #(.width(32)) divider_5 (
    .a(divider_4_rem), .b(32'h186a0), .out({divider_5_out, out_6}), .upper({32{1'b0}}), .rem(divider_5_rem));
  Divider #(.width(32)) divider_6 (
    .a(divider_5_rem), .b(32'h2710), .out({divider_6_out, out_7}), .upper({32{1'b0}}), .rem(divider_6_rem));
  Divider #(.width(32)) divider_7 (
    .a(divider_6_rem), .b(32'h3e8), .out({divider_7_out, out_8}), .upper({32{1'b0}}), .rem(divider_7_rem));
  Divider #(.width(32)) divider_8 (
    .a(divider_7_rem), .b(32'h64), .out({divider_8_out, out_9}), .upper({32{1'b0}}), .rem(divider_8_rem));
  Divider #(.width(32)) divider_9 (
    .a(divider_8_rem), .b(32'ha), .out({divider_9_out, out_10}), .upper({32{1'b0}}),
    .rem({divider_9_rem, out_11}));
endmodule

module \控制器  (
  input  [5:0] n,
  input  clear,
  input  clock,
  output n_i_1,
  output clk,
  output start,
  output clr
);

  wire comparator_1_gt, or_1_out, or_2_out;
  wire [7:0] counter_1_q;

  or or_1 (or_1_out, clear, clock);
  Counter #(.width(8), .max('hff), .ongoal("wrap"), .trigger("rising"), .behavior("new")) counter_1 (
    .load(1'b0), .D(8'h1), .count(1'b1), .Q(counter_1_q), .clk(clock), .clr(clear), .preset(1'b0), .down(1'b0));  // open: carry
  Shift_Register #(.width(1), .length(6), .parallel("true"), .trigger("rising")) shift_register_1 (
    .shift(1'b1), .in(1'b0), .clk(or_1_out), .out(n_i_1), .load(clear), .clr(1'b0), .d0(n[0]), .d1(n[1]),
    .d2(n[2]), .d3(n[3]), .d4(n[4]), .d5(n[5]));  // open: q0, q1, q2, q3, q4, q5
  and and_1 (clk, clock, comparator_1_gt);
  Comparator #(.width(8), .mode("twosComplement")) comparator_1 (
    .a(8'h6), .b(counter_1_q), .gt(comparator_1_gt));  // open: eq, lt
  or or_2 (or_2_out, start, n_i_1);
  D_Flip_Flop #(.trigger("rising"), .Pre_Clr_Positions("ABOVE_BELOW"), .NegatePresetClear("false"), .enable("false"), .NewFFLayout("true")) d_ff_1 (
    .clk(clock), .D(or_2_out), .Q(start), .preset(1'b0), .reset(clear));  // open: Qn

  assign clr = clear;
endmodule

module \斐波那契_Fibonacci_数列计算器  (
  input  [5:0] n,
  input  clear,
  input  clock,
  output [3:0] D9,
  output [3:0] D8,
  output [3:0] D7,
  output [3:0] D6,
  output [3:0] D5,
  output [3:0] D4,
  output [3:0] D3,
  output [3:0] D2,
  output [3:0] D1,
  output [3:0] D0
);

  wire \控制器_1_clk , \控制器_1_clr , \控制器_1_n_i_1 , \控制器_1_start ;
  wire [31:0] \矩阵快速幂算法迭代模块_1_fi ;

  \控制器  \u_控制器_1  (
    .n(n), .clear(clear), .clock(clock), .n_i_1(\控制器_1_n_i_1 ), .clk(\控制器_1_clk ), .start(\控制器_1_start ),
    .clr(\控制器_1_clr ));
  \矩阵快速幂算法迭代模块  \u_矩阵快速幂算法迭代模块_1  (
    .start(\控制器_1_start ), .clr(\控制器_1_clr ), .clk(\控制器_1_clk ), .Fi(\矩阵快速幂算法迭代模块_1_fi ),
    .n_i_1(\控制器_1_n_i_1 ));
  \Fibonacci数显示模块  \fibonacci数显示模块_1  (
    .in_1(\矩阵快速幂算法迭代模块_1_fi ), .out_2(D9), .out_3(D8), .out_4(D7), .out_5(D6), .out_6(D5), .out_7(D4),
    .out_8(D3), .out_9(D2), .out_10(D1), .out_11(D0));
endmodule

module \斐波那契_Fibonacci_数列计算器验证电路  (
  input  [5:0] in_1
);

  wire button_1_out, button_2_out;
  wire [3:0] \斐波那契_fibonacci_数列计算器_1_d0 , \斐波那契_fibonacci_数列计算器_1_d1 , \斐波那契_fibonacci_数列计算器_1_d2 ,
       \斐波那契_fibonacci_数列计算器_1_d3 , \斐波那契_fibonacci_数列计算器_1_d4 , \斐波那契_fibonacci_数列计算器_1_d5 ,
       \斐波那契_fibonacci_数列计算器_1_d6 , \斐波那契_fibonacci_数列计算器_1_d7 , \斐波那契_fibonacci_数列计算器_1_d8 ,
       \斐波那契_fibonacci_数列计算器_1_d9 ;

  Button button_1 (.out(button_1_out));
  Button button_2 (.out(button_2_out));
  \斐波那契_Fibonacci_数列计算器  \u_斐波那契_fibonacci_数列计算器_1  (
    .n(in_1), .clear(button_1_out), .clock(button_2_out), .D9(\斐波那契_fibonacci_数列计算器_1_d9 ),
    .D8(\斐波那契_fibonacci_数列计算器_1_d8 ), .D7(\斐波那契_fibonacci_数列计算器_1_d7 ), .D6(\斐波那契_fibonacci_数列计算器_1_d6 ),
    .D5(\斐波那契_fibonacci_数列计算器_1_d5 ), .D4(\斐波那契_fibonacci_数列计算器_1_d4 ), .D3(\斐波那契_fibonacci_数列计算器_1_d3 ),
    .D2(\斐波那契_fibonacci_数列计算器_1_d2 ), .D1(\斐波那契_fibonacci_数列计算器_1_d1 ), .D0(\斐波那契_fibonacci_数列计算器_1_d0 ));
  Hex_Digit_Display hex_digit_display_1 (.value(\斐波那契_fibonacci_数列计算器_1_d9 ), .dp(1'b0));
  Hex_Digit_Display hex_digit_display_2 (.value(\斐波那契_fibonacci_数列计算器_1_d7 ), .dp(1'b0));
  Hex_Digit_Display hex_digit_display_3 (.value(\斐波那契_fibonacci_数列计算器_1_d8 ), .dp(1'b0));
  Hex_Digit_Display hex_digit_display_4 (.value(\斐波那契_fibonacci_数列计算器_1_d6 ), .dp(1'b0));
  Hex_Digit_Display hex_digit_display_5 (.value(\斐波那契_fibonacci_数列计算器_1_d4 ), .dp(1'b0));
  Hex_Digit_Display hex_digit_display_6 (.value(\斐波那契_fibonacci_数列计算器_1_d5 ), .dp(1'b0));
  Hex_Digit_Display hex_digit_display_7 (.value(\斐波那契_fibonacci_数列计算器_1_d3 ), .dp(1'b0));
  Hex_Digit_Display hex_digit_display_8 (.value(\斐波那契_fibonacci_数列计算器_1_d2 ), .dp(1'b0));
  Hex_Digit_Display hex_digit_display_9 (.value(\斐波那契_fibonacci_数列计算器_1_d1 ), .dp(1'b0));
  Hex_Digit_Display hex_digit_display_10 (.value(\斐波那契_fibonacci_数列计算器_1_d0 ), .dp(1'b0));
endmodule
