// Logisim project 实验4-CS2003-U202015375-汪宇飞.circ as structural Verilog: 5 circuits, main circuit 四位除法器
module \四位除法器  (
  input  [3:0] n2,
  input  [3:0] d,
  output [3:0] rem,
  output [3:0] quot
);

  wire comparator_1_eq, comparator_1_gt, comparator_2_eq, comparator_3_eq, comparator_3_gt, comparator_4_eq,
       comparator_4_gt, comparator_5_eq, comparator_5_gt, or_2_out, or_4_out, or_6_out, or_8_out;
  wire [3:0] multiplexer_1_out, multiplexer_2_out, multiplexer_3_out, multiplexer_4_out, multiplexer_5_out,
       multiplexer_6_out, multiplexer_7_out, multiplexer_8_out, or_1_out, or_3_out, or_5_out, or_7_out,
       subtractor_1_out, subtractor_2_out, subtractor_3_out, subtractor_4_out;
  wire [7:0] shifter_1_out, shifter_2_out, shifter_3_out, shifter_4_out;

  Subtractor #(.width(4)) subtractor_1 (
    .a(shifter_1_out[7:4]), .b(d), .out(subtractor_1_out), .bin(1'b0));  // open: bout
  Shifter #(.width(8), .shift("ll")) shifter_1 (.in({4'b0000, n2}), .\dist (3'b001), .out(shifter_1_out));
  Multiplexer #(.select(1), .width(4), .disabled("Z"), .enable("false")) multiplexer_1 (
    .in0(shifter_1_out[7:4]), .in1(subtractor_1_out), .out(multiplexer_1_out), .sel(or_2_out));
  Comparator #(.width(4), .mode("unsigned")) comparator_1 (
    .a(shifter_1_out[7:4]), .b(d), .gt(comparator_1_gt), .eq(comparator_1_eq));  // open: lt
  Multiplexer #(.select(1), .width(4), .disabled("Z"), .enable("false")) multiplexer_2 (
    .in0(shifter_1_out[3:0]), .in1(or_1_out), .out(multiplexer_2_out), .sel(or_2_out));
  assign or_1_out = shifter_1_out[3:0] | 4'b0001;  // OR_Gate or_1, 4 bits wide
  or or_2 (or_2_out, comparator_1_gt, comparator_1_eq);
  Shifter #(.width(8), .shift("ll")) shifter_2 (
    .in({multiplexer_1_out, multiplexer_2_out}), .\dist (3'b001), .out(shifter_2_out));
  Subtractor #(.width(4)) subtractor_2 (
    .a(shifter_2_out[7:4]), .b(d), .out(subtractor_2_out), .bin(1'b0));  // open: bout
  Comparator #(.width(4), .mode("twosComplement")) comparator_2 (
    .a(d), .b(4'b0000), .eq(comparator_2_eq));  // open: gt, lt
  Multiplexer #(.select(1), .width(4), .disabled("Z"), .enable("false")) multiplexer_3 (
    .in0(shifter_2_out[7:4]), .in1(subtractor_2_out), .out(multiplexer_3_out), .sel(or_4_out));
  Comparator #(.width(4), .mode("unsigned")) comparator_3 (
    .a(shifter_2_out[7:4]), .b(d), .gt(comparator_3_gt), .eq(comparator_3_eq));  // open: lt
  Multiplexer #(.select(1), .width(4), .disabled("Z"), .enable("false")) multiplexer_4 (
    .in0(shifter_2_out[3:0]), .in1(or_3_out), .out(multiplexer_4_out), .sel(or_4_out));
  assign or_3_out = shifter_2_out[3:0] | 4'b0001;  // OR_Gate or_3, 4 bits wide
  or or_4 (or_4_out, comparator_3_gt, comparator_3_eq);
  Subtractor #(.width(4)) subtractor_3 (
    .a(shifter_3_out[7:4]), .b(d), .out(subtractor_3_out), .bin(1'b0));  // open: bout
  Shifter #(.width(8), .shift("ll")) shifter_3 (
    .in({multiplexer_3_out, multiplexer_4_out}), .\dist (3'b001), .out(shifter_3_out));
  assign or_5_out = shifter_3_out[3:0] | 4'b0001;  // OR_Gate or_5, 4 bits wide
  Multiplexer #(.select(1), .width(4), .disabled("Z"), .enable("false")) multiplexer_5 (
    .in0(shifter_3_out[7:4]), .in1(subtractor_3_out), .out(multiplexer_5_out), .sel(or_6_out));
  or or_6 (or_6_out, comparator_4_gt, comparator_4_eq);
  Comparator #(.width(4), .mode("unsigned")) comparator_4 (
    .a(shifter_3_out[7:4]), .b(d), .gt(comparator_4_gt), .eq(comparator_4_eq));  // open: lt
  Multiplexer #(.select(1), .width(4), .disabled("Z"), .enable("false")) multiplexer_6 (
    .in0(shifter_3_out[3:0]), .in1(or_5_out), .out(multiplexer_6_out), .sel(or_6_out));
  Subtractor #(.width(4)) subtractor_4 (
    .a(shifter_4_out[7:4]), .b(d), .out(subtractor_4_out), .bin(1'b0));  // open: bout
  Shifter #(.width(8), .shift("ll")) shifter_4 (
    .in({multiplexer_5_out, multiplexer_6_out}), .\dist (3'b001), .out(shifter_4_out));
  assign or_7_out = shifter_4_out[3:0] | 4'b0001;  // OR_Gate or_7, 4 bits wide
  Multiplexer #(.select(1), .width(4), .disabled("Z"), .enable("false")) multiplexer_7 (
    .in0(shifter_4_out[7:4]), .in1(subtractor_4_out), .out(multiplexer_7_out), .sel(or_8_out));
  or or_8 (or_8_out, comparator_5_gt, comparator_5_eq);
  Comparator #(.width(4), .mode("unsigned")) comparator_5 (
    .a(shifter_4_out[7:4]), .b(d), .gt(comparator_5_gt), .eq(comparator_5_eq));  // open: lt
  Multiplexer #(.select(1), .width(4), .disabled("Z"), .enable("false")) multiplexer_8 (
    .in0(shifter_4_out[3:0]), .in1(or_7_out), .out(multiplexer_8_out), .sel(or_8_out));
  Multiplexer #(.select(1), .width(4), .disabled("Z"), .enable("false")) multiplexer_9 (
    .in0(multiplexer_7_out), .in1(4'b0000), .out(rem), .sel(comparator_2_eq));
  Multiplexer #(.select(1), .width(4), .disabled("Z"), .enable("false")) multiplexer_10 (
    .in0(multiplexer_8_out), .in1(n2), .out(quot), .sel(comparator_2_eq));
endmodule

module \四位除法器测试电路  (
  input  [3:0] n2,
  input  [3:0] d,
  output [3:0] out_3,
  output [3:0] out_4
);

  wire [3:0] divider_1_out, divider_1_rem, \四位除法器_1_quot , \四位除法器_1_rem ;

  \四位除法器  \u_四位除法器_1  (.n2(n2), .d(d), .rem(\四位除法器_1_rem ), .quot(\四位除法器_1_quot ));
  Divider #(.width(4)) divider_1 (.a(n2), .b(d), .out(divider_1_out), .upper(4'b0000), .rem(divider_1_rem));
  assign out_3 = \四位除法器_1_quot  ^ divider_1_out;  // XOR_Gate xor_1, 4 bits wide
  assign out_4 = \四位除法器_1_rem  ^ divider_1_rem;  // XOR_Gate xor_2, 4 bits wide
endmodule

module \_32位除法器  (
  input  [31:0] n2,
  input  [31:0] d,
  output [31:0] rem,
  output [31:0] quot
);

  wire comparator_1_eq;
  wire [31:0] div1_1_quot_2, div1_1_rem_2, div1_2_quot_2, div1_2_rem_2, div1_3_quot_2, div1_3_rem_2,
       div1_4_quot_2, div1_4_rem_2, div1_5_quot_2, div1_5_rem_2, div1_6_quot_2, div1_6_rem_2, div1_7_quot_2,
       div1_7_rem_2, div1_8_quot_2, div1_8_rem_2, div1_9_quot_2, div1_9_rem_2, div1_10_quot_2, div1_10_rem_2,
       div1_11_quot_2, div1_11_rem_2, div1_12_quot_2, div1_12_rem_2, div1_13_quot_2, div1_13_rem_2,
       div1_14_quot_2, div1_14_rem_2, div1_15_quot_2, div1_15_rem_2, div1_16_quot_2, div1_16_rem_2,
       div1_17_quot_2, div1_17_rem_2, div1_18_quot_2, div1_18_rem_2, div1_19_quot_2, div1_19_rem_2,
       div1_20_quot_2, div1_20_rem_2, div1_21_quot_2, div1_21_rem_2, div1_22_quot_2, div1_22_rem_2,
       div1_23_quot_2, div1_23_rem_2, div1_24_quot_2, div1_24_rem_2, div1_25_quot_2, div1_25_rem_2,
       div1_26_quot_2, div1_26_rem_2, div1_27_quot_2, div1_27_rem_2, div1_28_quot_2, div1_28_rem_2,
       div1_29_quot_2, div1_29_rem_2, div1_30_quot_2, div1_30_rem_2, div1_31_quot_2, div1_31_rem_2,
       div1_32_quot_2, div1_32_rem_2;

  Div1 div1_1 (.d(d), .rem({32{1'b0}}), .quot(n2), .rem_2(div1_1_rem_2), .quot_2(div1_1_quot_2));
  Div1 div1_2 (.d(d), .rem(div1_25_rem_2), .quot(div1_25_quot_2), .rem_2(div1_2_rem_2), .quot_2(div1_2_quot_2));
  Div1 div1_3 (.d(d), .rem(div1_26_rem_2), .quot(div1_26_quot_2), .rem_2(div1_3_rem_2), .quot_2(div1_3_quot_2));
  Div1 div1_4 (.d(d), .rem(div1_27_rem_2), .quot(div1_27_quot_2), .rem_2(div1_4_rem_2), .quot_2(div1_4_quot_2));
  Div1 div1_5 (.d(d), .rem(div1_28_rem_2), .quot(div1_28_quot_2), .rem_2(div1_5_rem_2), .quot_2(div1_5_quot_2));
  Div1 div1_6 (.d(d), .rem(div1_29_rem_2), .quot(div1_29_quot_2), .rem_2(div1_6_rem_2), .quot_2(div1_6_quot_2));
  Div1 div1_7 (.d(d), .rem(div1_30_rem_2), .quot(div1_30_quot_2), .rem_2(div1_7_rem_2), .quot_2(div1_7_quot_2));
  Div1 div1_8 (.d(d), .rem(div1_31_rem_2), .quot(div1_31_quot_2), .rem_2(div1_8_rem_2), .quot_2(div1_8_quot_2));
  Div1 div1_9 (.d(d), .rem(div1_1_rem_2), .quot(div1_1_quot_2), .rem_2(div1_9_rem_2), .quot_2(div1_9_quot_2));
  Div1 div1_10 (.d(d), .rem(div1_2_rem_2), .quot(div1_2_quot_2), .rem_2(div1_10_rem_2), .quot_2(div1_10_quot_2));
  Div1 div1_11 (.d(d), .rem(div1_3_rem_2), .quot(div1_3_quot_2), .rem_2(div1_11_rem_2), .quot_2(div1_11_quot_2));
  Div1 div1_12 (.d(d), .rem(div1_4_rem_2), .quot(div1_4_quot_2), .rem_2(div1_12_rem_2), .quot_2(div1_12_quot_2));
  Div1 div1_13 (.d(d), .rem(div1_5_rem_2), .quot(div1_5_quot_2), .rem_2(div1_13_rem_2), .quot_2(div1_13_quot_2));
  Div1 div1_14 (.d(d), .rem(div1_6_rem_2), .quot(div1_6_quot_2), .rem_2(div1_14_rem_2), .quot_2(div1_14_quot_2));
  Div1 div1_15 (.d(d), .rem(div1_7_rem_2), .quot(div1_7_quot_2), .rem_2(div1_15_rem_2), .quot_2(div1_15_quot_2));
  Div1 div1_16 (.d(d), .rem(div1_8_rem_2), .quot(div1_8_quot_2), .rem_2(div1_16_rem_2), .quot_2(div1_16_quot_2));
  Div1 div1_17 (.d(d), .rem(div1_9_rem_2), .quot(div1_9_quot_2), .rem_2(div1_17_rem_2), .quot_2(div1_17_quot_2));
  Div1 div1_18 (.d(d), .rem(div1_10_rem_2), .quot(div1_10_quot_2), .rem_2(div1_18_rem_2), .quot_2(div1_18_quot_2));
  Div1 div1_19 (.d(d), .rem(div1_11_rem_2), .quot(div1_11_quot_2), .rem_2(div1_19_rem_2), .quot_2(div1_19_quot_2));
  Div1 div1_20 (.d(d), .rem(div1_12_rem_2), .quot(div1_12_quot_2), .rem_2(div1_20_rem_2), .quot_2(div1_20_quot_2));
  Div1 div1_21 (.d(d), .rem(div1_13_rem_2), .quot(div1_13_quot_2), .rem_2(div1_21_rem_2), .quot_2(div1_21_quot_2));
  Div1 div1_22 (.d(d), .rem(div1_14_rem_2), .quot(div1_14_quot_2), .rem_2(div1_22_rem_2), .quot_2(div1_22_quot_2));
  Div1 div1_23 (.d(d), .rem(div1_15_rem_2), .quot(div1_15_quot_2), .rem_2(div1_23_rem_2), .quot_2(div1_23_quot_2));
  Div1 div1_24 (.d(d), .rem(div1_16_rem_2), .quot(div1_16_quot_2), .rem_2(div1_24_rem_2), .quot_2(div1_24_quot_2));
  Div1 div1_25 (.d(d), .rem(div1_17_rem_2), .quot(div1_17_quot_2), .rem_2(div1_25_rem_2), .quot_2(div1_25_quot_2));
  Div1 div1_26 (.d(d), .rem(div1_18_rem_2), .quot(div1_18_quot_2), .rem_2(div1_26_rem_2), .quot_2(div1_26_quot_2));
  Div1 div1_27 (.d(d), .rem(div1_19_rem_2), .quot(div1_19_quot_2), .rem_2(div1_27_rem_2), .quot_2(div1_27_quot_2));
  Div1 div1_28 (.d(d), .rem(div1_20_rem_2), .quot(div1_20_quot_2), .rem_2(div1_28_rem_2), .quot_2(div1_28_quot_2));
  Div1 div1_29 (.d(d), .rem(div1_21_rem_2), .quot(div1_21_quot_2), .rem_2(div1_29_rem_2), .quot_2(div1_29_quot_2));
  Div1 div1_30 (.d(d), .rem(div1_22_rem_2), .quot(div1_22_quot_2), .rem_2(div1_30_rem_2), .quot_2(div1_30_quot_2));
  Div1 div1_31 (.d(d), .rem(div1_23_rem_2), .quot(div1_23_quot_2), .rem_2(div1_31_rem_2), .quot_2(div1_31_quot_2));
  Div1 div1_32 (.d(d), .rem(div1_24_rem_2), .quot(div1_24_quot_2), .rem_2(div1_32_rem_2), .quot_2(div1_32_quot_2));
  Comparator #(.width(32), .mode("twosComplement")) comparator_1 (
    .a(d), .b({32{1'b0}}), .eq(comparator_1_eq));  // open: gt, lt
  Multiplexer #(.select(1), .width(32), .disabled("Z"), .enable("false")) multiplexer_1 (
    .in0(div1_32_rem_2), .in1(d), .out(rem), .sel(comparator_1_eq));
  Multiplexer #(.select(1), .width(32), .disabled("Z"), .enable("false")) multiplexer_2 (
    .in0(div1_32_quot_2), .in1(n2), .out(quot), .sel(comparator_1_eq));
endmodule

module \_32位除法器测试电路  (
  input  [31:0] n2,
  input  [31:0] d,
  output [31:0] out_3,
  output [31:0] out_4
);

  wire [31:0] divider_1_out, divider_1_rem, \n32位除法器_1_quot , \n32位除法器_1_rem ;

  \_32位除法器  \u_32位除法器_1  (.n2(n2), .d(d), .rem(\n32位除法器_1_rem ), .quot(\n32位除法器_1_quot ));
  Divider #(.width(32)) divider_1 (.a(n2), .b(d), .out(divider_1_out), .upper({32{1'b0}}), .rem(divider_1_rem));
  assign out_3 = \n32位除法器_1_quot  ^ divider_1_out;  // XOR_Gate xor_1, 32 bits wide
  assign out_4 = \n32位除法器_1_rem  ^ divider_1_rem;  // XOR_Gate xor_2, 32 bits wide
endmodule

module Div1 (
  input  [31:0] d,
  input  [31:0] rem,
  input  [31:0] quot,
  output [31:0] rem_2,
  output [31:0] quot_2
);

  wire comparator_1_eq, comparator_1_gt, or_3_out;
  wire [31:0] or_1_out, or_2_out, shifter_1_out, shifter_2_out, shifter_3_out, subtractor_1_out;

  Shifter #(.width(32), .shift("ll")) shifter_1 (.in(rem), .\dist (5'b00001), .out(shifter_1_out));
  assign or_1_out = shifter_1_out | shifter_2_out;  // OR_Gate or_1, 32 bits wide
  Shifter #(.width(32), .shift("lr")) shifter_2 (.in(quot), .\dist ({5{1'b1}}), .out(shifter_2_out));
  Shifter #(.width(32), .shift("ll")) shifter_3 (.in(quot), .\dist (5'b00001), .out(shifter_3_out));
  Subtractor #(.width(32)) subtractor_1 (.a(or_1_out), .b(d), .out(subtractor_1_out), .bin(1'b0));  // open: bout
  Multiplexer #(.select(1), .width(32), .disabled("Z"), .enable("false")) multiplexer_1 (
    .in0(or_1_out), .in1(subtractor_1_out), .out(rem_2), .sel(or_3_out));
  Comparator #(.width(32), .mode("unsigned")) comparator_1 (
    .a(or_1_out), .b(d), .gt(comparator_1_gt), .eq(comparator_1_eq));  // open: lt
  Multiplexer #(.select(1), .width(32), .disabled("Z"), .enable("false")) multiplexer_2 (
    .in0(shifter_3_out), .in1(or_2_out), .out(quot_2), .sel(or_3_out));
  assign or_2_out = shifter_3_out | 32'h1;  // OR_Gate or_2, 32 bits wide
  or or_3 (or_3_out, comparator_1_gt, comparator_1_eq);
endmodule
